// Logisim project Adding.circ as structural Verilog: 4 circuits, main circuit addingtest
module addingtest (
  output P1,
  output P2,
  output P3,
  output P4,
  output O
);

  wire DipSwitch_1_sw1, DipSwitch_1_sw2, DipSwitch_1_sw3, DipSwitch_1_sw4, DipSwitch_1_sw5, DipSwitch_1_sw6,
       DipSwitch_1_sw7, DipSwitch_1_sw8;

  DipSwitch DipSwitch_1 (
    .sw1(DipSwitch_1_sw1), .sw2(DipSwitch_1_sw2), .sw3(DipSwitch_1_sw3), .sw4(DipSwitch_1_sw4),
    .sw5(DipSwitch_1_sw5), .sw6(DipSwitch_1_sw6), .sw7(DipSwitch_1_sw7), .sw8(DipSwitch_1_sw8));
  Additionneur Additionneur_1 (
    .A1(DipSwitch_1_sw1), .B1(DipSwitch_1_sw5), .A2(DipSwitch_1_sw2), .B2(DipSwitch_1_sw6),
    .A3(DipSwitch_1_sw3), .B3(DipSwitch_1_sw7), .A4(DipSwitch_1_sw4), .B4(DipSwitch_1_sw8), .P1(P1), .P2(P2),
    .P3(P3), .P4(P4), .O(O));
endmodule

module Additionneur (
  input  A1,
  input  B1,
  input  A2,
  input  B2,
  input  A3,
  input  B3,
  input  A4,
  input  B4,
  output P1,
  output P2,
  output P3,
  output P4,
  output O
);

  wire and_1_out, twobitadder_1_c2, twobitadder_1_s2, twobitadder_2_c2, twobitadder_2_s2, twobitadder_3_s2,
       xor_1_out;

  xor xor_1 (xor_1_out, A1, B1);
  and and_1 (and_1_out, A1, B1);
  twobitadder twobitadder_1 (.R(and_1_out), .A2(A2), .B2(B2), .S2(twobitadder_1_s2), .C2(twobitadder_1_c2));
  twobitadder twobitadder_2 (.R(twobitadder_1_c2), .A2(A3), .B2(B3), .S2(twobitadder_2_s2), .C2(twobitadder_2_c2));
  twobitadder twobitadder_3 (.R(twobitadder_2_c2), .A2(A4), .B2(B4), .S2(twobitadder_3_s2), .C2(O));
  CheckO CheckO_1 (.S(xor_1_out), .O(O), .P(P1));
  CheckO CheckO_2 (.S(twobitadder_1_s2), .O(O), .P(P2));
  CheckO CheckO_3 (.S(twobitadder_2_s2), .O(O), .P(P3));
  CheckO CheckO_4 (.S(twobitadder_3_s2), .O(O), .P(P4));
endmodule

module twobitadder (
  input  R,
  input  A2,
  input  B2,
  output S2,
  output C2
);

  wire and_1_out, and_2_out, xor_1_out;

  xor xor_1 (xor_1_out, A2, B2);
  and and_1 (and_1_out, A2, B2);
  xor xor_2 (S2, R, xor_1_out);
  and and_2 (and_2_out, R, xor_1_out);
  or or_1 (C2, and_2_out, and_1_out);
endmodule

module CheckO (
  input  S,
  input  O,
  output P
);

  wire not_1_out;

  not not_1 (not_1_out, O);
  and and_1 (P, S, not_1_out);
endmodule
