// Logisim project Alarm.circ as structural Verilog: 4 circuits, main circuit SongChoice
module SongChoice (
  input  RESET,
  input  HARRYCHOICE,
  input  ZELDACHOICE,
  input  PIRATECHOICE,
  input  SELECTIONMADE,
  output T0,
  output T1
);

  wire not_1_out, not_2_out, not_3_out, not_4_out, not_5_out, not_6_out;

  not not_1 (not_1_out, RESET);
  not not_2 (not_2_out, HARRYCHOICE);
  not not_3 (not_3_out, PIRATECHOICE);
  not not_4 (not_4_out, RESET);
  not not_5 (not_5_out, HARRYCHOICE);
  not not_6 (not_6_out, ZELDACHOICE);
  and and_1 (T0, not_1_out, not_2_out, ZELDACHOICE, not_3_out, SELECTIONMADE);
  and and_2 (T1, not_4_out, not_5_out, not_6_out, PIRATECHOICE, SELECTIONMADE);
endmodule

module AlarmDetector (
  input  [7:0] HIHOURCLOCK,
  input  [7:0] LOWHOURCLOCK,
  input  [7:0] HIMINCLOCK,
  input  [7:0] LOWMINCLOCK,
  input  [7:0] HIHOURALARM,
  input  [7:0] LOWHOURALARM,
  input  [7:0] HIMINALARM,
  input  [7:0] LOWMINALARM,
  input  ALARMACTIVATED,
  input  TURNOFF,
  output TRIGGERALARM
);

  wire and_1_out, and_2_out, and_3_out, clock_1_out, eightbitsequality_1_equal, eightbitsequality_2_equal,
       eightbitsequality_3_equal, eightbitsequality_4_equal, not_1_out, not_2_out, not_3_out, s_r_ff_2_q;

  eightbitsequality eightbitsequality_1 (.CLOCK(HIHOURCLOCK), .ALARM(HIHOURALARM), .EQUAL(eightbitsequality_1_equal));
  eightbitsequality eightbitsequality_2 (.CLOCK(LOWHOURCLOCK), .ALARM(LOWHOURALARM), .EQUAL(eightbitsequality_2_equal));
  eightbitsequality eightbitsequality_3 (.CLOCK(HIMINCLOCK), .ALARM(HIMINALARM), .EQUAL(eightbitsequality_3_equal));
  eightbitsequality eightbitsequality_4 (.CLOCK(LOWMINCLOCK), .ALARM(LOWMINALARM), .EQUAL(eightbitsequality_4_equal));
  and and_1 (and_1_out, eightbitsequality_1_equal, eightbitsequality_2_equal, eightbitsequality_3_equal, eightbitsequality_4_equal);
  not not_1 (not_1_out, TRIGGERALARM);
  and and_2 (and_2_out, TRIGGERALARM, TURNOFF);
  and and_3 (and_3_out, and_1_out, not_1_out, not_2_out, ALARMACTIVATED);
  Clock clock_1 (.out(clock_1_out));
  S_R_Flip_Flop s_r_ff_1 (
    .S(and_3_out), .R(and_2_out), .clk(clock_1_out), .Q(TRIGGERALARM));  // open: reset, Qn, preset
  S_R_Flip_Flop s_r_ff_2 (.S(and_2_out), .R(not_3_out), .clk(clock_1_out), .Q(s_r_ff_2_q));  // open: reset, Qn, preset
  not not_2 (not_2_out, s_r_ff_2_q);
  not not_3 (not_3_out, and_1_out);
endmodule

module onebitequality (
  input  B1,
  input  B2,
  output EQUAL
);

  wire and_1_out, and_2_out, not_1_out, not_2_out;

  not not_1 (not_1_out, B1);
  and and_1 (and_1_out, not_1_out, not_2_out);
  not not_2 (not_2_out, B2);
  and and_2 (and_2_out, B1, B2);
  or or_1 (EQUAL, and_1_out, and_2_out);
endmodule

module eightbitsequality (
  input  [7:0] CLOCK,
  input  [7:0] ALARM,
  output EQUAL
);

  wire onebitequality_1_equal, onebitequality_2_equal, onebitequality_3_equal, onebitequality_4_equal,
       onebitequality_5_equal, onebitequality_6_equal, onebitequality_7_equal, onebitequality_8_equal;

  onebitequality onebitequality_1 (.B1(CLOCK[0]), .B2(ALARM[0]), .EQUAL(onebitequality_1_equal));
  onebitequality onebitequality_2 (.B1(CLOCK[1]), .B2(ALARM[1]), .EQUAL(onebitequality_2_equal));
  onebitequality onebitequality_3 (.B1(CLOCK[2]), .B2(ALARM[2]), .EQUAL(onebitequality_3_equal));
  onebitequality onebitequality_4 (.B1(CLOCK[3]), .B2(ALARM[3]), .EQUAL(onebitequality_4_equal));
  onebitequality onebitequality_5 (.B1(CLOCK[4]), .B2(ALARM[4]), .EQUAL(onebitequality_5_equal));
  onebitequality onebitequality_6 (.B1(CLOCK[5]), .B2(ALARM[5]), .EQUAL(onebitequality_6_equal));
  onebitequality onebitequality_7 (.B1(CLOCK[6]), .B2(ALARM[6]), .EQUAL(onebitequality_7_equal));
  onebitequality onebitequality_8 (.B1(CLOCK[7]), .B2(ALARM[7]), .EQUAL(onebitequality_8_equal));
  and and_1 (EQUAL, onebitequality_1_equal, onebitequality_2_equal, onebitequality_3_equal, onebitequality_4_equal, onebitequality_5_equal, onebitequality_6_equal, onebitequality_7_equal, onebitequality_8_equal);
endmodule
