// Logisim project Alphabet.circ as structural Verilog: 13 circuits, main circuit Tester
module Tester (
);

  wire DipSwitch_1_sw1, DipSwitch_1_sw2, DipSwitch_1_sw3, DipSwitch_1_sw4, DipSwitch_1_sw5, sevensegA_Z_1_a,
       sevensegA_Z_1_b, sevensegA_Z_1_c, sevensegA_Z_1_d, sevensegA_Z_1_e, sevensegA_Z_1_f, sevensegA_Z_1_g;

  DipSwitch DipSwitch_1 (
    .sw1(DipSwitch_1_sw1), .sw2(DipSwitch_1_sw2), .sw3(DipSwitch_1_sw3), .sw4(DipSwitch_1_sw4),
    .sw5(DipSwitch_1_sw5));  // open: sw6, sw7, sw8
  sevensegA_Z2 sevensegA_Z_1 (
    .d(sevensegA_Z_1_d), .c(sevensegA_Z_1_c), .b(sevensegA_Z_1_b), .a(sevensegA_Z_1_a), .Z(DipSwitch_1_sw1),
    .Y(DipSwitch_1_sw2), .X(DipSwitch_1_sw3), .W(DipSwitch_1_sw4), .V(DipSwitch_1_sw5), .e(sevensegA_Z_1_e),
    .f(sevensegA_Z_1_f), .g(sevensegA_Z_1_g));
  _7_Segment_Display L_7_Segment_Display_1 (
    .g(sevensegA_Z_1_g), .f(sevensegA_Z_1_f), .a(sevensegA_Z_1_a), .b(sevensegA_Z_1_b), .e(sevensegA_Z_1_e),
    .d(sevensegA_Z_1_d), .c(sevensegA_Z_1_c));  // open: dp
endmodule

module func_a2 (
  input  V,
  input  W,
  input  X,
  input  Y,
  input  Z,
  output a
);

  wire and_1_out, and_2_out, and_3_out, and_4_out, and_5_out, and_6_out, and_7_out, and_8_out, and_9_out,
       not_1_out, not_2_out, not_3_out, not_4_out, not_5_out, not_6_out, not_7_out, not_8_out, not_9_out,
       not_10_out, not_11_out, not_12_out, not_13_out, not_14_out, not_15_out, not_16_out, not_17_out,
       not_18_out, not_19_out, not_20_out;

  not not_1 (not_1_out, W);
  not not_2 (not_2_out, X);
  not not_3 (not_3_out, Y);
  not not_4 (not_4_out, Z);
  not not_5 (not_5_out, V);
  not not_6 (not_6_out, W);
  not not_7 (not_7_out, Y);
  not not_8 (not_8_out, V);
  not not_9 (not_9_out, W);
  not not_10 (not_10_out, Z);
  not not_11 (not_11_out, V);
  not not_12 (not_12_out, Y);
  not not_13 (not_13_out, Z);
  not not_14 (not_14_out, V);
  not not_15 (not_15_out, W);
  not not_16 (not_16_out, X);
  not not_17 (not_17_out, Z);
  not not_18 (not_18_out, W);
  not not_19 (not_19_out, X);
  not not_20 (not_20_out, Y);
  and and_1 (and_1_out, not_1_out, not_2_out, not_3_out, not_4_out);
  and and_2 (and_2_out, not_5_out, not_6_out, X, not_7_out);
  and and_3 (and_3_out, not_8_out, not_9_out, X, not_10_out);
  and and_4 (and_4_out, not_11_out, X, not_12_out, not_13_out);
  and and_5 (and_5_out, not_14_out, W, X, Y, Z);
  and and_6 (and_6_out, V, not_15_out, not_16_out, not_17_out);
  and and_7 (and_7_out, V, not_18_out, X, Y, Z);
  and and_8 (and_8_out, V, W, not_19_out, Z);
  and and_9 (and_9_out, V, W, not_20_out, Z);
  or or_1 (a, and_1_out, and_2_out, and_3_out, and_4_out, and_5_out, and_6_out, and_7_out, and_8_out, and_9_out);
endmodule

module func_b2 (
  input  V,
  input  W,
  input  X,
  input  Y,
  input  Z,
  output b
);

  wire and_1_out, and_2_out, and_3_out, and_4_out, and_5_out, and_6_out, not_1_out, not_2_out, not_3_out,
       not_4_out, not_5_out, not_6_out, not_7_out, not_8_out, not_9_out, not_10_out, not_11_out, not_12_out;

  not not_1 (not_1_out, X);
  not not_2 (not_2_out, Y);
  not not_3 (not_3_out, Z);
  not not_4 (not_4_out, W);
  not not_5 (not_5_out, X);
  not not_6 (not_6_out, W);
  not not_7 (not_7_out, Z);
  not not_8 (not_8_out, V);
  not not_9 (not_9_out, X);
  not not_10 (not_10_out, Y);
  not not_11 (not_11_out, Y);
  not not_12 (not_12_out, Z);
  and and_1 (and_1_out, not_1_out, not_2_out, not_3_out);
  and and_2 (and_2_out, not_4_out, not_5_out, Y, Z);
  and and_3 (and_3_out, not_6_out, X, Y, not_7_out);
  and and_4 (and_4_out, not_8_out, X, Y, Z);
  and and_5 (and_5_out, W, not_9_out, not_10_out);
  and and_6 (and_6_out, V, not_11_out, not_12_out);
  or or_1 (b, and_1_out, and_2_out, and_3_out, and_4_out, and_5_out, and_6_out);
endmodule

module func_c2 (
  input  V,
  input  W,
  input  X,
  input  Y,
  input  Z,
  output c
);

  wire and_1_out, and_2_out, and_3_out, and_4_out, and_5_out, and_6_out, and_7_out, and_8_out, not_1_out,
       not_2_out, not_3_out, not_4_out, not_5_out, not_6_out, not_7_out, not_8_out, not_9_out, not_10_out,
       not_11_out, not_12_out, not_13_out, not_14_out, not_15_out, not_16_out, not_17_out;

  not not_1 (not_1_out, V);
  not not_2 (not_2_out, X);
  not not_3 (not_3_out, Y);
  not not_4 (not_4_out, X);
  not not_5 (not_5_out, Y);
  not not_6 (not_6_out, Z);
  not not_7 (not_7_out, W);
  not not_8 (not_8_out, X);
  not not_9 (not_9_out, V);
  not not_10 (not_10_out, W);
  not not_11 (not_11_out, V);
  not not_12 (not_12_out, Z);
  not not_13 (not_13_out, V);
  not not_14 (not_14_out, Y);
  not not_15 (not_15_out, X);
  not not_16 (not_16_out, Z);
  not not_17 (not_17_out, Y);
  and and_1 (and_1_out, not_1_out, not_2_out, not_3_out);
  and and_2 (and_2_out, not_4_out, not_5_out, not_6_out);
  and and_3 (and_3_out, not_7_out, not_8_out, Y, Z);
  and and_4 (and_4_out, not_9_out, not_10_out, X, Y);
  and and_5 (and_5_out, not_11_out, X, Y, not_12_out);
  and and_6 (and_6_out, not_13_out, W, not_14_out);
  and and_7 (and_7_out, V, not_15_out, not_16_out);
  and and_8 (and_8_out, V, X, not_17_out);
  or or_1 (c, and_1_out, and_2_out, and_3_out, and_4_out, and_5_out, and_6_out, and_7_out, and_8_out);
endmodule

module func_d2 (
  input  V,
  input  W,
  input  X,
  input  Y,
  input  Z,
  output d
);

  wire and_1_out, and_2_out, and_3_out, and_4_out, and_5_out, and_6_out, not_1_out, not_2_out, not_3_out,
       not_4_out, not_5_out, not_6_out, not_7_out, not_8_out;

  not not_1 (not_1_out, V);
  not not_2 (not_2_out, X);
  not not_3 (not_3_out, Z);
  not not_4 (not_4_out, W);
  not not_5 (not_5_out, Z);
  not not_6 (not_6_out, W);
  not not_7 (not_7_out, X);
  not not_8 (not_8_out, Y);
  and and_1 (and_1_out, not_1_out, not_2_out, Z);
  and and_2 (and_2_out, Y, not_3_out);
  and and_3 (and_3_out, not_4_out, X, not_5_out);
  and and_4 (and_4_out, V, not_6_out, X);
  and and_5 (and_5_out, V, W, not_7_out);
  and and_6 (and_6_out, V, W, not_8_out);
  or or_1 (d, and_1_out, and_2_out, and_3_out, and_4_out, and_5_out, and_6_out);
endmodule

module func_e2 (
  input  V,
  input  W,
  input  X,
  input  Y,
  input  Z,
  output e
);

  wire and_1_out, and_2_out, and_3_out, and_4_out, and_5_out, and_6_out, not_1_out, not_2_out, not_3_out,
       not_4_out, not_5_out, not_6_out, not_7_out, not_8_out, not_9_out;

  not not_1 (not_1_out, V);
  not not_2 (not_2_out, W);
  not not_3 (not_3_out, X);
  not not_4 (not_4_out, V);
  not not_5 (not_5_out, Y);
  not not_6 (not_6_out, V);
  not not_7 (not_7_out, X);
  not not_8 (not_8_out, Y);
  not not_9 (not_9_out, Z);
  and and_1 (and_1_out, not_1_out, not_2_out, not_3_out);
  and and_2 (and_2_out, not_4_out, Z);
  and and_3 (and_3_out, not_5_out, Z);
  and and_4 (and_4_out, not_6_out, not_7_out, Y);
  and and_5 (and_5_out, X, not_8_out);
  and and_6 (and_6_out, W, X, not_9_out);
  or or_1 (e, and_1_out, and_2_out, and_3_out, and_4_out, and_5_out, and_6_out);
endmodule

module func_f2 (
  input  V,
  input  W,
  input  X,
  input  Y,
  input  Z,
  output f
);

  wire and_1_out, and_2_out, and_3_out, and_4_out, and_5_out, not_1_out, not_2_out, not_3_out, not_4_out,
       not_5_out, not_6_out, not_7_out, not_8_out;

  not not_1 (not_1_out, V);
  not not_2 (not_2_out, W);
  not not_3 (not_3_out, Y);
  not not_4 (not_4_out, W);
  not not_5 (not_5_out, Z);
  not not_6 (not_6_out, V);
  not not_7 (not_7_out, X);
  not not_8 (not_8_out, Z);
  and and_1 (and_1_out, not_1_out, not_2_out, not_3_out);
  and and_2 (and_2_out, not_4_out, X, not_5_out);
  and and_3 (and_3_out, not_6_out, X, Y, Z);
  and and_4 (and_4_out, W, not_7_out, Y);
  and and_5 (and_5_out, V, not_8_out);
  or or_1 (f, and_1_out, and_2_out, and_3_out, and_4_out, and_5_out);
endmodule

module func_g2 (
  input  V,
  input  W,
  input  X,
  input  Y,
  input  Z,
  output g
);

  wire and_1_out, and_2_out, and_3_out, and_4_out, and_5_out, not_1_out, not_2_out, not_3_out, not_4_out,
       not_5_out, not_6_out, not_7_out;

  not not_1 (not_1_out, V);
  not not_2 (not_2_out, W);
  not not_3 (not_3_out, V);
  not not_4 (not_4_out, Z);
  not not_5 (not_5_out, W);
  not not_6 (not_6_out, V);
  not not_7 (not_7_out, X);
  and and_1 (and_1_out, not_1_out, not_2_out);
  and and_2 (and_2_out, not_3_out, Y, not_4_out);
  and and_3 (and_3_out, not_5_out, Y, Z);
  and and_4 (and_4_out, not_6_out, X, Z);
  and and_5 (and_5_out, V, not_7_out);
  or or_1 (g, and_1_out, and_2_out, and_3_out, and_4_out, and_5_out);
endmodule

module sevensegA_Z2 (
  input  V,
  input  W,
  input  X,
  input  Y,
  input  Z,
  output a,
  output b,
  output c,
  output d,
  output e,
  output f,
  output g
);

  func_a2 fonction_a_1 (.V(V), .W(W), .X(X), .Y(Y), .Z(Z), .a(a));
  func_b2 fonction_b_1 (.V(V), .W(W), .X(X), .Y(Y), .Z(Z), .b(b));
  func_c2 fonction_c_1 (.V(V), .W(W), .X(X), .Y(Y), .Z(Z), .c(c));
  func_d2 fonction_d_1 (.V(V), .W(W), .X(X), .Y(Y), .Z(Z), .d(d));
  func_e2 fonction_e_1 (.V(V), .W(W), .X(X), .Y(Y), .Z(Z), .e(e));
  func_f2 fonction_f_1 (.V(V), .W(W), .X(X), .Y(Y), .Z(Z), .f(f));
  func_g2 fonction_g_1 (.V(V), .W(W), .X(X), .Y(Y), .Z(Z), .g(g));
endmodule

module sevensegBUS2 (
  input  [5:0] LETTER,
  output [7:0] LETTERCODE
);

  sevensegA_Z2 sevensegA_Z2_1 (
    .d(LETTERCODE[3]), .c(LETTERCODE[2]), .b(LETTERCODE[1]), .a(LETTERCODE[0]), .Z(LETTER[1]), .Y(LETTER[2]),
    .X(LETTER[3]), .W(LETTER[4]), .V(LETTER[5]), .e(LETTERCODE[4]), .f(LETTERCODE[5]), .g(LETTERCODE[6]));

  assign LETTERCODE[7] = LETTER[0];
endmodule

module BUSAFFICHE (
  input  [7:0] Input_bus_1
);

  _7_Segment_Display L_7_Segment_Display_1 (
    .g(Input_bus_1[6]), .f(Input_bus_1[5]), .a(Input_bus_1[0]), .b(Input_bus_1[1]), .e(Input_bus_1[4]),
    .d(Input_bus_1[3]), .c(Input_bus_1[2]), .dp(Input_bus_1[7]));
endmodule

module onetoeight (
  input  [5:0] LETTER,
  output a,
  output b,
  output c,
  output d,
  output e,
  output f,
  output g,
  output deci
);

  sevensegBUS2 sevensegbus2_1 (.LETTER(LETTER), .LETTERCODE({deci, g, f, e, d, c, b, a}));
endmodule

module fivetoeight (
  input  [4:0] LETTERIN,
  output [7:0] letterout
);

  sevensegA_Z2 sevensegA_Z2_1 (
    .d(letterout[3]), .c(letterout[2]), .b(letterout[1]), .a(letterout[0]), .Z(LETTERIN[0]), .Y(LETTERIN[1]),
    .X(LETTERIN[2]), .W(LETTERIN[3]), .V(LETTERIN[4]), .e(letterout[4]), .f(letterout[5]), .g(letterout[6]));

  assign letterout[7] = 1'b0;
endmodule
