// Logisim project LEDController.circ as structural Verilog: 3 circuits, main circuit LEDDFF
module LEDDFF (
  input  LED8IN,
  input  LED7IN,
  input  LED6IN,
  input  LED5IN,
  input  LED4IN,
  input  LED3IN,
  input  LED2IN,
  input  LED1IN,
  input  clock,
  output LED8,
  output LED7,
  output LED6,
  output LED5,
  output LED4,
  output LED3,
  output LED2,
  output LED1
);

  D_Flip_Flop d_ff_1 (.D(LED8IN), .clk(clock), .Q(LED8));  // open: Qn, preset, reset
  D_Flip_Flop d_ff_2 (.D(LED7IN), .clk(clock), .Q(LED7));  // open: Qn, preset, reset
  D_Flip_Flop d_ff_3 (.D(LED6IN), .clk(clock), .Q(LED6));  // open: Qn, preset, reset
  D_Flip_Flop d_ff_4 (.D(LED5IN), .clk(clock), .Q(LED5));  // open: Qn, preset, reset
  D_Flip_Flop d_ff_5 (.D(LED4IN), .clk(clock), .Q(LED4));  // open: Qn, preset, reset
  D_Flip_Flop d_ff_6 (.D(LED3IN), .clk(clock), .Q(LED3));  // open: Qn, preset, reset
  D_Flip_Flop d_ff_7 (.D(LED2IN), .clk(clock), .Q(LED2));  // open: Qn, preset, reset
  D_Flip_Flop d_ff_8 (.D(LED1IN), .clk(clock), .Q(LED1));  // open: Qn, preset, reset
endmodule

module anim1states (
  input  ENABLE,
  input  LED8,
  input  LED7,
  input  LED6,
  input  LED5,
  input  LED4,
  input  LED3,
  input  LED2,
  input  LED1,
  output LED8O,
  output LED7O,
  output LED6O,
  output LED5O,
  output LED4O,
  output LED3O,
  output LED2O,
  output LED1O
);

  wire and_1_out, and_2_out, and_3_out, and_4_out, and_5_out, and_6_out, and_7_out, and_8_out, and_9_out,
       and_10_out, and_11_out, and_12_out, and_13_out, and_14_out, and_15_out, and_16_out, and_17_out,
       and_18_out, and_19_out, and_20_out, and_21_out, and_22_out, and_23_out, and_24_out, and_25_out,
       and_26_out, and_27_out, and_28_out, and_29_out, and_30_out, and_31_out, and_32_out, and_33_out,
       and_34_out, and_35_out, and_36_out, and_37_out, and_38_out, and_39_out, and_40_out, and_41_out,
       and_42_out, and_43_out, and_44_out, and_45_out, and_46_out, and_47_out, and_48_out, and_49_out,
       and_50_out, and_51_out, and_52_out, and_53_out, and_54_out, and_55_out, and_56_out, and_57_out,
       and_58_out, and_59_out, and_60_out, and_61_out, and_62_out, and_63_out, and_64_out, and_65_out,
       and_66_out, and_67_out, and_68_out, not_1_out, not_2_out, not_3_out, not_4_out, not_5_out, not_6_out,
       not_7_out, not_8_out, not_9_out, not_10_out, not_11_out, not_12_out, not_13_out, not_14_out,
       not_15_out, not_16_out, not_17_out, not_18_out, not_19_out, not_20_out, not_21_out, not_22_out,
       not_23_out, not_24_out, not_25_out, not_26_out, not_27_out, not_28_out, not_29_out, not_30_out,
       not_31_out, not_32_out, not_33_out, not_34_out, not_35_out, not_36_out;

  not not_1 (not_1_out, LED6);
  not not_2 (not_2_out, LED8);
  not not_3 (not_3_out, LED4);
  not not_4 (not_4_out, LED6);
  not not_5 (not_5_out, LED2);
  not not_6 (not_6_out, LED7);
  not not_7 (not_7_out, LED5);
  not not_8 (not_8_out, LED3);
  not not_9 (not_9_out, LED1);
  not not_10 (not_10_out, LED6);
  not not_11 (not_11_out, LED8);
  not not_12 (not_12_out, LED4);
  not not_13 (not_13_out, LED6);
  not not_14 (not_14_out, LED2);
  not not_15 (not_15_out, LED7);
  not not_16 (not_16_out, LED5);
  not not_17 (not_17_out, LED3);
  not not_18 (not_18_out, LED1);
  not not_19 (not_19_out, LED6);
  not not_20 (not_20_out, LED8);
  not not_21 (not_21_out, LED4);
  not not_22 (not_22_out, LED6);
  not not_23 (not_23_out, LED2);
  not not_24 (not_24_out, LED7);
  not not_25 (not_25_out, LED5);
  not not_26 (not_26_out, LED3);
  not not_27 (not_27_out, LED1);
  not not_28 (not_28_out, LED6);
  not not_29 (not_29_out, LED8);
  not not_30 (not_30_out, LED4);
  not not_31 (not_31_out, LED6);
  not not_32 (not_32_out, LED2);
  not not_33 (not_33_out, LED7);
  not not_34 (not_34_out, LED5);
  not not_35 (not_35_out, LED3);
  not not_36 (not_36_out, LED1);
  and and_1 (and_1_out, ENABLE, LED1);
  and and_2 (and_2_out, ENABLE, not_1_out, LED2);
  and and_3 (and_3_out, ENABLE, LED3);
  and and_4 (and_4_out, ENABLE, not_2_out, LED4);
  and and_5 (and_5_out, ENABLE, LED5);
  and and_6 (and_6_out, ENABLE, LED6, not_3_out);
  and and_7 (and_7_out, ENABLE, LED7);
  and and_8 (and_8_out, ENABLE, LED8, not_4_out);
  and and_9 (and_9_out, ENABLE, LED8, not_5_out);
  and and_10 (and_10_out, ENABLE, not_6_out);
  and and_11 (and_11_out, ENABLE, not_7_out);
  and and_12 (and_12_out, ENABLE, not_8_out);
  and and_13 (and_13_out, ENABLE, not_9_out);
  and and_14 (and_14_out, ENABLE, LED2);
  and and_15 (and_15_out, ENABLE, LED4);
  and and_16 (and_16_out, ENABLE, LED6);
  and and_17 (and_17_out, ENABLE, LED8);
  and and_18 (and_18_out, ENABLE, LED1);
  and and_19 (and_19_out, ENABLE, not_10_out, LED2);
  and and_20 (and_20_out, ENABLE, LED3);
  and and_21 (and_21_out, ENABLE, not_11_out, LED4);
  and and_22 (and_22_out, ENABLE, LED5);
  and and_23 (and_23_out, ENABLE, LED6, not_12_out);
  and and_24 (and_24_out, ENABLE, LED7);
  and and_25 (and_25_out, ENABLE, LED8, not_13_out);
  and and_26 (and_26_out, ENABLE, LED8, not_14_out);
  and and_27 (and_27_out, ENABLE, not_15_out);
  and and_28 (and_28_out, ENABLE, not_16_out);
  and and_29 (and_29_out, ENABLE, not_17_out);
  and and_30 (and_30_out, ENABLE, not_18_out);
  and and_31 (and_31_out, ENABLE, LED2);
  and and_32 (and_32_out, ENABLE, LED4);
  and and_33 (and_33_out, ENABLE, LED6);
  and and_34 (and_34_out, ENABLE, LED8);
  and and_35 (and_35_out, ENABLE, LED1);
  and and_36 (and_36_out, ENABLE, not_19_out, LED2);
  and and_37 (and_37_out, ENABLE, LED3);
  and and_38 (and_38_out, ENABLE, not_20_out, LED4);
  and and_39 (and_39_out, ENABLE, LED5);
  and and_40 (and_40_out, ENABLE, LED6, not_21_out);
  and and_41 (and_41_out, ENABLE, LED7);
  and and_42 (and_42_out, ENABLE, LED8, not_22_out);
  and and_43 (and_43_out, ENABLE, LED8, not_23_out);
  and and_44 (and_44_out, ENABLE, not_24_out);
  and and_45 (and_45_out, ENABLE, not_25_out);
  and and_46 (and_46_out, ENABLE, not_26_out);
  and and_47 (and_47_out, ENABLE, not_27_out);
  and and_48 (and_48_out, ENABLE, LED2);
  and and_49 (and_49_out, ENABLE, LED4);
  and and_50 (and_50_out, ENABLE, LED6);
  and and_51 (and_51_out, ENABLE, LED8);
  and and_52 (and_52_out, ENABLE, LED1);
  and and_53 (and_53_out, ENABLE, not_28_out, LED2);
  and and_54 (and_54_out, ENABLE, LED3);
  and and_55 (and_55_out, ENABLE, not_29_out, LED4);
  and and_56 (and_56_out, ENABLE, LED5);
  and and_57 (and_57_out, ENABLE, LED6, not_30_out);
  and and_58 (and_58_out, ENABLE, LED7);
  and and_59 (and_59_out, ENABLE, LED8, not_31_out);
  and and_60 (and_60_out, ENABLE, LED8, not_32_out);
  and and_61 (and_61_out, ENABLE, not_33_out);
  and and_62 (and_62_out, ENABLE, not_34_out);
  and and_63 (and_63_out, ENABLE, not_35_out);
  and and_64 (and_64_out, ENABLE, not_36_out);
  and and_65 (and_65_out, ENABLE, LED2);
  and and_66 (and_66_out, ENABLE, LED4);
  and and_67 (and_67_out, ENABLE, LED6);
  and and_68 (and_68_out, ENABLE, LED8);
  or or_1 (LED8O, and_1_out, and_2_out, and_3_out, and_4_out, and_5_out, and_6_out, and_7_out, and_8_out, and_9_out);
  or or_2 (LED7O, and_10_out, and_11_out, and_12_out, and_13_out, and_14_out, and_15_out, and_16_out, and_17_out);
  or or_3 (LED6O, and_18_out, and_19_out, and_20_out, and_21_out, and_22_out, and_23_out, and_24_out, and_25_out, and_26_out);
  or or_4 (LED5O, and_27_out, and_28_out, and_29_out, and_30_out, and_31_out, and_32_out, and_33_out, and_34_out);
  or or_5 (LED4O, and_35_out, and_36_out, and_37_out, and_38_out, and_39_out, and_40_out, and_41_out, and_42_out, and_43_out);
  or or_6 (LED3O, and_44_out, and_45_out, and_46_out, and_47_out, and_48_out, and_49_out, and_50_out, and_51_out);
  or or_7 (LED2O, and_52_out, and_53_out, and_54_out, and_55_out, and_56_out, and_57_out, and_58_out, and_59_out, and_60_out);
  or or_8 (LED1O, and_61_out, and_62_out, and_63_out, and_64_out, and_65_out, and_66_out, and_67_out, and_68_out);
endmodule

module anim1 (
  input  ENABLE,
  output LED8,
  output LED7,
  output LED6,
  output LED5,
  output LED4,
  output LED3,
  output LED2,
  output LED1
);

  wire anim1states_1_led1o, anim1states_1_led2o, anim1states_1_led3o, anim1states_1_led4o,
       anim1states_1_led5o, anim1states_1_led6o, anim1states_1_led7o, anim1states_1_led8o, clock_1_out;

  anim1states anim1states_1 (
    .ENABLE(ENABLE), .LED8(LED8), .LED7(LED7), .LED6(LED6), .LED5(LED5), .LED4(LED4), .LED3(LED3),
    .LED2(LED2), .LED1(LED1), .LED8O(anim1states_1_led8o), .LED7O(anim1states_1_led7o),
    .LED6O(anim1states_1_led6o), .LED5O(anim1states_1_led5o), .LED4O(anim1states_1_led4o),
    .LED3O(anim1states_1_led3o), .LED2O(anim1states_1_led2o), .LED1O(anim1states_1_led1o));
  Clock #(.highDuration(16000), .lowDuration(16000)) clock_1 (.out(clock_1_out));
  LEDDFF LEDDFF_1 (
    .LED8IN(anim1states_1_led8o), .LED7IN(anim1states_1_led7o), .LED6IN(anim1states_1_led6o),
    .LED5IN(anim1states_1_led5o), .LED4IN(anim1states_1_led4o), .LED3IN(anim1states_1_led3o),
    .LED2IN(anim1states_1_led2o), .LED1IN(anim1states_1_led1o), .clock(clock_1_out), .LED8(LED8),
    .LED7(LED7), .LED6(LED6), .LED5(LED5), .LED4(LED4), .LED3(LED3), .LED2(LED2), .LED1(LED1));
endmodule
