// Logisim project MAINCIRCUIT.circ as structural Verilog: 47 circuits, main circuit main
module main (
  input  SELECTION,
  input  CYCLE,
  output BUZZER
);

  wire ALARMACTIV, ALLOWMUS, ALOFF, and_1_out, buttonFSM_1_cycle, buzz, buzzer_t, CAL, calcmode, ccalc,
       CCHRONO, CHANAL, chrono, clock_1_out, CMUSIC, ctimer, CZONES, d_ff_1_q, d_ff_2_q,
       demultiplexer_1_out1, demultiplexer_1_out2, demultiplexer_1_out3, demultiplexer_1_out4,
       demultiplexer_1_out5, demultiplexer_1_out6, demultiplexer_1_out7, demultiplexer_1_out8, FLIP, fnum,
       himin, LEDAnim_1_led1, LEDAnim_1_led2, LEDAnim_1_led3, LEDAnim_1_led4, LEDAnim_1_led5, LEDAnim_1_led6,
       LEDAnim_1_led7, LEDAnim_1_led8, LongPressReset_1_selectout, lowms, LP, msg, operator, or_1_out,
       or_2_out, or_3_out, or_4_out, or_5_out, or_7_out, r, secondnum, setting, showans, Splitter1to6IN_1_b0,
       Splitter1to6IN_1_b1, Splitter1to6IN_1_b2, Splitter1to6IN_1_b3, Splitter1to6IN_1_b4,
       Splitter1to6IN_1_b5, SubMenus_1_chanalarm, SubMenus_1_done, tdone, toff, tset, tsetout, zp;
  wire [2:0] musAff_1_harryplaying, submenuscontroller_1_t0;
  wire [3:0] conditionSetTime_1_pout, FSM_FINAL_1_p1, mode_clock_1_day0out, mode_clock_1_day1out,
       mode_clock_1_h0out, mode_clock_1_h1out;
  wire [4:1] setnumbs;
  wire [6:0] MODES;
  wire [7:0] AlarmAffichage_1_hiday, AlarmAffichage_1_hihour, AlarmAffichage_1_himin,
       AlarmAffichage_1_lowday, AlarmAffichage_1_lowhour, AlarmAffichage_1_lowmin, calcAff_1_aff1,
       calcAff_1_aff2, calcAff_1_aff3, calcAff_1_aff4, calcAff_1_aff5, calcAff_1_aff6,
       chronoAffiche_1_chrono1, chronoAffiche_1_chrono2, chronoAffiche_1_chrono3, chronoAffiche_1_chrono4,
       chronoAffiche_1_chrono5, chronoAffiche_1_chrono6, dhi, dlow, GIGAPLEX_1_aff1, GIGAPLEX_1_aff2,
       GIGAPLEX_1_aff3, GIGAPLEX_1_aff4, GIGAPLEX_1_aff5, GIGAPLEX_1_aff6, hhi, hlow, MainMenuAff_firstdig,
       MainMenuAff_fithdig, MainMenuAff_fourthdig, MainMenuAff_seconddig, MainMenuAff_sixthdig,
       MainMenuAff_thirddig, mode_clock_1_himin, mode_clock_1_lowmin, MSGAFF_1_aff1, MSGAFF_1_aff2,
       MSGAFF_1_aff3, MSGAFF_1_aff4, MSGAFF_1_aff5, MSGAFF_1_aff6, musAff_1_aff1, musAff_1_aff2,
       musAff_1_aff3, musAff_1_aff4, musAff_1_aff5, musAff_1_aff6, RINGANIMATION_1_aff1,
       RINGANIMATION_1_aff2, RINGANIMATION_1_aff3, RINGANIMATION_1_aff4, RINGANIMATION_1_aff5,
       RINGANIMATION_1_aff6, TIMERAFF_1_aff1, TIMERAFF_1_aff2, TIMERAFF_1_aff3, TIMERAFF_1_aff4,
       TIMERAFF_1_aff5, TIMERAFF_1_aff6, zonesAffichage_1_aff1z, zonesAffichage_1_aff2z,
       zonesAffichage_1_aff3z, zonesAffichage_1_aff4z, zonesAffichage_1_aff5z, zonesAffichage_1_aff6z;
  wire [15:0] info, sp2_busout, Splitter2to1OUT_1_busout, Splitter2to1OUT_3_busout, Splitter2to1OUT_4_busout,
       Splitter2to1OUT_5_busout, Splitter2to1OUT_6_busout, Splitter2to1OUT_7_busout,
       Splitter2to1OUT_8_busout, Splitter2to1OUT_9_busout;
  wire [31:0] sp4_busout, Splitter4to1OUT_1_busout, Splitter4to1OUT_3_busout, Splitter4to1OUT_4_busout,
       Splitter4to1OUT_5_busout, Splitter4to1OUT_6_busout, Splitter4to1OUT_7_busout,
       Splitter4to1OUT_8_busout, Splitter4to1OUT_9_busout;

  Clock clock_1 (.out(clock_1_out));
  D_Flip_Flop d_ff_1 (.D(CYCLE), .clk(clock_1_out), .Q(d_ff_1_q));  // open: Qn, preset, reset
  DipSwitch #(.number(10)) DipSwitch_1 (
    .sw1(lowms), .sw2(setnumbs[1]), .sw3(setnumbs[2]), .sw4(setnumbs[3]), .sw5(setnumbs[4]), .sw6(himin),
    .sw8(toff), .sw9(ALOFF), .sw10(ALARMACTIV));  // open: sw7
  D_Flip_Flop d_ff_2 (.D(SELECTION), .clk(clock_1_out), .Q(d_ff_2_q));  // open: Qn, preset, reset
  LED ALARM (.in(ALARMACTIV));
  or or_1 (or_1_out, SubMenus_1_done, r);
  LongPressReset LongPressReset_1 (.SELECTION(d_ff_2_q), .RESET(r), .SELECTOUT(LongPressReset_1_selectout));
  buttonFSM buttonFSM_1 (
    .BUTTON(d_ff_1_q), .SETTIME(MODES[0]), .FLIP(FLIP), .MUSIC(MODES[1]), .ALARM(CHANAL),
    .MUSALARM(MODES[3]), .TRIGGERIN(MODES[4]), .ZONES(MODES[5]), .CYCLE(buttonFSM_1_cycle), .CHRONO(chrono),
    .TIMER(MODES[6]), .CALC(calcmode), .CYCLEMUSIC(CMUSIC), .CYCLEALARM(CAL), .CZONES(CZONES),
    .CCHRONO(CCHRONO), .CTIMER(ctimer), .CCALC(ccalc));  // open: TRIGGEROUT
  fourxconv fourxconv_1 (
    .D1(info[3:0]), .D0(info[7:4]), .H1(info[11:8]), .H0(info[15:12]),
    .dip({setnumbs[2], setnumbs[3], setnumbs[4], himin}), .settime(MODES[0]), .DAYHHIOUT(dhi),
    .DAYLOWOUT(dlow), .HOURHIOUT(hhi), .HOURLOWOUT(hlow));
  Splitter1to6IN Splitter1to6IN_1 (
    .B4(Splitter1to6IN_1_b4), .B3(Splitter1to6IN_1_b3), .B2(Splitter1to6IN_1_b2), .B1(Splitter1to6IN_1_b1),
    .B0(Splitter1to6IN_1_b0), .BUSIN({lowms, setnumbs[1], setnumbs[2], setnumbs[3], setnumbs[4], himin}),
    .B5(Splitter1to6IN_1_b5));
  or or_2 (or_2_out, r, ~ALLOWMUS);  // OR_Gate
  FSM_FINAL FSM_FINAL_1 (
    .B(buttonFSM_1_cycle), .RESET(or_1_out), .P1(FSM_FINAL_1_p1[0]), .P2(FSM_FINAL_1_p1[1]),
    .P3(FSM_FINAL_1_p1[2]), .P4(FSM_FINAL_1_p1[3]));
  mode_clock mode_clock_1 (
    .RESET(r), .FLIP(FLIP), .SETDIGIT(MODES[0]), .HHOUR(Splitter1to6IN_1_b0), .LHOUR(Splitter1to6IN_1_b1),
    .HMIN(Splitter1to6IN_1_b2), .LMIN(Splitter1to6IN_1_b3), .HSEC(Splitter1to6IN_1_b4),
    .LSEC(Splitter1to6IN_1_b5), .HIMIN(mode_clock_1_himin), .LOWMIN(mode_clock_1_lowmin),
    .DAY1OUT(mode_clock_1_day1out), .DAY0OUT(mode_clock_1_day0out), .H1OUT(mode_clock_1_h1out),
    .H0OUT(mode_clock_1_h0out));  // open: HIHOUR, LOWHOUR, HIDAY, LOWDAY
  musAff musAff_1 (
    .CYCLE(CMUSIC), .RESET(or_2_out), .BUZZER(buzzer_t), .HARRYPLAYING(musAff_1_harryplaying[0]),
    .ZELDAPLAYING(zp), .ODEPLAYING(musAff_1_harryplaying[2]), .AFF1(musAff_1_aff1), .AFF2(musAff_1_aff2),
    .AFF3(musAff_1_aff3), .AFF4(musAff_1_aff4), .AFF5(musAff_1_aff5), .AFF6(musAff_1_aff6));
  Splitter4to1OUT sp4 (
    .BUSOUT(sp4_busout), .CENTER2(musAff_1_aff3), .MSB(musAff_1_aff4), .CENTER1(musAff_1_aff2),
    .LSB(musAff_1_aff1));
  Splitter2to1OUT sp2 (.BUSOUT(sp2_busout), .MSB(musAff_1_aff6), .LSB(musAff_1_aff5));
  Demultiplexer #(.select(4), .enable("false")) demultiplexer_1 (
    .out1(demultiplexer_1_out1), .out2(demultiplexer_1_out2), .out3(demultiplexer_1_out3),
    .out4(demultiplexer_1_out4), .out5(demultiplexer_1_out5), .out6(demultiplexer_1_out6),
    .out7(demultiplexer_1_out7), .out8(demultiplexer_1_out8), .in(1'b1), .sel(FSM_FINAL_1_p1));  // open: out0, out9, out10, out11, out12, out13, out14, out15
  conditionSetTime conditionSetTime_1 (.POUT(conditionSetTime_1_pout), .SETTIME(MODES[0]), .PENTER(FSM_FINAL_1_p1));
  Splitter4to1OUT Splitter4to1OUT_1 (
    .BUSOUT(Splitter4to1OUT_1_busout), .CENTER2(MainMenuAff_thirddig), .MSB(MainMenuAff_fourthdig),
    .CENTER1(MainMenuAff_seconddig), .LSB(MainMenuAff_firstdig));
  MainMenuAffichage MainMenuAff (
    .OPTIONS(conditionSetTime_1_pout), .HIMIN(mode_clock_1_himin), .LOWMIN(mode_clock_1_lowmin),
    .HIHOUR(hhi), .LOWHOUR(hlow), .HIDAY(dhi), .LOWDAY(dlow), .FIRSTDIG(MainMenuAff_firstdig),
    .SECONDDIG(MainMenuAff_seconddig), .THIRDDIG(MainMenuAff_thirddig), .FOURTHDIG(MainMenuAff_fourthdig),
    .FITHDIG(MainMenuAff_fithdig), .SIXTHDIG(MainMenuAff_sixthdig));
  Splitter2to1OUT Splitter2to1OUT_1 (
    .BUSOUT(Splitter2to1OUT_1_busout), .MSB(MainMenuAff_sixthdig), .LSB(MainMenuAff_fithdig));
  AlarmAffichage AlarmAffichage_1 (
    .HIMINCLOCK(mode_clock_1_himin), .LMINCLOCK(mode_clock_1_lowmin), .HIHOURCLOCK(hhi), .LHOURCLOCK(hlow),
    .CYCLEALARM(CAL), .SHIHOUR(setnumbs[3]), .SLOWHOUR(setnumbs[2]), .SHIMIN(setnumbs[1]), .SLOWMIN(lowms),
    .RESET(r), .ALARMACTI(ALARMACTIV), .TURNOFF(ALOFF), .HARRYCHOICE(musAff_1_harryplaying[0]),
    .ZELDACHOICE(zp), .PIRATECHOICE(musAff_1_harryplaying[2]), .MODIFY(CHANAL), .TRIGGER(MODES[4]),
    .HIDAY(AlarmAffichage_1_hiday), .LOWDAY(AlarmAffichage_1_lowday), .HIHOUR(AlarmAffichage_1_hihour),
    .LOWHOUR(AlarmAffichage_1_lowhour), .HIMIN(AlarmAffichage_1_himin), .LOWMIN(AlarmAffichage_1_lowmin),
    .BUZZ(buzz));
  Splitter4to1OUT Splitter4to1OUT_4 (
    .BUSOUT(Splitter4to1OUT_4_busout), .CENTER2(AlarmAffichage_1_hihour), .MSB(AlarmAffichage_1_lowhour),
    .CENTER1(AlarmAffichage_1_lowday), .LSB(AlarmAffichage_1_hiday));
  Splitter2to1OUT Splitter2to1OUT_4 (
    .BUSOUT(Splitter2to1OUT_4_busout), .MSB(AlarmAffichage_1_lowmin), .LSB(AlarmAffichage_1_himin));
  SubMenus SubMenus_1 (
    .SETTIMER(setting), .CHANMUS(MODES[1]), .CHANMUSIC(MODES[3]), .CHANTIME(MODES[0]),
    .CURMUSIC(demultiplexer_1_out7), .RESET(r), .CHANMODEALARM(CHANAL), .CHRONO(demultiplexer_1_out3),
    .MOTIV(demultiplexer_1_out6), .TOFF(toff), .TIMER(demultiplexer_1_out2), .LONGPRESSCALC(LP),
    .TIMERUNNING(tsetout), .CURZONES(demultiplexer_1_out4), .CURSETTIME(demultiplexer_1_out1),
    .CALC(demultiplexer_1_out8), .SELECTION(LongPressReset_1_selectout), .CHANALARM(SubMenus_1_chanalarm),
    .DONE(SubMenus_1_done), .CURALARM(demultiplexer_1_out5), .CHANMODEZONES(MODES[5]),
    .CHANMODETIMER(MODES[6]), .TIMERACTIV(tset), .CHANCHRONO(chrono), .CHANMSG(msg), .FIRSTNUM(fnum),
    .CHANGECALC(calcmode), .OPERATOR(operator), .SECONDNUM(secondnum), .SHOWANS(showans));
  RINGANIMATION RINGANIMATION_1 (
    .AFF1(RINGANIMATION_1_aff1), .AFF2(RINGANIMATION_1_aff2), .AFF3(RINGANIMATION_1_aff3),
    .AFF4(RINGANIMATION_1_aff4), .AFF5(RINGANIMATION_1_aff5), .AFF6(RINGANIMATION_1_aff6));
  Splitter4to1OUT Splitter4to1OUT_3 (
    .BUSOUT(Splitter4to1OUT_3_busout), .CENTER2(RINGANIMATION_1_aff3), .MSB(RINGANIMATION_1_aff4),
    .CENTER1(RINGANIMATION_1_aff2), .LSB(RINGANIMATION_1_aff1));
  Splitter2to1OUT Splitter2to1OUT_3 (
    .BUSOUT(Splitter2to1OUT_3_busout), .MSB(RINGANIMATION_1_aff6), .LSB(RINGANIMATION_1_aff5));
  or or_3 (or_3_out, r, ~calcmode);  // OR_Gate
  zonesAffichage zonesAffichage_1 (
    .DAY1(mode_clock_1_day1out), .DAY0(mode_clock_1_day0out), .HOUR1(mode_clock_1_h1out),
    .HOUR0(mode_clock_1_h0out), .CYCLEZONES(CZONES), .RESET(r), .AFF1Z(zonesAffichage_1_aff1z),
    .AFF2Z(zonesAffichage_1_aff2z), .AFF3Z(zonesAffichage_1_aff3z), .AFF4Z(zonesAffichage_1_aff4z),
    .AFF5Z(zonesAffichage_1_aff5z), .AFF6Z(zonesAffichage_1_aff6z), .INFO(info));
  chronoAffiche chronoAffiche_1 (
    .reset(r), .start_stop(CCHRONO), .chrono1(chronoAffiche_1_chrono1), .chrono2(chronoAffiche_1_chrono2),
    .chrono3(chronoAffiche_1_chrono3), .chrono4(chronoAffiche_1_chrono4), .chrono5(chronoAffiche_1_chrono5),
    .chrono6(chronoAffiche_1_chrono6));
  or or_4 (or_4_out, r, toff);
  Splitter4to1OUT Splitter4to1OUT_5 (
    .BUSOUT(Splitter4to1OUT_5_busout), .CENTER2(zonesAffichage_1_aff3z), .MSB(zonesAffichage_1_aff4z),
    .CENTER1(zonesAffichage_1_aff2z), .LSB(zonesAffichage_1_aff1z));
  Splitter2to1OUT Splitter2to1OUT_5 (
    .BUSOUT(Splitter2to1OUT_5_busout), .MSB(zonesAffichage_1_aff6z), .LSB(zonesAffichage_1_aff5z));
  Splitter4to1OUT Splitter4to1OUT_6 (
    .BUSOUT(Splitter4to1OUT_6_busout), .CENTER2(chronoAffiche_1_chrono3), .MSB(chronoAffiche_1_chrono4),
    .CENTER1(chronoAffiche_1_chrono2), .LSB(chronoAffiche_1_chrono1));
  Splitter2to1OUT Splitter2to1OUT_6 (
    .BUSOUT(Splitter2to1OUT_6_busout), .MSB(chronoAffiche_1_chrono6), .LSB(chronoAffiche_1_chrono5));
  MSGAFF MSGAFF_1 (
    .AFF4(MSGAFF_1_aff4), .AFF2(MSGAFF_1_aff2), .PLAY(msg), .AFF1(MSGAFF_1_aff1), .AFF3(MSGAFF_1_aff3),
    .AFF5(MSGAFF_1_aff5), .AFF6(MSGAFF_1_aff6));
  Splitter4to1OUT Splitter4to1OUT_7 (
    .BUSOUT(Splitter4to1OUT_7_busout), .CENTER2(MSGAFF_1_aff3), .MSB(MSGAFF_1_aff4), .CENTER1(MSGAFF_1_aff2),
    .LSB(MSGAFF_1_aff1));
  Splitter2to1OUT Splitter2to1OUT_7 (.BUSOUT(Splitter2to1OUT_7_busout), .MSB(MSGAFF_1_aff6), .LSB(MSGAFF_1_aff5));
  calcAff calcAff_1 (
    .AFF4(calcAff_1_aff4), .RESET(or_3_out), .CYCLE(ccalc), .CHANGE4(showans), .AFF3(calcAff_1_aff3),
    .SETNUMB({setnumbs, lowms}), .CHANGE1(fnum), .CHANGE3(secondnum), .AFF2(calcAff_1_aff2),
    .AFF1(calcAff_1_aff1), .CHANGE2(operator), .AFF5(calcAff_1_aff5), .AFF6(calcAff_1_aff6), .LP(LP));
  Splitter4to1OUT Splitter4to1OUT_9 (
    .BUSOUT(Splitter4to1OUT_9_busout), .CENTER2(calcAff_1_aff3), .MSB(calcAff_1_aff4),
    .CENTER1(calcAff_1_aff2), .LSB(calcAff_1_aff1));
  Splitter2to1OUT Splitter2to1OUT_9 (.BUSOUT(Splitter2to1OUT_9_busout), .MSB(calcAff_1_aff6), .LSB(calcAff_1_aff5));
  TIMERAFF TIMERAFF_1 (
    .AFF3(TIMERAFF_1_aff3), .SETHIMIN(himin), .B(ctimer), .SETLOWMIN(setnumbs[4]), .RESET(or_4_out),
    .SETLOWSEC(setnumbs[2]), .SETHIMS(setnumbs[1]), .TIMERSET(tset), .AFF2(TIMERAFF_1_aff2),
    .SETTINGTIME(setting), .SETLOWMS(lowms), .AFF1(TIMERAFF_1_aff1), .SETHISEC(setnumbs[3]),
    .AFF4(TIMERAFF_1_aff4), .AFF5(TIMERAFF_1_aff5), .AFF6(TIMERAFF_1_aff6), .BUZZER(tdone), .TIMEST(tsetout));
  Splitter4to1OUT Splitter4to1OUT_8 (
    .BUSOUT(Splitter4to1OUT_8_busout), .CENTER2(TIMERAFF_1_aff3), .MSB(TIMERAFF_1_aff4),
    .CENTER1(TIMERAFF_1_aff2), .LSB(TIMERAFF_1_aff1));
  Splitter2to1OUT Splitter2to1OUT_8 (.BUSOUT(Splitter2to1OUT_8_busout), .MSB(TIMERAFF_1_aff6), .LSB(TIMERAFF_1_aff5));
  or or_5 (or_5_out, MODES[0], MODES[1], CHANAL, MODES[3], MODES[5], MODES[6], chrono, msg, calcmode);
  or or_6 (ALLOWMUS, MODES[1], MODES[3]);
  or or_7 (or_7_out, MODES[6], chrono);
  LED EDIT (.in(or_5_out));
  submenuscontroller submenuscontroller_1 (
    .CHOOSINGFIRST(SubMenus_1_chanalarm), .CHOOSINGSECOND(ALLOWMUS), .TRIGGER(MODES[4]),
    .CHOOSINGZONES(MODES[5]), .CHOOSINGTC(or_7_out), .MSGMODE(msg), .CALCMODE(calcmode),
    .T0(submenuscontroller_1_t0[0]), .T1(submenuscontroller_1_t0[1]), .T2(submenuscontroller_1_t0[2]));
  and and_1 (and_1_out, buzzer_t, ALLOWMUS);
  GIGAPLEX GIGAPLEX_1 (
    .OPTIONS(submenuscontroller_1_t0), .FCLOCK(Splitter4to1OUT_1_busout), .SCLOCK(Splitter2to1OUT_1_busout),
    .FALARM(Splitter4to1OUT_4_busout), .SALARM(Splitter2to1OUT_4_busout), .FMUS(sp4_busout),
    .SMUS(sp2_busout), .FRING(Splitter4to1OUT_3_busout), .SRING(Splitter2to1OUT_3_busout),
    .FZONES(Splitter4to1OUT_5_busout), .SZONES(Splitter2to1OUT_5_busout), .FTIMER(Splitter4to1OUT_8_busout),
    .STIMER(Splitter2to1OUT_8_busout), .FCHRONO(Splitter4to1OUT_6_busout),
    .SCHRONO(Splitter2to1OUT_6_busout), .FMSG(Splitter4to1OUT_7_busout), .SMSG(Splitter2to1OUT_7_busout),
    .FCALCL(Splitter4to1OUT_9_busout), .SCALC(Splitter2to1OUT_9_busout), .CHRONO(chrono),
    .AFF1(GIGAPLEX_1_aff1), .AFF2(GIGAPLEX_1_aff2), .AFF3(GIGAPLEX_1_aff3), .AFF4(GIGAPLEX_1_aff4),
    .AFF5(GIGAPLEX_1_aff5), .AFF6(GIGAPLEX_1_aff6));
  or or_8 (BUZZER, and_1_out, tdone, buzz);
  LEDAnim LEDAnim_1 (
    .MUSICMODE(MODES[1]), .ZELDAQ(zp), .LED8(LEDAnim_1_led8), .LED7(LEDAnim_1_led7), .LED6(LEDAnim_1_led6),
    .LED5(LEDAnim_1_led5), .LED4(LEDAnim_1_led4), .LED3(LEDAnim_1_led3), .LED2(LEDAnim_1_led2),
    .LED1(LEDAnim_1_led1));
  LED LED8 (.in(LEDAnim_1_led8));
  LED LED7 (.in(LEDAnim_1_led7));
  LED LED6 (.in(LEDAnim_1_led6));
  LED LED5 (.in(LEDAnim_1_led5));
  LED LED4 (.in(LEDAnim_1_led4));
  LED LED3 (.in(LEDAnim_1_led3));
  LED LED2 (.in(LEDAnim_1_led2));
  LED LED1 (.in(LEDAnim_1_led1));
  _7_Segment_Display AFF1 (
    .g(GIGAPLEX_1_aff1[6]), .f(GIGAPLEX_1_aff1[5]), .a(GIGAPLEX_1_aff1[0]), .b(GIGAPLEX_1_aff1[1]),
    .e(GIGAPLEX_1_aff1[4]), .d(GIGAPLEX_1_aff1[3]), .c(GIGAPLEX_1_aff1[2]), .dp(GIGAPLEX_1_aff1[7]));
  _7_Segment_Display AFF2 (
    .g(GIGAPLEX_1_aff2[6]), .f(GIGAPLEX_1_aff2[5]), .a(GIGAPLEX_1_aff2[0]), .b(GIGAPLEX_1_aff2[1]),
    .e(GIGAPLEX_1_aff2[4]), .d(GIGAPLEX_1_aff2[3]), .c(GIGAPLEX_1_aff2[2]), .dp(GIGAPLEX_1_aff2[7]));
  _7_Segment_Display AFF3 (
    .g(GIGAPLEX_1_aff3[6]), .f(GIGAPLEX_1_aff3[5]), .a(GIGAPLEX_1_aff3[0]), .b(GIGAPLEX_1_aff3[1]),
    .e(GIGAPLEX_1_aff3[4]), .d(GIGAPLEX_1_aff3[3]), .c(GIGAPLEX_1_aff3[2]), .dp(GIGAPLEX_1_aff3[7]));
  _7_Segment_Display AFF4 (
    .g(GIGAPLEX_1_aff4[6]), .f(GIGAPLEX_1_aff4[5]), .a(GIGAPLEX_1_aff4[0]), .b(GIGAPLEX_1_aff4[1]),
    .e(GIGAPLEX_1_aff4[4]), .d(GIGAPLEX_1_aff4[3]), .c(GIGAPLEX_1_aff4[2]), .dp(GIGAPLEX_1_aff4[7]));
  _7_Segment_Display AFF5 (
    .g(GIGAPLEX_1_aff5[6]), .f(GIGAPLEX_1_aff5[5]), .a(GIGAPLEX_1_aff5[0]), .b(GIGAPLEX_1_aff5[1]),
    .e(GIGAPLEX_1_aff5[4]), .d(GIGAPLEX_1_aff5[3]), .c(GIGAPLEX_1_aff5[2]), .dp(GIGAPLEX_1_aff5[7]));
  _7_Segment_Display AFF6 (
    .g(GIGAPLEX_1_aff6[6]), .f(GIGAPLEX_1_aff6[5]), .a(GIGAPLEX_1_aff6[0]), .b(GIGAPLEX_1_aff6[1]),
    .e(GIGAPLEX_1_aff6[4]), .d(GIGAPLEX_1_aff6[3]), .c(GIGAPLEX_1_aff6[2]), .dp(GIGAPLEX_1_aff6[7]));

  // Other names for the same wires on the sheet: SETTIME = MODES[0]; musicmode = MODES[1];
  //   MODES (some bits) = {calcmode, chrono, CHANAL}; TRIGGER = MODES[4]; zactiv = MODES[5]; timermode = MODES[6];
  //   setnumbs[0] = lowms; sixdip[5:0] = {lowms, setnumbs[1], setnumbs[2], setnumbs[3], setnumbs[4], himin}
endmodule

module FSM_FINAL (
  input  B,
  input  RESET,
  output P1,
  output P2,
  output P3,
  output P4
);

  wire Additionneur_1_p1, Additionneur_1_p2, Additionneur_1_p3, Additionneur_1_p4, and_1_out, clock_1_out,
       d_ff_1_q, d_ff_2_q, d_ff_3_q, d_ff_4_q, d_ff_5_q, LongPressMachine_1_outputting, not_1_out, not_2_out,
       not_3_out, not_4_out, or_1_out;

  Clock clock_1 (.out(clock_1_out));
  LongPressMachine LongPressMachine_1 (.B(B), .OUTPUTTING(LongPressMachine_1_outputting));
  Additionneur Additionneur_1 (
    .A1(P1), .B1(LongPressMachine_1_outputting), .A2(P2), .B2(1'b0), .A3(P3), .B3(1'b0), .A4(P4), .B4(1'b0),
    .P1(Additionneur_1_p1), .P2(Additionneur_1_p2), .P3(Additionneur_1_p3), .P4(Additionneur_1_p4));  // open: O
  D_Flip_Flop d_ff_1 (.D(Additionneur_1_p1), .clk(clock_1_out), .Q(d_ff_1_q));  // open: Qn, preset, reset
  D_Flip_Flop d_ff_2 (.D(Additionneur_1_p2), .clk(clock_1_out), .Q(d_ff_2_q));  // open: Qn, preset, reset
  D_Flip_Flop d_ff_3 (.D(Additionneur_1_p3), .clk(clock_1_out), .Q(d_ff_3_q));  // open: Qn, preset, reset
  D_Flip_Flop d_ff_4 (.D(Additionneur_1_p4), .clk(clock_1_out), .Q(d_ff_4_q));  // open: Qn, preset, reset
  D_Flip_Flop d_ff_5 (.D(RESET), .clk(clock_1_out), .Q(d_ff_5_q));  // open: Qn, preset, reset
  and and_1 (and_1_out, d_ff_1_q, d_ff_4_q);
  Multiplexer #(.enable("false")) multiplexer_1 (.in0(d_ff_1_q), .in1(1'b0), .out(P1), .sel(or_1_out));
  Multiplexer #(.enable("false")) multiplexer_2 (.in0(d_ff_2_q), .in1(1'b0), .out(P2), .sel(or_1_out));
  Multiplexer #(.enable("false")) multiplexer_3 (.in0(d_ff_3_q), .in1(1'b0), .out(P3), .sel(or_1_out));
  Multiplexer #(.enable("false")) multiplexer_4 (.in0(d_ff_4_q), .in1(1'b0), .out(P4), .sel(or_1_out));
  or or_1 (or_1_out, and_1_out, d_ff_5_q);
  not not_1 (not_1_out, P1);
  not not_2 (not_2_out, P2);
  // AND_Gate and_2 has open pins: in0=not_1_out, in1=not_2_out, in2=not_3_out, in3=not_4_out, out=open
  not not_3 (not_3_out, P3);
  not not_4 (not_4_out, P4);
endmodule

module States (
  input  B,
  input  BP,
  output BPout,
  output S
);

  wire not_1_out;

  and and_1 (S, B, not_1_out);
  not not_1 (not_1_out, BP);

  assign BPout = B;
endmodule

module FirstLetterMAIN (
  input  [5:0] M1,
  input  [5:0] M2,
  input  [5:0] M3,
  input  [5:0] M4,
  input  [5:0] M5,
  input  [5:0] M6,
  input  [5:0] M7,
  input  [5:0] M8,
  output [7:0] L1,
  output [7:0] L2,
  output [7:0] L3,
  output [7:0] L4,
  output [7:0] L5,
  output [7:0] L6,
  output [7:0] L7,
  output [7:0] L8
);

  sevensegBUS2 sevensegBUS2_1 (.LETTER(M1), .LETTERCODE(L1));
  sevensegBUS2 sevensegBUS2_2 (.LETTER(M2), .LETTERCODE(L2));
  sevensegBUS2 sevensegBUS2_3 (.LETTER(M3), .LETTERCODE(L3));
  sevensegBUS2 sevensegBUS2_4 (.LETTER(M4), .LETTERCODE(L4));
  sevensegBUS2 sevensegBUS2_5 (.LETTER(M5), .LETTERCODE(L5));
  sevensegBUS2 sevensegBUS2_6 (.LETTER(M6), .LETTERCODE(L6));
  sevensegBUS2 sevensegBUS2_7 (.LETTER(M7), .LETTERCODE(L7));
  sevensegBUS2 sevensegBUS2_8 (.LETTER(M8), .LETTERCODE(L8));
endmodule

module DIGIT (
  input  [7:0] CLOCK,
  input  [5:0] M1,
  input  [3:0] OPTIONS,
  input  [5:0] M2,
  input  [5:0] M3,
  input  [5:0] M4,
  input  [5:0] M5,
  input  [5:0] M6,
  input  [5:0] M7,
  input  [5:0] M8,
  output [7:0] AFF
);

  wire [7:0] FirstLetterMAIN_1_l1, FirstLetterMAIN_1_l2, FirstLetterMAIN_1_l3, FirstLetterMAIN_1_l4,
       FirstLetterMAIN_1_l5, FirstLetterMAIN_1_l6, FirstLetterMAIN_1_l7, FirstLetterMAIN_1_l8;

  FirstLetterMAIN FirstLetterMAIN_1 (
    .M1(M1), .M2(M2), .M3(M3), .M4(M4), .M5(M5), .M6(M6), .M7(M7), .M8(M8), .L1(FirstLetterMAIN_1_l1),
    .L2(FirstLetterMAIN_1_l2), .L3(FirstLetterMAIN_1_l3), .L4(FirstLetterMAIN_1_l4),
    .L5(FirstLetterMAIN_1_l5), .L6(FirstLetterMAIN_1_l6), .L7(FirstLetterMAIN_1_l7), .L8(FirstLetterMAIN_1_l8));
  Multiplexer #(.select(4), .width(8), .enable("false")) multiplexer_1 (
    .in0(CLOCK), .in1(FirstLetterMAIN_1_l1), .in2(FirstLetterMAIN_1_l2), .in3(FirstLetterMAIN_1_l3),
    .in4(FirstLetterMAIN_1_l4), .in5(FirstLetterMAIN_1_l5), .in6(FirstLetterMAIN_1_l6),
    .in7(FirstLetterMAIN_1_l7), .in8(FirstLetterMAIN_1_l8), .out(AFF), .sel(OPTIONS));  // open: in9, in10, in11, in12, in13, in14, in15
endmodule

module Selectable (
  input  RESET,
  input  current,
  input  SELECTION,
  output CHANGING,
  output DONE
);

  wire and_1_out, and_2_out, not_1_out, or_1_out, or_2_out, or_3_out, s_r_ff_2_q, selectFSM_1_resetchange,
       selectFSM_1_resettrans, selectFSM_1_setchange, selectFSM_1_settrans;

  or or_1 (or_1_out, RESET, ~current);  // OR_Gate
  selectFSM selectFSM_1 (
    .BUTT(SELECTION), .CHANGE(CHANGING), .TRANS(s_r_ff_2_q), .SETCHANGE(selectFSM_1_setchange),
    .RESETCHANGE(selectFSM_1_resetchange), .SETTRANS(selectFSM_1_settrans),
    .RESETTRANS(selectFSM_1_resettrans));
  and and_1 (and_1_out, current, selectFSM_1_setchange);
  and and_2 (and_2_out, current, selectFSM_1_resetchange);
  or or_2 (or_2_out, selectFSM_1_resettrans, or_1_out);
  or or_3 (or_3_out, or_1_out, and_2_out);
  S_R_Flip_Flop s_r_ff_1 (.Q(CHANGING), .reset(or_3_out), .preset(and_1_out));  // open: S, R, clk, Qn
  S_R_Flip_Flop s_r_ff_2 (.Q(s_r_ff_2_q), .reset(or_2_out), .preset(selectFSM_1_settrans));  // open: S, R, clk, Qn
  not not_1 (not_1_out, CHANGING);
  and and_3 (DONE, not_1_out, s_r_ff_2_q);
endmodule

module selectFSM (
  input  BUTT,
  input  CHANGE,
  input  TRANS,
  output SETCHANGE,
  output RESETCHANGE,
  output SETTRANS,
  output RESETTRANS
);

  wire not_1_out, not_2_out, not_3_out, not_4_out, not_5_out, not_6_out;

  not not_1 (not_1_out, CHANGE);
  not not_2 (not_2_out, TRANS);
  not not_3 (not_3_out, BUTT);
  not not_4 (not_4_out, TRANS);
  not not_5 (not_5_out, BUTT);
  not not_6 (not_6_out, CHANGE);
  and and_1 (SETCHANGE, BUTT, not_1_out, not_2_out);
  and and_2 (RESETCHANGE, BUTT, CHANGE, TRANS);
  and and_3 (SETTRANS, not_3_out, CHANGE, not_4_out);
  and and_4 (RESETTRANS, not_5_out, not_6_out, TRANS);
endmodule

module buttonFSM (
  input  BUTTON,
  input  SETTIME,
  input  MUSIC,
  input  ALARM,
  input  MUSALARM,
  input  TRIGGERIN,
  input  ZONES,
  input  CHRONO,
  input  TIMER,
  input  CALC,
  output FLIP,
  output CYCLE,
  output CYCLEMUSIC,
  output CYCLEALARM,
  output TRIGGEROUT,
  output CZONES,
  output CCHRONO,
  output CTIMER,
  output CCALC
);

  wire and_1_out, and_2_out, and_3_out, and_4_out, and_5_out, and_6_out, and_7_out, and_8_out, and_11_out,
       and_12_out, and_13_out, not_1_out, not_2_out, not_3_out, not_4_out, not_5_out, not_6_out, not_7_out,
       not_8_out, not_9_out, not_10_out, not_11_out, not_12_out, not_13_out, not_14_out, not_15_out,
       not_16_out, not_17_out, not_18_out, not_19_out, not_20_out, not_21_out, not_22_out, not_23_out,
       not_24_out, not_25_out, not_26_out, not_27_out, not_28_out, not_29_out, not_30_out, not_31_out,
       not_32_out, not_33_out, not_34_out, not_35_out, not_36_out, not_37_out, not_38_out, not_39_out,
       not_40_out, not_41_out, not_42_out, not_43_out, not_44_out, not_45_out, not_46_out, not_47_out,
       not_48_out, not_49_out, not_50_out, not_51_out, not_52_out, not_53_out, not_54_out, not_55_out,
       not_56_out, not_57_out, not_58_out, not_59_out, not_60_out, not_61_out, not_62_out, not_63_out,
       not_64_out, not_65_out, not_66_out, not_67_out, not_68_out, not_69_out, not_70_out, or_1_out;

  not not_1 (not_1_out, MUSIC);
  not not_2 (not_2_out, ALARM);
  not not_3 (not_3_out, MUSALARM);
  not not_4 (not_4_out, TRIGGERIN);
  not not_5 (not_5_out, CHRONO);
  not not_6 (not_6_out, TIMER);
  not not_7 (not_7_out, CALC);
  not not_8 (not_8_out, SETTIME);
  not not_9 (not_9_out, MUSIC);
  not not_10 (not_10_out, ALARM);
  not not_11 (not_11_out, MUSALARM);
  not not_12 (not_12_out, TRIGGERIN);
  not not_13 (not_13_out, ZONES);
  not not_14 (not_14_out, CHRONO);
  not not_15 (not_15_out, TIMER);
  not not_16 (not_16_out, CALC);
  not not_17 (not_17_out, SETTIME);
  not not_18 (not_18_out, MUSIC);
  not not_19 (not_19_out, TRIGGERIN);
  not not_20 (not_20_out, ZONES);
  not not_21 (not_21_out, SETTIME);
  not not_22 (not_22_out, MUSIC);
  not not_23 (not_23_out, TRIGGERIN);
  not not_24 (not_24_out, SETTIME);
  not not_25 (not_25_out, ALARM);
  not not_26 (not_26_out, MUSALARM);
  not not_27 (not_27_out, TRIGGERIN);
  not not_28 (not_28_out, SETTIME);
  not not_29 (not_29_out, MUSIC);
  not not_30 (not_30_out, MUSALARM);
  not not_31 (not_31_out, TRIGGERIN);
  not not_32 (not_32_out, CHRONO);
  not not_33 (not_33_out, TIMER);
  not not_34 (not_34_out, CALC);
  not not_35 (not_35_out, ZONES);
  not not_36 (not_36_out, SETTIME);
  not not_37 (not_37_out, MUSIC);
  not not_38 (not_38_out, ALARM);
  not not_39 (not_39_out, MUSALARM);
  not not_40 (not_40_out, TRIGGERIN);
  not not_41 (not_41_out, CHRONO);
  not not_42 (not_42_out, TIMER);
  not not_43 (not_43_out, CALC);
  not not_44 (not_44_out, SETTIME);
  not not_45 (not_45_out, MUSIC);
  not not_46 (not_46_out, ALARM);
  not not_47 (not_47_out, MUSALARM);
  not not_48 (not_48_out, TRIGGERIN);
  not not_49 (not_49_out, ZONES);
  not not_50 (not_50_out, TIMER);
  not not_51 (not_51_out, CALC);
  not not_52 (not_52_out, SETTIME);
  not not_53 (not_53_out, MUSIC);
  not not_54 (not_54_out, ALARM);
  not not_55 (not_55_out, MUSALARM);
  not not_56 (not_56_out, TRIGGERIN);
  not not_57 (not_57_out, ZONES);
  not not_58 (not_58_out, CHRONO);
  not not_59 (not_59_out, CALC);
  not not_60 (not_60_out, SETTIME);
  not not_61 (not_61_out, MUSIC);
  not not_62 (not_62_out, ALARM);
  not not_63 (not_63_out, MUSALARM);
  not not_64 (not_64_out, TRIGGERIN);
  not not_65 (not_65_out, ZONES);
  not not_66 (not_66_out, CHRONO);
  not not_67 (not_67_out, TIMER);
  and and_1 (and_1_out, BUTTON, TRIGGERIN, not_35_out);
  and and_2 (and_2_out, BUTTON, MUSALARM, TRIGGERIN);
  and and_3 (and_3_out, BUTTON, ALARM, TRIGGERIN);
  and and_4 (and_4_out, BUTTON, MUSIC, TRIGGERIN);
  and and_5 (and_5_out, BUTTON, SETTIME, TRIGGERIN);
  and and_6 (and_6_out, BUTTON, TRIGGERIN, CHRONO);
  and and_7 (and_7_out, BUTTON, TRIGGERIN, TIMER);
  and and_8 (and_8_out, BUTTON, TRIGGERIN, CALC);
  and and_9 (FLIP, BUTTON, SETTIME, not_1_out, not_2_out, not_3_out, not_4_out, not_5_out, not_6_out, not_7_out);
  and and_10 (CYCLE, BUTTON, not_8_out, not_9_out, not_10_out, not_11_out, not_12_out, not_13_out, not_14_out, not_15_out, not_16_out);
  and and_11 (and_11_out, BUTTON, not_17_out, not_18_out, MUSALARM, not_19_out, not_20_out);
  or or_1 (or_1_out, and_11_out, and_12_out, and_13_out);
  and and_12 (and_12_out, BUTTON, not_21_out, not_22_out, ALARM, MUSALARM, not_23_out);
  and and_13 (and_13_out, BUTTON, not_24_out, MUSIC, not_25_out, not_26_out, not_27_out);
  not not_68 (not_68_out, CHRONO);
  not not_69 (not_69_out, TIMER);
  not not_70 (not_70_out, CALC);
  and and_14 (CYCLEALARM, BUTTON, not_28_out, not_29_out, ALARM, not_30_out, not_31_out, not_32_out, not_33_out, not_34_out);
  and and_15 (CZONES, BUTTON, not_36_out, not_37_out, not_38_out, not_39_out, not_40_out, ZONES, not_41_out, not_42_out, not_43_out);
  and and_16 (CCHRONO, BUTTON, not_44_out, not_45_out, not_46_out, not_47_out, not_48_out, not_49_out, CHRONO, not_50_out, not_51_out);
  and and_17 (CTIMER, BUTTON, not_52_out, not_53_out, not_54_out, not_55_out, not_56_out, not_57_out, not_58_out, TIMER, not_59_out);
  and and_18 (CCALC, BUTTON, not_60_out, not_61_out, not_62_out, not_63_out, not_64_out, not_65_out, not_66_out, not_67_out, CALC);
  and and_19 (CYCLEMUSIC, or_1_out, not_68_out, not_69_out, not_70_out);
  or or_2 (TRIGGEROUT, and_1_out, and_2_out, and_3_out, and_4_out, and_5_out, and_6_out, and_7_out, and_8_out);
endmodule

module settimechecker (
  input  P,
  input  SETTIME,
  output Pout
);

  wire not_1_out;

  not not_1 (not_1_out, SETTIME);
  and and_1 (Pout, P, not_1_out);
endmodule

module conditionSetTime (
  input  SETTIME,
  input  [3:0] PENTER,
  output [3:0] POUT
);

  settimechecker settimechecker_1 (.P(PENTER[0]), .SETTIME(SETTIME), .Pout(POUT[0]));
  settimechecker settimechecker_2 (.P(PENTER[1]), .SETTIME(SETTIME), .Pout(POUT[1]));
  settimechecker settimechecker_3 (.P(PENTER[2]), .SETTIME(SETTIME), .Pout(POUT[2]));
  settimechecker settimechecker_4 (.P(PENTER[3]), .SETTIME(SETTIME), .Pout(POUT[3]));
endmodule

module MainMenuAffichage (
  input  [3:0] OPTIONS,
  input  [7:0] HIMIN,
  input  [7:0] LOWMIN,
  input  [7:0] HIHOUR,
  input  [7:0] LOWHOUR,
  input  [7:0] HIDAY,
  input  [7:0] LOWDAY,
  output [7:0] FIRSTDIG,
  output [7:0] SECONDDIG,
  output [7:0] THIRDDIG,
  output [7:0] FOURTHDIG,
  output [7:0] FITHDIG,
  output [7:0] SIXTHDIG
);

  DIGIT FIRST (
    .M7(6'b011000), .CLOCK(HIDAY), .M6(6'b011000), .M1(6'b100100), .M5({6{1'b0}}), .OPTIONS(OPTIONS),
    .M4(6'b110010), .M2(6'b100110), .M3(6'b000100), .M8(6'b000100), .AFF(FIRSTDIG));
  DIGIT SECOND (
    .M7(6'b101000), .CLOCK(LOWDAY), .M6(6'b011100), .M1(6'b001000), .M5(6'b010110), .OPTIONS(OPTIONS),
    .M4(6'b011100), .M2(6'b010000), .M3(6'b001110), .M8({6{1'b0}}), .AFF(SECONDDIG));
  DIGIT THIRD (
    .M7(6'b100100), .CLOCK(HIHOUR), .M6(6'b100110), .M1(6'b100110), .M5({6{1'b0}}), .OPTIONS(OPTIONS),
    .M4(6'b011010), .M2(6'b011000), .M3(6'b100010), .M8(6'b010110), .AFF(THIRDDIG));
  DIGIT FOURTH (
    .M7(6'b010000), .CLOCK(LOWHOUR), .M6(6'b010000), .M1(6'b111110), .M5(6'b100010), .OPTIONS(OPTIONS),
    .M4(6'b001000), .M2(6'b001000), .M3(6'b011100), .M8(6'b000100), .AFF(FOURTHDIG));
  DIGIT FITH (
    .M7(6'b000100), .CLOCK(HIMIN), .M6(6'b101010), .M1(6'b111110), .M5(6'b011000), .OPTIONS(OPTIONS),
    .M4(6'b100100), .M2(6'b100010), .M3(6'b011010), .M8(6'b111110), .AFF(FITHDIG));
  DIGIT SIXTH (
    .M7(6'b111110), .CLOCK(LOWMIN), .M6(6'b111110), .M1(6'b111110), .M5(6'b111110), .OPTIONS(OPTIONS),
    .M4(6'b111110), .M2(6'b111110), .M3(6'b011100), .M8(6'b111110), .AFF(SIXTHDIG));
endmodule

module Splitter4to1OUT (
  input  [7:0] LSB,
  input  [7:0] CENTER1,
  input  [7:0] CENTER2,
  input  [7:0] MSB,
  output [31:0] BUSOUT
);


  assign BUSOUT = {MSB, CENTER2, CENTER1, LSB};
endmodule

module Splitter1to4IN (
  input  [31:0] BUSIN,
  output [7:0] LSB,
  output [7:0] C1,
  output [7:0] C2,
  output [7:0] MSB
);


  assign C1 = BUSIN[15:8];
  assign C2 = BUSIN[23:16];
  assign LSB = BUSIN[7:0];
  assign MSB = BUSIN[31:24];
endmodule

module Splitter2to1OUT (
  input  [7:0] LSB,
  input  [7:0] MSB,
  output [15:0] BUSOUT
);


  assign BUSOUT = {MSB, LSB};
endmodule

module Splitter1to2IN (
  input  [15:0] BUSIN,
  output [7:0] LSB,
  output [7:0] MSB
);


  assign LSB = BUSIN[7:0];
  assign MSB = BUSIN[15:8];
endmodule

module Splitter1to6IN (
  input  [5:0] BUSIN,
  output B0,
  output B1,
  output B2,
  output B3,
  output B4,
  output B5
);


  assign B0 = BUSIN[0];
  assign B1 = BUSIN[1];
  assign B2 = BUSIN[2];
  assign B3 = BUSIN[3];
  assign B4 = BUSIN[4];
  assign B5 = BUSIN[5];
endmodule

module LongPressDetector (
  input  BUTTON,
  input  RESET,
  output LONGPRESSMODE
);

  wire TimeSelector_1_output_1;

  TimeSelector TimeSelector_1 (
    .RESET(RESET), .Input_3(1'b1), .Input_5(1'b1), .Input_6(1'b0), .T0(1'b0), .SET(BUTTON), .Input_4(1'b0),
    .Output_1(TimeSelector_1_output_1), .T1(1'b0));
  not not_1 (LONGPRESSMODE, TimeSelector_1_output_1);
endmodule

module LongPressMachine (
  input  B,
  output OUTPUTTING
);

  wire and_1_out, clock_1_out, clock_2_out, d_ff_1_q, d_ff_2_q, LongPressDetector_1_longpressmode, not_1_out,
       states2_bpout, states2_s, States_1_bpout, States_1_s, t_ff_1_q;

  not not_1 (not_1_out, B);
  LongPressDetector LongPressDetector_1 (
    .BUTTON(B), .RESET(not_1_out), .LONGPRESSMODE(LongPressDetector_1_longpressmode));
  States States_1 (.B(B), .BP(d_ff_1_q), .BPout(States_1_bpout), .S(States_1_s));
  Clock #(.highDuration(4000), .lowDuration(4000)) clock_1 (.out(clock_1_out));
  D_Flip_Flop d_ff_1 (.D(States_1_bpout), .clk(clock_2_out), .Q(d_ff_1_q));  // open: Qn, preset, reset
  Clock clock_2 (.out(clock_2_out));
  T_Flip_Flop t_ff_1 (
    .T(LongPressDetector_1_longpressmode), .clk(clock_1_out), .Q(t_ff_1_q));  // open: Qn, reset, preset
  and and_1 (and_1_out, t_ff_1_q, LongPressDetector_1_longpressmode);
  or or_1 (OUTPUTTING, states2_s, States_1_s);
  States states2 (.B(and_1_out), .BP(d_ff_2_q), .BPout(states2_bpout), .S(states2_s));
  D_Flip_Flop d_ff_2 (.D(states2_bpout), .clk(clock_2_out), .Q(d_ff_2_q));  // open: Qn, preset, reset
endmodule

module setTimerAlarmAff (
  input  CYCLE,
  input  RESET,
  input  SHIHOUR,
  input  SLOWHOUR,
  input  SHIMIN,
  input  SLOWMIN,
  output [6:0] HIHOUR,
  output [6:0] LOWHOUR,
  output [6:0] HIMIN,
  output [6:0] LOWMIN
);

  wire [3:0] AlarmSetter_1_hihourcode, AlarmSetter_1_himincode, AlarmSetter_1_lowhourcode,
       AlarmSetter_1_lowmincode;

  AlarmSetter AlarmSetter_1 (
    .CYCLE(CYCLE), .RESET(RESET), .SHIHOUR(SHIHOUR), .SLOWHOUR(SLOWHOUR), .SHIMIN(SHIMIN), .SLOWMIN(SLOWMIN),
    .HIHOURCODE(AlarmSetter_1_hihourcode), .LOWHOURCODE(AlarmSetter_1_lowhourcode),
    .HIMINCODE(AlarmSetter_1_himincode), .LOWMINCODE(AlarmSetter_1_lowmincode));
  numb_4_to_7 numb_4_to_7_1 (.NUMBER(AlarmSetter_1_hihourcode), .EN(1'b1), .NUMBOUT(HIHOUR));
  numb_4_to_7 numb_4_to_7_2 (.NUMBER(AlarmSetter_1_lowhourcode), .EN(1'b1), .NUMBOUT(LOWHOUR));
  numb_4_to_7 numb_4_to_7_3 (.NUMBER(AlarmSetter_1_himincode), .EN(1'b1), .NUMBOUT(HIMIN));
  numb_4_to_7 numb_4_to_7_4 (.NUMBER(AlarmSetter_1_lowmincode), .EN(1'b1), .NUMBOUT(LOWMIN));
endmodule

module AlarmAffichage (
  input  [7:0] HIMINCLOCK,
  input  [7:0] LMINCLOCK,
  input  [7:0] HIHOURCLOCK,
  input  [7:0] LHOURCLOCK,
  input  CYCLEALARM,
  input  SHIHOUR,
  input  SLOWHOUR,
  input  SHIMIN,
  input  SLOWMIN,
  input  RESET,
  input  ALARMACTI,
  input  TURNOFF,
  input  HARRYCHOICE,
  input  ZELDACHOICE,
  input  PIRATECHOICE,
  input  MODIFY,
  output TRIGGER,
  output [7:0] HIDAY,
  output [7:0] LOWDAY,
  output [7:0] HIHOUR,
  output [7:0] LOWHOUR,
  output [7:0] HIMIN,
  output [7:0] LOWMIN,
  output BUZZ
);

  wire and_1_out, and_2_out, and_3_out, and_4_out, and_5_out, and_6_out, and_7_out, clock_1_out,
       HarryPotter_1_buzzer, LegendOfZelda_1_buzzer, normalpress_1_outp, normalpress_2_outp,
       OdeOfJoy_1_buzzer, or_1_out, or_2_out, or_3_out, or_4_out, or_5_out, or_6_out, or_7_out, or_9_out,
       s_r_ff_1_q, s_r_ff_2_q, s_r_ff_3_q, s_r_ff_4_q, THELP_outputting;

  LongPressMachine THELP (.B(CYCLEALARM), .OUTPUTTING(THELP_outputting));
  and and_1 (and_1_out, HARRYCHOICE, MODIFY);
  and and_2 (and_2_out, ZELDACHOICE, MODIFY);
  and and_3 (and_3_out, PIRATECHOICE, MODIFY);
  normalpress normalpress_1 (.B(MODIFY), .OUTP(normalpress_1_outp));
  setTimerAlarmAff setTimerAlarmAff_1 (
    .CYCLE(THELP_outputting), .RESET(RESET), .SHIHOUR(SHIHOUR), .SLOWHOUR(SLOWHOUR), .SHIMIN(SHIMIN),
    .SLOWMIN(SLOWMIN), .HIHOUR(HIHOUR[6:0]), .LOWHOUR(LOWHOUR[6:0]), .HIMIN(HIMIN[6:0]), .LOWMIN(LOWMIN[6:0]));
  S_R_Flip_Flop s_r_ff_1 (.S(and_1_out), .R(or_1_out), .clk(clock_1_out), .Q(s_r_ff_1_q));  // open: reset, Qn, preset
  or or_1 (or_1_out, normalpress_1_outp, and_2_out, RESET, and_3_out);
  S_R_Flip_Flop s_r_ff_2 (.S(and_2_out), .R(or_2_out), .clk(clock_1_out), .Q(s_r_ff_2_q));  // open: reset, Qn, preset
  or or_2 (or_2_out, normalpress_1_outp, and_1_out, and_3_out, RESET);
  S_R_Flip_Flop s_r_ff_3 (.S(and_3_out), .R(or_3_out), .clk(clock_1_out), .Q(s_r_ff_3_q));  // open: reset, Qn, preset
  Clock clock_1 (.out(clock_1_out));
  or or_3 (or_3_out, normalpress_1_outp, and_2_out, and_1_out, RESET);
  and and_4 (and_4_out, s_r_ff_1_q, normalpress_2_outp);
  and and_5 (and_5_out, s_r_ff_2_q, normalpress_2_outp);
  and and_6 (and_6_out, s_r_ff_3_q, normalpress_2_outp);
  normalpress normalpress_2 (.B(TRIGGER), .OUTP(normalpress_2_outp));
  or or_4 (or_4_out, TURNOFF, RESET);
  and and_7 (and_7_out, or_4_out, s_r_ff_4_q);
  or or_5 (or_5_out, RESET, and_7_out);
  or or_6 (or_6_out, RESET, and_7_out);
  or or_7 (or_7_out, and_7_out, RESET);
  AlarmDetector AlarmDetector_1 (
    .HIHOURCLOCK(HIHOURCLOCK), .LOWHOURCLOCK(LHOURCLOCK), .HIMINCLOCK(HIMINCLOCK), .LOWMINCLOCK(LMINCLOCK),
    .HIHOURALARM({SHIHOUR, HIHOUR[6:0]}), .LOWHOURALARM({SLOWHOUR, LOWHOUR[6:0]}),
    .HIMINALARM({SHIMIN, HIMIN[6:0]}), .LOWMINALARM({SLOWMIN, LOWMIN[6:0]}), .ALARMACTIVATED(ALARMACTI),
    .TURNOFF(or_4_out), .TRIGGERALARM(TRIGGER));
  HarryPotter HarryPotter_1 (.SET(and_4_out), .RESET(or_5_out), .BUZZER(HarryPotter_1_buzzer));  // open: HARRYPLAYING
  LegendOfZelda LegendOfZelda_1 (
    .SET(and_5_out), .RESET(or_6_out), .BUZZER(LegendOfZelda_1_buzzer));  // open: ZELDAPLAYING
  OdeOfJoy OdeOfJoy_1 (.RESET(or_7_out), .SET(and_6_out), .BUZZER(OdeOfJoy_1_buzzer));  // open: PIRATEPLAYING
  or or_8 (BUZZ, HarryPotter_1_buzzer, LegendOfZelda_1_buzzer, OdeOfJoy_1_buzzer);
  S_R_Flip_Flop s_r_ff_4 (.S(TRIGGER), .R(or_9_out), .clk(clock_1_out), .Q(s_r_ff_4_q));  // open: reset, Qn, preset
  or or_9 (or_9_out, and_7_out, RESET);

  assign HIDAY = {8{1'b0}};
  assign HIHOUR[7] = SHIHOUR;
  assign HIMIN[7] = SHIMIN;
  assign LOWDAY = {8{1'b0}};
  assign LOWHOUR[7] = SLOWHOUR;
  assign LOWMIN[7] = SLOWMIN;
endmodule

module submenuscontroller (
  input  CHOOSINGFIRST,
  input  CHOOSINGSECOND,
  input  TRIGGER,
  input  CHOOSINGZONES,
  input  CHOOSINGTC,
  input  MSGMODE,
  input  CALCMODE,
  output T0,
  output T1,
  output T2
);

  wire and_1_out, and_2_out, and_3_out, and_4_out, and_5_out, and_6_out, and_7_out, and_8_out, and_9_out,
       not_1_out, not_2_out, not_3_out, not_4_out, not_5_out, not_6_out, not_7_out, not_8_out, not_9_out,
       not_10_out, not_11_out, not_12_out, not_13_out, not_14_out, not_15_out, not_16_out, not_17_out,
       not_18_out, not_19_out, not_20_out, not_21_out, not_22_out, not_23_out, not_24_out, not_25_out,
       not_26_out;

  not not_1 (not_1_out, CHOOSINGSECOND);
  not not_2 (not_2_out, CHOOSINGZONES);
  not not_3 (not_3_out, MSGMODE);
  not not_4 (not_4_out, CHOOSINGSECOND);
  not not_5 (not_5_out, CHOOSINGZONES);
  not not_6 (not_6_out, MSGMODE);
  not not_7 (not_7_out, CHOOSINGSECOND);
  not not_8 (not_8_out, CHOOSINGFIRST);
  not not_9 (not_9_out, CHOOSINGZONES);
  not not_10 (not_10_out, CHOOSINGTC);
  not not_11 (not_11_out, CHOOSINGFIRST);
  not not_12 (not_12_out, CHOOSINGZONES);
  not not_13 (not_13_out, CHOOSINGTC);
  not not_14 (not_14_out, CHOOSINGFIRST);
  not not_15 (not_15_out, CHOOSINGFIRST);
  not not_16 (not_16_out, CHOOSINGSECOND);
  not not_17 (not_17_out, TRIGGER);
  not not_18 (not_18_out, CHOOSINGTC);
  not not_19 (not_19_out, CHOOSINGFIRST);
  not not_20 (not_20_out, CHOOSINGSECOND);
  not not_21 (not_21_out, TRIGGER);
  not not_22 (not_22_out, CHOOSINGTC);
  not not_23 (not_23_out, CHOOSINGFIRST);
  not not_24 (not_24_out, CHOOSINGSECOND);
  not not_25 (not_25_out, TRIGGER);
  not not_26 (not_26_out, MSGMODE);
  and and_1 (and_1_out, not_1_out, not_2_out, not_3_out, CALCMODE);
  and and_2 (and_2_out, not_4_out, not_5_out, CHOOSINGTC, not_6_out);
  and and_3 (and_3_out, CHOOSINGFIRST, not_7_out);
  and and_4 (and_4_out, not_8_out, not_9_out, not_10_out, CALCMODE);
  and and_5 (and_5_out, not_11_out, not_12_out, not_13_out, MSGMODE);
  and and_6 (and_6_out, not_14_out, CHOOSINGSECOND);
  and and_7 (and_7_out, not_15_out, not_16_out, not_17_out, not_18_out, CALCMODE);
  and and_8 (and_8_out, not_19_out, not_20_out, not_21_out, not_22_out, MSGMODE);
  and and_9 (and_9_out, not_23_out, not_24_out, not_25_out, CHOOSINGTC, not_26_out);
  or or_1 (T0, and_1_out, and_2_out, TRIGGER, and_3_out);
  or or_2 (T1, and_4_out, and_5_out, TRIGGER, and_6_out);
  or or_3 (T2, and_7_out, and_8_out, and_9_out, CHOOSINGZONES);
endmodule

module twosubsv2 (
  input  RESET,
  input  CURRENT,
  input  SELECTION,
  output CHANGE1,
  output CHANGING,
  output CHANGE2,
  output DONE
);

  wire and_1_out, and_2_out, not_1_out, not_2_out, or_1_out, or_2_out, or_3_out, or_4_out, s_r_ff_2_q,
       s_r_ff_3_q, selectFSMforThree_1_rc1, selectFSMforThree_1_rc2, selectFSMforThree_1_rd,
       selectFSMforThree_1_sc1, selectFSMforThree_1_sc2, selectFSMforThree_1_sd;

  or or_1 (or_1_out, RESET, ~CURRENT);  // OR_Gate
  selectFSMforThree selectFSMforThree_1 (
    .B(SELECTION), .C1(CHANGE1), .C2(s_r_ff_2_q), .D(s_r_ff_3_q), .SC1(selectFSMforThree_1_sc1),
    .RC1(selectFSMforThree_1_rc1), .SC2(selectFSMforThree_1_sc2), .RC2(selectFSMforThree_1_rc2),
    .SD(selectFSMforThree_1_sd), .RD(selectFSMforThree_1_rd));
  or or_2 (or_2_out, or_1_out, and_2_out);
  and and_1 (and_1_out, CURRENT, selectFSMforThree_1_sc1);
  and and_2 (and_2_out, CURRENT, selectFSMforThree_1_rc1);
  or or_3 (or_3_out, selectFSMforThree_1_rc2, or_1_out);
  S_R_Flip_Flop s_r_ff_1 (.Q(CHANGE1), .reset(or_2_out), .preset(and_1_out));  // open: S, R, clk, Qn
  S_R_Flip_Flop s_r_ff_2 (.Q(s_r_ff_2_q), .reset(or_3_out), .preset(selectFSMforThree_1_sc2));  // open: S, R, clk, Qn
  or or_4 (or_4_out, selectFSMforThree_1_rd, or_1_out);
  not not_1 (not_1_out, CHANGE1);
  S_R_Flip_Flop s_r_ff_3 (.Q(s_r_ff_3_q), .reset(or_4_out), .preset(selectFSMforThree_1_sd));  // open: S, R, clk, Qn
  and and_3 (CHANGE2, not_1_out, s_r_ff_2_q);
  not not_2 (not_2_out, CHANGE2);
  and and_4 (DONE, not_2_out, s_r_ff_3_q);
  or or_5 (CHANGING, CHANGE1, CHANGE2);
endmodule

module selectFSMforThree (
  input  B,
  input  C1,
  input  C2,
  input  D,
  output SC1,
  output RC1,
  output SC2,
  output RC2,
  output SD,
  output RD
);

  wire not_1_out, not_2_out, not_3_out, not_4_out, not_5_out, not_6_out, not_7_out, not_8_out, not_9_out,
       not_10_out, not_11_out, not_12_out, not_13_out, not_14_out;

  not not_1 (not_1_out, C1);
  not not_2 (not_2_out, C2);
  not not_3 (not_3_out, D);
  not not_4 (not_4_out, D);
  not not_5 (not_5_out, B);
  not not_6 (not_6_out, C2);
  not not_7 (not_7_out, D);
  not not_8 (not_8_out, C1);
  not not_9 (not_9_out, B);
  not not_10 (not_10_out, C1);
  not not_11 (not_11_out, D);
  not not_12 (not_12_out, B);
  not not_13 (not_13_out, C1);
  not not_14 (not_14_out, C2);
  and and_1 (SC1, B, not_1_out, not_2_out, not_3_out);
  and and_2 (RC1, B, C1, C2, not_4_out);
  and and_3 (SC2, not_5_out, C1, not_6_out, not_7_out);
  and and_4 (RC2, B, not_8_out, C2, D);
  and and_5 (SD, not_9_out, not_10_out, C2, not_11_out);
  and and_6 (RD, not_12_out, not_13_out, not_14_out, D);
endmodule

module musAff (
  input  CYCLE,
  input  RESET,
  output BUZZER,
  output HARRYPLAYING,
  output ZELDAPLAYING,
  output ODEPLAYING,
  output [7:0] AFF1,
  output [7:0] AFF2,
  output [7:0] AFF3,
  output [7:0] AFF4,
  output [7:0] AFF5,
  output [7:0] AFF6
);

  wire Affichage1_1_v0, Affichage1_1_w0, Affichage1_1_x0, Affichage1_1_y0, Affichage1_1_z0, Affichage2_1_v1,
       Affichage2_1_w1, Affichage2_1_x1, Affichage2_1_y1, Affichage2_1_z1, Affichage3_1_v2, Affichage3_1_w2,
       Affichage3_1_x2, Affichage3_1_y2, Affichage3_1_z2, Affichage4_1_v3, Affichage4_1_w3, Affichage4_1_x3,
       Affichage4_1_y3, Affichage4_1_z3, Affichage5_1_v4, Affichage5_1_w4, Affichage5_1_x4, Affichage5_1_y4,
       Affichage5_1_z4, Affichage6_1_v5, Affichage6_1_w5, Affichage6_1_x5, Affichage6_1_y5, Affichage6_1_z5,
       MP3_1_harryplay, MP3_1_pirateplay, MP3_1_zeldaplay;

  MP3 MP3_1 (
    .CYCLE(CYCLE), .RESET(RESET), .HARRYPLAY(MP3_1_harryplay), .ZELDAPLAY(MP3_1_zeldaplay), .BUZZER(BUZZER),
    .PIRATEPLAY(MP3_1_pirateplay), .ZELDALIGHT(ZELDAPLAYING), .PIRATELIGHT(ODEPLAYING),
    .HARRYLIGHT(HARRYPLAYING));
  Affichage1 Affichage1_1 (
    .HARRY(MP3_1_harryplay), .ZELDA(MP3_1_zeldaplay), .PIRATE(MP3_1_pirateplay), .V0(Affichage1_1_v0),
    .W0(Affichage1_1_w0), .X0(Affichage1_1_x0), .Y0(Affichage1_1_y0), .Z0(Affichage1_1_z0));
  Affichage2 Affichage2_1 (
    .HARRY(MP3_1_harryplay), .ZELDA(MP3_1_zeldaplay), .PIRATE(MP3_1_pirateplay), .V1(Affichage2_1_v1),
    .W1(Affichage2_1_w1), .X1(Affichage2_1_x1), .Y1(Affichage2_1_y1), .Z1(Affichage2_1_z1));
  Affichage3 Affichage3_1 (
    .HARRY(MP3_1_harryplay), .ZELDA(MP3_1_zeldaplay), .PIRATE(MP3_1_pirateplay), .V2(Affichage3_1_v2),
    .W2(Affichage3_1_w2), .X2(Affichage3_1_x2), .Y2(Affichage3_1_y2), .Z2(Affichage3_1_z2));
  Affichage4 Affichage4_1 (
    .HARRY(MP3_1_harryplay), .ZELDA(MP3_1_zeldaplay), .PIRATE(MP3_1_pirateplay), .V3(Affichage4_1_v3),
    .W3(Affichage4_1_w3), .X3(Affichage4_1_x3), .Y3(Affichage4_1_y3), .Z3(Affichage4_1_z3));
  Affichage5 Affichage5_1 (
    .HARRY(MP3_1_harryplay), .ZELDA(MP3_1_zeldaplay), .PIRATE(MP3_1_pirateplay), .V4(Affichage5_1_v4),
    .W4(Affichage5_1_w4), .X4(Affichage5_1_x4), .Y4(Affichage5_1_y4), .Z4(Affichage5_1_z4));
  Affichage6 Affichage6_1 (
    .HARRY(MP3_1_harryplay), .ZELDA(MP3_1_zeldaplay), .PIRATE(MP3_1_pirateplay), .V5(Affichage6_1_v5),
    .W5(Affichage6_1_w5), .X5(Affichage6_1_x5), .Y5(Affichage6_1_y5), .Z5(Affichage6_1_z5));
  sevensegA_Z sevensegA_Z_1 (
    .d(AFF1[3]), .b(AFF1[1]), .Z(Affichage1_1_z0), .X(Affichage1_1_x0), .V(Affichage1_1_v0),
    .W(Affichage1_1_w0), .Y(Affichage1_1_y0), .a(AFF1[0]), .c(AFF1[2]), .e(AFF1[4]), .f(AFF1[5]), .g(AFF1[6]));
  sevensegA_Z sevensegA_Z_2 (
    .d(AFF2[3]), .b(AFF2[1]), .Z(Affichage2_1_z1), .X(Affichage2_1_x1), .V(Affichage2_1_v1),
    .W(Affichage2_1_w1), .Y(Affichage2_1_y1), .a(AFF2[0]), .c(AFF2[2]), .e(AFF2[4]), .f(AFF2[5]), .g(AFF2[6]));
  sevensegA_Z sevensegA_Z_3 (
    .d(AFF3[3]), .b(AFF3[1]), .Z(Affichage3_1_z2), .X(Affichage3_1_x2), .V(Affichage3_1_v2),
    .W(Affichage3_1_w2), .Y(Affichage3_1_y2), .a(AFF3[0]), .c(AFF3[2]), .e(AFF3[4]), .f(AFF3[5]), .g(AFF3[6]));
  sevensegA_Z sevensegA_Z_4 (
    .d(AFF4[3]), .b(AFF4[1]), .Z(Affichage4_1_z3), .X(Affichage4_1_x3), .V(Affichage4_1_v3),
    .W(Affichage4_1_w3), .Y(Affichage4_1_y3), .a(AFF4[0]), .c(AFF4[2]), .e(AFF4[4]), .f(AFF4[5]), .g(AFF4[6]));
  sevensegA_Z sevensegA_Z_5 (
    .d(AFF5[3]), .b(AFF5[1]), .Z(Affichage5_1_z4), .X(Affichage5_1_x4), .V(Affichage5_1_v4),
    .W(Affichage5_1_w4), .Y(Affichage5_1_y4), .a(AFF5[0]), .c(AFF5[2]), .e(AFF5[4]), .f(AFF5[5]), .g(AFF5[6]));
  sevensegA_Z sevensegA_Z_6 (
    .d(AFF6[3]), .b(AFF6[1]), .Z(Affichage6_1_z5), .X(Affichage6_1_x5), .V(Affichage6_1_v5),
    .W(Affichage6_1_w5), .Y(Affichage6_1_y5), .a(AFF6[0]), .c(AFF6[2]), .e(AFF6[4]), .f(AFF6[5]), .g(AFF6[6]));

  assign AFF1[7] = 1'b0;
  assign AFF2[7] = 1'b0;
  assign AFF3[7] = 1'b0;
  assign AFF4[7] = 1'b0;
  assign AFF5[7] = 1'b0;
  assign AFF6[7] = 1'b0;
endmodule

module RINGANIMATION (
  output [7:0] AFF1,
  output [7:0] AFF2,
  output [7:0] AFF3,
  output [7:0] AFF4,
  output [7:0] AFF5,
  output [7:0] AFF6
);

  wire [5:0] or_1_out, or_2_out, or_3_out, or_4_out, or_5_out, or_6_out, simpleAnim_1_option1,
       simpleAnim_1_option2, simpleAnim_2_option1, simpleAnim_2_option2, simpleAnim_3_option1,
       simpleAnim_3_option2, simpleAnim_4_option1, simpleAnim_4_option2, simpleAnim_5_option1,
       simpleAnim_5_option2, simpleAnim_6_option1, simpleAnim_6_option2;

  simpleAnim simpleAnim_1 (.letter(6'b100010), .option1(simpleAnim_1_option1), .option2(simpleAnim_1_option2));
  simpleAnim simpleAnim_2 (.letter(6'b010000), .option1(simpleAnim_2_option1), .option2(simpleAnim_2_option2));
  simpleAnim simpleAnim_3 (.letter(6'b011010), .option1(simpleAnim_3_option1), .option2(simpleAnim_3_option2));
  simpleAnim simpleAnim_4 (.letter(6'b001100), .option1(simpleAnim_4_option1), .option2(simpleAnim_4_option2));
  simpleAnim simpleAnim_5 (.letter(6'b111110), .option1(simpleAnim_5_option1), .option2(simpleAnim_5_option2));
  simpleAnim simpleAnim_6 (.letter(6'b111110), .option1(simpleAnim_6_option1), .option2(simpleAnim_6_option2));
  assign or_1_out = simpleAnim_1_option1 | simpleAnim_5_option2;  // OR_Gate or_1, 6 bits wide
  assign or_2_out = simpleAnim_2_option1 | simpleAnim_6_option2;  // OR_Gate or_2, 6 bits wide
  assign or_3_out = simpleAnim_3_option1 | simpleAnim_1_option2;  // OR_Gate or_3, 6 bits wide
  assign or_4_out = simpleAnim_4_option1 | simpleAnim_2_option2;  // OR_Gate or_4, 6 bits wide
  assign or_5_out = simpleAnim_5_option1 | simpleAnim_3_option2;  // OR_Gate or_5, 6 bits wide
  assign or_6_out = simpleAnim_6_option1 | simpleAnim_4_option2;  // OR_Gate or_6, 6 bits wide
  sevensegBUS2 sevensegBUS2_1 (.LETTER(or_1_out), .LETTERCODE(AFF1));
  sevensegBUS2 sevensegBUS2_2 (.LETTER(or_2_out), .LETTERCODE(AFF2));
  sevensegBUS2 sevensegBUS2_3 (.LETTER(or_3_out), .LETTERCODE(AFF3));
  sevensegBUS2 sevensegBUS2_4 (.LETTER(or_4_out), .LETTERCODE(AFF4));
  sevensegBUS2 sevensegBUS2_5 (.LETTER(or_5_out), .LETTERCODE(AFF5));
  sevensegBUS2 sevensegBUS2_6 (.LETTER(or_6_out), .LETTERCODE(AFF6));

  // Notes on the sheet:
  //   R
  //   I
  //   N
  //   G
  //   BLANK
endmodule

module simpleAnim (
  input  [5:0] letter,
  output [5:0] option1,
  output [5:0] option2
);

  wire clock_1_out, d_ff_1_q, twobitadder_1_s2;

  twobitadder twobitadder_1 (.A2(d_ff_1_q), .B2(1'b1), .S2(twobitadder_1_s2));  // open: R, C2
  Clock #(.highDuration(12000), .lowDuration(12000)) clock_1 (.out(clock_1_out));
  D_Flip_Flop d_ff_1 (.D(twobitadder_1_s2), .clk(clock_1_out), .Q(d_ff_1_q));  // open: Qn, preset, reset
  Demultiplexer #(.width(6), .enable("false")) demultiplexer_1 (
    .out0(option1), .out1(option2), .in(letter), .sel(d_ff_1_q));
endmodule

module animviewer (
);

  wire [7:0] RINGANIMATION_1_aff1, RINGANIMATION_1_aff2, RINGANIMATION_1_aff3, RINGANIMATION_1_aff4,
       RINGANIMATION_1_aff5, RINGANIMATION_1_aff6;

  RINGANIMATION RINGANIMATION_1 (
    .AFF1(RINGANIMATION_1_aff1), .AFF2(RINGANIMATION_1_aff2), .AFF3(RINGANIMATION_1_aff3),
    .AFF4(RINGANIMATION_1_aff4), .AFF5(RINGANIMATION_1_aff5), .AFF6(RINGANIMATION_1_aff6));
  BUSAFFICHE BUSAFFICHE_1 (.Input_bus_1(RINGANIMATION_1_aff1));
  BUSAFFICHE BUSAFFICHE_2 (.Input_bus_1(RINGANIMATION_1_aff2));
  BUSAFFICHE BUSAFFICHE_3 (.Input_bus_1(RINGANIMATION_1_aff3));
  BUSAFFICHE BUSAFFICHE_4 (.Input_bus_1(RINGANIMATION_1_aff4));
  BUSAFFICHE BUSAFFICHE_5 (.Input_bus_1(RINGANIMATION_1_aff5));
  BUSAFFICHE BUSAFFICHE_6 (.Input_bus_1(RINGANIMATION_1_aff6));
endmodule

module GIGAPLEX (
  input  [2:0] OPTIONS,
  input  [31:0] FCLOCK,
  input  [15:0] SCLOCK,
  input  [31:0] FALARM,
  input  [15:0] SALARM,
  input  [31:0] FMUS,
  input  [15:0] SMUS,
  input  [31:0] FRING,
  input  [15:0] SRING,
  input  [31:0] FZONES,
  input  [15:0] SZONES,
  input  [31:0] FTIMER,
  input  [15:0] STIMER,
  input  [31:0] FCHRONO,
  input  [15:0] SCHRONO,
  input  [31:0] FMSG,
  input  [15:0] SMSG,
  input  [31:0] FCALCL,
  input  [15:0] SCALC,
  input  CHRONO,
  output [7:0] AFF1,
  output [7:0] AFF2,
  output [7:0] AFF3,
  output [7:0] AFF4,
  output [7:0] AFF5,
  output [7:0] AFF6
);

  wire [7:0] multiplexer_1_out, multiplexer_2_out, multiplexer_3_out, multiplexer_4_out, multiplexer_5_out,
       multiplexer_6_out, Splitter1to2IN_1_lsb, Splitter1to2IN_1_msb, Splitter1to2IN_2_lsb,
       Splitter1to2IN_2_msb, Splitter1to2IN_3_lsb, Splitter1to2IN_3_msb, Splitter1to2IN_4_lsb,
       Splitter1to2IN_4_msb, Splitter1to2IN_5_lsb, Splitter1to2IN_5_msb, Splitter1to2IN_6_lsb,
       Splitter1to2IN_6_msb, Splitter1to2IN_7_lsb, Splitter1to2IN_7_msb, Splitter1to2IN_8_lsb,
       Splitter1to2IN_8_msb, Splitter1to2IN_9_lsb, Splitter1to2IN_9_msb, Splitter1to4IN_1_c1,
       Splitter1to4IN_1_c2, Splitter1to4IN_1_lsb, Splitter1to4IN_1_msb, Splitter1to4IN_2_c1,
       Splitter1to4IN_2_c2, Splitter1to4IN_2_lsb, Splitter1to4IN_2_msb, Splitter1to4IN_3_c1,
       Splitter1to4IN_3_c2, Splitter1to4IN_3_lsb, Splitter1to4IN_3_msb, Splitter1to4IN_4_c1,
       Splitter1to4IN_4_c2, Splitter1to4IN_4_lsb, Splitter1to4IN_4_msb, Splitter1to4IN_5_c1,
       Splitter1to4IN_5_c2, Splitter1to4IN_5_lsb, Splitter1to4IN_5_msb, Splitter1to4IN_6_c1,
       Splitter1to4IN_6_c2, Splitter1to4IN_6_lsb, Splitter1to4IN_6_msb, Splitter1to4IN_7_c1,
       Splitter1to4IN_7_c2, Splitter1to4IN_7_lsb, Splitter1to4IN_7_msb, Splitter1to4IN_8_c1,
       Splitter1to4IN_8_c2, Splitter1to4IN_8_lsb, Splitter1to4IN_8_msb, Splitter1to4IN_9_c1,
       Splitter1to4IN_9_c2, Splitter1to4IN_9_lsb, Splitter1to4IN_9_msb;

  Splitter1to4IN Splitter1to4IN_1 (
    .BUSIN(FCLOCK), .LSB(Splitter1to4IN_1_lsb), .C1(Splitter1to4IN_1_c1), .C2(Splitter1to4IN_1_c2),
    .MSB(Splitter1to4IN_1_msb));
  Splitter1to2IN Splitter1to2IN_1 (.MSB(Splitter1to2IN_1_msb), .LSB(Splitter1to2IN_1_lsb), .BUSIN(SCLOCK));
  Splitter1to4IN Splitter1to4IN_2 (
    .BUSIN(FALARM), .LSB(Splitter1to4IN_2_lsb), .C1(Splitter1to4IN_2_c1), .C2(Splitter1to4IN_2_c2),
    .MSB(Splitter1to4IN_2_msb));
  Splitter1to2IN Splitter1to2IN_2 (.MSB(Splitter1to2IN_2_msb), .LSB(Splitter1to2IN_2_lsb), .BUSIN(SALARM));
  Splitter1to4IN Splitter1to4IN_3 (
    .BUSIN(FMUS), .LSB(Splitter1to4IN_3_lsb), .C1(Splitter1to4IN_3_c1), .C2(Splitter1to4IN_3_c2),
    .MSB(Splitter1to4IN_3_msb));
  Splitter1to2IN Splitter1to2IN_3 (.MSB(Splitter1to2IN_3_msb), .LSB(Splitter1to2IN_3_lsb), .BUSIN(SMUS));
  Splitter1to4IN Splitter1to4IN_4 (
    .BUSIN(FRING), .LSB(Splitter1to4IN_4_lsb), .C1(Splitter1to4IN_4_c1), .C2(Splitter1to4IN_4_c2),
    .MSB(Splitter1to4IN_4_msb));
  Splitter1to2IN Splitter1to2IN_4 (.MSB(Splitter1to2IN_4_msb), .LSB(Splitter1to2IN_4_lsb), .BUSIN(SRING));
  Splitter1to4IN Splitter1to4IN_5 (
    .BUSIN(FZONES), .LSB(Splitter1to4IN_5_lsb), .C1(Splitter1to4IN_5_c1), .C2(Splitter1to4IN_5_c2),
    .MSB(Splitter1to4IN_5_msb));
  Splitter1to2IN Splitter1to2IN_5 (.MSB(Splitter1to2IN_5_msb), .LSB(Splitter1to2IN_5_lsb), .BUSIN(SZONES));
  Splitter1to4IN Splitter1to4IN_6 (
    .BUSIN(FTIMER), .LSB(Splitter1to4IN_6_lsb), .C1(Splitter1to4IN_6_c1), .C2(Splitter1to4IN_6_c2),
    .MSB(Splitter1to4IN_6_msb));
  Splitter1to2IN Splitter1to2IN_6 (.MSB(Splitter1to2IN_6_msb), .LSB(Splitter1to2IN_6_lsb), .BUSIN(STIMER));
  Splitter1to4IN Splitter1to4IN_7 (
    .BUSIN(FCHRONO), .LSB(Splitter1to4IN_7_lsb), .C1(Splitter1to4IN_7_c1), .C2(Splitter1to4IN_7_c2),
    .MSB(Splitter1to4IN_7_msb));
  Splitter1to2IN Splitter1to2IN_7 (.MSB(Splitter1to2IN_7_msb), .LSB(Splitter1to2IN_7_lsb), .BUSIN(SCHRONO));
  Splitter1to4IN Splitter1to4IN_8 (
    .BUSIN(FMSG), .LSB(Splitter1to4IN_8_lsb), .C1(Splitter1to4IN_8_c1), .C2(Splitter1to4IN_8_c2),
    .MSB(Splitter1to4IN_8_msb));
  Splitter1to2IN Splitter1to2IN_8 (.MSB(Splitter1to2IN_8_msb), .LSB(Splitter1to2IN_8_lsb), .BUSIN(SMSG));
  Splitter1to4IN Splitter1to4IN_9 (
    .BUSIN(FCALCL), .LSB(Splitter1to4IN_9_lsb), .C1(Splitter1to4IN_9_c1), .C2(Splitter1to4IN_9_c2),
    .MSB(Splitter1to4IN_9_msb));
  Splitter1to2IN Splitter1to2IN_9 (.MSB(Splitter1to2IN_9_msb), .LSB(Splitter1to2IN_9_lsb), .BUSIN(SCALC));
  Multiplexer #(.width(8), .enable("false")) multiplexer_1 (
    .in0(Splitter1to4IN_6_lsb), .in1(Splitter1to4IN_7_lsb), .out(multiplexer_1_out), .sel(CHRONO));
  Multiplexer #(.width(8), .enable("false")) multiplexer_2 (
    .in0(Splitter1to4IN_6_c1), .in1(Splitter1to4IN_7_c1), .out(multiplexer_2_out), .sel(CHRONO));
  Multiplexer #(.width(8), .enable("false")) multiplexer_3 (
    .in0(Splitter1to4IN_6_c2), .in1(Splitter1to4IN_7_c2), .out(multiplexer_3_out), .sel(CHRONO));
  Multiplexer #(.width(8), .enable("false")) multiplexer_4 (
    .in0(Splitter1to4IN_6_msb), .in1(Splitter1to4IN_7_msb), .out(multiplexer_4_out), .sel(CHRONO));
  Multiplexer #(.width(8), .enable("false")) multiplexer_5 (
    .in0(Splitter1to2IN_6_lsb), .in1(Splitter1to2IN_7_lsb), .out(multiplexer_5_out), .sel(CHRONO));
  Multiplexer #(.width(8), .enable("false")) multiplexer_6 (
    .in0(Splitter1to2IN_6_msb), .in1(Splitter1to2IN_7_msb), .out(multiplexer_6_out), .sel(CHRONO));
  Multiplexer #(.select(3), .width(8), .enable("false")) multiplexer_7 (
    .in0(Splitter1to4IN_1_lsb), .in1(Splitter1to4IN_2_lsb), .in2(Splitter1to4IN_3_lsb),
    .in3(Splitter1to4IN_4_lsb), .in4(Splitter1to4IN_5_lsb), .in5(multiplexer_1_out),
    .in6(Splitter1to4IN_8_lsb), .in7(Splitter1to4IN_9_lsb), .out(AFF1), .sel(OPTIONS));
  Multiplexer #(.select(3), .width(8), .enable("false")) multiplexer_8 (
    .in0(Splitter1to4IN_1_c1), .in1(Splitter1to4IN_2_c1), .in2(Splitter1to4IN_3_c1),
    .in3(Splitter1to4IN_4_c1), .in4(Splitter1to4IN_5_c1), .in5(multiplexer_2_out), .in6(Splitter1to4IN_8_c1),
    .in7(Splitter1to4IN_9_c1), .out(AFF2), .sel(OPTIONS));
  Multiplexer #(.select(3), .width(8), .enable("false")) multiplexer_9 (
    .in0(Splitter1to4IN_1_c2), .in1(Splitter1to4IN_2_c2), .in2(Splitter1to4IN_3_c2),
    .in3(Splitter1to4IN_4_c2), .in4(Splitter1to4IN_5_c2), .in5(multiplexer_3_out), .in6(Splitter1to4IN_8_c2),
    .in7(Splitter1to4IN_9_c2), .out(AFF3), .sel(OPTIONS));
  Multiplexer #(.select(3), .width(8), .enable("false")) multiplexer_10 (
    .in0(Splitter1to4IN_1_msb), .in1(Splitter1to4IN_2_msb), .in2(Splitter1to4IN_3_msb),
    .in3(Splitter1to4IN_4_msb), .in4(Splitter1to4IN_5_msb), .in5(multiplexer_4_out),
    .in6(Splitter1to4IN_8_msb), .in7(Splitter1to4IN_9_msb), .out(AFF4), .sel(OPTIONS));
  Multiplexer #(.select(3), .width(8), .enable("false")) multiplexer_11 (
    .in0(Splitter1to2IN_1_lsb), .in1(Splitter1to2IN_2_lsb), .in2(Splitter1to2IN_3_lsb),
    .in3(Splitter1to2IN_4_lsb), .in4(Splitter1to2IN_5_lsb), .in5(multiplexer_5_out),
    .in6(Splitter1to2IN_8_lsb), .in7(Splitter1to2IN_9_lsb), .out(AFF5), .sel(OPTIONS));
  Multiplexer #(.select(3), .width(8), .enable("false")) multiplexer_12 (
    .in0(Splitter1to2IN_1_msb), .in1(Splitter1to2IN_2_msb), .in2(Splitter1to2IN_3_msb),
    .in3(Splitter1to2IN_4_msb), .in4(Splitter1to2IN_5_msb), .in5(multiplexer_6_out),
    .in6(Splitter1to2IN_8_msb), .in7(Splitter1to2IN_9_msb), .out(AFF6), .sel(OPTIONS));

  // Other names for the same wires on the sheet: chronomode = CHRONO
endmodule

module SubMenus (
  input  SELECTION,
  input  CURSETTIME,
  input  TIMER,
  input  CHRONO,
  input  CURZONES,
  input  CURALARM,
  input  MOTIV,
  input  CURMUSIC,
  input  CALC,
  input  RESET,
  input  LONGPRESSCALC,
  input  TIMERUNNING,
  input  TOFF,
  output CHANTIME,
  output CHANMUS,
  output DONE,
  output CHANALARM,
  output CHANMODEALARM,
  output CHANMUSIC,
  output CHANMODEZONES,
  output SETTIMER,
  output CHANMODETIMER,
  output TIMERACTIV,
  output CHANCHRONO,
  output CHANMSG,
  output FIRSTNUM,
  output CHANGECALC,
  output OPERATOR,
  output SECONDNUM,
  output SHOWANS
);

  wire Selectable_1_done, Selectable_2_done, Selectable_3_done, Selectable_4_done, Selectable_5_done,
       threesubmenus_1_done, timertwosubs_1_done, twosubsv2_1_done;

  Selectable Selectable_1 (
    .RESET(RESET), .current(CURSETTIME), .SELECTION(SELECTION), .CHANGING(CHANTIME), .DONE(Selectable_1_done));
  Selectable Selectable_2 (
    .RESET(RESET), .current(CURMUSIC), .SELECTION(SELECTION), .CHANGING(CHANMUS), .DONE(Selectable_2_done));
  twosubsv2 twosubsv2_1 (
    .RESET(RESET), .CURRENT(CURALARM), .SELECTION(SELECTION), .CHANGE1(CHANALARM), .CHANGING(CHANMODEALARM),
    .CHANGE2(CHANMUSIC), .DONE(twosubsv2_1_done));
  Selectable Selectable_5 (
    .RESET(RESET), .current(CURZONES), .SELECTION(SELECTION), .CHANGING(CHANMODEZONES),
    .DONE(Selectable_5_done));
  timertwosubs timertwosubs_1 (
    .RESET(RESET), .CURRENT(TIMER), .SELECTION(SELECTION), .TIMERUNNING(TIMERUNNING), .TOFF(TOFF),
    .CHANGE1(SETTIMER), .CHANGING(CHANMODETIMER), .CHANGE2(TIMERACTIV), .DONE(timertwosubs_1_done));
  Selectable Selectable_3 (
    .RESET(RESET), .current(CHRONO), .SELECTION(SELECTION), .CHANGING(CHANCHRONO), .DONE(Selectable_3_done));
  Selectable Selectable_4 (
    .RESET(RESET), .current(MOTIV), .SELECTION(SELECTION), .CHANGING(CHANMSG), .DONE(Selectable_4_done));
  threesubmenus threesubmenus_1 (
    .RESET(RESET), .CURRENT(CALC), .SELECTION(SELECTION), .LONG(LONGPRESSCALC), .CHANGE1(FIRSTNUM),
    .CHANGING(CHANGECALC), .CHANGE2(OPERATOR), .CHANGE3(SECONDNUM), .CHANGE4(SHOWANS),
    .DONE(threesubmenus_1_done));
  or or_1 (DONE, Selectable_1_done, Selectable_2_done, twosubsv2_1_done, Selectable_5_done, timertwosubs_1_done, Selectable_3_done, Selectable_4_done, threesubmenus_1_done);
endmodule

module zonesAffichage (
  input  [3:0] DAY1,
  input  [3:0] DAY0,
  input  [3:0] HOUR1,
  input  [3:0] HOUR0,
  input  CYCLEZONES,
  input  RESET,
  output [7:0] AFF1Z,
  output [7:0] AFF2Z,
  output [7:0] AFF3Z,
  output [7:0] AFF4Z,
  output [7:0] AFF5Z,
  output [7:0] AFF6Z,
  output [15:0] INFO
);

  wire LongPressMachine_1_outputting;
  wire [2:0] zone_mode_1_zcode;

  LongPressMachine LongPressMachine_1 (.B(CYCLEZONES), .OUTPUTTING(LongPressMachine_1_outputting));
  zone_mode zone_mode_1 (
    .OD1(DAY1), .OD0(DAY0), .OH1(HOUR1), .OH0(HOUR0), .CYCLEZONE(LongPressMachine_1_outputting),
    .RESET(RESET), .ZD1(INFO[3:0]), .ZD0(INFO[7:4]), .ZH1(INFO[11:8]), .ZH0(INFO[15:12]),
    .Zcode(zone_mode_1_zcode));
  zonesCountries zonesCountries_1 (
    .CTRL(zone_mode_1_zcode), .AFF1(AFF1Z), .AFF2(AFF2Z), .AFF3(AFF3Z), .AFF4(AFF4Z), .AFF5(AFF5Z),
    .AFF6(AFF6Z));
endmodule

module zonesCountries (
  input  [2:0] CTRL,
  output [7:0] AFF1,
  output [7:0] AFF2,
  output [7:0] AFF3,
  output [7:0] AFF4,
  output [7:0] AFF5,
  output [7:0] AFF6
);

  wire [7:0] sevensegBUS2_1_lettercode, sevensegBUS2_2_lettercode, sevensegBUS2_3_lettercode,
       sevensegBUS2_4_lettercode, sevensegBUS2_5_lettercode, sevensegBUS2_6_lettercode,
       sevensegBUS2_7_lettercode, sevensegBUS2_8_lettercode, sevensegBUS2_9_lettercode,
       sevensegBUS2_10_lettercode, sevensegBUS2_11_lettercode, sevensegBUS2_12_lettercode,
       sevensegBUS2_13_lettercode, sevensegBUS2_14_lettercode, sevensegBUS2_15_lettercode,
       sevensegBUS2_17_lettercode, sevensegBUS2_18_lettercode, sevensegBUS2_19_lettercode;

  sevensegBUS2 sevensegBUS2_1 (.LETTER(6'b000010), .LETTERCODE(sevensegBUS2_1_lettercode));
  sevensegBUS2 sevensegBUS2_2 (.LETTER(6'b100010), .LETTERCODE(sevensegBUS2_2_lettercode));
  sevensegBUS2 sevensegBUS2_3 (.LETTER(6'b011010), .LETTERCODE(sevensegBUS2_3_lettercode));
  sevensegBUS2 sevensegBUS2_4 (.LETTER(6'b011110), .LETTERCODE(sevensegBUS2_4_lettercode));
  sevensegBUS2 sevensegBUS2_5 (.LETTER(6'b100110), .LETTERCODE(sevensegBUS2_5_lettercode));
  sevensegBUS2 sevensegBUS2_6 (.LETTER(6'b010110), .LETTERCODE(sevensegBUS2_6_lettercode));
  sevensegBUS2 sevensegBUS2_10 (.LETTER(6'b000010), .LETTERCODE(sevensegBUS2_10_lettercode));
  sevensegBUS2 sevensegBUS2_11 (.LETTER(6'b100010), .LETTERCODE(sevensegBUS2_11_lettercode));
  sevensegBUS2 sevensegBUS2_12 (.LETTER({6{1'b0}}), .LETTERCODE(sevensegBUS2_12_lettercode));
  sevensegBUS2 sevensegBUS2_7 (.LETTER(6'b101100), .LETTERCODE(sevensegBUS2_7_lettercode));
  sevensegBUS2 sevensegBUS2_8 (.LETTER({6{1'b0}}), .LETTERCODE(sevensegBUS2_8_lettercode));
  sevensegBUS2 sevensegBUS2_9 (.LETTER(6'b100100), .LETTERCODE(sevensegBUS2_9_lettercode));
  sevensegBUS2 sevensegBUS2_17 (.LETTER(6'b101100), .LETTERCODE(sevensegBUS2_17_lettercode));
  sevensegBUS2 sevensegBUS2_18 (.LETTER(6'b001000), .LETTERCODE(sevensegBUS2_18_lettercode));
  sevensegBUS2 sevensegBUS2_19 (.LETTER(6'b010110), .LETTERCODE(sevensegBUS2_19_lettercode));
  sevensegBUS2 sevensegBUS2_13 (.LETTER({6{1'b0}}), .LETTERCODE(sevensegBUS2_13_lettercode));
  sevensegBUS2 sevensegBUS2_14 (.LETTER(6'b101010), .LETTERCODE(sevensegBUS2_14_lettercode));
  sevensegBUS2 sevensegBUS2_15 (.LETTER({6{1'b0}}), .LETTERCODE(sevensegBUS2_15_lettercode));
  sevensegBUS2 sevensegBUS2_16 (.LETTER(6'b111110), .LETTERCODE(AFF4));
  Multiplexer #(.select(3), .width(8), .enable("false")) multiplexer_1 (
    .in0(sevensegBUS2_1_lettercode), .in1(sevensegBUS2_4_lettercode), .in2(sevensegBUS2_10_lettercode),
    .in3(sevensegBUS2_7_lettercode), .in4(sevensegBUS2_17_lettercode), .in5(sevensegBUS2_13_lettercode),
    .out(AFF1), .sel(CTRL));  // open: in6, in7
  Multiplexer #(.select(3), .width(8), .enable("false")) multiplexer_2 (
    .in0(sevensegBUS2_2_lettercode), .in1(sevensegBUS2_5_lettercode), .in2(sevensegBUS2_11_lettercode),
    .in3(sevensegBUS2_8_lettercode), .in4(sevensegBUS2_18_lettercode), .in5(sevensegBUS2_14_lettercode),
    .out(AFF2), .sel(CTRL));  // open: in6, in7
  Multiplexer #(.select(3), .width(8), .enable("false")) multiplexer_3 (
    .in0(sevensegBUS2_3_lettercode), .in1(sevensegBUS2_6_lettercode), .in2(sevensegBUS2_12_lettercode),
    .in3(sevensegBUS2_9_lettercode), .in4(sevensegBUS2_19_lettercode), .in5(sevensegBUS2_15_lettercode),
    .out(AFF3), .sel(CTRL));  // open: in6, in7

  assign AFF5 = AFF4;
  assign AFF6 = AFF4;

  // Notes on the sheet:
  //   B
  //   R
  //   N
  //   P
  //   T
  //   L
  //   B
  //   R
  //   A
  //   W
  //   A
  //   S
  //   W
  //   E
  //   L
  //   A
  //   V
  //   A
  //   BLANK
endmodule

module normalpress (
  input  B,
  output OUTP
);

  wire clock_1_out, d_ff_1_q, States_1_bpout;

  States States_1 (.B(B), .BP(d_ff_1_q), .BPout(States_1_bpout), .S(OUTP));
  D_Flip_Flop d_ff_1 (.D(States_1_bpout), .clk(clock_1_out), .Q(d_ff_1_q));  // open: Qn, preset, reset
  Clock clock_1 (.out(clock_1_out));
endmodule

module chronoAffiche (
  input  reset,
  input  start_stop,
  output [7:0] chrono1,
  output [7:0] chrono2,
  output [7:0] chrono3,
  output [7:0] chrono4,
  output [7:0] chrono5,
  output [7:0] chrono6
);

  wire LongPress2Butts_1_reset, LongPress2Butts_1_set, or_1_out;
  wire [3:0] chronometre_1_chrcs0, chronometre_1_chrcs1, chronometre_1_chrm0, chronometre_1_chrm1,
       chronometre_1_chrs0, chronometre_1_chrs1;

  LongPress2Butts LongPress2Butts_1 (.BUTTON(start_stop), .RESET(LongPress2Butts_1_reset), .SET(LongPress2Butts_1_set));
  or or_1 (or_1_out, reset, LongPress2Butts_1_reset);
  chronometre chronometre_1 (
    .RESET(or_1_out), .EN(LongPress2Butts_1_set), .chrCS0(chronometre_1_chrcs0),
    .chrCS1(chronometre_1_chrcs1), .chrS0(chronometre_1_chrs0), .chrS1(chronometre_1_chrs1),
    .chrM0(chronometre_1_chrm0), .chrM1(chronometre_1_chrm1));
  numb_4_to_8 centSec0 (.NUMB(chronometre_1_chrcs0), .EN(1'b1), .numbout(chrono6));
  numb_4_to_8 centSec1 (.NUMB(chronometre_1_chrcs1), .EN(1'b1), .numbout(chrono5));
  numb_4_to_8 sec_0 (.NUMB(chronometre_1_chrs0), .EN(1'b1), .numbout(chrono4));
  numb_4_to_8 sec_1 (.NUMB(chronometre_1_chrs1), .EN(1'b1), .numbout(chrono3));
  numb_4_to_8 min_0 (.NUMB(chronometre_1_chrm0), .EN(1'b1), .numbout(chrono2));
  numb_4_to_8 min_1 (.NUMB(chronometre_1_chrm1), .EN(1'b1), .numbout(chrono1));
endmodule

module LongPress2Butts (
  input  BUTTON,
  output RESET,
  output SET
);

  wire clock_1_out, d_ff_1_q, not_1_out, States_1_bpout;

  not not_1 (not_1_out, BUTTON);
  LongPressDetector LongPressDetector_1 (.BUTTON(BUTTON), .RESET(not_1_out), .LONGPRESSMODE(RESET));
  States States_1 (.B(BUTTON), .BP(d_ff_1_q), .BPout(States_1_bpout), .S(SET));
  D_Flip_Flop d_ff_1 (.D(States_1_bpout), .clk(clock_1_out), .Q(d_ff_1_q));  // open: Qn, preset, reset
  Clock clock_1 (.out(clock_1_out));
endmodule

module MSGAFF (
  input  PLAY,
  output [7:0] AFF1,
  output [7:0] AFF2,
  output [7:0] AFF3,
  output [7:0] AFF4,
  output [7:0] AFF5,
  output [7:0] AFF6
);

  wire [4:0] allscreens_1_aff1, allscreens_1_aff2, allscreens_1_aff3, allscreens_1_aff4, allscreens_1_aff5,
       allscreens_1_aff6;

  allscreens allscreens_1 (
    .PLAY(PLAY), .AFF6(allscreens_1_aff6), .AFF5(allscreens_1_aff5), .AFF4(allscreens_1_aff4),
    .AFF3(allscreens_1_aff3), .AFF2(allscreens_1_aff2), .AFF1(allscreens_1_aff1));
  fivetoeight fivetoeight_1 (.LETTERIN(allscreens_1_aff6), .letterout(AFF6));
  fivetoeight fivetoeight_2 (.LETTERIN(allscreens_1_aff5), .letterout(AFF5));
  fivetoeight fivetoeight_3 (.LETTERIN(allscreens_1_aff4), .letterout(AFF4));
  fivetoeight fivetoeight_4 (.LETTERIN(allscreens_1_aff3), .letterout(AFF3));
  fivetoeight fivetoeight_5 (.LETTERIN(allscreens_1_aff2), .letterout(AFF2));
  fivetoeight fivetoeight_6 (.LETTERIN(allscreens_1_aff1), .letterout(AFF1));
endmodule

module TIMERAFF (
  input  B,
  input  SETLOWMS,
  input  SETHIMS,
  input  SETLOWSEC,
  input  SETHISEC,
  input  SETLOWMIN,
  input  SETHIMIN,
  input  SETTINGTIME,
  input  TIMERSET,
  input  RESET,
  output [7:0] AFF1,
  output [7:0] AFF2,
  output [7:0] AFF3,
  output [7:0] AFF4,
  output [7:0] AFF5,
  output [7:0] AFF6,
  output TIMEST,
  output BUZZER
);

  wire and_1_out, and_8_out, and_9_out, and_11_out, C_1_output_1, clock_1_out, clock_2_out, d_ff_1_q,
       d_ff_2_q, d_ff_3_q, d_ff_3_qn, LongPress2Butts_1_reset, LongPress2Butts_1_set, normalpress_1_outp,
       or_1_out, or_2_out, or_3_out, s_r_ff_2_q, s_r_ff_3_q, timer_1_timerdone, timerstates_1_startout,
       timerstates_1_stopout;
  wire [3:0] timer_1_himin, timer_1_hims, timer_1_hisec, timer_1_lowmin, timer_1_lowms, timer_1_lowsec,
       TIMERSETTER_1_himin, TIMERSETTER_1_hims, TIMERSETTER_1_hisec, TIMERSETTER_1_lowmin,
       TIMERSETTER_1_lowms, TIMERSETTER_1_lowsec;
  wire [6:0] numb_4_to_7_1_numbout, numb_4_to_7_2_numbout, numb_4_to_7_3_numbout, numb_4_to_7_4_numbout,
       numb_4_to_7_5_numbout, numb_4_to_7_6_numbout;
  wire [7:7] and_2_out, and_3_out, and_4_out, and_5_out, and_6_out, and_7_out;

  normalpress normalpress_1 (.B(TIMERSET), .OUTP(normalpress_1_outp));
  S_R_Flip_Flop s_r_ff_1 (.Q(TIMEST), .reset(RESET), .preset(normalpress_1_outp));  // open: S, R, clk, Qn
  and and_1 (and_1_out, ~SETTINGTIME, ~TIMEST);  // AND_Gate
  and and_2 (and_2_out[7], SETTINGTIME, SETLOWMS);
  and and_3 (and_3_out[7], SETTINGTIME, SETHIMS);
  and and_4 (and_4_out[7], SETTINGTIME, SETLOWSEC);
  and and_5 (and_5_out[7], SETTINGTIME, SETHISEC);
  and and_6 (and_6_out[7], SETTINGTIME, SETLOWMIN);
  and and_7 (and_7_out[7], SETTINGTIME, SETHIMIN);
  and and_8 (and_8_out, LongPress2Butts_1_set, and_9_out);
  LongPress2Butts LongPress2Butts_1 (.BUTTON(B), .RESET(LongPress2Butts_1_reset), .SET(LongPress2Butts_1_set));
  or or_1 (or_1_out, LongPress2Butts_1_reset, RESET);
  timerstates timerstates_1 (
    .B(and_8_out), .START(s_r_ff_2_q), .STARTOUT(timerstates_1_startout), .STOPOUT(timerstates_1_stopout));
  and and_9 (and_9_out, TIMEST, ~LongPress2Butts_1_reset, ~RESET);  // AND_Gate
  D_Flip_Flop d_ff_1 (.D(timerstates_1_startout), .clk(clock_1_out), .Q(d_ff_1_q));  // open: Qn, preset, reset
  Clock clock_1 (.out(clock_1_out));
  TIMERSETTER TIMERSETTER_1 (
    .CYCLE(LongPress2Butts_1_set), .RESET(RESET), .SETLOWMS(and_2_out[7]), .SETHIMS(and_3_out[7]),
    .SETLOWSEC(and_4_out[7]), .SETHISEC(and_5_out[7]), .SETLOWMIN(and_6_out[7]), .SETHIMIN(and_7_out[7]),
    .LOWMS(TIMERSETTER_1_lowms), .HIMS(TIMERSETTER_1_hims), .LOWSEC(TIMERSETTER_1_lowsec),
    .HISEC(TIMERSETTER_1_hisec), .LOWMIN(TIMERSETTER_1_lowmin), .HIMIN(TIMERSETTER_1_himin));
  D_Flip_Flop d_ff_2 (.D(timerstates_1_stopout), .clk(clock_1_out), .Q(d_ff_2_q));  // open: Qn, preset, reset
  or or_2 (or_2_out, d_ff_2_q, LongPress2Butts_1_reset);
  S_R_Flip_Flop s_r_ff_2 (.Q(s_r_ff_2_q), .reset(or_3_out), .preset(d_ff_1_q));  // open: S, R, clk, Qn
  or or_3 (or_3_out, or_2_out, and_1_out);
  timer timer_1 (
    .COUNT(s_r_ff_2_q), .TIMERSET(and_9_out), .NUMB1(TIMERSETTER_1_lowms), .NUMB2(TIMERSETTER_1_hims),
    .NUMB3(TIMERSETTER_1_lowsec), .NUMB4(TIMERSETTER_1_hisec), .NUMB5(TIMERSETTER_1_lowmin),
    .NUMB6(TIMERSETTER_1_himin), .lowms(timer_1_lowms), .hims(timer_1_hims), .lowsec(timer_1_lowsec),
    .hisec(timer_1_hisec), .lowmin(timer_1_lowmin), .himin(timer_1_himin), .TIMERDONE(timer_1_timerdone));
  S_R_Flip_Flop s_r_ff_3 (
    .S(timer_1_timerdone), .R(or_1_out), .clk(clock_1_out), .Q(s_r_ff_3_q));  // open: reset, Qn, preset
  numb_4_to_7 numb_4_to_7_1 (.NUMBER(timer_1_lowms), .EN(1'b1), .NUMBOUT(numb_4_to_7_1_numbout));
  numb_4_to_7 numb_4_to_7_2 (.NUMBER(timer_1_hims), .EN(1'b1), .NUMBOUT(numb_4_to_7_2_numbout));
  numb_4_to_7 numb_4_to_7_3 (.NUMBER(timer_1_lowsec), .EN(1'b1), .NUMBOUT(numb_4_to_7_3_numbout));
  numb_4_to_7 numb_4_to_7_4 (.NUMBER(timer_1_hisec), .EN(1'b1), .NUMBOUT(numb_4_to_7_4_numbout));
  numb_4_to_7 numb_4_to_7_5 (.NUMBER(timer_1_lowmin), .EN(1'b1), .NUMBOUT(numb_4_to_7_5_numbout));
  numb_4_to_7 numb_4_to_7_6 (.NUMBER(timer_1_himin), .EN(1'b1), .NUMBOUT(numb_4_to_7_6_numbout));
  C C_1 (.Output_1(C_1_output_1), .Input_1(s_r_ff_3_q));
  and and_10 (BUZZER, C_1_output_1, TIMEST);
  D_Flip_Flop d_ff_3 (.D(d_ff_3_qn), .clk(clock_2_out), .Q(d_ff_3_q), .Qn(d_ff_3_qn));  // open: preset, reset
  Clock #(.highDuration(16000), .lowDuration(16000)) clock_2 (.out(clock_2_out));
  Multiplexer #(.width(8), .enable("false")) multiplexer_1 (
    .in0({and_7_out[7], numb_4_to_7_6_numbout}), .in1({8{1'b0}}), .out(AFF1), .sel(and_11_out));
  Multiplexer #(.width(8), .enable("false")) multiplexer_2 (
    .in0({and_6_out[7], numb_4_to_7_5_numbout}), .in1({8{1'b0}}), .out(AFF2), .sel(and_11_out));
  Multiplexer #(.width(8), .enable("false")) multiplexer_3 (
    .in0({and_5_out[7], numb_4_to_7_4_numbout}), .in1({8{1'b0}}), .out(AFF3), .sel(and_11_out));
  Multiplexer #(.width(8), .enable("false")) multiplexer_4 (
    .in0({and_4_out[7], numb_4_to_7_3_numbout}), .in1({8{1'b0}}), .out(AFF4), .sel(and_11_out));
  Multiplexer #(.width(8), .enable("false")) multiplexer_5 (
    .in0({and_3_out[7], numb_4_to_7_2_numbout}), .in1({8{1'b0}}), .out(AFF5), .sel(and_11_out));
  Multiplexer #(.width(8), .enable("false")) multiplexer_6 (
    .in0({and_2_out[7], numb_4_to_7_1_numbout}), .in1({8{1'b0}}), .out(AFF6), .sel(and_11_out));
  and and_11 (and_11_out, ~TIMEST, d_ff_3_q);  // AND_Gate
endmodule

module selectFSMforFour (
  input  B,
  input  C1,
  input  C2,
  input  C3,
  input  D,
  input  DD,
  input  LP,
  output S1,
  output R1,
  output S2,
  output R2,
  output S3,
  output R3,
  output SD,
  output RD,
  output SDD,
  output RDD
);

  wire and_1_out, and_4_out, and_6_out, and_8_out, and_10_out, not_1_out, not_2_out, not_3_out, not_4_out,
       not_5_out, not_6_out, not_7_out, not_8_out, not_9_out, not_10_out, not_11_out, not_12_out, not_13_out,
       not_14_out, not_15_out, not_16_out, not_17_out, not_18_out, not_19_out, not_20_out, not_21_out,
       not_22_out, not_23_out, not_24_out, not_25_out, not_26_out, not_27_out, not_28_out, not_29_out,
       not_30_out, not_31_out, not_32_out, not_33_out, not_34_out, not_35_out, not_36_out, not_37_out,
       not_38_out, not_39_out, not_40_out, not_41_out, not_42_out, not_43_out, not_44_out, not_45_out,
       not_46_out, not_47_out;

  not not_1 (not_1_out, C1);
  not not_2 (not_2_out, C2);
  not not_3 (not_3_out, C3);
  not not_4 (not_4_out, D);
  not not_5 (not_5_out, DD);
  not not_6 (not_6_out, C3);
  not not_7 (not_7_out, D);
  not not_8 (not_8_out, DD);
  not not_9 (not_9_out, LP);
  not not_10 (not_10_out, B);
  not not_11 (not_11_out, C2);
  not not_12 (not_12_out, C3);
  not not_13 (not_13_out, D);
  not not_14 (not_14_out, DD);
  not not_15 (not_15_out, LP);
  not not_16 (not_16_out, C1);
  not not_17 (not_17_out, D);
  not not_18 (not_18_out, DD);
  not not_19 (not_19_out, B);
  not not_20 (not_20_out, C1);
  not not_21 (not_21_out, C3);
  not not_22 (not_22_out, D);
  not not_23 (not_23_out, DD);
  not not_24 (not_24_out, LP);
  not not_25 (not_25_out, C1);
  not not_26 (not_26_out, C2);
  not not_27 (not_27_out, DD);
  not not_28 (not_28_out, B);
  not not_29 (not_29_out, C1);
  not not_30 (not_30_out, C2);
  not not_31 (not_31_out, D);
  not not_32 (not_32_out, DD);
  not not_33 (not_33_out, LP);
  not not_34 (not_34_out, C1);
  not not_35 (not_35_out, C2);
  not not_36 (not_36_out, C3);
  not not_37 (not_37_out, B);
  not not_38 (not_38_out, C1);
  not not_39 (not_39_out, C2);
  not not_40 (not_40_out, C3);
  not not_41 (not_41_out, DD);
  not not_42 (not_42_out, LP);
  not not_43 (not_43_out, B);
  not not_44 (not_44_out, C1);
  not not_45 (not_45_out, C2);
  not not_46 (not_46_out, C3);
  not not_47 (not_47_out, D);
  and and_1 (and_1_out, B, not_1_out, not_2_out, not_3_out, not_4_out, not_5_out);
  and and_2 (R1, B, C1, C2, not_6_out, not_7_out, not_8_out, not_9_out);
  and and_3 (S2, not_10_out, C1, not_11_out, not_12_out, not_13_out, not_14_out, not_15_out);
  and and_4 (and_4_out, B, not_16_out, C2, C3, not_17_out, not_18_out);
  and and_5 (S3, not_19_out, not_20_out, C2, not_21_out, not_22_out, not_23_out, not_24_out);
  and and_6 (and_6_out, B, not_25_out, not_26_out, C3, D, not_27_out);
  and and_7 (SD, not_28_out, not_29_out, not_30_out, C3, not_31_out, not_32_out, not_33_out);
  and and_8 (and_8_out, B, not_34_out, not_35_out, not_36_out, D, DD);
  and and_9 (SDD, not_37_out, not_38_out, not_39_out, not_40_out, D, not_41_out, not_42_out);
  and and_10 (and_10_out, not_43_out, not_44_out, not_45_out, not_46_out, not_47_out, DD);
  or or_1 (S1, and_1_out, LP);
  or or_2 (R2, and_4_out, LP);
  or or_3 (R3, and_6_out, LP);
  or or_4 (RD, and_8_out, LP);
  or or_5 (RDD, and_10_out, LP);
endmodule

module threesubmenus (
  input  RESET,
  input  CURRENT,
  input  SELECTION,
  input  LONG,
  output CHANGE1,
  output CHANGING,
  output CHANGE2,
  output CHANGE3,
  output CHANGE4,
  output DONE
);

  wire and_1_out, and_2_out, not_1_out, not_2_out, or_1_out, or_2_out, or_3_out, or_4_out, or_5_out,
       or_6_out, s_r_ff_2_q, s_r_ff_3_q, s_r_ff_4_q, s_r_ff_5_q, selectFSMforFour_1_r1,
       selectFSMforFour_1_r2, selectFSMforFour_1_r3, selectFSMforFour_1_rd, selectFSMforFour_1_rdd,
       selectFSMforFour_1_s1, selectFSMforFour_1_s2, selectFSMforFour_1_s3, selectFSMforFour_1_sd,
       selectFSMforFour_1_sdd;

  or or_1 (or_1_out, RESET, ~CURRENT);  // OR_Gate
  selectFSMforFour selectFSMforFour_1 (
    .B(SELECTION), .C1(CHANGE1), .C2(s_r_ff_2_q), .C3(s_r_ff_4_q), .D(s_r_ff_5_q), .DD(s_r_ff_3_q),
    .LP(LONG), .S1(selectFSMforFour_1_s1), .R1(selectFSMforFour_1_r1), .S2(selectFSMforFour_1_s2),
    .R2(selectFSMforFour_1_r2), .S3(selectFSMforFour_1_s3), .R3(selectFSMforFour_1_r3),
    .SD(selectFSMforFour_1_sd), .RD(selectFSMforFour_1_rd), .SDD(selectFSMforFour_1_sdd),
    .RDD(selectFSMforFour_1_rdd));
  or or_2 (or_2_out, or_1_out, and_2_out);
  and and_1 (and_1_out, CURRENT, selectFSMforFour_1_s1);
  and and_2 (and_2_out, CURRENT, selectFSMforFour_1_r1);
  or or_3 (or_3_out, selectFSMforFour_1_r2, or_1_out);
  or or_4 (or_4_out, or_1_out, selectFSMforFour_1_rdd);
  S_R_Flip_Flop s_r_ff_1 (.Q(CHANGE1), .reset(or_2_out), .preset(and_1_out));  // open: S, R, clk, Qn
  S_R_Flip_Flop s_r_ff_2 (.Q(s_r_ff_2_q), .reset(or_3_out), .preset(selectFSMforFour_1_s2));  // open: S, R, clk, Qn
  or or_5 (or_5_out, selectFSMforFour_1_r3, or_1_out);
  or or_6 (or_6_out, selectFSMforFour_1_rd, or_1_out);
  S_R_Flip_Flop s_r_ff_3 (.Q(s_r_ff_3_q), .reset(or_4_out), .preset(selectFSMforFour_1_sdd));  // open: S, R, clk, Qn
  not not_1 (not_1_out, CHANGE1);
  S_R_Flip_Flop s_r_ff_4 (.Q(s_r_ff_4_q), .reset(or_5_out), .preset(selectFSMforFour_1_s3));  // open: S, R, clk, Qn
  S_R_Flip_Flop s_r_ff_5 (.Q(s_r_ff_5_q), .reset(or_6_out), .preset(selectFSMforFour_1_sd));  // open: S, R, clk, Qn
  and and_3 (CHANGE2, not_1_out, s_r_ff_2_q);
  not not_2 (not_2_out, CHANGE2);
  and and_4 (DONE, ~CHANGE4, s_r_ff_3_q);  // AND_Gate
  and and_5 (CHANGE3, not_2_out, s_r_ff_4_q);
  and and_6 (CHANGE4, ~CHANGE3, s_r_ff_5_q);  // AND_Gate
  or or_7 (CHANGING, CHANGE1, CHANGE4, CHANGE3, CHANGE2);
endmodule

module calcAff (
  input  CYCLE,
  input  CHANGE1,
  input  CHANGE2,
  input  CHANGE3,
  input  CHANGE4,
  input  RESET,
  input  [4:0] SETNUMB,
  output [7:0] AFF1,
  output [7:0] AFF2,
  output [7:0] AFF3,
  output [7:0] AFF4,
  output [7:0] AFF5,
  output [7:0] AFF6,
  output LP
);

  wire and_1_out, fullCalculator_1_negativer, LongPress2Butts_1_set;
  wire [1:0] calcucontroller_1_t0;
  wire [3:0] calcNumbSetter_1_hinum, calcNumbSetter_1_lownumb, calcNumbSetter_1_midnum,
       calcNumbSetter_1_negorpos, calcNumbSetter_2_hinum, calcNumbSetter_2_lownumb, calcNumbSetter_2_midnum,
       calcNumbSetter_2_negorpos, fullCalculator_1_number0, fullCalculator_1_number1,
       fullCalculator_1_number2;
  wire [6:0] numb_4_to_7_1_numbout, numb_4_to_7_2_numbout, numb_4_to_7_3_numbout, numb_4_to_7_4_numbout,
       numb_4_to_7_5_numbout, numb_4_to_7_6_numbout;
  wire [7:0] negativecoder_1_negaff, numb_4_to_8_1_numbout, numb_4_to_8_2_numbout, numb_4_to_8_3_numbout,
       numb_4_to_8_4_numbout, numb_4_to_8_5_numbout, operatorsAff_1_aff4, operatorsAff_1_aff5,
       operatorsAff_1_aff6;

  LongPress2Butts LongPress2Butts_1 (.BUTTON(CYCLE), .RESET(LP), .SET(LongPress2Butts_1_set));
  and and_1 (and_1_out, LongPress2Butts_1_set, CHANGE2);
  calcucontroller calcucontroller_1 (
    .CHANGE1(CHANGE1), .CHANGE2(CHANGE2), .CHANGE3(CHANGE3), .CHANGE4(CHANGE4), .T1(calcucontroller_1_t0[1]),
    .T0(calcucontroller_1_t0[0]));
  calcNumbSetter calcNumbSetter_1 (
    .CYCLE(LongPress2Butts_1_set), .RESET(RESET), .NEGATIVE(SETNUMB[3]), .SETHINUMB(SETNUMB[2]),
    .SETMIDNUMB(SETNUMB[1]), .SETLOWNUMB(SETNUMB[0]), .ENABLE(CHANGE1), .NEGORPOS(calcNumbSetter_1_negorpos),
    .HINUM(calcNumbSetter_1_hinum), .MIDNUM(calcNumbSetter_1_midnum), .LOWNUMB(calcNumbSetter_1_lownumb));
  operatorsAff operatorsAff_1 (
    .CYC(and_1_out), .AFF4(operatorsAff_1_aff4), .AFF5(operatorsAff_1_aff5), .AFF6(operatorsAff_1_aff6));
  calcNumbSetter calcNumbSetter_2 (
    .CYCLE(LongPress2Butts_1_set), .RESET(RESET), .NEGATIVE(SETNUMB[4]), .SETHINUMB(SETNUMB[2]),
    .SETMIDNUMB(SETNUMB[1]), .SETLOWNUMB(SETNUMB[0]), .ENABLE(CHANGE3), .NEGORPOS(calcNumbSetter_2_negorpos),
    .HINUM(calcNumbSetter_2_hinum), .MIDNUM(calcNumbSetter_2_midnum), .LOWNUMB(calcNumbSetter_2_lownumb));
  numb_4_to_7 numb_4_to_7_1 (.NUMBER(calcNumbSetter_1_hinum), .EN(1'b1), .NUMBOUT(numb_4_to_7_1_numbout));
  numb_4_to_7 numb_4_to_7_2 (.NUMBER(calcNumbSetter_1_midnum), .EN(1'b1), .NUMBOUT(numb_4_to_7_2_numbout));
  numb_4_to_7 numb_4_to_7_3 (.NUMBER(calcNumbSetter_1_lownumb), .EN(1'b1), .NUMBOUT(numb_4_to_7_3_numbout));
  numb_4_to_8 numb_4_to_8_1 (.NUMB(calcNumbSetter_1_negorpos), .EN(1'b1), .numbout(numb_4_to_8_1_numbout));
  fullCalculator fullCalculator_1 (
    .FIRST2(calcNumbSetter_1_hinum), .FIRST1(calcNumbSetter_1_midnum), .FIRST0(calcNumbSetter_1_lownumb),
    .SECOND2(calcNumbSetter_2_hinum), .SECOND1(calcNumbSetter_2_midnum), .SECOND0(calcNumbSetter_2_lownumb),
    .cycleop(and_1_out), .firstNeg(SETNUMB[3]), .secondNeg(SETNUMB[4]), .number0(fullCalculator_1_number0),
    .number1(fullCalculator_1_number1), .number2(fullCalculator_1_number2),
    .negativeR(fullCalculator_1_negativer));
  numb_4_to_7 numb_4_to_7_4 (.NUMBER(calcNumbSetter_2_hinum), .EN(1'b1), .NUMBOUT(numb_4_to_7_4_numbout));
  numb_4_to_7 numb_4_to_7_5 (.NUMBER(calcNumbSetter_2_midnum), .EN(1'b1), .NUMBOUT(numb_4_to_7_5_numbout));
  numb_4_to_7 numb_4_to_7_6 (.NUMBER(calcNumbSetter_2_lownumb), .EN(1'b1), .NUMBOUT(numb_4_to_7_6_numbout));
  numb_4_to_8 numb_4_to_8_5 (.NUMB(calcNumbSetter_2_negorpos), .EN(1'b1), .numbout(numb_4_to_8_5_numbout));
  numb_4_to_8 numb_4_to_8_2 (.NUMB(fullCalculator_1_number2), .EN(1'b1), .numbout(numb_4_to_8_2_numbout));
  numb_4_to_8 numb_4_to_8_3 (.NUMB(fullCalculator_1_number1), .EN(1'b1), .numbout(numb_4_to_8_3_numbout));
  numb_4_to_8 numb_4_to_8_4 (.NUMB(fullCalculator_1_number0), .EN(1'b1), .numbout(numb_4_to_8_4_numbout));
  negativecoder negativecoder_1 (.negative(fullCalculator_1_negativer), .negaff(negativecoder_1_negaff));
  Multiplexer #(.select(2), .width(8), .enable("false")) multiplexer_1 (
    .in0({8{1'b0}}), .in1({8{1'b0}}), .in2({8{1'b0}}), .in3(8'h48), .out(AFF1), .sel(calcucontroller_1_t0));
  Multiplexer #(.select(2), .width(8), .enable("false")) multiplexer_2 (
    .in0({8{1'b0}}), .in1({8{1'b0}}), .in2({8{1'b0}}), .in3({8{1'b0}}), .out(AFF2), .sel(calcucontroller_1_t0));
  Multiplexer #(.select(2), .width(8), .enable("false")) multiplexer_3 (
    .in0(numb_4_to_8_1_numbout), .in1({8{1'b0}}), .in2(numb_4_to_8_5_numbout), .in3(negativecoder_1_negaff),
    .out(AFF3), .sel(calcucontroller_1_t0));
  Multiplexer #(.select(2), .width(8), .enable("false")) multiplexer_4 (
    .in0({SETNUMB[2], numb_4_to_7_1_numbout}), .in1(operatorsAff_1_aff4),
    .in2({SETNUMB[2], numb_4_to_7_4_numbout}), .in3(numb_4_to_8_2_numbout), .out(AFF4),
    .sel(calcucontroller_1_t0));
  Multiplexer #(.select(2), .width(8), .enable("false")) multiplexer_5 (
    .in0({SETNUMB[1], numb_4_to_7_2_numbout}), .in1(operatorsAff_1_aff5),
    .in2({SETNUMB[1], numb_4_to_7_5_numbout}), .in3(numb_4_to_8_3_numbout), .out(AFF5),
    .sel(calcucontroller_1_t0));
  Multiplexer #(.select(2), .width(8), .enable("false")) multiplexer_6 (
    .in0({SETNUMB[0], numb_4_to_7_3_numbout}), .in1(operatorsAff_1_aff6),
    .in2({SETNUMB[0], numb_4_to_7_6_numbout}), .in3(numb_4_to_8_4_numbout), .out(AFF6),
    .sel(calcucontroller_1_t0));
endmodule

module operatorsAff (
  input  CYC,
  output [7:0] AFF4,
  output [7:0] AFF5,
  output [7:0] AFF6
);

  wire [1:0] select_op_1_op;
  wire [4:0] multiplexer_1_out, multiplexer_2_out, multiplexer_3_out;

  select_op select_op_1 (.cycleop(CYC), .P(select_op_1_op), .op(select_op_1_op));
  Multiplexer #(.select(2), .width(5), .enable("false")) multiplexer_1 (
    .in0({5{1'b0}}), .in1(5'b10010), .in2(5'b01100), .in3(5'b00011), .out(multiplexer_1_out),
    .sel(select_op_1_op));
  Multiplexer #(.select(2), .width(5), .enable("false")) multiplexer_2 (
    .in0(5'b00011), .in1(5'b10100), .in2(5'b10100), .in3(5'b01000), .out(multiplexer_2_out),
    .sel(select_op_1_op));
  Multiplexer #(.select(2), .width(5), .enable("false")) multiplexer_3 (
    .in0(5'b00011), .in1(5'b00001), .in2(5'b01011), .in3(5'b10101), .out(multiplexer_3_out),
    .sel(select_op_1_op));
  fivetoeight fivetoeight_1 (.LETTERIN(multiplexer_1_out), .letterout(AFF4));
  fivetoeight fivetoeight_2 (.LETTERIN(multiplexer_2_out), .letterout(AFF5));
  fivetoeight fivetoeight_3 (.LETTERIN(multiplexer_3_out), .letterout(AFF6));

  // Notes on the sheet:
  //   A
  //   D
  //   S
  //   U
  //   B
  //   M
  //   L
  //   I
  //   V
endmodule

module negativecoder (
  input  negative,
  output [7:0] negaff
);


  assign negaff = {1'b0, negative, {6{1'b0}}};
endmodule

module calcucontroller (
  input  CHANGE1,
  input  CHANGE2,
  input  CHANGE3,
  input  CHANGE4,
  output T1,
  output T0
);

  or or_1 (T1, CHANGE4, CHANGE3);
  or or_2 (T0, CHANGE4, CHANGE2);
endmodule

module LEDAnim (
  input  MUSICMODE,
  input  ZELDAQ,
  output LED8,
  output LED7,
  output LED6,
  output LED5,
  output LED4,
  output LED3,
  output LED2,
  output LED1
);

  wire and_1_out, not_1_out, s_r_ff_1_q;

  and and_1 (and_1_out, MUSICMODE, ZELDAQ);
  S_R_Flip_Flop s_r_ff_1 (.Q(s_r_ff_1_q), .reset(not_1_out), .preset(and_1_out));  // open: S, R, clk, Qn
  not not_1 (not_1_out, MUSICMODE);
  anim1 anim1_1 (
    .ENABLE(s_r_ff_1_q), .LED8(LED8), .LED7(LED7), .LED6(LED6), .LED5(LED5), .LED4(LED4), .LED3(LED3),
    .LED2(LED2), .LED1(LED1));
endmodule

module LongPressReset (
  input  SELECTION,
  output RESET,
  output SELECTOUT
);

  wire not_1_out;

  not not_1 (not_1_out, SELECTION);
  LongPressDetector LongPressDetector_1 (.BUTTON(SELECTION), .RESET(not_1_out), .LONGPRESSMODE(RESET));
  and and_1 (SELECTOUT, ~RESET, SELECTION);  // AND_Gate
endmodule

module timertwosubs (
  input  RESET,
  input  CURRENT,
  input  SELECTION,
  input  TIMERUNNING,
  input  TOFF,
  output CHANGE1,
  output CHANGING,
  output CHANGE2,
  output DONE
);

  wire and_1_out, and_2_out, and_3_out, and_4_out, and_5_out, and_6_out, and_7_out, and_8_out, and_9_out,
       not_1_out, not_2_out, or_1_out, or_2_out, or_3_out, or_4_out, or_5_out, or_6_out, s_r_ff_2_q,
       s_r_ff_3_q, selectFSMTimer_1_rc1, selectFSMTimer_1_rc2, selectFSMTimer_1_rd, selectFSMTimer_1_sc1,
       selectFSMTimer_1_sc2, selectFSMTimer_1_sd;

  or or_1 (or_1_out, RESET, ~CURRENT);  // OR_Gate
  and and_1 (and_1_out, ~RESET, TIMERUNNING);  // AND_Gate
  and and_2 (and_2_out, ~TIMERUNNING, or_1_out);  // AND_Gate
  selectFSMTimer selectFSMTimer_1 (
    .B(SELECTION), .C1(CHANGE1), .C2(s_r_ff_2_q), .D(s_r_ff_3_q), .TRUNNING(and_1_out), .TOFF(TOFF),
    .SC1(selectFSMTimer_1_sc1), .RC1(selectFSMTimer_1_rc1), .SC2(selectFSMTimer_1_sc2),
    .RC2(selectFSMTimer_1_rc2), .SD(selectFSMTimer_1_sd), .RD(selectFSMTimer_1_rd));
  and and_3 (and_3_out, and_1_out, selectFSMTimer_1_sc1);
  or or_2 (or_2_out, or_1_out, and_5_out);
  and and_4 (and_4_out, CURRENT, selectFSMTimer_1_sc1);
  and and_5 (and_5_out, CURRENT, selectFSMTimer_1_rc1);
  or or_3 (or_3_out, selectFSMTimer_1_rc2, and_2_out);
  and and_6 (and_6_out, selectFSMTimer_1_rc1, TIMERUNNING);
  or or_4 (or_4_out, and_7_out, and_6_out);
  and and_7 (and_7_out, or_2_out, ~and_1_out);  // AND_Gate
  S_R_Flip_Flop s_r_ff_1 (.Q(CHANGE1), .reset(or_4_out), .preset(or_5_out));  // open: S, R, clk, Qn
  or or_5 (or_5_out, and_4_out, and_3_out);
  S_R_Flip_Flop s_r_ff_2 (.Q(s_r_ff_2_q), .reset(or_3_out), .preset(selectFSMTimer_1_sc2));  // open: S, R, clk, Qn
  or or_6 (or_6_out, selectFSMTimer_1_rd, and_2_out);
  not not_1 (not_1_out, CHANGE1);
  S_R_Flip_Flop s_r_ff_3 (.Q(s_r_ff_3_q), .reset(or_6_out), .preset(selectFSMTimer_1_sd));  // open: S, R, clk, Qn
  and and_8 (and_8_out, not_1_out, s_r_ff_2_q);
  and and_9 (and_9_out, ~and_1_out, CHANGE1);  // AND_Gate
  and and_10 (CHANGE2, and_8_out, CURRENT);
  not not_2 (not_2_out, and_8_out);
  and and_11 (DONE, not_2_out, s_r_ff_3_q);
  or or_7 (CHANGING, and_9_out, CHANGE2);
endmodule

module selectFSMTimer (
  input  B,
  input  C1,
  input  C2,
  input  D,
  input  TRUNNING,
  input  TOFF,
  output SC1,
  output RC1,
  output SC2,
  output RC2,
  output SD,
  output RD
);

  wire and_1_out, and_2_out, and_3_out, and_4_out, and_9_out, and_10_out, and_11_out, not_1_out, not_2_out,
       not_3_out, not_4_out, not_5_out, not_6_out, not_7_out, not_8_out, not_9_out, not_10_out, not_11_out,
       not_12_out, not_13_out, not_14_out, not_15_out, not_16_out, not_17_out, not_18_out, not_19_out,
       not_20_out, not_21_out, not_22_out, not_23_out, not_24_out;

  not not_1 (not_1_out, C1);
  not not_2 (not_2_out, C2);
  not not_3 (not_3_out, D);
  not not_4 (not_4_out, C1);
  not not_5 (not_5_out, C2);
  not not_6 (not_6_out, D);
  not not_7 (not_7_out, B);
  not not_8 (not_8_out, C1);
  not not_9 (not_9_out, C1);
  not not_10 (not_10_out, C2);
  not not_11 (not_11_out, D);
  not not_12 (not_12_out, D);
  not not_13 (not_13_out, B);
  not not_14 (not_14_out, C2);
  not not_15 (not_15_out, D);
  not not_16 (not_16_out, C1);
  not not_17 (not_17_out, B);
  not not_18 (not_18_out, C1);
  not not_19 (not_19_out, D);
  not not_20 (not_20_out, B);
  not not_21 (not_21_out, C1);
  not not_22 (not_22_out, C2);
  not not_23 (not_23_out, B);
  not not_24 (not_24_out, B);
  and and_1 (and_1_out, not_1_out, not_2_out, not_3_out, TOFF);
  and and_2 (and_2_out, not_4_out, not_5_out, not_6_out, TRUNNING);
  and and_3 (and_3_out, not_7_out, not_8_out, C2, D, TOFF);
  and and_4 (and_4_out, B, not_9_out, not_10_out, not_11_out);
  and and_5 (RC1, B, C1, C2, not_12_out);
  and and_6 (SC2, not_13_out, C1, not_14_out, not_15_out);
  and and_7 (RC2, B, not_16_out, C2, D);
  and and_8 (SD, not_17_out, not_18_out, C2, not_19_out);
  and and_9 (and_9_out, not_20_out, not_21_out, not_22_out, D);
  and and_10 (and_10_out, not_23_out, C1, C2, D, TOFF);
  and and_11 (and_11_out, not_24_out, C1, C2, D, TRUNNING);
  or or_1 (SC1, and_1_out, and_2_out, and_3_out, and_4_out);
  or or_2 (RD, and_9_out, and_10_out, and_11_out);
endmodule

module fourxconv (
  input  [3:0] D1,
  input  [3:0] D0,
  input  [3:0] H1,
  input  [3:0] H0,
  input  [3:0] dip,
  input  settime,
  output [7:0] DAYHHIOUT,
  output [7:0] DAYLOWOUT,
  output [7:0] HOURHIOUT,
  output [7:0] HOURLOWOUT
);

  and and_1 (DAYHHIOUT[7], dip[0], settime);
  and and_2 (DAYLOWOUT[7], dip[1], settime);
  and and_3 (HOURHIOUT[7], dip[2], settime);
  and and_4 (HOURLOWOUT[7], dip[3], settime);
  numb_4_to_7 numb_4_to_7_1 (.NUMBER(D1), .EN(1'b1), .NUMBOUT(DAYHHIOUT[6:0]));
  numb_4_to_7 numb_4_to_7_2 (.NUMBER(D0), .EN(1'b1), .NUMBOUT(DAYLOWOUT[6:0]));
  numb_4_to_7 numb_4_to_7_3 (.NUMBER(H1), .EN(1'b1), .NUMBOUT(HOURHIOUT[6:0]));
  numb_4_to_7 numb_4_to_7_4 (.NUMBER(H0), .EN(1'b1), .NUMBOUT(HOURLOWOUT[6:0]));
endmodule
