// Logisim project MSG.circ as structural Verilog: 2 circuits, main circuit onescreen
module onescreen (
  input  SET,
  output [4:0] LETTER,
  output ACTIVATE
);

  wire Additionneurmsg_1_p1, Additionneurmsg_1_p2, Additionneurmsg_1_p3, Additionneurmsg_1_p4, and_1_out,
       and_2_out, clock_1_out, d_ff_1_q, d_ff_1_qn, d_ff_2_q, d_ff_3_q, d_ff_4_q, d_ff_5_q, not_1_out,
       or_1_out;
  wire [3:0] multiplexer_3_out;
  wire [4:0] multiplexer_1_out;

  not not_1 (not_1_out, SET);
  D_Flip_Flop d_ff_1 (.D(d_ff_1_qn), .clk(clock_1_out), .Q(d_ff_1_q), .Qn(d_ff_1_qn));  // open: preset, reset
  Clock #(.highDuration(3500), .lowDuration(3500)) clock_1 (.out(clock_1_out));
  and and_1 (and_1_out, SET, d_ff_1_q);
  Multiplexer #(.select(4), .width(5), .enable("false")) multiplexer_1 (
    .in0(5'b11000), .in1(5'b01110), .in2(5'b10100), .in3({5{1'b1}}), .in4(5'b00010), .in5({5{1'b0}}),
    .in6(5'b01101), .in7({5{1'b1}}), .in8(5'b00011), .in9(5'b01110), .in10({5{1'b1}}), .in11(5'b01000),
    .in12(5'b10011), .in13({5{1'b1}}), .out(multiplexer_1_out), .sel(multiplexer_3_out));  // open: in14, in15
  Additionneurmsg Additionneurmsg_1 (
    .A1(multiplexer_3_out[0]), .B1(and_1_out), .A2(multiplexer_3_out[1]), .B2(1'b0),
    .A3(multiplexer_3_out[2]), .B3(1'b0), .A4(multiplexer_3_out[3]), .B4(1'b0), .P1(Additionneurmsg_1_p1),
    .P2(Additionneurmsg_1_p2), .P3(Additionneurmsg_1_p3), .P4(Additionneurmsg_1_p4));  // open: O
  Multiplexer #(.width(5), .enable("false")) multiplexer_2 (
    .in0({5{1'b1}}), .in1(multiplexer_1_out), .out(LETTER), .sel(SET));
  D_Flip_Flop d_ff_2 (.D(Additionneurmsg_1_p1), .clk(clock_1_out), .Q(d_ff_2_q));  // open: Qn, preset, reset
  D_Flip_Flop d_ff_3 (.D(Additionneurmsg_1_p2), .clk(clock_1_out), .Q(d_ff_3_q));  // open: Qn, preset, reset
  D_Flip_Flop d_ff_4 (.D(Additionneurmsg_1_p3), .clk(clock_1_out), .Q(d_ff_4_q));  // open: Qn, preset, reset
  D_Flip_Flop d_ff_5 (.D(Additionneurmsg_1_p4), .clk(clock_1_out), .Q(d_ff_5_q));  // open: Qn, preset, reset
  or or_1 (or_1_out, and_2_out, not_1_out);
  and and_2 (and_2_out, ~d_ff_2_q, d_ff_3_q, d_ff_4_q, d_ff_5_q);  // AND_Gate
  Multiplexer #(.enable("false")) multiplexer_3 (
    .in0(d_ff_2_q), .in1(1'b0), .out(multiplexer_3_out[0]), .sel(or_1_out));
  Multiplexer #(.enable("false")) multiplexer_4 (
    .in0(d_ff_3_q), .in1(1'b0), .out(multiplexer_3_out[1]), .sel(or_1_out));
  Multiplexer #(.enable("false")) multiplexer_5 (
    .in0(d_ff_4_q), .in1(1'b0), .out(multiplexer_3_out[2]), .sel(or_1_out));
  Multiplexer #(.enable("false")) multiplexer_6 (
    .in0(d_ff_5_q), .in1(1'b0), .out(multiplexer_3_out[3]), .sel(or_1_out));
  and and_3 (ACTIVATE, multiplexer_3_out[0], ~multiplexer_3_out[1], ~multiplexer_3_out[2], ~multiplexer_3_out[3], ~not_1_out);  // AND_Gate

  // Notes on the sheet:
  //   Y
  //   O
  //   U
  //   C
  //   A
  //   N
  //   D
  //   I
  //   T
  //   SPACE
endmodule

module allscreens (
  input  PLAY,
  output [4:0] AFF6,
  output [4:0] AFF5,
  output [4:0] AFF4,
  output [4:0] AFF3,
  output [4:0] AFF2,
  output [4:0] AFF1
);

  wire not_1_out, onescreen_1_activate, onescreen_2_activate, onescreen_3_activate, onescreen_4_activate,
       onescreen_5_activate, s_r_ff_1_q, s_r_ff_2_q, s_r_ff_3_q, s_r_ff_4_q, s_r_ff_5_q;

  not not_1 (not_1_out, PLAY);
  S_R_Flip_Flop s_r_ff_1 (.Q(s_r_ff_1_q), .reset(not_1_out), .preset(onescreen_1_activate));  // open: S, R, clk, Qn
  S_R_Flip_Flop s_r_ff_2 (.Q(s_r_ff_2_q), .reset(not_1_out), .preset(onescreen_2_activate));  // open: S, R, clk, Qn
  S_R_Flip_Flop s_r_ff_3 (.Q(s_r_ff_3_q), .reset(not_1_out), .preset(onescreen_3_activate));  // open: S, R, clk, Qn
  S_R_Flip_Flop s_r_ff_4 (.Q(s_r_ff_4_q), .reset(not_1_out), .preset(onescreen_4_activate));  // open: S, R, clk, Qn
  S_R_Flip_Flop s_r_ff_5 (.Q(s_r_ff_5_q), .reset(not_1_out), .preset(onescreen_5_activate));  // open: S, R, clk, Qn
  onescreen onescreen_1 (.SET(PLAY), .LETTER(AFF6), .ACTIVATE(onescreen_1_activate));
  onescreen onescreen_2 (.SET(s_r_ff_1_q), .LETTER(AFF5), .ACTIVATE(onescreen_2_activate));
  onescreen onescreen_3 (.SET(s_r_ff_2_q), .LETTER(AFF4), .ACTIVATE(onescreen_3_activate));
  onescreen onescreen_4 (.SET(s_r_ff_3_q), .LETTER(AFF3), .ACTIVATE(onescreen_4_activate));
  onescreen onescreen_5 (.SET(s_r_ff_4_q), .LETTER(AFF2), .ACTIVATE(onescreen_5_activate));
  onescreen onescreen_6 (.SET(s_r_ff_5_q), .LETTER(AFF1));  // open: ACTIVATE
endmodule
