// Logisim project MusiqueUnggatedAttempt2.circ as structural Verilog: 46 circuits, main circuit TimeSelector
module Affichage (
  input  CYCLE,
  input  RESET,
  output BUZZER,
  output HARRY,
  output PIRATE,
  output ZELDA,
  output [7:0] AFF1,
  output [7:0] AFF2,
  output [7:0] AFF3,
  output [7:0] AFF4,
  output [7:0] AFF5,
  output [7:0] AFF6
);

  wire Affichage1_1_v0, Affichage1_1_w0, Affichage1_1_x0, Affichage1_1_y0, Affichage1_1_z0, Affichage2_1_v1,
       Affichage2_1_w1, Affichage2_1_x1, Affichage2_1_y1, Affichage2_1_z1, Affichage3_1_v2, Affichage3_1_w2,
       Affichage3_1_x2, Affichage3_1_y2, Affichage3_1_z2, Affichage4_1_v3, Affichage4_1_w3, Affichage4_1_x3,
       Affichage4_1_y3, Affichage4_1_z3, Affichage5_1_v4, Affichage5_1_w4, Affichage5_1_x4, Affichage5_1_y4,
       Affichage5_1_z4, Affichage6_1_v5, Affichage6_1_w5, Affichage6_1_x5, Affichage6_1_y5, Affichage6_1_z5,
       MP3_1_harryplay, MP3_1_pirateplay, MP3_1_zeldaplay;

  MP3 MP3_1 (
    .CYCLE(CYCLE), .RESET(RESET), .HARRYPLAY(MP3_1_harryplay), .ZELDAPLAY(MP3_1_zeldaplay), .BUZZER(BUZZER),
    .PIRATEPLAY(MP3_1_pirateplay), .ZELDALIGHT(ZELDA), .PIRATELIGHT(PIRATE), .HARRYLIGHT(HARRY));
  Affichage1 Affichage1_1 (
    .HARRY(MP3_1_harryplay), .ZELDA(MP3_1_zeldaplay), .PIRATE(MP3_1_pirateplay), .V0(Affichage1_1_v0),
    .W0(Affichage1_1_w0), .X0(Affichage1_1_x0), .Y0(Affichage1_1_y0), .Z0(Affichage1_1_z0));
  Affichage2 Affichage2_1 (
    .HARRY(MP3_1_harryplay), .ZELDA(MP3_1_zeldaplay), .PIRATE(MP3_1_pirateplay), .V1(Affichage2_1_v1),
    .W1(Affichage2_1_w1), .X1(Affichage2_1_x1), .Y1(Affichage2_1_y1), .Z1(Affichage2_1_z1));
  Affichage3 Affichage3_1 (
    .HARRY(MP3_1_harryplay), .ZELDA(MP3_1_zeldaplay), .PIRATE(MP3_1_pirateplay), .V2(Affichage3_1_v2),
    .W2(Affichage3_1_w2), .X2(Affichage3_1_x2), .Y2(Affichage3_1_y2), .Z2(Affichage3_1_z2));
  Affichage4 Affichage4_1 (
    .HARRY(MP3_1_harryplay), .ZELDA(MP3_1_zeldaplay), .PIRATE(MP3_1_pirateplay), .V3(Affichage4_1_v3),
    .W3(Affichage4_1_w3), .X3(Affichage4_1_x3), .Y3(Affichage4_1_y3), .Z3(Affichage4_1_z3));
  Affichage5 Affichage5_1 (
    .HARRY(MP3_1_harryplay), .ZELDA(MP3_1_zeldaplay), .PIRATE(MP3_1_pirateplay), .V4(Affichage5_1_v4),
    .W4(Affichage5_1_w4), .X4(Affichage5_1_x4), .Y4(Affichage5_1_y4), .Z4(Affichage5_1_z4));
  Affichage6 Affichage6_1 (
    .HARRY(MP3_1_harryplay), .ZELDA(MP3_1_zeldaplay), .PIRATE(MP3_1_pirateplay), .V5(Affichage6_1_v5),
    .W5(Affichage6_1_w5), .X5(Affichage6_1_x5), .Y5(Affichage6_1_y5), .Z5(Affichage6_1_z5));
  sevensegA_Z sevensegA_Z_1 (
    .d(AFF1[3]), .b(AFF1[1]), .Z(Affichage1_1_z0), .X(Affichage1_1_x0), .V(Affichage1_1_v0),
    .W(Affichage1_1_w0), .Y(Affichage1_1_y0), .a(AFF1[0]), .c(AFF1[2]), .e(AFF1[4]), .f(AFF1[5]), .g(AFF1[6]));
  sevensegA_Z sevensegA_Z_2 (
    .d(AFF2[3]), .b(AFF2[1]), .Z(Affichage2_1_z1), .X(Affichage2_1_x1), .V(Affichage2_1_v1),
    .W(Affichage2_1_w1), .Y(Affichage2_1_y1), .a(AFF2[0]), .c(AFF2[2]), .e(AFF2[4]), .f(AFF2[5]), .g(AFF2[6]));
  sevensegA_Z sevensegA_Z_3 (
    .d(AFF3[3]), .b(AFF3[1]), .Z(Affichage3_1_z2), .X(Affichage3_1_x2), .V(Affichage3_1_v2),
    .W(Affichage3_1_w2), .Y(Affichage3_1_y2), .a(AFF3[0]), .c(AFF3[2]), .e(AFF3[4]), .f(AFF3[5]), .g(AFF3[6]));
  sevensegA_Z sevensegA_Z_4 (
    .d(AFF4[3]), .b(AFF4[1]), .Z(Affichage4_1_z3), .X(Affichage4_1_x3), .V(Affichage4_1_v3),
    .W(Affichage4_1_w3), .Y(Affichage4_1_y3), .a(AFF4[0]), .c(AFF4[2]), .e(AFF4[4]), .f(AFF4[5]), .g(AFF4[6]));
  sevensegA_Z sevensegA_Z_5 (
    .d(AFF5[3]), .b(AFF5[1]), .Z(Affichage5_1_z4), .X(Affichage5_1_x4), .V(Affichage5_1_v4),
    .W(Affichage5_1_w4), .Y(Affichage5_1_y4), .a(AFF5[0]), .c(AFF5[2]), .e(AFF5[4]), .f(AFF5[5]), .g(AFF5[6]));
  sevensegA_Z sevensegA_Z_6 (
    .d(AFF6[3]), .b(AFF6[1]), .Z(Affichage6_1_z5), .X(Affichage6_1_x5), .V(Affichage6_1_v5),
    .W(Affichage6_1_w5), .Y(Affichage6_1_y5), .a(AFF6[0]), .c(AFF6[2]), .e(AFF6[4]), .f(AFF6[5]), .g(AFF6[6]));

  assign AFF1[7] = 1'b0;
  assign AFF2[7] = 1'b0;
  assign AFF3[7] = 1'b0;
  assign AFF4[7] = 1'b0;
  assign AFF5[7] = 1'b0;
  assign AFF6[7] = 1'b0;
endmodule

module MP3 (
  input  CYCLE,
  input  RESET,
  output HARRYPLAY,
  output ZELDAPLAY,
  output BUZZER,
  output PIRATEPLAY,
  output ZELDALIGHT,
  output PIRATELIGHT,
  output HARRYLIGHT
);

  wire and_1_out, HarryPotter_1_buzzer, HesAPirate_1_buzzer, LegendOfZelda_1_buzzer, or_1_out, or_2_out,
       or_3_out, or_4_out, s_r_ff_1_q, SongSelector_1_harry, SongSelector_1_pirate, SongSelector_1_zelda;

  or or_1 (or_1_out, RESET, and_1_out);
  S_R_Flip_Flop s_r_ff_1 (.Q(s_r_ff_1_q), .reset(RESET), .preset(CYCLE));  // open: S, R, clk, Qn
  and and_1 (and_1_out, ~HARRYPLAY, ~ZELDAPLAY, ~PIRATEPLAY, ~s_r_ff_1_q);  // AND_Gate
  SongSelector SongSelector_1 (
    .CYCLE(CYCLE), .RESET(or_1_out), .ZELDACHOICE(ZELDALIGHT), .Harry(SongSelector_1_harry),
    .Zelda(SongSelector_1_zelda), .Pirate(SongSelector_1_pirate), .PIRATECHOICE(PIRATELIGHT),
    .HARRYCHOICE(HARRYLIGHT));
  or or_2 (or_2_out, SongSelector_1_zelda, or_1_out, SongSelector_1_pirate);
  or or_3 (or_3_out, SongSelector_1_harry, or_1_out, SongSelector_1_pirate);
  or or_4 (or_4_out, SongSelector_1_harry, or_1_out, SongSelector_1_zelda);
  HarryPotter HarryPotter_1 (
    .SET(SongSelector_1_harry), .RESET(or_2_out), .HARRYPLAYING(HARRYPLAY), .BUZZER(HarryPotter_1_buzzer));
  LegendOfZelda LegendOfZelda_1 (
    .SET(SongSelector_1_zelda), .RESET(or_3_out), .ZELDAPLAYING(ZELDAPLAY), .BUZZER(LegendOfZelda_1_buzzer));
  OdeOfJoy HesAPirate_1 (
    .RESET(or_4_out), .SET(SongSelector_1_pirate), .PIRATEPLAYING(PIRATEPLAY), .BUZZER(HesAPirate_1_buzzer));
  or or_5 (BUZZER, HarryPotter_1_buzzer, LegendOfZelda_1_buzzer, HesAPirate_1_buzzer);
endmodule

module SongSelector (
  input  CYCLE,
  input  RESET,
  output ZELDACHOICE,
  output Harry,
  output Zelda,
  output Pirate,
  output PIRATECHOICE,
  output HARRYCHOICE
);

  wire buttonSelector_1_rt0, buttonSelector_1_rt1, buttonSelector_1_rt2, buttonSelector_1_rt3,
       buttonSelector_1_st0, buttonSelector_1_st1, buttonSelector_1_st2, buttonSelector_1_st3, clock_1_out,
       d_ff_1_q, not_1_out, not_2_out, or_1_out, or_2_out, or_3_out, or_4_out, s_r_ff_3_q, s_r_ff_4_q;

  D_Flip_Flop d_ff_1 (.D(CYCLE), .clk(clock_1_out), .Q(d_ff_1_q));  // open: Qn, preset, reset
  Clock clock_1 (.out(clock_1_out));
  buttonSelector buttonSelector_1 (
    .B(d_ff_1_q), .T0(ZELDACHOICE), .T1(PIRATECHOICE), .T2(s_r_ff_3_q), .T3(s_r_ff_4_q), .R(RESET),
    .ST0(buttonSelector_1_st0), .RT0(buttonSelector_1_rt0), .ST1(buttonSelector_1_st1),
    .RT1(buttonSelector_1_rt1), .ST2(buttonSelector_1_st2), .RT2(buttonSelector_1_rt2),
    .ST3(buttonSelector_1_st3), .RT3(buttonSelector_1_rt3));
  S_R_Flip_Flop s_r_ff_1 (.Q(ZELDACHOICE), .reset(or_1_out), .preset(buttonSelector_1_st0));  // open: S, R, clk, Qn
  or or_1 (or_1_out, buttonSelector_1_rt0, RESET);
  S_R_Flip_Flop s_r_ff_2 (.Q(PIRATECHOICE), .reset(or_2_out), .preset(buttonSelector_1_st1));  // open: S, R, clk, Qn
  or or_2 (or_2_out, buttonSelector_1_rt1, RESET);
  S_R_Flip_Flop s_r_ff_3 (.Q(s_r_ff_3_q), .reset(or_3_out), .preset(buttonSelector_1_st2));  // open: S, R, clk, Qn
  or or_3 (or_3_out, buttonSelector_1_rt2, RESET);
  S_R_Flip_Flop s_r_ff_4 (.Q(s_r_ff_4_q), .reset(or_4_out), .preset(buttonSelector_1_st3));  // open: S, R, clk, Qn
  or or_4 (or_4_out, buttonSelector_1_rt3, RESET);
  Demultiplexer #(.select(2), .enable("false")) demultiplexer_1 (
    .out0(Harry), .out1(Zelda), .out2(Pirate), .in(d_ff_1_q), .sel({PIRATECHOICE, ZELDACHOICE}));  // open: out3
  not not_1 (not_1_out, PIRATECHOICE);
  not not_2 (not_2_out, ZELDACHOICE);
  and and_1 (HARRYCHOICE, not_1_out, not_2_out);
endmodule

module buttonSelector (
  input  B,
  input  T0,
  input  T1,
  input  T2,
  input  T3,
  input  R,
  output ST0,
  output RT0,
  output ST1,
  output RT1,
  output ST2,
  output RT2,
  output ST3,
  output RT3
);

  wire and_2_out, and_4_out, and_6_out, and_8_out, not_1_out, not_2_out, not_3_out, not_4_out, not_5_out,
       not_6_out, not_7_out, not_8_out, not_9_out, not_10_out, not_11_out, not_12_out, not_13_out,
       not_14_out, not_15_out, not_16_out, not_17_out, not_18_out, not_19_out, not_20_out, not_21_out,
       not_22_out, not_23_out, not_24_out, not_25_out, not_26_out, not_27_out, not_28_out, not_29_out;

  not not_1 (not_1_out, T0);
  not not_2 (not_2_out, T1);
  not not_3 (not_3_out, T2);
  not not_4 (not_4_out, T3);
  not not_5 (not_5_out, R);
  not not_6 (not_6_out, T1);
  not not_7 (not_7_out, T3);
  not not_8 (not_8_out, T0);
  not not_9 (not_9_out, T1);
  not not_10 (not_10_out, T3);
  not not_11 (not_11_out, R);
  not not_12 (not_12_out, T0);
  not not_13 (not_13_out, T2);
  not not_14 (not_14_out, B);
  not not_15 (not_15_out, T1);
  not not_16 (not_16_out, T2);
  not not_17 (not_17_out, T3);
  not not_18 (not_18_out, R);
  not not_19 (not_19_out, B);
  not not_20 (not_20_out, T0);
  not not_21 (not_21_out, T3);
  not not_22 (not_22_out, T0);
  not not_23 (not_23_out, T2);
  not not_24 (not_24_out, T3);
  not not_25 (not_25_out, R);
  not not_26 (not_26_out, B);
  not not_27 (not_27_out, T0);
  not not_28 (not_28_out, T1);
  not not_29 (not_29_out, T2);
  and and_1 (ST0, B, not_1_out, not_2_out, not_3_out, not_4_out, not_5_out);
  and and_2 (and_2_out, B, T0, not_6_out, T2, not_7_out);
  or or_1 (RT0, and_2_out, R);
  and and_3 (ST1, B, not_8_out, not_9_out, T2, not_10_out, not_11_out);
  or or_2 (RT1, R, and_4_out);
  and and_4 (and_4_out, B, not_12_out, T1, not_13_out, T3);
  and and_5 (ST2, not_14_out, T0, not_15_out, not_16_out, not_17_out, not_18_out);
  and and_6 (and_6_out, not_19_out, not_20_out, T2, not_21_out);
  or or_3 (RT2, and_6_out, R);
  and and_7 (ST3, B, not_22_out, T1, not_23_out, not_24_out, not_25_out);
  and and_8 (and_8_out, not_26_out, not_27_out, not_28_out, not_29_out, T3);
  or or_4 (RT3, and_8_out, R);
endmodule

module HarryPotter (
  input  SET,
  input  RESET,
  output HARRYPLAYING,
  output BUZZER
);

  wire A2_1_output_1, and_1_out, B2_1_output_1, B_1_outp, B_2_outp, Ds_1_output_1, E_1_output_1,
       E_2_output_1, E_3_output_1, F_1_output_1, F_2_output_1, F_3_output_1, Fs_1_output_1, G_1_output_1,
       G_2_output_1, MusicLoop_1_resetout, MusicLoop_1_setout, not_1_out, not_2_out, NoteLength_1_nxt,
       NoteLength_1_play, NoteLength_2_nxt, NoteLength_2_play, NoteLength_3_nxt, NoteLength_3_play,
       NoteLength_4_nxt, NoteLength_4_play, NoteLength_5_nxt, NoteLength_5_play, NoteLength_6_nxt,
       NoteLength_6_play, NoteLength_7_nxt, NoteLength_7_play, NoteLength_8_nxt, NoteLength_8_play,
       NoteLength_9_nxt, NoteLength_9_play, NoteLength_10_nxt, NoteLength_10_play, NoteLength_11_nxt,
       NoteLength_11_play, NoteLength_12_nxt, NoteLength_12_play, NoteLength_13_nxt, NoteLength_13_play,
       NoteLength_14_nxt, or_1_out, or_2_out, SRlatch_1_q, TimeSelector_1_output_1;

  or or_1 (or_1_out, SET, MusicLoop_1_setout);
  MusicLoop MusicLoop_1 (
    .RESET(RESET), .SET(SET), .FINISH(not_2_out), .SETOUT(MusicLoop_1_setout), .RESETOUT(MusicLoop_1_resetout));
  or or_2 (or_2_out, MusicLoop_1_resetout, RESET);
  SRlatch SRlatch_1 (.RESET(or_2_out), .SET(or_1_out), .Q(SRlatch_1_q));
  or or_3 (HARRYPLAYING, not_2_out, SRlatch_1_q);
  not not_1 (not_1_out, SRlatch_1_q);
  TimeSelector TimeSelector_1 (
    .RESET(not_1_out), .Input_3(1'b0), .Input_5(1'b0), .Input_6(1'b0), .T0(1'b0), .SET(SRlatch_1_q),
    .Input_4(1'b1), .Output_1(TimeSelector_1_output_1), .T1(1'b0));
  NoteLength NoteLength_2 (
    .I0(1'b1), .I1(1'b1), .I2(1'b0), .I3(1'b0), .E(TimeSelector_1_output_1), .T1(1'b0), .T2(1'b0),
    .PLAY(NoteLength_2_play), .NXT(NoteLength_2_nxt));
  NoteLength NoteLength_3 (
    .I0(1'b1), .I1(1'b0), .I2(1'b0), .I3(1'b0), .E(NoteLength_2_nxt), .T1(1'b0), .T2(1'b0),
    .PLAY(NoteLength_3_play), .NXT(NoteLength_3_nxt));
  NoteLength NoteLength_5 (
    .I0(1'b0), .I1(1'b1), .I2(1'b0), .I3(1'b0), .E(NoteLength_3_nxt), .T1(1'b0), .T2(1'b0),
    .PLAY(NoteLength_5_play), .NXT(NoteLength_5_nxt));
  NoteLength NoteLength_7 (
    .I0(1'b0), .I1(1'b0), .I2(1'b1), .I3(1'b0), .E(NoteLength_5_nxt), .T1(1'b0), .T2(1'b0),
    .PLAY(NoteLength_7_play), .NXT(NoteLength_7_nxt));
  NoteLength NoteLength_9 (
    .I0(1'b0), .I1(1'b1), .I2(1'b0), .I3(1'b0), .E(NoteLength_7_nxt), .T1(1'b0), .T2(1'b0),
    .PLAY(NoteLength_9_play), .NXT(NoteLength_9_nxt));
  NoteLength NoteLength_11 (
    .I0(1'b1), .I1(1'b0), .I2(1'b1), .I3(1'b0), .E(NoteLength_9_nxt), .T1(1'b0), .T2(1'b0),
    .PLAY(NoteLength_11_play), .NXT(NoteLength_11_nxt));
  NoteLength NoteLength_13 (
    .I0(1'b1), .I1(1'b0), .I2(1'b1), .I3(1'b0), .E(NoteLength_11_nxt), .T1(1'b0), .T2(1'b0),
    .PLAY(NoteLength_13_play), .NXT(NoteLength_13_nxt));
  and and_1 (and_1_out, SRlatch_1_q, TimeSelector_1_output_1);
  NoteLength NoteLength_4 (
    .I0(1'b1), .I1(1'b0), .I2(1'b0), .I3(1'b0), .E(NoteLength_1_nxt), .T1(1'b0), .T2(1'b0),
    .PLAY(NoteLength_4_play), .NXT(NoteLength_4_nxt));
  NoteLength NoteLength_6 (
    .I0(1'b0), .I1(1'b1), .I2(1'b0), .I3(1'b0), .E(NoteLength_4_nxt), .T1(1'b0), .T2(1'b0),
    .PLAY(NoteLength_6_play), .NXT(NoteLength_6_nxt));
  NoteLength NoteLength_8 (
    .I0(1'b0), .I1(1'b0), .I2(1'b1), .I3(1'b0), .E(NoteLength_6_nxt), .T1(1'b0), .T2(1'b0),
    .PLAY(NoteLength_8_play), .NXT(NoteLength_8_nxt));
  NoteLength NoteLength_1 (
    .I0(1'b1), .I1(1'b1), .I2(1'b0), .I3(1'b0), .E(NoteLength_13_nxt), .T1(1'b0), .T2(1'b0),
    .PLAY(NoteLength_1_play), .NXT(NoteLength_1_nxt));
  NoteLength NoteLength_10 (
    .I0(1'b0), .I1(1'b1), .I2(1'b0), .I3(1'b0), .E(NoteLength_8_nxt), .T1(1'b0), .T2(1'b0),
    .PLAY(NoteLength_10_play), .NXT(NoteLength_10_nxt));
  NoteLength NoteLength_12 (
    .I0(1'b1), .I1(1'b0), .I2(1'b1), .I3(1'b0), .E(NoteLength_10_nxt), .T1(1'b0), .T2(1'b0),
    .PLAY(NoteLength_12_play), .NXT(NoteLength_12_nxt));
  B B_1 (.Input_1(and_1_out), .outp(B_1_outp));
  E E_1 (.Output_1(E_1_output_1), .Input_1(NoteLength_2_play));
  G G_1 (.Output_1(G_1_output_1), .Input_1(NoteLength_3_play));
  F F_1 (.Output_1(F_1_output_1), .Input_1(NoteLength_5_play));
  E E_2 (.Output_1(E_2_output_1), .Input_1(NoteLength_7_play));
  B2 B2_1 (.Output_1(B2_1_output_1), .Input_1(NoteLength_9_play));
  A2 A2_1 (.Output_1(A2_1_output_1), .Input_1(NoteLength_11_play));
  Fs Fs_1 (.Output_1(Fs_1_output_1), .Input_1(NoteLength_13_play));
  E E_3 (.Output_1(E_3_output_1), .Input_1(NoteLength_1_play));
  G G_2 (.Output_1(G_2_output_1), .Input_1(NoteLength_4_play));
  F F_2 (.Output_1(F_2_output_1), .Input_1(NoteLength_6_play));
  Ds Ds_1 (.Output_1(Ds_1_output_1), .Input_1(NoteLength_8_play));
  F F_3 (.Output_1(F_3_output_1), .Input_1(NoteLength_10_play));
  B B_2 (.Input_1(NoteLength_12_play), .outp(B_2_outp));
  NoteLength NoteLength_14 (
    .I0(1'b1), .I1(1'b0), .I2(1'b0), .I3(1'b0), .E(NoteLength_12_nxt), .T1(1'b0), .T2(1'b0),
    .NXT(NoteLength_14_nxt));  // open: PLAY
  or or_4 (BUZZER, B_1_outp, E_1_output_1, G_1_output_1, F_3_output_1, B_2_outp, F_1_output_1, E_2_output_1, B2_1_output_1, A2_1_output_1, Fs_1_output_1, E_3_output_1, G_2_output_1, F_2_output_1, Ds_1_output_1);
  not not_2 (not_2_out, NoteLength_14_nxt);
endmodule

module LegendOfZelda (
  input  SET,
  input  RESET,
  output ZELDAPLAYING,
  output BUZZER
);

  wire A2_1_output_1, A2_2_output_1, A2_3_output_1, A_1_output_1, A_2_output_1, A_3_output_1, and_1_out,
       B_1_outp, C_1_output_1, D_1_output_1, E_1_output_1, E_2_output_1, E_3_output_1, E_4_output_1,
       E_5_output_1, F_1_output_1, F_2_output_1, F_3_output_1, G_1_output_1, G_2_output_1, G_3_output_1,
       MusicLoop_1_resetout, MusicLoop_1_setout, not_1_out, not_2_out, NoteLength_1_nxt, NoteLength_1_play,
       NoteLength_2_nxt, NoteLength_3_nxt, NoteLength_3_play, NoteLength_4_nxt, NoteLength_4_play,
       NoteLength_5_nxt, NoteLength_5_play, NoteLength_6_nxt, NoteLength_6_play, NoteLength_7_nxt,
       NoteLength_7_play, NoteLength_8_nxt, NoteLength_8_play, NoteLength_9_nxt, NoteLength_9_play,
       NoteLength_10_nxt, NoteLength_10_play, NoteLength_11_nxt, NoteLength_11_play, NoteLength_12_nxt,
       NoteLength_12_play, NoteLength_13_nxt, NoteLength_13_play, NoteLength_14_nxt, NoteLength_14_play,
       NoteLength_15_nxt, NoteLength_16_nxt, NoteLength_16_play, NoteLength_17_nxt, NoteLength_17_play,
       NoteLength_18_nxt, NoteLength_18_play, NoteLength_19_nxt, NoteLength_19_play, NoteLength_20_nxt,
       NoteLength_20_play, NoteLength_21_nxt, NoteLength_22_nxt, NoteLength_22_play, NoteLength_23_nxt,
       NoteLength_24_nxt, NoteLength_25_nxt, or_1_out, or_2_out, SRlatch_1_q, TimeSelector_1_output_1;

  or or_1 (or_1_out, SET, MusicLoop_1_setout);
  MusicLoop MusicLoop_1 (
    .RESET(RESET), .SET(SET), .FINISH(not_1_out), .SETOUT(MusicLoop_1_setout), .RESETOUT(MusicLoop_1_resetout));
  or or_2 (or_2_out, MusicLoop_1_resetout, RESET);
  SRlatch SRlatch_1 (.RESET(or_2_out), .SET(or_1_out), .Q(SRlatch_1_q));
  not not_1 (not_1_out, NoteLength_21_nxt);
  not not_2 (not_2_out, SRlatch_1_q);
  or or_3 (ZELDAPLAYING, not_1_out, SRlatch_1_q);
  TimeSelector TimeSelector_1 (
    .RESET(not_2_out), .Input_3(1'b0), .Input_5(1'b1), .Input_6(1'b0), .T0(1'b1), .SET(SRlatch_1_q),
    .Input_4(1'b0), .Output_1(TimeSelector_1_output_1), .T1(1'b0));
  NoteLength NoteLength_1 (
    .I0(1'b0), .I1(1'b1), .I2(1'b1), .I3(1'b0), .E(TimeSelector_1_output_1), .T1(1'b1), .T2(1'b0),
    .PLAY(NoteLength_1_play), .NXT(NoteLength_1_nxt));
  NoteLength NoteLength_3 (
    .I0(1'b0), .I1(1'b1), .I2(1'b0), .I3(1'b0), .E(NoteLength_1_nxt), .T1(1'b1), .T2(1'b0),
    .PLAY(NoteLength_3_play), .NXT(NoteLength_3_nxt));
  NoteLength NoteLength_5 (
    .I0(1'b1), .I1(1'b0), .I2(1'b0), .I3(1'b0), .E(NoteLength_23_nxt), .T1(1'b1), .T2(1'b0),
    .PLAY(NoteLength_5_play), .NXT(NoteLength_5_nxt));
  NoteLength NoteLength_7 (
    .I0(1'b1), .I1(1'b0), .I2(1'b0), .I3(1'b0), .E(NoteLength_5_nxt), .T1(1'b1), .T2(1'b0),
    .PLAY(NoteLength_7_play), .NXT(NoteLength_7_nxt));
  NoteLength NoteLength_9 (
    .I0(1'b1), .I1(1'b0), .I2(1'b0), .I3(1'b0), .E(NoteLength_7_nxt), .T1(1'b1), .T2(1'b0),
    .PLAY(NoteLength_9_play), .NXT(NoteLength_9_nxt));
  NoteLength NoteLength_11 (
    .I0(1'b1), .I1(1'b0), .I2(1'b0), .I3(1'b0), .E(NoteLength_9_nxt), .T1(1'b1), .T2(1'b0),
    .PLAY(NoteLength_11_play), .NXT(NoteLength_11_nxt));
  NoteLength NoteLength_13 (
    .I0(1'b0), .I1(1'b0), .I2(1'b0), .I3(1'b1), .E(NoteLength_11_nxt), .T1(1'b1), .T2(1'b0),
    .PLAY(NoteLength_13_play), .NXT(NoteLength_13_nxt));
  NoteLength NoteLength_15 (
    .I0(1'b0), .I1(1'b1), .I2(1'b0), .I3(1'b0), .E(NoteLength_12_nxt), .T1(1'b1), .T2(1'b0),
    .NXT(NoteLength_15_nxt));  // open: PLAY
  NoteLength NoteLength_17 (
    .I0(1'b0), .I1(1'b1), .I2(1'b0), .I3(1'b0), .E(NoteLength_15_nxt), .T1(1'b1), .T2(1'b0),
    .PLAY(NoteLength_17_play), .NXT(NoteLength_17_nxt));
  NoteLength NoteLength_19 (
    .I0(1'b0), .I1(1'b1), .I2(1'b0), .I3(1'b0), .E(NoteLength_25_nxt), .T1(1'b1), .T2(1'b0),
    .PLAY(NoteLength_19_play), .NXT(NoteLength_19_nxt));
  NoteLength NoteLength_21 (
    .I0(1'b1), .I1(1'b0), .I2(1'b0), .I3(1'b0), .E(NoteLength_22_nxt), .T1(1'b1), .T2(1'b0),
    .NXT(NoteLength_21_nxt));  // open: PLAY
  and and_1 (and_1_out, SRlatch_1_q, TimeSelector_1_output_1);
  NoteLength NoteLength_2 (
    .I0(1'b0), .I1(1'b1), .I2(1'b0), .I3(1'b0), .E(NoteLength_13_nxt), .T1(1'b1), .T2(1'b0),
    .NXT(NoteLength_2_nxt));  // open: PLAY
  NoteLength NoteLength_4 (
    .I0(1'b0), .I1(1'b1), .I2(1'b0), .I3(1'b0), .E(NoteLength_2_nxt), .T1(1'b1), .T2(1'b0),
    .PLAY(NoteLength_4_play), .NXT(NoteLength_4_nxt));
  NoteLength NoteLength_6 (
    .I0(1'b0), .I1(1'b1), .I2(1'b0), .I3(1'b0), .E(NoteLength_24_nxt), .T1(1'b1), .T2(1'b0),
    .PLAY(NoteLength_6_play), .NXT(NoteLength_6_nxt));
  NoteLength NoteLength_8 (
    .I0(1'b0), .I1(1'b1), .I2(1'b0), .I3(1'b0), .E(NoteLength_6_nxt), .T1(1'b1), .T2(1'b0),
    .PLAY(NoteLength_8_play), .NXT(NoteLength_8_nxt));
  NoteLength NoteLength_10 (
    .I0(1'b0), .I1(1'b1), .I2(1'b0), .I3(1'b0), .E(NoteLength_8_nxt), .T1(1'b1), .T2(1'b0),
    .PLAY(NoteLength_10_play), .NXT(NoteLength_10_nxt));
  NoteLength NoteLength_14 (
    .I0(1'b0), .I1(1'b1), .I2(1'b0), .I3(1'b0), .E(NoteLength_19_nxt), .T1(1'b1), .T2(1'b0),
    .PLAY(NoteLength_14_play), .NXT(NoteLength_14_nxt));
  NoteLength NoteLength_16 (
    .I0(1'b0), .I1(1'b1), .I2(1'b0), .I3(1'b0), .E(NoteLength_14_nxt), .T1(1'b1), .T2(1'b0),
    .PLAY(NoteLength_16_play), .NXT(NoteLength_16_nxt));
  NoteLength NoteLength_18 (
    .I0(1'b1), .I1(1'b1), .I2(1'b0), .I3(1'b0), .E(NoteLength_16_nxt), .T1(1'b1), .T2(1'b0),
    .PLAY(NoteLength_18_play), .NXT(NoteLength_18_nxt));
  NoteLength NoteLength_20 (
    .I0(1'b0), .I1(1'b1), .I2(1'b0), .I3(1'b0), .E(NoteLength_18_nxt), .T1(1'b1), .T2(1'b0),
    .PLAY(NoteLength_20_play), .NXT(NoteLength_20_nxt));
  NoteLength NoteLength_22 (
    .I0(1'b0), .I1(1'b0), .I2(1'b0), .I3(1'b1), .E(NoteLength_20_nxt), .T1(1'b1), .T2(1'b0),
    .PLAY(NoteLength_22_play), .NXT(NoteLength_22_nxt));
  NoteLength NoteLength_12 (
    .I0(1'b0), .I1(1'b0), .I2(1'b0), .I3(1'b1), .E(NoteLength_10_nxt), .T1(1'b1), .T2(1'b0),
    .PLAY(NoteLength_12_play), .NXT(NoteLength_12_nxt));
  A A_1 (.Output_1(A_1_output_1), .Input_1(and_1_out));
  E E_1 (.Output_1(E_1_output_1), .Input_1(NoteLength_1_play));
  A A_2 (.Output_1(A_2_output_1), .Input_1(NoteLength_3_play));
  A A_3 (.Output_1(A_3_output_1), .Input_1(NoteLength_5_play));
  B B_1 (.Input_1(NoteLength_7_play), .outp(B_1_outp));
  C C_1 (.Output_1(C_1_output_1), .Input_1(NoteLength_9_play));
  D D_1 (.Output_1(D_1_output_1), .Input_1(NoteLength_11_play));
  E E_2 (.Output_1(E_2_output_1), .Input_1(NoteLength_13_play));
  E E_3 (.Output_1(E_3_output_1), .Input_1(NoteLength_4_play));
  E E_4 (.Output_1(E_4_output_1), .Input_1(NoteLength_6_play));
  F F_1 (.Output_1(F_1_output_1), .Input_1(NoteLength_8_play));
  G G_1 (.Output_1(G_1_output_1), .Input_1(NoteLength_10_play));
  A2 A2_1 (.Output_1(A2_1_output_1), .Input_1(NoteLength_12_play));
  A2 A2_2 (.Output_1(A2_2_output_1), .Input_1(NoteLength_17_play));
  A2 A2_3 (.Output_1(A2_3_output_1), .Input_1(NoteLength_19_play));
  G G_2 (.Output_1(G_2_output_1), .Input_1(NoteLength_14_play));
  F F_2 (.Output_1(F_2_output_1), .Input_1(NoteLength_16_play));
  G G_3 (.Output_1(G_3_output_1), .Input_1(NoteLength_18_play));
  F F_3 (.Output_1(F_3_output_1), .Input_1(NoteLength_20_play));
  E E_5 (.Output_1(E_5_output_1), .Input_1(NoteLength_22_play));
  or or_4 (BUZZER, G_3_output_1, F_3_output_1, A_1_output_1, A2_3_output_1, E_1_output_1, A_2_output_1, G_1_output_1, A2_1_output_1, A_3_output_1, B_1_outp, C_1_output_1, D_1_output_1, E_2_output_1, A2_2_output_1, E_3_output_1, E_4_output_1, F_1_output_1, F_2_output_1, G_2_output_1, E_5_output_1);
  NoteLength NoteLength_23 (
    .I0(1'b1), .I1(1'b0), .I2(1'b0), .I3(1'b0), .E(NoteLength_3_nxt), .T1(1'b1), .T2(1'b0),
    .NXT(NoteLength_23_nxt));  // open: PLAY
  NoteLength NoteLength_24 (
    .I0(1'b1), .I1(1'b0), .I2(1'b0), .I3(1'b0), .E(NoteLength_4_nxt), .T1(1'b1), .T2(1'b0),
    .NXT(NoteLength_24_nxt));  // open: PLAY
  NoteLength NoteLength_25 (
    .I0(1'b1), .I1(1'b0), .I2(1'b0), .I3(1'b0), .E(NoteLength_17_nxt), .T1(1'b1), .T2(1'b0),
    .NXT(NoteLength_25_nxt));  // open: PLAY
endmodule

module OdeOfJoy (
  input  RESET,
  input  SET,
  output PIRATEPLAYING,
  output BUZZER
);

  wire and_1_out, C_1_output_1, C_2_output_1, D_1_output_1, D_2_output_1, D_3_output_1, D_4_output_1,
       E_1_output_1, E_2_output_1, E_3_output_1, E_4_output_1, E_5_output_1, F_1_output_1, F_2_output_1,
       G_1_output_1, G_2_output_1, MusicLoop_1_resetout, MusicLoop_1_setout, not_1_out, not_2_out,
       NoteLength_1_nxt, NoteLength_1_play, NoteLength_2_nxt, NoteLength_2_play, NoteLength_3_nxt,
       NoteLength_3_play, NoteLength_4_nxt, NoteLength_4_play, NoteLength_5_nxt, NoteLength_5_play,
       NoteLength_6_nxt, NoteLength_6_play, NoteLength_7_nxt, NoteLength_7_play, NoteLength_8_nxt,
       NoteLength_8_play, NoteLength_9_nxt, NoteLength_9_play, NoteLength_10_nxt, NoteLength_10_play,
       NoteLength_11_nxt, NoteLength_11_play, NoteLength_12_nxt, NoteLength_12_play, NoteLength_13_nxt,
       NoteLength_13_play, NoteLength_14_nxt, NoteLength_14_play, NoteLength_16_nxt, NoteLength_17_nxt,
       NoteLength_18_nxt, NoteLength_21_nxt, or_1_out, or_2_out, SRlatch_1_q, TimeSelector_1_output_1,
       waiter_nxt;

  or or_1 (or_1_out, SET, MusicLoop_1_setout);
  MusicLoop MusicLoop_1 (
    .RESET(RESET), .SET(SET), .FINISH(not_2_out), .SETOUT(MusicLoop_1_setout), .RESETOUT(MusicLoop_1_resetout));
  or or_2 (or_2_out, MusicLoop_1_resetout, RESET);
  SRlatch SRlatch_1 (.RESET(or_2_out), .SET(or_1_out), .Q(SRlatch_1_q));
  not not_1 (not_1_out, SRlatch_1_q);
  or or_3 (PIRATEPLAYING, not_2_out, SRlatch_1_q);
  TimeSelector TimeSelector_1 (
    .RESET(not_1_out), .Input_3(1'b0), .Input_5(1'b1), .Input_6(1'b0), .T0(1'b0), .SET(SRlatch_1_q),
    .Input_4(1'b0), .Output_1(TimeSelector_1_output_1), .T1(1'b1));
  NoteLength NoteLength_1 (
    .I0(1'b0), .I1(1'b0), .I2(1'b1), .I3(1'b0), .E(waiter_nxt), .T1(1'b0), .T2(1'b1),
    .PLAY(NoteLength_1_play), .NXT(NoteLength_1_nxt));
  NoteLength NoteLength_3 (
    .I0(1'b0), .I1(1'b0), .I2(1'b1), .I3(1'b0), .E(NoteLength_1_nxt), .T1(1'b0), .T2(1'b1),
    .PLAY(NoteLength_3_play), .NXT(NoteLength_3_nxt));
  NoteLength NoteLength_5 (
    .I0(1'b0), .I1(1'b0), .I2(1'b1), .I3(1'b0), .E(NoteLength_3_nxt), .T1(1'b0), .T2(1'b1),
    .PLAY(NoteLength_5_play), .NXT(NoteLength_5_nxt));
  NoteLength NoteLength_7 (
    .I0(1'b0), .I1(1'b0), .I2(1'b1), .I3(1'b0), .E(NoteLength_16_nxt), .T1(1'b0), .T2(1'b1),
    .PLAY(NoteLength_7_play), .NXT(NoteLength_7_nxt));
  NoteLength NoteLength_9 (
    .I0(1'b0), .I1(1'b0), .I2(1'b1), .I3(1'b0), .E(NoteLength_7_nxt), .T1(1'b0), .T2(1'b1),
    .PLAY(NoteLength_9_play), .NXT(NoteLength_9_nxt));
  NoteLength NoteLength_11 (
    .I0(1'b0), .I1(1'b0), .I2(1'b1), .I3(1'b0), .E(NoteLength_9_nxt), .T1(1'b0), .T2(1'b1),
    .PLAY(NoteLength_11_play), .NXT(NoteLength_11_nxt));
  NoteLength NoteLength_13 (
    .I0(1'b0), .I1(1'b0), .I2(1'b1), .I3(1'b0), .E(NoteLength_11_nxt), .T1(1'b0), .T2(1'b1),
    .PLAY(NoteLength_13_play), .NXT(NoteLength_13_nxt));
  and and_1 (and_1_out, SRlatch_1_q, TimeSelector_1_output_1);
  NoteLength NoteLength_2 (
    .I0(1'b0), .I1(1'b0), .I2(1'b1), .I3(1'b0), .E(NoteLength_13_nxt), .T1(1'b0), .T2(1'b1),
    .PLAY(NoteLength_2_play), .NXT(NoteLength_2_nxt));
  NoteLength NoteLength_4 (
    .I0(1'b0), .I1(1'b0), .I2(1'b1), .I3(1'b0), .E(NoteLength_17_nxt), .T1(1'b0), .T2(1'b1),
    .PLAY(NoteLength_4_play), .NXT(NoteLength_4_nxt));
  NoteLength NoteLength_6 (
    .I0(1'b0), .I1(1'b0), .I2(1'b1), .I3(1'b0), .E(NoteLength_4_nxt), .T1(1'b0), .T2(1'b1),
    .PLAY(NoteLength_6_play), .NXT(NoteLength_6_nxt));
  NoteLength NoteLength_8 (
    .I0(1'b0), .I1(1'b0), .I2(1'b1), .I3(1'b0), .E(NoteLength_6_nxt), .T1(1'b0), .T2(1'b1),
    .PLAY(NoteLength_8_play), .NXT(NoteLength_8_nxt));
  NoteLength NoteLength_10 (
    .I0(1'b0), .I1(1'b1), .I2(1'b1), .I3(1'b0), .E(NoteLength_18_nxt), .T1(1'b0), .T2(1'b1),
    .PLAY(NoteLength_10_play), .NXT(NoteLength_10_nxt));
  NoteLength NoteLength_12 (
    .I0(1'b0), .I1(1'b1), .I2(1'b0), .I3(1'b0), .E(NoteLength_10_nxt), .T1(1'b0), .T2(1'b1),
    .PLAY(NoteLength_12_play), .NXT(NoteLength_12_nxt));
  NoteLength NoteLength_14 (
    .I0(1'b0), .I1(1'b0), .I2(1'b0), .I3(1'b1), .E(NoteLength_12_nxt), .T1(1'b0), .T2(1'b1),
    .PLAY(NoteLength_14_play), .NXT(NoteLength_14_nxt));
  E E_1 (.Output_1(E_1_output_1), .Input_1(and_1_out));
  E E_2 (.Output_1(E_2_output_1), .Input_1(NoteLength_1_play));
  F F_1 (.Output_1(F_1_output_1), .Input_1(NoteLength_3_play));
  G G_1 (.Output_1(G_1_output_1), .Input_1(NoteLength_5_play));
  G G_2 (.Output_1(G_2_output_1), .Input_1(NoteLength_7_play));
  F F_2 (.Output_1(F_2_output_1), .Input_1(NoteLength_9_play));
  E E_3 (.Output_1(E_3_output_1), .Input_1(NoteLength_11_play));
  D D_1 (.Output_1(D_1_output_1), .Input_1(NoteLength_13_play));
  C C_1 (.Output_1(C_1_output_1), .Input_1(NoteLength_2_play));
  C C_2 (.Output_1(C_2_output_1), .Input_1(NoteLength_4_play));
  D D_2 (.Output_1(D_2_output_1), .Input_1(NoteLength_6_play));
  E E_4 (.Output_1(E_4_output_1), .Input_1(NoteLength_8_play));
  E E_5 (.Output_1(E_5_output_1), .Input_1(NoteLength_10_play));
  D D_3 (.Output_1(D_3_output_1), .Input_1(NoteLength_12_play));
  D D_4 (.Output_1(D_4_output_1), .Input_1(NoteLength_14_play));
  or or_4 (BUZZER, E_1_output_1, E_2_output_1, F_1_output_1, E_4_output_1, D_3_output_1, G_1_output_1, G_2_output_1, D_4_output_1, F_2_output_1, E_3_output_1, D_1_output_1, C_1_output_1, C_2_output_1, D_2_output_1, E_5_output_1);
  NoteLength NoteLength_21 (
    .I0(1'b0), .I1(1'b0), .I2(1'b1), .I3(1'b0), .E(NoteLength_14_nxt), .T1(1'b0), .T2(1'b1),
    .NXT(NoteLength_21_nxt));  // open: PLAY
  not not_2 (not_2_out, NoteLength_21_nxt);
  NoteLength waiter (
    .I0(1'b1), .I1(1'b0), .I2(1'b0), .I3(1'b0), .E(TimeSelector_1_output_1), .T1(1'b0), .T2(1'b1),
    .NXT(waiter_nxt));  // open: PLAY
  NoteLength NoteLength_16 (
    .I0(1'b1), .I1(1'b0), .I2(1'b0), .I3(1'b0), .E(NoteLength_5_nxt), .T1(1'b0), .T2(1'b1),
    .NXT(NoteLength_16_nxt));  // open: PLAY
  NoteLength NoteLength_17 (
    .I0(1'b1), .I1(1'b0), .I2(1'b0), .I3(1'b0), .E(NoteLength_2_nxt), .T1(1'b0), .T2(1'b1),
    .NXT(NoteLength_17_nxt));  // open: PLAY
  NoteLength NoteLength_18 (
    .I0(1'b1), .I1(1'b0), .I2(1'b0), .I3(1'b0), .E(NoteLength_8_nxt), .T1(1'b0), .T2(1'b1),
    .NXT(NoteLength_18_nxt));  // open: PLAY
endmodule

module MusicLoop (
  input  RESET,
  input  SET,
  input  FINISH,
  output SETOUT,
  output RESETOUT
);

  wire clock_1_out, SRlatch_1_q, StatesLoop_1_resetout, StatesLoop_1_setout;

  SRlatch SRlatch_1 (.RESET(RESET), .SET(SET), .Q(SRlatch_1_q));
  StatesLoop StatesLoop_1 (
    .Q(SRlatch_1_q), .FINISH(FINISH), .SETIN(SETOUT), .RESETIN(RESETOUT), .SETOUT(StatesLoop_1_setout),
    .RESETOUT(StatesLoop_1_resetout));
  Clock clock_1 (.out(clock_1_out));
  D_Flip_Flop d_ff_1 (.D(StatesLoop_1_setout), .clk(clock_1_out), .Q(SETOUT));  // open: Qn, preset, reset
  D_Flip_Flop d_ff_2 (.D(StatesLoop_1_resetout), .clk(clock_1_out), .Q(RESETOUT));  // open: Qn, preset, reset
endmodule

module StatesLoop (
  input  Q,
  input  FINISH,
  input  SETIN,
  input  RESETIN,
  output SETOUT,
  output RESETOUT
);

  wire not_1_out, not_2_out, not_3_out, not_4_out;

  not not_1 (not_1_out, FINISH);
  not not_2 (not_2_out, SETIN);
  not not_3 (not_3_out, SETIN);
  not not_4 (not_4_out, RESETIN);
  and and_1 (SETOUT, Q, not_1_out, not_2_out, RESETIN);
  and and_2 (RESETOUT, Q, FINISH, not_3_out, not_4_out);
endmodule

module NoteLength (
  input  I0,
  input  I1,
  input  I2,
  input  I3,
  input  E,
  input  T1,
  input  T2,
  output PLAY,
  output NXT
);

  wire not_1_out;

  not not_1 (not_1_out, E);
  TimeSelector TimeSelector_1 (
    .RESET(E), .Input_3(I0), .Input_5(I2), .Input_6(I3), .T0(T1), .SET(not_1_out), .Input_4(I1),
    .Output_1(NXT), .T1(T2));
  and and_1 (PLAY, NXT, not_1_out);
endmodule

module TimeSelector (
  input  T1,
  input  T0,
  input  Input_3,
  input  Input_4,
  input  Input_5,
  input  Input_6,
  input  SET,
  input  RESET,
  output Output_1
);

  wire and_1_out, and_2_out, Compteur_1_p0, Compteur_1_p1, Compteur_1_p2, Compteur_1_p3, or_1_out,
       SRlatch_1_q, SRlatch_2_q, SRlatch_3_q, xnor_1_out, xnor_2_out, xnor_3_out, xnor_4_out;

  SRlatch SRlatch_1 (.RESET(RESET), .SET(SET), .Q(SRlatch_1_q));
  or or_1 (or_1_out, RESET, SRlatch_3_q);
  Compteurv2 Compteur_1 (
    .SET(SRlatch_1_q), .RESET(or_1_out), .T1(T1), .T0(T0), .P0(Compteur_1_p0), .P1(Compteur_1_p1),
    .P2(Compteur_1_p2), .P3(Compteur_1_p3));
  xnor xnor_1 (xnor_1_out, Compteur_1_p0, Input_3);
  xnor xnor_2 (xnor_2_out, Compteur_1_p1, Input_4);
  xnor xnor_3 (xnor_3_out, Input_5, Compteur_1_p2);
  xnor xnor_4 (xnor_4_out, Input_6, Compteur_1_p3);
  and and_1 (and_1_out, xnor_1_out, xnor_2_out, xnor_3_out, xnor_4_out);
  SRlatch SRlatch_2 (.RESET(RESET), .SET(and_1_out), .Q(SRlatch_2_q));
  and and_2 (and_2_out, SRlatch_2_q, SRlatch_1_q);
  SRlatch SRlatch_3 (.RESET(RESET), .SET(and_2_out), .Q(SRlatch_3_q));
  not not_1 (Output_1, SRlatch_3_q);
endmodule

module Compteurv2 (
  input  SET,
  input  RESET,
  input  T1,
  input  T0,
  output P0,
  output P1,
  output P2,
  output P3
);

  wire and_1_out, and_2_out, and_3_out, and_4_out, and_5_out, and_6_out, and_7_out, and_8_out, and_9_out,
       and_10_out, and_11_out, and_12_out, d_ff_1_q, d_ff_2_q, d_ff_3_q, d_ff_4_q, d_ff_5_q, d_ff_6_q,
       d_ff_7_q, d_ff_8_q, d_ff_9_q, d_ff_10_q, d_ff_11_q, d_ff_12_q, HARRY_out, newdig0_9_1_p1out,
       newdig0_9_1_p2out, newdig0_9_1_p3out, newdig0_9_1_p4out, ODE_out, or_3_out, or_4_out, or_5_out,
       or_6_out, or_9_out, or_10_out, or_11_out, or_12_out, or_13_out, or_14_out, or_15_out, or_16_out,
       TempoPicker_1_harry, TempoPicker_1_pirate, TempoPicker_1_zelda, ZELDA_out;

  Clock #(.highDuration(6400), .lowDuration(6400)) HARRY (.out(HARRY_out));
  TempoPicker TempoPicker_1 (
    .T1(T1), .T0(T0), .HARRY(TempoPicker_1_harry), .ZELDA(TempoPicker_1_zelda), .PIRATE(TempoPicker_1_pirate));
  newdig0_9 newdig0_9_1 (
    .P0(P0), .P1(P1), .SET(SET), .P2(P2), .P3(P3), .RESET(RESET), .P1OUT(newdig0_9_1_p1out),
    .P2OUT(newdig0_9_1_p2out), .P3OUT(newdig0_9_1_p3out), .P4OUT(newdig0_9_1_p4out));
  D_Flip_Flop d_ff_1 (.D(newdig0_9_1_p1out), .clk(HARRY_out), .Q(d_ff_1_q));  // open: Qn, preset, reset
  D_Flip_Flop d_ff_2 (.D(newdig0_9_1_p2out), .clk(HARRY_out), .Q(d_ff_2_q));  // open: Qn, preset, reset
  D_Flip_Flop d_ff_3 (.D(newdig0_9_1_p3out), .clk(HARRY_out), .Q(d_ff_3_q));  // open: Qn, preset, reset
  D_Flip_Flop d_ff_4 (.D(newdig0_9_1_p4out), .clk(HARRY_out), .Q(d_ff_4_q));  // open: Qn, preset, reset
  or or_1 (P1, and_2_out, and_6_out, and_10_out);
  or or_2 (P0, and_1_out, and_5_out, and_9_out);
  and and_1 (and_1_out, or_3_out, TempoPicker_1_harry);
  or or_3 (or_3_out, d_ff_1_q, RESET);
  or or_4 (or_4_out, d_ff_2_q, RESET);
  or or_5 (or_5_out, d_ff_3_q, RESET);
  or or_6 (or_6_out, d_ff_4_q, RESET);
  or or_7 (P2, and_3_out, and_7_out, and_11_out);
  and and_2 (and_2_out, or_4_out, TempoPicker_1_harry);
  or or_8 (P3, and_4_out, and_8_out, and_12_out);
  and and_3 (and_3_out, or_5_out, TempoPicker_1_harry);
  and and_4 (and_4_out, or_6_out, TempoPicker_1_harry);
  Clock #(.highDuration(3776), .lowDuration(3776)) ZELDA (.out(ZELDA_out));
  D_Flip_Flop d_ff_5 (.D(newdig0_9_1_p1out), .clk(ZELDA_out), .Q(d_ff_5_q));  // open: Qn, preset, reset
  D_Flip_Flop d_ff_6 (.D(newdig0_9_1_p2out), .clk(ZELDA_out), .Q(d_ff_6_q));  // open: Qn, preset, reset
  D_Flip_Flop d_ff_7 (.D(newdig0_9_1_p3out), .clk(ZELDA_out), .Q(d_ff_7_q));  // open: Qn, preset, reset
  D_Flip_Flop d_ff_8 (.D(newdig0_9_1_p4out), .clk(ZELDA_out), .Q(d_ff_8_q));  // open: Qn, preset, reset
  and and_5 (and_5_out, or_9_out, TempoPicker_1_zelda);
  or or_9 (or_9_out, d_ff_5_q, RESET);
  or or_10 (or_10_out, d_ff_6_q, RESET);
  or or_11 (or_11_out, d_ff_7_q, RESET);
  or or_12 (or_12_out, d_ff_8_q, RESET);
  and and_6 (and_6_out, or_10_out, TempoPicker_1_zelda);
  and and_7 (and_7_out, or_11_out, TempoPicker_1_zelda);
  and and_8 (and_8_out, or_12_out, TempoPicker_1_zelda);
  Clock #(.highDuration(3000), .lowDuration(3000)) ODE (.out(ODE_out));
  D_Flip_Flop d_ff_9 (.D(newdig0_9_1_p1out), .clk(ODE_out), .Q(d_ff_9_q));  // open: Qn, preset, reset
  D_Flip_Flop d_ff_10 (.D(newdig0_9_1_p2out), .clk(ODE_out), .Q(d_ff_10_q));  // open: Qn, preset, reset
  D_Flip_Flop d_ff_11 (.D(newdig0_9_1_p3out), .clk(ODE_out), .Q(d_ff_11_q));  // open: Qn, preset, reset
  D_Flip_Flop d_ff_12 (.D(newdig0_9_1_p4out), .clk(ODE_out), .Q(d_ff_12_q));  // open: Qn, preset, reset
  or or_13 (or_13_out, d_ff_9_q, RESET);
  or or_14 (or_14_out, d_ff_10_q, RESET);
  buf or_15 (or_15_out, d_ff_11_q);  // OR_Gate
  or or_16 (or_16_out, d_ff_12_q, RESET);
  and and_9 (and_9_out, or_13_out, TempoPicker_1_pirate);
  and and_10 (and_10_out, or_14_out, TempoPicker_1_pirate);
  and and_11 (and_11_out, or_15_out, TempoPicker_1_pirate);
  and and_12 (and_12_out, or_16_out, TempoPicker_1_pirate);
endmodule

module TempoPicker (
  input  T1,
  input  T0,
  output HARRY,
  output ZELDA,
  output PIRATE
);

  wire not_1_out, not_2_out, not_3_out, not_4_out;

  not not_1 (not_1_out, T1);
  and and_1 (HARRY, not_1_out, not_2_out);
  not not_2 (not_2_out, T0);
  not not_3 (not_3_out, T1);
  and and_2 (ZELDA, not_3_out, T0);
  and and_3 (PIRATE, T1, not_4_out);
  not not_4 (not_4_out, T0);
endmodule

module newdig0_9 (
  input  P0,
  input  P1,
  input  SET,
  input  P2,
  input  P3,
  input  RESET,
  output P1OUT,
  output P2OUT,
  output P3OUT,
  output P4OUT
);

  wire and_1_out, and_2_out, and_3_out, and_4_out, and_5_out, and_6_out, and_7_out, and_8_out, and_9_out,
       and_10_out, and_11_out, and_12_out, and_13_out, and_14_out, and_15_out, and_16_out, and_17_out,
       not_1_out, not_2_out, not_3_out, not_4_out, not_5_out, not_6_out, not_7_out, not_8_out, not_9_out,
       not_10_out, not_11_out, not_12_out, not_13_out, not_14_out, not_15_out, not_16_out, not_17_out,
       not_18_out, not_19_out, not_20_out, not_21_out, not_22_out, not_23_out, not_24_out, not_25_out,
       not_26_out, not_27_out, not_28_out, not_29_out, or_1_out, or_2_out;

  not not_1 (not_1_out, P0);
  not not_2 (not_2_out, P1);
  not not_3 (not_3_out, P0);
  not not_4 (not_4_out, P3);
  not not_5 (not_5_out, SET);
  not not_6 (not_6_out, P1);
  not not_7 (not_7_out, P1);
  not not_8 (not_8_out, P0);
  not not_9 (not_9_out, P3);
  not not_10 (not_10_out, SET);
  not not_11 (not_11_out, P1);
  not not_12 (not_12_out, P3);
  not not_13 (not_13_out, SET);
  not not_14 (not_14_out, RESET);
  not not_15 (not_15_out, RESET);
  not not_16 (not_16_out, P0);
  not not_17 (not_17_out, RESET);
  not not_18 (not_18_out, P1);
  not not_19 (not_19_out, RESET);
  not not_20 (not_20_out, RESET);
  not not_21 (not_21_out, P2);
  not not_22 (not_22_out, SET);
  not not_23 (not_23_out, RESET);
  not not_24 (not_24_out, RESET);
  not not_25 (not_25_out, P0);
  not not_26 (not_26_out, RESET);
  not not_27 (not_27_out, P3);
  and and_1 (and_1_out, not_1_out, not_2_out, SET);
  and and_2 (and_2_out, not_3_out, SET, not_4_out);
  and and_3 (and_3_out, P0, not_5_out);
  and and_4 (and_4_out, P0, not_6_out, P2, P3);
  and and_5 (and_5_out, not_7_out, SET, P2, P3);
  and and_6 (and_6_out, not_8_out, P1, not_9_out);
  and and_7 (and_7_out, P1, not_10_out);
  and and_8 (and_8_out, P0, not_11_out, SET, not_12_out);
  and and_9 (and_9_out, P0, P1, P3);
  and and_10 (and_10_out, not_13_out, not_14_out, P2);
  and and_11 (and_11_out, not_15_out, not_16_out, P2);
  and and_12 (and_12_out, not_17_out, not_18_out, P2);
  and and_13 (and_13_out, not_19_out, P2, P3);
  and and_14 (and_14_out, SET, not_20_out, P0, P1, not_21_out);
  and and_15 (and_15_out, not_22_out, not_23_out, P3);
  and and_16 (and_16_out, not_24_out, not_25_out, P3);
  and and_17 (and_17_out, SET, not_26_out, P0, P1, P2, not_27_out);
  or or_1 (or_1_out, and_1_out, and_2_out, and_3_out, and_4_out);
  not not_28 (not_28_out, RESET);
  or or_2 (or_2_out, and_5_out, and_6_out, and_7_out, and_8_out, and_9_out);
  not not_29 (not_29_out, RESET);
  or or_3 (P3OUT, and_10_out, and_11_out, and_12_out, and_13_out, and_14_out);
  or or_4 (P4OUT, and_15_out, and_16_out, and_17_out);
  and and_18 (P1OUT, or_1_out, not_28_out);
  and and_19 (P2OUT, or_2_out, not_29_out);
endmodule

module SRlatch (
  input  RESET,
  input  SET,
  output Q
);

  wire nor_2_out;

  nor nor_1 (Q, RESET, nor_2_out);
  nor nor_2 (nor_2_out, Q, SET);
endmodule

module A (
  input  Input_1,
  output Output_1
);

  wire clock_1_out, d_ff_1_q, d_ff_1_qn;

  Clock #(.highDuration(29), .lowDuration(29)) clock_1 (.out(clock_1_out));
  D_Flip_Flop d_ff_1 (.D(d_ff_1_qn), .clk(clock_1_out), .Q(d_ff_1_q), .Qn(d_ff_1_qn));  // open: preset, reset
  and and_1 (Output_1, Input_1, d_ff_1_q);
endmodule

module A2 (
  input  Input_1,
  output Output_1
);

  wire clock_1_out, d_ff_1_q, d_ff_1_qn;

  Clock #(.highDuration(15), .lowDuration(14)) clock_1 (.out(clock_1_out));
  D_Flip_Flop d_ff_1 (.D(d_ff_1_qn), .clk(clock_1_out), .Q(d_ff_1_q), .Qn(d_ff_1_qn));  // open: preset, reset
  and and_1 (Output_1, Input_1, d_ff_1_q);
endmodule

module B (
  input  Input_1,
  output outp
);

  wire clock_1_out, d_ff_1_q, d_ff_1_qn;

  Clock #(.highDuration(26), .lowDuration(26)) clock_1 (.out(clock_1_out));
  D_Flip_Flop d_ff_1 (.D(d_ff_1_qn), .clk(clock_1_out), .Q(d_ff_1_q), .Qn(d_ff_1_qn));  // open: preset, reset
  and and_1 (outp, Input_1, d_ff_1_q);
endmodule

module B2 (
  input  Input_1,
  output Output_1
);

  wire clock_1_out, d_ff_1_q, d_ff_1_qn;

  Clock #(.highDuration(13), .lowDuration(13)) clock_1 (.out(clock_1_out));
  D_Flip_Flop d_ff_1 (.D(d_ff_1_qn), .clk(clock_1_out), .Q(d_ff_1_q), .Qn(d_ff_1_qn));  // open: preset, reset
  and and_1 (Output_1, Input_1, d_ff_1_q);
endmodule

module C (
  input  Input_1,
  output Output_1
);

  wire clock_1_out, d_ff_1_q, d_ff_1_qn;

  Clock #(.highDuration(24), .lowDuration(25)) clock_1 (.out(clock_1_out));
  D_Flip_Flop d_ff_1 (.D(d_ff_1_qn), .clk(clock_1_out), .Q(d_ff_1_q), .Qn(d_ff_1_qn));  // open: preset, reset
  and and_1 (Output_1, Input_1, d_ff_1_q);
endmodule

module D (
  input  Input_1,
  output Output_1
);

  wire clock_1_out, d_ff_1_q, d_ff_1_qn;

  Clock #(.highDuration(22), .lowDuration(22)) clock_1 (.out(clock_1_out));
  D_Flip_Flop d_ff_1 (.D(d_ff_1_qn), .clk(clock_1_out), .Q(d_ff_1_q), .Qn(d_ff_1_qn));  // open: preset, reset
  and and_1 (Output_1, Input_1, d_ff_1_q);
endmodule

module E (
  input  Input_1,
  output Output_1
);

  wire clock_1_out, d_ff_1_q, d_ff_1_qn;

  Clock #(.highDuration(20), .lowDuration(19)) clock_1 (.out(clock_1_out));
  D_Flip_Flop d_ff_1 (.D(d_ff_1_qn), .clk(clock_1_out), .Q(d_ff_1_q), .Qn(d_ff_1_qn));  // open: preset, reset
  and and_1 (Output_1, Input_1, d_ff_1_q);
endmodule

module Ds (
  input  Input_1,
  output Output_1
);

  wire clock_1_out, d_ff_1_q, d_ff_1_qn;

  Clock #(.highDuration(21), .lowDuration(20)) clock_1 (.out(clock_1_out));
  D_Flip_Flop d_ff_1 (.D(d_ff_1_qn), .clk(clock_1_out), .Q(d_ff_1_q), .Qn(d_ff_1_qn));  // open: preset, reset
  and and_1 (Output_1, Input_1, d_ff_1_q);
endmodule

module F (
  input  Input_1,
  output Output_1
);

  wire clock_1_out, d_ff_1_q, d_ff_1_qn;

  Clock #(.highDuration(19), .lowDuration(18)) clock_1 (.out(clock_1_out));
  D_Flip_Flop d_ff_1 (.D(d_ff_1_qn), .clk(clock_1_out), .Q(d_ff_1_q), .Qn(d_ff_1_qn));  // open: preset, reset
  and and_1 (Output_1, Input_1, d_ff_1_q);
endmodule

module Fs (
  input  Input_1,
  output Output_1
);

  wire clock_1_out, d_ff_1_q, d_ff_1_qn;

  Clock #(.highDuration(17), .lowDuration(18)) clock_1 (.out(clock_1_out));
  D_Flip_Flop d_ff_1 (.D(d_ff_1_qn), .clk(clock_1_out), .Q(d_ff_1_q), .Qn(d_ff_1_qn));  // open: preset, reset
  and and_1 (Output_1, Input_1, d_ff_1_q);
endmodule

module G (
  input  Input_1,
  output Output_1
);

  wire clock_1_out, d_ff_1_q, d_ff_1_qn;

  Clock #(.highDuration(17), .lowDuration(16)) clock_1 (.out(clock_1_out));
  D_Flip_Flop d_ff_1 (.D(d_ff_1_qn), .clk(clock_1_out), .Q(d_ff_1_q), .Qn(d_ff_1_qn));  // open: preset, reset
  and and_1 (Output_1, Input_1, d_ff_1_q);
endmodule

module Glow (
  input  Input_1,
  output Output_1
);

  wire clock_1_out, s_r_ff_1_q, s_r_ff_1_qn;

  Clock #(.highDuration(30), .lowDuration(30)) clock_1 (.out(clock_1_out));
  S_R_Flip_Flop s_r_ff_1 (
    .S(s_r_ff_1_qn), .clk(clock_1_out), .Q(s_r_ff_1_q), .Qn(s_r_ff_1_qn));  // open: R, reset, preset
  and and_1 (Output_1, Input_1, s_r_ff_1_q);
endmodule

module Elow (
  input  Input_1,
  output Outputing
);

  wire clock_1_out, d_ff_1_q, d_ff_1_qn;

  Clock #(.highDuration(33), .lowDuration(33)) clock_1 (.out(clock_1_out));
  D_Flip_Flop d_ff_1 (.D(d_ff_1_qn), .clk(clock_1_out), .Q(d_ff_1_q), .Qn(d_ff_1_qn));  // open: preset, reset
  and and_1 (Outputing, Input_1, d_ff_1_q);
endmodule

module Affichage1 (
  input  HARRY,
  input  ZELDA,
  input  PIRATE,
  output V0,
  output W0,
  output X0,
  output Y0,
  output Z0
);

  wire and_1_out, not_1_out, not_2_out, not_6_out;

  not not_1 (not_1_out, HARRY);
  not not_2 (not_2_out, PIRATE);
  not not_3 (W0, HARRY);
  not not_4 (X0, ZELDA);
  not not_5 (Y0, ZELDA);
  not not_6 (not_6_out, PIRATE);
  and and_1 (and_1_out, not_1_out, not_2_out);
  or or_1 (Z0, not_6_out, ZELDA, HARRY);
  or or_2 (V0, and_1_out, ZELDA);
endmodule

module Affichage2 (
  input  HARRY,
  input  ZELDA,
  input  PIRATE,
  output V1,
  output W1,
  output X1,
  output Y1,
  output Z1
);

  wire and_2_out, and_3_out, and_4_out, and_5_out, not_1_out, not_2_out, not_3_out, not_4_out, not_5_out,
       not_6_out, not_7_out, not_8_out, not_9_out, not_10_out, not_11_out, not_12_out;

  not not_1 (not_1_out, HARRY);
  not not_2 (not_2_out, ZELDA);
  not not_3 (not_3_out, PIRATE);
  not not_4 (not_4_out, HARRY);
  not not_5 (not_5_out, ZELDA);
  not not_6 (not_6_out, PIRATE);
  not not_7 (not_7_out, HARRY);
  not not_8 (not_8_out, PIRATE);
  not not_9 (not_9_out, HARRY);
  not not_10 (not_10_out, ZELDA);
  not not_11 (not_11_out, HARRY);
  not not_12 (not_12_out, ZELDA);
  and and_1 (V1, not_1_out, not_2_out, not_3_out);
  and and_2 (and_2_out, not_4_out, not_5_out, not_6_out);
  and and_3 (and_3_out, ZELDA, PIRATE);
  and and_4 (and_4_out, HARRY, PIRATE);
  and and_5 (and_5_out, not_7_out, not_8_out);
  and and_6 (Y1, not_9_out, not_10_out);
  and and_7 (Z1, not_11_out, not_12_out);
  or or_1 (W1, and_2_out, and_3_out, and_4_out);
  or or_2 (X1, and_5_out, ZELDA);
endmodule

module Affichage3 (
  input  HARRY,
  input  ZELDA,
  input  PIRATE,
  output V2,
  output W2,
  output X2,
  output Y2,
  output Z2
);

  wire and_1_out, and_2_out, and_3_out, and_5_out, not_1_out, not_2_out, not_3_out, not_4_out, not_5_out,
       not_6_out, not_7_out, not_8_out, not_9_out, not_10_out;

  not not_1 (not_1_out, ZELDA);
  not not_2 (not_2_out, PIRATE);
  not not_3 (not_3_out, ZELDA);
  not not_4 (not_4_out, HARRY);
  not not_5 (not_5_out, PIRATE);
  not not_6 (not_6_out, HARRY);
  not not_7 (not_7_out, ZELDA);
  not not_8 (not_8_out, HARRY);
  not not_9 (not_9_out, PIRATE);
  not not_10 (not_10_out, PIRATE);
  and and_1 (and_1_out, not_1_out, not_2_out);
  and and_2 (and_2_out, HARRY, not_3_out);
  and and_3 (and_3_out, not_4_out, not_5_out);
  and and_4 (X2, not_6_out, not_7_out);
  and and_5 (and_5_out, not_8_out, not_9_out);
  or or_1 (Z2, not_10_out, ZELDA, HARRY);
  or or_2 (V2, and_1_out, and_2_out);
  or or_3 (W2, and_3_out, ZELDA);
  or or_4 (Y2, and_5_out, ZELDA);
endmodule

module Affichage4 (
  input  HARRY,
  input  ZELDA,
  input  PIRATE,
  output V3,
  output W3,
  output X3,
  output Y3,
  output Z3
);

  wire and_3_out, not_1_out, not_2_out, not_3_out, not_4_out, not_5_out, not_6_out, not_7_out, not_8_out,
       not_9_out;

  not not_1 (not_1_out, ZELDA);
  not not_2 (not_2_out, HARRY);
  not not_3 (not_3_out, ZELDA);
  not not_4 (not_4_out, HARRY);
  not not_5 (not_5_out, ZELDA);
  not not_6 (not_6_out, HARRY);
  not not_7 (not_7_out, HARRY);
  not not_8 (not_8_out, ZELDA);
  or or_1 (V3, not_1_out, HARRY);
  and and_1 (W3, not_2_out, not_3_out);
  and and_2 (X3, not_4_out, not_5_out);
  or or_2 (Y3, not_6_out, ZELDA);
  and and_3 (and_3_out, not_7_out, not_8_out);
  not not_9 (not_9_out, PIRATE);
  or or_3 (Z3, and_3_out, not_9_out);
endmodule

module Affichage5 (
  input  HARRY,
  input  ZELDA,
  input  PIRATE,
  output V4,
  output W4,
  output X4,
  output Y4,
  output Z4
);

  wire and_2_out, and_3_out, not_2_out, not_3_out, not_4_out, not_5_out, not_6_out, not_7_out, not_8_out;

  not not_1 (V4, ZELDA);
  not not_2 (not_2_out, ZELDA);
  not not_3 (not_3_out, HARRY);
  not not_4 (not_4_out, ZELDA);
  not not_5 (not_5_out, HARRY);
  not not_6 (not_6_out, ZELDA);
  not not_7 (not_7_out, HARRY);
  not not_8 (not_8_out, ZELDA);
  or or_1 (W4, not_2_out, HARRY);
  and and_1 (X4, not_3_out, not_4_out);
  and and_2 (and_2_out, not_5_out, not_6_out);
  and and_3 (and_3_out, not_7_out, not_8_out);
  or or_2 (Y4, and_2_out, PIRATE);
  or or_3 (Z4, and_3_out, PIRATE);
endmodule

module Affichage6 (
  input  HARRY,
  input  ZELDA,
  input  PIRATE,
  output V5,
  output W5,
  output X5,
  output Y5,
  output Z5
);

  wire and_1_out, and_2_out, and_3_out, and_4_out, not_1_out, not_2_out, not_3_out, not_4_out, not_5_out,
       not_6_out, not_7_out, not_8_out, not_9_out, not_10_out, not_11_out, not_12_out;

  not not_1 (not_1_out, HARRY);
  not not_2 (not_2_out, ZELDA);
  not not_3 (not_3_out, HARRY);
  not not_4 (not_4_out, ZELDA);
  not not_5 (not_5_out, HARRY);
  not not_6 (not_6_out, ZELDA);
  not not_7 (not_7_out, HARRY);
  not not_8 (not_8_out, ZELDA);
  and and_1 (and_1_out, not_1_out, not_2_out);
  not not_9 (not_9_out, PIRATE);
  and and_2 (and_2_out, not_3_out, not_4_out);
  not not_10 (not_10_out, PIRATE);
  and and_3 (and_3_out, not_5_out, not_6_out);
  not not_11 (not_11_out, PIRATE);
  and and_4 (and_4_out, not_7_out, not_8_out);
  not not_12 (not_12_out, PIRATE);
  or or_1 (V5, and_1_out, not_9_out);
  or or_2 (W5, and_2_out, not_10_out);
  or or_3 (Y5, and_3_out, not_11_out);
  or or_4 (Z5, and_4_out, not_12_out);

  assign X5 = 1'b1;
endmodule

module func_a (
  input  V,
  input  W,
  input  X,
  input  Y,
  input  Z,
  output a
);

  wire and_1_out, and_2_out, and_3_out, and_4_out, and_5_out, and_6_out, and_7_out, and_8_out, and_9_out,
       not_1_out, not_2_out, not_3_out, not_4_out, not_5_out, not_6_out, not_7_out, not_8_out, not_9_out,
       not_10_out, not_11_out, not_12_out, not_13_out, not_14_out, not_15_out, not_16_out, not_17_out,
       not_18_out, not_19_out, not_20_out;

  not not_1 (not_1_out, W);
  not not_2 (not_2_out, X);
  not not_3 (not_3_out, Y);
  not not_4 (not_4_out, Z);
  not not_5 (not_5_out, V);
  not not_6 (not_6_out, W);
  not not_7 (not_7_out, Y);
  not not_8 (not_8_out, V);
  not not_9 (not_9_out, W);
  not not_10 (not_10_out, Z);
  not not_11 (not_11_out, V);
  not not_12 (not_12_out, Y);
  not not_13 (not_13_out, Z);
  not not_14 (not_14_out, V);
  not not_15 (not_15_out, W);
  not not_16 (not_16_out, X);
  not not_17 (not_17_out, Z);
  not not_18 (not_18_out, W);
  not not_19 (not_19_out, X);
  not not_20 (not_20_out, Y);
  and and_1 (and_1_out, not_1_out, not_2_out, not_3_out, not_4_out);
  and and_2 (and_2_out, not_5_out, not_6_out, X, not_7_out);
  and and_3 (and_3_out, not_8_out, not_9_out, X, not_10_out);
  and and_4 (and_4_out, not_11_out, X, not_12_out, not_13_out);
  and and_5 (and_5_out, not_14_out, W, X, Y, Z);
  and and_6 (and_6_out, V, not_15_out, not_16_out, not_17_out);
  and and_7 (and_7_out, V, not_18_out, X, Y, Z);
  and and_8 (and_8_out, V, W, not_19_out, Z);
  and and_9 (and_9_out, V, W, not_20_out, Z);
  or or_1 (a, and_1_out, and_2_out, and_3_out, and_4_out, and_5_out, and_6_out, and_7_out, and_8_out, and_9_out);
endmodule

module func_b (
  input  V,
  input  W,
  input  X,
  input  Y,
  input  Z,
  output b
);

  wire and_1_out, and_2_out, and_3_out, and_4_out, and_5_out, and_6_out, not_1_out, not_2_out, not_3_out,
       not_4_out, not_5_out, not_6_out, not_7_out, not_8_out, not_9_out, not_10_out, not_11_out, not_12_out;

  not not_1 (not_1_out, X);
  not not_2 (not_2_out, Y);
  not not_3 (not_3_out, Z);
  not not_4 (not_4_out, W);
  not not_5 (not_5_out, X);
  not not_6 (not_6_out, W);
  not not_7 (not_7_out, Z);
  not not_8 (not_8_out, V);
  not not_9 (not_9_out, X);
  not not_10 (not_10_out, Y);
  not not_11 (not_11_out, Y);
  not not_12 (not_12_out, Z);
  and and_1 (and_1_out, not_1_out, not_2_out, not_3_out);
  and and_2 (and_2_out, not_4_out, not_5_out, Y, Z);
  and and_3 (and_3_out, not_6_out, X, Y, not_7_out);
  and and_4 (and_4_out, not_8_out, X, Y, Z);
  and and_5 (and_5_out, W, not_9_out, not_10_out);
  and and_6 (and_6_out, V, not_11_out, not_12_out);
  or or_1 (b, and_1_out, and_2_out, and_3_out, and_4_out, and_5_out, and_6_out);
endmodule

module func_c (
  input  V,
  input  W,
  input  X,
  input  Y,
  input  Z,
  output c
);

  wire and_1_out, and_2_out, and_3_out, and_4_out, and_5_out, and_6_out, and_7_out, and_8_out, not_1_out,
       not_2_out, not_3_out, not_4_out, not_5_out, not_6_out, not_7_out, not_8_out, not_9_out, not_10_out,
       not_11_out, not_12_out, not_13_out, not_14_out, not_15_out, not_16_out, not_17_out;

  not not_1 (not_1_out, V);
  not not_2 (not_2_out, X);
  not not_3 (not_3_out, Y);
  not not_4 (not_4_out, X);
  not not_5 (not_5_out, Y);
  not not_6 (not_6_out, Z);
  not not_7 (not_7_out, W);
  not not_8 (not_8_out, X);
  not not_9 (not_9_out, V);
  not not_10 (not_10_out, W);
  not not_11 (not_11_out, V);
  not not_12 (not_12_out, Z);
  not not_13 (not_13_out, V);
  not not_14 (not_14_out, Y);
  not not_15 (not_15_out, X);
  not not_16 (not_16_out, Z);
  not not_17 (not_17_out, Y);
  and and_1 (and_1_out, not_1_out, not_2_out, not_3_out);
  and and_2 (and_2_out, not_4_out, not_5_out, not_6_out);
  and and_3 (and_3_out, not_7_out, not_8_out, Y, Z);
  and and_4 (and_4_out, not_9_out, not_10_out, X, Y);
  and and_5 (and_5_out, not_11_out, X, Y, not_12_out);
  and and_6 (and_6_out, not_13_out, W, not_14_out);
  and and_7 (and_7_out, V, not_15_out, not_16_out);
  and and_8 (and_8_out, V, X, not_17_out);
  or or_1 (c, and_1_out, and_2_out, and_3_out, and_4_out, and_5_out, and_6_out, and_7_out, and_8_out);
endmodule

module func_d (
  input  V,
  input  W,
  input  X,
  input  Y,
  input  Z,
  output d
);

  wire and_1_out, and_2_out, and_3_out, and_4_out, and_5_out, and_6_out, not_1_out, not_2_out, not_3_out,
       not_4_out, not_5_out, not_6_out, not_7_out, not_8_out;

  not not_1 (not_1_out, V);
  not not_2 (not_2_out, X);
  not not_3 (not_3_out, Z);
  not not_4 (not_4_out, W);
  not not_5 (not_5_out, Z);
  not not_6 (not_6_out, W);
  not not_7 (not_7_out, X);
  not not_8 (not_8_out, Y);
  and and_1 (and_1_out, not_1_out, not_2_out, Z);
  and and_2 (and_2_out, Y, not_3_out);
  and and_3 (and_3_out, not_4_out, X, not_5_out);
  and and_4 (and_4_out, V, not_6_out, X);
  and and_5 (and_5_out, V, W, not_7_out);
  and and_6 (and_6_out, V, W, not_8_out);
  or or_1 (d, and_1_out, and_2_out, and_3_out, and_4_out, and_5_out, and_6_out);
endmodule

module func_e (
  input  V,
  input  W,
  input  X,
  input  Y,
  input  Z,
  output e
);

  wire and_1_out, and_2_out, and_3_out, and_4_out, and_5_out, and_6_out, not_1_out, not_2_out, not_3_out,
       not_4_out, not_5_out, not_6_out, not_7_out, not_8_out, not_9_out;

  not not_1 (not_1_out, V);
  not not_2 (not_2_out, W);
  not not_3 (not_3_out, X);
  not not_4 (not_4_out, V);
  not not_5 (not_5_out, Y);
  not not_6 (not_6_out, V);
  not not_7 (not_7_out, X);
  not not_8 (not_8_out, Y);
  not not_9 (not_9_out, Z);
  and and_1 (and_1_out, not_1_out, not_2_out, not_3_out);
  and and_2 (and_2_out, not_4_out, Z);
  and and_3 (and_3_out, not_5_out, Z);
  and and_4 (and_4_out, not_6_out, not_7_out, Y);
  and and_5 (and_5_out, X, not_8_out);
  and and_6 (and_6_out, W, X, not_9_out);
  or or_1 (e, and_1_out, and_2_out, and_3_out, and_4_out, and_5_out, and_6_out);
endmodule

module func_f (
  input  V,
  input  W,
  input  X,
  input  Y,
  input  Z,
  output f
);

  wire and_1_out, and_2_out, and_3_out, and_4_out, and_5_out, not_1_out, not_2_out, not_3_out, not_4_out,
       not_5_out, not_6_out, not_7_out, not_8_out;

  not not_1 (not_1_out, V);
  not not_2 (not_2_out, W);
  not not_3 (not_3_out, Y);
  not not_4 (not_4_out, W);
  not not_5 (not_5_out, Z);
  not not_6 (not_6_out, V);
  not not_7 (not_7_out, X);
  not not_8 (not_8_out, Z);
  and and_1 (and_1_out, not_1_out, not_2_out, not_3_out);
  and and_2 (and_2_out, not_4_out, X, not_5_out);
  and and_3 (and_3_out, not_6_out, X, Y, Z);
  and and_4 (and_4_out, W, not_7_out, Y);
  and and_5 (and_5_out, V, not_8_out);
  or or_1 (f, and_1_out, and_2_out, and_3_out, and_4_out, and_5_out);
endmodule

module func_g (
  input  V,
  input  W,
  input  X,
  input  Y,
  input  Z,
  output g
);

  wire and_1_out, and_2_out, and_3_out, and_4_out, and_5_out, not_1_out, not_2_out, not_3_out, not_4_out,
       not_5_out, not_6_out, not_7_out;

  not not_1 (not_1_out, V);
  not not_2 (not_2_out, W);
  not not_3 (not_3_out, V);
  not not_4 (not_4_out, Z);
  not not_5 (not_5_out, W);
  not not_6 (not_6_out, V);
  not not_7 (not_7_out, X);
  and and_1 (and_1_out, not_1_out, not_2_out);
  and and_2 (and_2_out, not_3_out, Y, not_4_out);
  and and_3 (and_3_out, not_5_out, Y, Z);
  and and_4 (and_4_out, not_6_out, X, Z);
  and and_5 (and_5_out, V, not_7_out);
  or or_1 (g, and_1_out, and_2_out, and_3_out, and_4_out, and_5_out);
endmodule

module sevensegA_Z (
  input  V,
  input  W,
  input  X,
  input  Y,
  input  Z,
  output a,
  output b,
  output c,
  output d,
  output e,
  output f,
  output g
);

  func_a fonction_a_1 (.V(V), .W(W), .X(X), .Y(Y), .Z(Z), .a(a));
  func_b fonction_b_1 (.V(V), .W(W), .X(X), .Y(Y), .Z(Z), .b(b));
  func_c fonction_c_1 (.V(V), .W(W), .X(X), .Y(Y), .Z(Z), .c(c));
  func_d fonction_d_1 (.V(V), .W(W), .X(X), .Y(Y), .Z(Z), .d(d));
  func_e fonction_e_1 (.V(V), .W(W), .X(X), .Y(Y), .Z(Z), .e(e));
  func_f fonction_f_1 (.V(V), .W(W), .X(X), .Y(Y), .Z(Z), .f(f));
  func_g fonction_g_1 (.V(V), .W(W), .X(X), .Y(Y), .Z(Z), .g(g));
endmodule

module sevensegBUS (
  input  [5:0] LETTER,
  output [7:0] LETTERCODE
);

  sevensegA_Z sevensega_z_1 (
    .d(LETTERCODE[3]), .b(LETTERCODE[1]), .Z(LETTER[1]), .X(LETTER[3]), .V(LETTER[5]), .W(LETTER[4]),
    .Y(LETTER[2]), .a(LETTERCODE[0]), .c(LETTERCODE[2]), .e(LETTERCODE[4]), .f(LETTERCODE[5]),
    .g(LETTERCODE[6]));

  assign LETTERCODE[7] = LETTER[0];
endmodule

module BUSAFFICHEv2 (
  input  [7:0] in_1
);

  _7_Segment_Display u_7_segment_display_1 (
    .g(in_1[6]), .f(in_1[5]), .a(in_1[0]), .b(in_1[1]), .e(in_1[4]), .d(in_1[3]), .c(in_1[2]), .dp(in_1[7]));
endmodule

module onetoeightv2 (
  input  [5:0] LETTER,
  output a,
  output b,
  output c,
  output d,
  output e,
  output f,
  output g,
  output deci
);

  sevensegBUS sevensegbus_1 (.LETTER(LETTER), .LETTERCODE({deci, g, f, e, d, c, b, a}));
endmodule

module Ecopied (
  input  inp,
  output outp
);

  wire clock_1_out;

  and and_1 (outp, inp, clock_1_out);
  Clock #(.highDuration(20), .lowDuration(19)) clock_1 (.out(clock_1_out));
endmodule
