// Logisim project NumberAffichage.circ as structural Verilog: 12 circuits, main circuit func_a_numb
module func_a_numb (
  input  EN,
  input  W,
  input  X,
  input  Y,
  input  Z,
  output a
);

  wire and_1_out, and_2_out, and_3_out, and_4_out, and_5_out, not_1_out, not_2_out, not_3_out, not_4_out,
       not_5_out, not_6_out, not_7_out, not_8_out;

  not not_1 (not_1_out, X);
  not not_2 (not_2_out, Z);
  not not_3 (not_3_out, W);
  not not_4 (not_4_out, W);
  not not_5 (not_5_out, X);
  not not_6 (not_6_out, Y);
  not not_7 (not_7_out, Y);
  not not_8 (not_8_out, Z);
  and and_1 (and_1_out, EN, not_1_out, not_2_out);
  and and_2 (and_2_out, EN, not_3_out, Y);
  and and_3 (and_3_out, EN, not_4_out, X, Z);
  and and_4 (and_4_out, EN, W, not_5_out, not_6_out);
  and and_5 (and_5_out, EN, W, not_7_out, not_8_out);
  or or_1 (a, and_1_out, and_2_out, and_3_out, and_4_out, and_5_out);
endmodule

module func_b_num (
  input  EN,
  input  W,
  input  X,
  input  Y,
  input  Z,
  output b
);

  wire and_1_out, and_2_out, and_3_out, and_4_out, not_1_out, not_2_out, not_3_out, not_4_out, not_5_out,
       not_6_out, not_7_out, not_8_out;

  not not_1 (not_1_out, W);
  not not_2 (not_2_out, Y);
  not not_3 (not_3_out, Z);
  not not_4 (not_4_out, X);
  not not_5 (not_5_out, Y);
  not not_6 (not_6_out, X);
  not not_7 (not_7_out, Z);
  not not_8 (not_8_out, W);
  and and_1 (and_1_out, EN, not_1_out, not_2_out, not_3_out);
  and and_2 (and_2_out, EN, not_4_out, not_5_out);
  and and_3 (and_3_out, EN, not_6_out, not_7_out);
  and and_4 (and_4_out, EN, not_8_out, Y, Z);
  or or_1 (b, and_1_out, and_2_out, and_3_out, and_4_out);
endmodule

module func_c_numb (
  input  EN,
  input  W,
  input  X,
  input  Y,
  input  Z,
  output c
);

  wire and_1_out, and_2_out, and_3_out, and_4_out, not_1_out, not_2_out, not_3_out, not_4_out, not_5_out;

  not not_1 (not_1_out, W);
  not not_2 (not_2_out, Y);
  not not_3 (not_3_out, W);
  not not_4 (not_4_out, W);
  not not_5 (not_5_out, X);
  and and_1 (and_1_out, EN, not_1_out, not_2_out);
  and and_2 (and_2_out, EN, not_3_out, Z);
  and and_3 (and_3_out, EN, not_4_out, X);
  and and_4 (and_4_out, EN, W, not_5_out);
  or or_1 (c, and_1_out, and_2_out, and_3_out, and_4_out);
endmodule

module func_d_numb (
  input  EN,
  input  W,
  input  X,
  input  Y,
  input  Z,
  output d
);

  wire and_1_out, and_2_out, and_3_out, and_4_out, and_5_out, and_6_out, not_1_out, not_2_out, not_3_out,
       not_4_out, not_5_out, not_6_out, not_7_out, not_8_out, not_9_out, not_10_out, not_11_out, not_12_out;

  not not_1 (not_1_out, W);
  not not_2 (not_2_out, X);
  not not_3 (not_3_out, Z);
  not not_4 (not_4_out, W);
  not not_5 (not_5_out, X);
  not not_6 (not_6_out, W);
  not not_7 (not_7_out, Z);
  not not_8 (not_8_out, W);
  not not_9 (not_9_out, Y);
  not not_10 (not_10_out, Y);
  not not_11 (not_11_out, Z);
  not not_12 (not_12_out, X);
  and and_1 (and_1_out, EN, not_1_out, not_2_out, not_3_out);
  and and_2 (and_2_out, EN, not_4_out, not_5_out, Y);
  and and_3 (and_3_out, EN, not_6_out, Y, not_7_out);
  and and_4 (and_4_out, EN, not_8_out, X, not_9_out, Z);
  and and_5 (and_5_out, EN, W, not_10_out, not_11_out);
  and and_6 (and_6_out, EN, W, not_12_out, Z);
  or or_1 (d, and_1_out, and_2_out, and_3_out, and_4_out, and_5_out, and_6_out);
endmodule

module func_e_numb (
  input  EN,
  input  W,
  input  X,
  input  Y,
  input  Z,
  output e
);

  wire and_1_out, and_2_out, and_3_out, and_4_out, not_1_out, not_2_out, not_3_out, not_4_out, not_5_out,
       not_6_out;

  not not_1 (not_1_out, X);
  not not_2 (not_2_out, Z);
  not not_3 (not_3_out, W);
  not not_4 (not_4_out, Z);
  not not_5 (not_5_out, X);
  not not_6 (not_6_out, Y);
  and and_1 (and_1_out, EN, not_1_out, not_2_out);
  and and_2 (and_2_out, EN, not_3_out, Y, not_4_out);
  and and_3 (and_3_out, EN, W, not_5_out, Y);
  and and_4 (and_4_out, EN, W, X, not_6_out);
  or or_1 (e, and_1_out, and_2_out, and_3_out, and_4_out);
endmodule

module func_f_numb (
  input  EN,
  input  W,
  input  X,
  input  Y,
  input  Z,
  output f
);

  wire and_1_out, and_2_out, and_3_out, and_4_out, not_1_out, not_2_out, not_3_out, not_4_out, not_5_out,
       not_6_out, not_7_out;

  not not_1 (not_1_out, Y);
  not not_2 (not_2_out, Z);
  not not_3 (not_3_out, W);
  not not_4 (not_4_out, Y);
  not not_5 (not_5_out, W);
  not not_6 (not_6_out, Z);
  not not_7 (not_7_out, X);
  and and_1 (and_1_out, EN, not_1_out, not_2_out);
  and and_2 (and_2_out, EN, not_3_out, X, not_4_out);
  and and_3 (and_3_out, EN, not_5_out, X, not_6_out);
  and and_4 (and_4_out, EN, W, not_7_out);
  or or_1 (f, and_1_out, and_2_out, and_3_out, and_4_out);
endmodule

module func_g_numb (
  input  EN,
  input  W,
  input  X,
  input  Y,
  input  Z,
  output g
);

  wire and_1_out, and_2_out, and_3_out, and_4_out, and_5_out, not_1_out, not_2_out, not_3_out, not_4_out,
       not_5_out, not_6_out;

  not not_1 (not_1_out, X);
  not not_2 (not_2_out, Z);
  not not_3 (not_3_out, W);
  not not_4 (not_4_out, Y);
  not not_5 (not_5_out, X);
  not not_6 (not_6_out, Y);
  and and_1 (and_1_out, EN, not_1_out, Y);
  and and_2 (and_2_out, EN, Y, not_2_out);
  and and_3 (and_3_out, EN, not_3_out, X, not_4_out);
  and and_4 (and_4_out, EN, W, not_5_out);
  and and_5 (and_5_out, EN, W, not_6_out, Z);
  or or_1 (g, and_1_out, and_2_out, and_3_out, and_4_out, and_5_out);
endmodule

module affiche_0_9 (
  input  [3:0] number,
  input  EN,
  output a,
  output b,
  output c,
  output d,
  output e,
  output f,
  output g
);

  func_a_numb func_a_numb_1 (.EN(EN), .W(number[3]), .X(number[2]), .Y(number[1]), .Z(number[0]), .a(a));
  func_b_num func_b_num_1 (.EN(EN), .W(number[3]), .X(number[2]), .Y(number[1]), .Z(number[0]), .b(b));
  func_c_numb func_c_numb_1 (.EN(EN), .W(number[3]), .X(number[2]), .Y(number[1]), .Z(number[0]), .c(c));
  func_d_numb func_d_numb_1 (.EN(EN), .W(number[3]), .X(number[2]), .Y(number[1]), .Z(number[0]), .d(d));
  func_e_numb func_e_numb_1 (.EN(EN), .W(number[3]), .X(number[2]), .Y(number[1]), .Z(number[0]), .e(e));
  func_f_numb func_f_numb_1 (.EN(EN), .W(number[3]), .X(number[2]), .Y(number[1]), .Z(number[0]), .f(f));
  func_g_numb func_g_numb_1 (.EN(EN), .W(number[3]), .X(number[2]), .Y(number[1]), .Z(number[0]), .g(g));
endmodule

module numb_4_to_7 (
  input  [3:0] NUMBER,
  input  EN,
  output [6:0] NUMBOUT
);

  affiche_0_9 affiche_0_9_1 (
    .number(NUMBER), .EN(EN), .a(NUMBOUT[0]), .b(NUMBOUT[1]), .c(NUMBOUT[2]), .d(NUMBOUT[3]), .e(NUMBOUT[4]),
    .f(NUMBOUT[5]), .g(NUMBOUT[6]));
endmodule

module numb_4_to_8 (
  input  [3:0] NUMB,
  input  EN,
  output [7:0] numbout
);

  numb_4_to_7 numb_4_to_7_1 (.NUMBER(NUMB), .EN(EN), .NUMBOUT(numbout[6:0]));

  assign numbout[7] = 1'b0;
endmodule

module numb_7_to_8 (
  input  [6:0] NUMBIN,
  output [7:0] NUMBOUT
);


  assign NUMBOUT = {1'b0, NUMBIN};
endmodule

module numbafftester (
  input  [3:0] in_1
);

  wire affiche_0_9_1_a, affiche_0_9_1_b, affiche_0_9_1_c, affiche_0_9_1_d, affiche_0_9_1_e, affiche_0_9_1_f,
       affiche_0_9_1_g;

  affiche_0_9 affiche_0_9_1 (
    .number(in_1), .EN(1'b1), .a(affiche_0_9_1_a), .b(affiche_0_9_1_b), .c(affiche_0_9_1_c),
    .d(affiche_0_9_1_d), .e(affiche_0_9_1_e), .f(affiche_0_9_1_f), .g(affiche_0_9_1_g));
  _7_Segment_Display u_7_segment_display_1 (
    .g(affiche_0_9_1_g), .f(affiche_0_9_1_f), .a(affiche_0_9_1_a), .b(affiche_0_9_1_b), .e(affiche_0_9_1_e),
    .d(affiche_0_9_1_d), .c(affiche_0_9_1_c));  // open: dp
endmodule
