// Logisim project Timer.circ as structural Verilog: 6 circuits, main circuit STATESTIMER
module STATESTIMER (
  input  MAX,
  input  COUNT,
  input  P3,
  input  P2,
  input  P1,
  input  P0,
  output P3OUT,
  output P2OUT,
  output P1OUT,
  output P0OUT,
  output OVERFLOW
);

  wire and_1_out, and_2_out, and_3_out, and_4_out, and_5_out, and_6_out, and_7_out, and_8_out, and_9_out,
       and_10_out, and_11_out, and_12_out, and_13_out, and_14_out, and_15_out, and_16_out, and_17_out,
       and_18_out, and_19_out, and_20_out, and_21_out, not_1_out, not_2_out, not_3_out, not_4_out, not_5_out,
       not_6_out, not_7_out, not_8_out, not_9_out, not_10_out, not_11_out, not_12_out, not_13_out,
       not_14_out, not_15_out, not_16_out, not_17_out, not_18_out, not_19_out, not_20_out, not_21_out,
       not_22_out, not_23_out, not_24_out, not_25_out, not_26_out, not_27_out, not_28_out, not_29_out,
       not_30_out, not_31_out, not_32_out, not_33_out, not_34_out;

  not not_1 (not_1_out, COUNT);
  not not_2 (not_2_out, P2);
  not not_3 (not_3_out, P1);
  not not_4 (not_4_out, MAX);
  not not_5 (not_5_out, P3);
  not not_6 (not_6_out, P2);
  not not_7 (not_7_out, P1);
  not not_8 (not_8_out, P0);
  not not_9 (not_9_out, COUNT);
  not not_10 (not_10_out, COUNT);
  not not_11 (not_11_out, P3);
  not not_12 (not_12_out, P0);
  not not_13 (not_13_out, COUNT);
  not not_14 (not_14_out, COUNT);
  not not_15 (not_15_out, P3);
  not not_16 (not_16_out, P1);
  not not_17 (not_17_out, P0);
  not not_18 (not_18_out, P0);
  not not_19 (not_19_out, COUNT);
  not not_20 (not_20_out, COUNT);
  not not_21 (not_21_out, P3);
  not not_22 (not_22_out, COUNT);
  not not_23 (not_23_out, P2);
  not not_24 (not_24_out, P1);
  not not_25 (not_25_out, MAX);
  not not_26 (not_26_out, P0);
  not not_27 (not_27_out, P0);
  not not_28 (not_28_out, P0);
  not not_29 (not_29_out, P0);
  not not_30 (not_30_out, COUNT);
  not not_31 (not_31_out, P3);
  not not_32 (not_32_out, P2);
  not not_33 (not_33_out, P1);
  not not_34 (not_34_out, P0);
  and and_1 (and_1_out, not_1_out, P3, not_2_out, not_3_out);
  and and_2 (and_2_out, P3, P0);
  and and_3 (and_3_out, not_4_out, COUNT, not_5_out, not_6_out, not_7_out, not_8_out);
  and and_4 (and_4_out, MAX, not_9_out, P3);
  and and_5 (and_5_out, not_10_out, not_11_out, P2);
  and and_6 (and_6_out, P2, P0);
  and and_7 (and_7_out, P2, P1);
  and and_8 (and_8_out, COUNT, P3, not_12_out);
  and and_9 (and_9_out, MAX, not_13_out, P2);
  and and_10 (and_10_out, not_14_out, not_15_out, P1);
  and and_11 (and_11_out, P1, P0);
  and and_12 (and_12_out, COUNT, P2, not_16_out, not_17_out);
  and and_13 (and_13_out, COUNT, P3, not_18_out);
  and and_14 (and_14_out, MAX, not_19_out, P1);
  and and_15 (and_15_out, not_20_out, not_21_out, P0);
  and and_16 (and_16_out, not_22_out, not_23_out, not_24_out, P0);
  and and_17 (and_17_out, not_25_out, COUNT, not_26_out);
  and and_18 (and_18_out, COUNT, P1, not_27_out);
  and and_19 (and_19_out, COUNT, P2, not_28_out);
  and and_20 (and_20_out, COUNT, P3, not_29_out);
  and and_21 (and_21_out, MAX, not_30_out, P0);
  and and_22 (OVERFLOW, not_31_out, not_32_out, not_33_out, not_34_out);
  or or_1 (P3OUT, and_1_out, and_2_out, and_3_out, and_4_out);
  or or_2 (P2OUT, and_5_out, and_6_out, and_7_out, and_8_out, and_9_out);
  or or_3 (P1OUT, and_10_out, and_11_out, and_12_out, and_13_out, and_14_out);
  or or_4 (P0OUT, and_15_out, and_16_out, and_17_out, and_18_out, and_19_out, and_20_out, and_21_out);
endmodule

module FSMTIMER (
  input  MAX,
  input  COUNT,
  input  LONGPRESS,
  input  [3:0] NUMB,
  output P3,
  output P2,
  output P1,
  output P0,
  output OVERFLOW
);

  wire and_1_out, clock_1_out, d_ff_1_q, d_ff_2_q, d_ff_3_q, d_ff_4_q, STATESTIMER_1_p0out,
       STATESTIMER_1_p1out, STATESTIMER_1_p2out, STATESTIMER_1_p3out;

  and and_1 (and_1_out, COUNT, LONGPRESS);
  STATESTIMER STATESTIMER_1 (
    .MAX(MAX), .COUNT(and_1_out), .P3(P3), .P2(P2), .P1(P1), .P0(P0), .P3OUT(STATESTIMER_1_p3out),
    .P2OUT(STATESTIMER_1_p2out), .P1OUT(STATESTIMER_1_p1out), .P0OUT(STATESTIMER_1_p0out), .OVERFLOW(OVERFLOW));
  Clock #(.highDuration(320), .lowDuration(320)) clock_1 (.out(clock_1_out));
  D_Flip_Flop d_ff_1 (.D(STATESTIMER_1_p3out), .clk(clock_1_out), .Q(d_ff_1_q));  // open: Qn, preset, reset
  D_Flip_Flop d_ff_2 (.D(STATESTIMER_1_p2out), .clk(clock_1_out), .Q(d_ff_2_q));  // open: Qn, preset, reset
  D_Flip_Flop d_ff_3 (.D(STATESTIMER_1_p1out), .clk(clock_1_out), .Q(d_ff_3_q));  // open: Qn, preset, reset
  D_Flip_Flop d_ff_4 (.D(STATESTIMER_1_p0out), .clk(clock_1_out), .Q(d_ff_4_q));  // open: Qn, preset, reset
  Multiplexer #(.enable("false")) multiplexer_1 (.in0(NUMB[3]), .in1(d_ff_1_q), .out(P3), .sel(LONGPRESS));
  Multiplexer #(.enable("false")) multiplexer_2 (.in0(NUMB[2]), .in1(d_ff_2_q), .out(P2), .sel(LONGPRESS));
  Multiplexer #(.enable("false")) multiplexer_3 (.in0(NUMB[1]), .in1(d_ff_3_q), .out(P1), .sel(LONGPRESS));
  Multiplexer #(.enable("false")) multiplexer_4 (.in0(NUMB[0]), .in1(d_ff_4_q), .out(P0), .sel(LONGPRESS));
endmodule

module timer (
  input  COUNT,
  input  TIMERSET,
  input  [3:0] NUMB1,
  input  [3:0] NUMB2,
  input  [3:0] NUMB3,
  input  [3:0] NUMB4,
  input  [3:0] NUMB5,
  input  [3:0] NUMB6,
  output [3:0] lowms,
  output [3:0] hims,
  output [3:0] lowsec,
  output [3:0] hisec,
  output [3:0] lowmin,
  output [3:0] himin,
  output TIMERDONE
);

  wire and_1_out, and_2_out, and_3_out, and_4_out, and_5_out, and_6_out, and_7_out, and_8_out, and_9_out,
       and_10_out, and_11_out, and_12_out, and_13_out, and_14_out, minhi_overflow, minlow_overflow,
       mshi_overflow, mslow_overflow, sechi_overflow, seclow_overflow;

  and and_1 (and_1_out, mslow_overflow, mshi_overflow);
  and and_2 (and_2_out, and_1_out, seclow_overflow);
  and and_3 (and_3_out, and_2_out, sechi_overflow);
  and and_4 (and_4_out, and_3_out, minlow_overflow);
  and and_5 (and_5_out, COUNT, mslow_overflow);
  and and_6 (and_6_out, COUNT, and_1_out);
  and and_7 (and_7_out, and_14_out, sechi_overflow);
  and and_8 (and_8_out, COUNT, and_2_out);
  and and_9 (and_9_out, and_3_out, COUNT);
  and and_10 (and_10_out, 1'b1, minhi_overflow);
  and and_11 (and_11_out, and_4_out, COUNT);
  and and_12 (and_12_out, mshi_overflow, and_13_out);
  and and_13 (and_13_out, and_7_out, seclow_overflow);
  and and_14 (and_14_out, and_10_out, minlow_overflow);
  FSMTIMER mslow (
    .MAX(and_12_out), .COUNT(COUNT), .LONGPRESS(TIMERSET), .NUMB(NUMB1), .P3(lowms[3]), .P2(lowms[2]),
    .P1(lowms[1]), .P0(lowms[0]), .OVERFLOW(mslow_overflow));
  FSMTIMER mshi (
    .MAX(and_13_out), .COUNT(and_5_out), .LONGPRESS(TIMERSET), .NUMB(NUMB2), .P3(hims[3]), .P2(hims[2]),
    .P1(hims[1]), .P0(hims[0]), .OVERFLOW(mshi_overflow));
  FSMTIMER seclow (
    .MAX(and_7_out), .COUNT(and_6_out), .LONGPRESS(TIMERSET), .NUMB(NUMB3), .P3(lowsec[3]), .P2(lowsec[2]),
    .P1(lowsec[1]), .P0(lowsec[0]), .OVERFLOW(seclow_overflow));
  FSMTIMERSECHI sechi (
    .MAX(and_14_out), .COUNT(and_8_out), .LONGPRESS(TIMERSET), .Input_bus_1(NUMB4), .P3(hisec[3]),
    .P2(hisec[2]), .P1(hisec[1]), .P0(hisec[0]), .OVERFLOW(sechi_overflow));
  FSMTIMER minlow (
    .MAX(and_10_out), .COUNT(and_9_out), .LONGPRESS(TIMERSET), .NUMB(NUMB5), .P3(lowmin[3]), .P2(lowmin[2]),
    .P1(lowmin[1]), .P0(lowmin[0]), .OVERFLOW(minlow_overflow));
  FSMTIMER minhi (
    .MAX(1'b1), .COUNT(and_11_out), .LONGPRESS(TIMERSET), .NUMB(NUMB6), .P3(himin[3]), .P2(himin[2]),
    .P1(himin[1]), .P0(himin[0]), .OVERFLOW(minhi_overflow));
  and and_15 (TIMERDONE, COUNT, mslow_overflow, mshi_overflow, seclow_overflow, sechi_overflow, minlow_overflow, minhi_overflow);
endmodule

module FSMTIMERSECHI (
  input  MAX,
  input  COUNT,
  input  LONGPRESS,
  input  [3:0] Input_bus_1,
  output P3,
  output P2,
  output P1,
  output P0,
  output OVERFLOW
);

  wire clock_1_out, d_ff_1_q, d_ff_2_q, d_ff_3_q, d_ff_4_q, STATESSECHI_1_p0out, STATESSECHI_1_p1out,
       STATESSECHI_1_p2out, STATESSECHI_1_p3out;

  STATESSECHI STATESSECHI_1 (
    .MAX(MAX), .COUNT(COUNT), .P3(P3), .P2(P2), .P1(P1), .P0(P0), .P3OUT(STATESSECHI_1_p3out),
    .P2OUT(STATESSECHI_1_p2out), .P1OUT(STATESSECHI_1_p1out), .P0OUT(STATESSECHI_1_p0out), .OVERFLOW(OVERFLOW));
  Clock #(.highDuration(320), .lowDuration(320)) clock_1 (.out(clock_1_out));
  D_Flip_Flop d_ff_1 (.D(STATESSECHI_1_p3out), .clk(clock_1_out), .Q(d_ff_1_q));  // open: Qn, preset, reset
  D_Flip_Flop d_ff_2 (.D(STATESSECHI_1_p2out), .clk(clock_1_out), .Q(d_ff_2_q));  // open: Qn, preset, reset
  D_Flip_Flop d_ff_3 (.D(STATESSECHI_1_p1out), .clk(clock_1_out), .Q(d_ff_3_q));  // open: Qn, preset, reset
  D_Flip_Flop d_ff_4 (.D(STATESSECHI_1_p0out), .clk(clock_1_out), .Q(d_ff_4_q));  // open: Qn, preset, reset
  Multiplexer #(.enable("false")) multiplexer_1 (.in0(Input_bus_1[3]), .in1(d_ff_1_q), .out(P3), .sel(LONGPRESS));
  Multiplexer #(.enable("false")) multiplexer_2 (.in0(Input_bus_1[2]), .in1(d_ff_2_q), .out(P2), .sel(LONGPRESS));
  Multiplexer #(.enable("false")) multiplexer_3 (.in0(Input_bus_1[1]), .in1(d_ff_3_q), .out(P1), .sel(LONGPRESS));
  Multiplexer #(.enable("false")) multiplexer_4 (.in0(Input_bus_1[0]), .in1(d_ff_4_q), .out(P0), .sel(LONGPRESS));
endmodule

module STATESSECHI (
  input  MAX,
  input  COUNT,
  input  P3,
  input  P2,
  input  P1,
  input  P0,
  output P3OUT,
  output P2OUT,
  output P1OUT,
  output P0OUT,
  output OVERFLOW
);

  wire and_1_out, and_2_out, and_3_out, and_4_out, and_5_out, and_6_out, and_7_out, and_8_out, and_9_out,
       and_10_out, and_11_out, and_12_out, and_13_out, and_14_out, and_15_out, and_16_out, and_17_out,
       and_18_out, and_19_out, and_20_out, and_21_out, not_1_out, not_2_out, not_3_out, not_4_out, not_5_out,
       not_6_out, not_7_out, not_8_out, not_9_out, not_10_out, not_11_out, not_12_out, not_13_out,
       not_14_out, not_15_out, not_16_out, not_17_out, not_18_out, not_19_out, not_20_out, not_21_out,
       not_22_out, not_23_out, not_24_out, not_25_out, not_26_out, not_27_out, not_28_out, not_29_out,
       not_30_out, not_31_out, not_32_out, not_33_out;

  not not_1 (not_1_out, COUNT);
  not not_2 (not_2_out, P2);
  not not_3 (not_3_out, P1);
  not not_4 (not_4_out, COUNT);
  not not_5 (not_5_out, COUNT);
  not not_6 (not_6_out, P3);
  not not_7 (not_7_out, MAX);
  not not_8 (not_8_out, P2);
  not not_9 (not_9_out, P1);
  not not_10 (not_10_out, P0);
  not not_11 (not_11_out, P0);
  not not_12 (not_12_out, COUNT);
  not not_13 (not_13_out, COUNT);
  not not_14 (not_14_out, P3);
  not not_15 (not_15_out, P1);
  not not_16 (not_16_out, P0);
  not not_17 (not_17_out, P0);
  not not_18 (not_18_out, COUNT);
  not not_19 (not_19_out, COUNT);
  not not_20 (not_20_out, P3);
  not not_21 (not_21_out, COUNT);
  not not_22 (not_22_out, P2);
  not not_23 (not_23_out, P1);
  not not_24 (not_24_out, MAX);
  not not_25 (not_25_out, P0);
  not not_26 (not_26_out, P0);
  not not_27 (not_27_out, P0);
  not not_28 (not_28_out, P0);
  not not_29 (not_29_out, COUNT);
  not not_30 (not_30_out, P3);
  not not_31 (not_31_out, P2);
  not not_32 (not_32_out, P1);
  not not_33 (not_33_out, P0);
  and and_1 (and_1_out, not_1_out, P3, not_2_out, not_3_out);
  and and_2 (and_2_out, P3, P0);
  and and_3 (and_3_out, MAX, not_4_out, P3);
  and and_4 (and_4_out, not_5_out, not_6_out, P2);
  and and_5 (and_5_out, P2, P0);
  and and_6 (and_6_out, P2, P1);
  and and_7 (and_7_out, not_7_out, COUNT, not_8_out, not_9_out, not_10_out);
  and and_8 (and_8_out, COUNT, P3, not_11_out);
  and and_9 (and_9_out, MAX, not_12_out, P2);
  and and_10 (and_10_out, not_13_out, not_14_out, P1);
  and and_11 (and_11_out, P1, P0);
  and and_12 (and_12_out, COUNT, P2, not_15_out, not_16_out);
  and and_13 (and_13_out, COUNT, P3, not_17_out);
  and and_14 (and_14_out, MAX, not_18_out, P1);
  and and_15 (and_15_out, not_19_out, not_20_out, P0);
  and and_16 (and_16_out, not_21_out, not_22_out, not_23_out, P0);
  and and_17 (and_17_out, not_24_out, COUNT, not_25_out);
  and and_18 (and_18_out, COUNT, P1, not_26_out);
  and and_19 (and_19_out, COUNT, P2, not_27_out);
  and and_20 (and_20_out, COUNT, P3, not_28_out);
  and and_21 (and_21_out, MAX, not_29_out, P0);
  and and_22 (OVERFLOW, not_30_out, not_31_out, not_32_out, not_33_out);
  or or_1 (P3OUT, and_1_out, and_2_out, and_3_out);
  or or_2 (P2OUT, and_4_out, and_5_out, and_6_out, and_7_out, and_8_out, and_9_out);
  or or_3 (P1OUT, and_10_out, and_11_out, and_12_out, and_13_out, and_14_out);
  or or_4 (P0OUT, and_15_out, and_16_out, and_17_out, and_18_out, and_19_out, and_20_out, and_21_out);
endmodule

module timerstates (
  input  B,
  input  START,
  output STARTOUT,
  output STOPOUT
);

  wire not_1_out;

  not not_1 (not_1_out, START);
  and and_1 (STOPOUT, B, START);
  and and_2 (STARTOUT, B, not_1_out);
endmodule
