// Logisim project calculate_finalv2.circ as structural Verilog
module fullCalculator (
  input  [3:0] FIRST2,
  input  [3:0] FIRST1,
  input  [3:0] FIRST0,
  input  [3:0] SECOND2,
  input  [3:0] SECOND1,
  input  [3:0] SECOND0,
  input  cycleop,
  input  firstNeg,
  input  secondNeg,
  output [3:0] number0,
  output [3:0] number1,
  output [3:0] number2,
  output negativeR
);

  wire a_minus_b_uf;
  wire [1:0] select_op_1_op;
  wire [2:0] neg_result_1_output_bus_1;
  wire [3:0] change8_4_1_digit0, change8_4_1_digit1, change8_4_1_digit2, change24_4_1_numb, change24_4_2_numb;
  wire [7:0] a_dividedBy_b_rest, a_minus_b_ao, a_plus_b_ao, a_times_b_multr, b_minus_a_ao, change34_8_1_numb,
       change34_8_2_numb, multiplexer_1_out;

  select_op select_op_1 (.cycleop(cycleop), .P(select_op_1_op), .op(select_op_1_op));
  change34_8 change34_8_1 (.dig2(FIRST2), .dig1(FIRST1), .dig0(FIRST0), .numb(change34_8_1_numb));
  change34_8 change34_8_2 (.dig2(SECOND2), .dig1(SECOND1), .dig0(SECOND0), .numb(change34_8_2_numb));
  change24_4 change24_4_1 (.first1(FIRST1), .first0(FIRST0), .numb(change24_4_1_numb));
  change24_4 change24_4_2 (.first1(SECOND1), .first0(SECOND0), .numb(change24_4_2_numb));
  addsub8bit a_plus_b (.minus(1'b0), .aIA(change34_8_1_numb), .aIB(change34_8_2_numb), .AO(a_plus_b_ao));  // open: UF
  addsub8bit a_minus_b (
    .minus(1'b1), .aIA(change34_8_1_numb), .aIB(change34_8_2_numb), .AO(a_minus_b_ao), .UF(a_minus_b_uf));
  addsub8bit b_minus_a (.minus(1'b1), .aIA(change34_8_2_numb), .aIB(change34_8_1_numb), .AO(b_minus_a_ao));  // open: UF
  multi4bit a_times_b (.A(change24_4_1_numb), .B(change24_4_2_numb), .multR(a_times_b_multr));
  divis4bit a_dividedBy_b (
    .denomB(change24_4_2_numb), .nomA(change24_4_1_numb), .Q(a_dividedBy_b_rest[3:0]),
    .rest(a_dividedBy_b_rest[7:4]));
  neg_result neg_result_1 (
    .a_bUF(a_minus_b_uf), .op1(select_op_1_op[1]), .op0(select_op_1_op[0]), .fneg(firstNeg),
    .sneg(secondNeg), .rneg(negativeR), .Output_bus_1(neg_result_1_output_bus_1));
  Multiplexer #(.select(3), .width(8), .enable("false")) multiplexer_1 (
    .in0(a_plus_b_ao), .in1(a_minus_b_ao), .in2(a_times_b_multr), .in3(a_dividedBy_b_rest),
    .in4(b_minus_a_ao), .in5(8'hdd), .in6(8'hdd), .in7(8'hdd), .out(multiplexer_1_out),
    .sel(neg_result_1_output_bus_1));
  change8_4 change8_4_1 (
    .S(multiplexer_1_out), .digit0(change8_4_1_digit0), .digit1(change8_4_1_digit1),
    .digit2(change8_4_1_digit2));
  Multiplexer #(.select(2), .width(12), .enable("false")) multiplexer_2 (
    .in0({change8_4_1_digit2, change8_4_1_digit1, change8_4_1_digit0}),
    .in1({change8_4_1_digit2, change8_4_1_digit1, change8_4_1_digit0}),
    .in2({change8_4_1_digit2, change8_4_1_digit1, change8_4_1_digit0}),
    .in3({a_dividedBy_b_rest[3:0], 4'b1101, a_dividedBy_b_rest[7:4]}), .out({number2, number1, number0}),
    .sel(select_op_1_op));
endmodule

module fullAdder (
  input  cIn,
  input  Ia,
  input  Ib,
  output S,
  output cOut
);

  wire and_1_out, and_2_out, or_1_out, xor_1_out;

  xor xor_1 (xor_1_out, Ia, Ib);
  or or_1 (or_1_out, Ia, Ib);
  and and_1 (and_1_out, Ia, Ib);
  xor xor_2 (S, xor_1_out, cIn);
  and and_2 (and_2_out, or_1_out, cIn);
  or or_2 (cOut, and_1_out, and_2_out);
endmodule

module addsub8bit (
  input  minus,
  input  [7:0] aIA,
  input  [7:0] aIB,
  output [7:0] AO,
  output UF
);

  wire fullAdder_1_cout, fullAdder_2_cout, fullAdder_3_cout, fullAdder_4_cout, fullAdder_5_cout,
       fullAdder_6_cout, fullAdder_7_cout, fullAdder_8_cout, xor_1_out, xor_2_out, xor_3_out, xor_4_out,
       xor_5_out, xor_6_out, xor_7_out, xor_8_out;

  xor xor_1 (xor_1_out, aIB[0], minus);
  xor xor_2 (xor_2_out, aIB[1], minus);
  xor xor_3 (xor_3_out, aIB[2], minus);
  xor xor_4 (xor_4_out, aIB[3], minus);
  xor xor_5 (xor_5_out, aIB[4], minus);
  xor xor_6 (xor_6_out, aIB[5], minus);
  xor xor_7 (xor_7_out, aIB[6], minus);
  xor xor_8 (xor_8_out, aIB[7], minus);
  fullAdder fullAdder_1 (.cIn(minus), .Ia(aIA[0]), .Ib(xor_1_out), .S(AO[0]), .cOut(fullAdder_1_cout));
  fullAdder fullAdder_2 (.cIn(fullAdder_1_cout), .Ia(aIA[1]), .Ib(xor_2_out), .S(AO[1]), .cOut(fullAdder_2_cout));
  fullAdder fullAdder_3 (.cIn(fullAdder_2_cout), .Ia(aIA[2]), .Ib(xor_3_out), .S(AO[2]), .cOut(fullAdder_3_cout));
  fullAdder fullAdder_4 (.cIn(fullAdder_3_cout), .Ia(aIA[3]), .Ib(xor_4_out), .S(AO[3]), .cOut(fullAdder_4_cout));
  fullAdder fullAdder_5 (.cIn(fullAdder_4_cout), .Ia(aIA[4]), .Ib(xor_5_out), .S(AO[4]), .cOut(fullAdder_5_cout));
  fullAdder fullAdder_6 (.cIn(fullAdder_5_cout), .Ia(aIA[5]), .Ib(xor_6_out), .S(AO[5]), .cOut(fullAdder_6_cout));
  fullAdder fullAdder_7 (.cIn(fullAdder_6_cout), .Ia(aIA[6]), .Ib(xor_7_out), .S(AO[6]), .cOut(fullAdder_7_cout));
  fullAdder fullAdder_8 (.cIn(fullAdder_7_cout), .Ia(aIA[7]), .Ib(xor_8_out), .S(AO[7]), .cOut(fullAdder_8_cout));
  not not_1 (UF, fullAdder_8_cout);
endmodule

module sousMUX (
  input  BI,
  input  D,
  input  S,
  input  N,
  output BO,
  output R
);

  wire and_1_out, and_2_out, and_3_out, and_4_out, and_5_out, and_6_out, and_7_out, not_1_out, not_2_out,
       not_3_out, not_4_out, not_5_out, not_6_out, not_7_out, not_8_out, or_2_out;

  not not_1 (not_1_out, D);
  not not_2 (not_2_out, D);
  not not_3 (not_3_out, D);
  not not_4 (not_4_out, S);
  not not_5 (not_5_out, D);
  not not_6 (not_6_out, BI);
  not not_7 (not_7_out, S);
  not not_8 (not_8_out, BI);
  and and_1 (and_1_out, not_1_out, BI);
  and and_2 (and_2_out, not_2_out, S);
  and and_3 (and_3_out, S, BI);
  and and_4 (and_4_out, not_3_out, not_4_out, BI);
  and and_5 (and_5_out, not_5_out, S, not_6_out);
  and and_6 (and_6_out, D, not_7_out, not_8_out);
  and and_7 (and_7_out, D, S, BI);
  or or_1 (BO, and_1_out, and_2_out, and_3_out);
  or or_2 (or_2_out, and_4_out, and_5_out, and_6_out, and_7_out);
  Multiplexer #(.enable("false")) multiplexer_1 (.in0(or_2_out), .in1(D), .out(R), .sel(N));
endmodule

module divis4bit (
  input  [3:0] denomB,
  input  [3:0] nomA,
  output [3:0] Q,
  output [3:0] rest
);

  wire sousMUX_1_bo, sousMUX_1_r, sousMUX_2_bo, sousMUX_2_r, sousMUX_3_bo, sousMUX_3_r, sousMUX_4_bo,
       sousMUX_4_r, sousMUX_5_bo, sousMUX_5_r, sousMUX_6_bo, sousMUX_7_bo, sousMUX_7_r, sousMUX_8_bo,
       sousMUX_8_r, sousMUX_9_bo, sousMUX_9_r, sousMUX_10_bo, sousMUX_10_r, sousMUX_11_bo, sousMUX_12_bo,
       sousMUX_12_r, sousMUX_13_bo, sousMUX_13_r, sousMUX_14_bo, sousMUX_14_r, sousMUX_15_bo, sousMUX_15_r,
       sousMUX_16_bo, sousMUX_17_bo, sousMUX_18_bo, sousMUX_19_bo, sousMUX_20_bo, sousMUX_21_bo;

  sousMUX sousMUX_17 (.BI(1'b0), .D(nomA[0]), .S(denomB[0]), .N(sousMUX_21_bo), .BO(sousMUX_17_bo), .R(rest[0]));
  sousMUX sousMUX_12 (.BI(1'b0), .D(nomA[1]), .S(denomB[0]), .N(sousMUX_16_bo), .BO(sousMUX_12_bo), .R(sousMUX_12_r));
  sousMUX sousMUX_18 (
    .BI(sousMUX_17_bo), .D(sousMUX_12_r), .S(denomB[1]), .N(sousMUX_21_bo), .BO(sousMUX_18_bo), .R(rest[1]));
  sousMUX sousMUX_7 (.BI(1'b0), .D(nomA[2]), .S(denomB[0]), .N(sousMUX_11_bo), .BO(sousMUX_7_bo), .R(sousMUX_7_r));
  sousMUX sousMUX_13 (
    .BI(sousMUX_12_bo), .D(sousMUX_7_r), .S(denomB[1]), .N(sousMUX_16_bo), .BO(sousMUX_13_bo),
    .R(sousMUX_13_r));
  sousMUX sousMUX_19 (
    .BI(sousMUX_18_bo), .D(sousMUX_13_r), .S(denomB[2]), .N(sousMUX_21_bo), .BO(sousMUX_19_bo), .R(rest[2]));
  sousMUX sousMUX_2 (.BI(1'b0), .D(nomA[3]), .S(denomB[0]), .N(sousMUX_6_bo), .BO(sousMUX_2_bo), .R(sousMUX_2_r));
  sousMUX sousMUX_8 (
    .BI(sousMUX_7_bo), .D(sousMUX_2_r), .S(denomB[1]), .N(sousMUX_11_bo), .BO(sousMUX_8_bo), .R(sousMUX_8_r));
  sousMUX sousMUX_14 (
    .BI(sousMUX_13_bo), .D(sousMUX_8_r), .S(denomB[2]), .N(sousMUX_16_bo), .BO(sousMUX_14_bo),
    .R(sousMUX_14_r));
  sousMUX sousMUX_20 (
    .BI(sousMUX_19_bo), .D(sousMUX_14_r), .S(denomB[3]), .N(sousMUX_21_bo), .BO(sousMUX_20_bo), .R(rest[3]));
  sousMUX sousMUX_1 (.BI(1'b0), .D(1'b0), .S(denomB[0]), .N(sousMUX_1_bo), .BO(sousMUX_1_bo), .R(sousMUX_1_r));
  sousMUX sousMUX_3 (
    .BI(sousMUX_2_bo), .D(sousMUX_1_r), .S(denomB[1]), .N(sousMUX_6_bo), .BO(sousMUX_3_bo), .R(sousMUX_3_r));
  sousMUX sousMUX_9 (
    .BI(sousMUX_8_bo), .D(sousMUX_3_r), .S(denomB[2]), .N(sousMUX_11_bo), .BO(sousMUX_9_bo), .R(sousMUX_9_r));
  sousMUX sousMUX_15 (
    .BI(sousMUX_14_bo), .D(sousMUX_9_r), .S(denomB[3]), .N(sousMUX_16_bo), .BO(sousMUX_15_bo),
    .R(sousMUX_15_r));
  sousMUX sousMUX_21 (
    .BI(sousMUX_20_bo), .D(sousMUX_15_r), .S(1'b0), .N(sousMUX_21_bo), .BO(sousMUX_21_bo));  // open: R
  not not_1 (Q[0], sousMUX_21_bo);
  sousMUX sousMUX_4 (.BI(sousMUX_3_bo), .D(1'b0), .S(denomB[2]), .N(sousMUX_6_bo), .BO(sousMUX_4_bo), .R(sousMUX_4_r));
  sousMUX sousMUX_10 (
    .BI(sousMUX_9_bo), .D(sousMUX_4_r), .S(denomB[3]), .N(sousMUX_11_bo), .BO(sousMUX_10_bo), .R(sousMUX_10_r));
  sousMUX sousMUX_16 (
    .BI(sousMUX_15_bo), .D(sousMUX_10_r), .S(1'b0), .N(sousMUX_16_bo), .BO(sousMUX_16_bo));  // open: R
  not not_2 (Q[1], sousMUX_16_bo);
  sousMUX sousMUX_5 (.BI(sousMUX_4_bo), .D(1'b0), .S(denomB[3]), .N(sousMUX_6_bo), .BO(sousMUX_5_bo), .R(sousMUX_5_r));
  sousMUX sousMUX_11 (.BI(sousMUX_10_bo), .D(sousMUX_5_r), .S(1'b0), .N(sousMUX_11_bo), .BO(sousMUX_11_bo));  // open: R
  not not_3 (Q[2], sousMUX_11_bo);
  sousMUX sousMUX_6 (.BI(sousMUX_5_bo), .D(1'b0), .S(1'b0), .N(sousMUX_6_bo), .BO(sousMUX_6_bo));  // open: R
  not not_4 (Q[3], sousMUX_6_bo);
endmodule

module multi4bit (
  input  [3:0] A,
  input  [3:0] B,
  output [7:0] multR
);

  wire add4bit_1_c, add4bit_1_c1, add4bit_1_c2, add4bit_1_c3, add4bit_2_c, add4bit_2_c1, add4bit_2_c2,
       add4bit_2_c3, and_2_out, and_3_out, and_4_out, and_5_out, and_6_out, and_7_out, and_8_out, and_9_out,
       and_10_out, and_11_out, and_12_out, and_13_out, and_14_out, and_15_out, and_16_out;

  and and_1 (multR[0], A[0], B[0]);
  and and_2 (and_2_out, A[1], B[0]);
  and and_3 (and_3_out, A[2], B[0]);
  and and_4 (and_4_out, A[3], B[0]);
  and and_5 (and_5_out, A[0], B[1]);
  and and_6 (and_6_out, A[1], B[1]);
  and and_7 (and_7_out, A[2], B[1]);
  and and_8 (and_8_out, A[3], B[1]);
  and and_9 (and_9_out, A[0], B[2]);
  and and_10 (and_10_out, A[1], B[2]);
  and and_11 (and_11_out, A[2], B[2]);
  and and_12 (and_12_out, A[3], B[2]);
  and and_13 (and_13_out, A[0], B[3]);
  and and_14 (and_14_out, A[1], B[3]);
  and and_15 (and_15_out, A[2], B[3]);
  and and_16 (and_16_out, A[3], B[3]);
  add4bit add4bit_1 (
    .Cin(1'b0), .A0(and_2_out), .B0(and_5_out), .A1(and_3_out), .B1(and_6_out), .A2(and_4_out),
    .B2(and_7_out), .A3(1'b0), .B3(and_8_out), .C0(multR[1]), .C1(add4bit_1_c1), .C2(add4bit_1_c2),
    .C3(add4bit_1_c3), .C(add4bit_1_c));
  add4bit add4bit_2 (
    .Cin(1'b0), .A0(add4bit_1_c1), .B0(and_9_out), .A1(add4bit_1_c2), .B1(and_10_out), .A2(add4bit_1_c3),
    .B2(and_11_out), .A3(add4bit_1_c), .B3(and_12_out), .C0(multR[2]), .C1(add4bit_2_c1), .C2(add4bit_2_c2),
    .C3(add4bit_2_c3), .C(add4bit_2_c));
  add4bit add4bit_3 (
    .Cin(1'b0), .A0(add4bit_2_c1), .B0(and_13_out), .A1(add4bit_2_c2), .B1(and_14_out), .A2(add4bit_2_c3),
    .B2(and_15_out), .A3(add4bit_2_c), .B3(and_16_out), .C0(multR[3]), .C1(multR[4]), .C2(multR[5]),
    .C3(multR[6]), .C(multR[7]));
endmodule

module add4bit (
  input  Cin,
  input  A0,
  input  B0,
  input  A1,
  input  B1,
  input  A2,
  input  B2,
  input  A3,
  input  B3,
  output C0,
  output C1,
  output C2,
  output C3,
  output C
);

  wire fullAdder_1_cout, fullAdder_2_cout, fullAdder_3_cout, xor_1_out, xor_2_out, xor_3_out, xor_4_out;

  xor xor_1 (xor_1_out, B0, Cin);
  xor xor_2 (xor_2_out, B1, Cin);
  xor xor_3 (xor_3_out, B2, Cin);
  xor xor_4 (xor_4_out, B3, Cin);
  fullAdder fullAdder_1 (.cIn(Cin), .Ia(A0), .Ib(xor_1_out), .S(C0), .cOut(fullAdder_1_cout));
  fullAdder fullAdder_2 (.cIn(fullAdder_1_cout), .Ia(A1), .Ib(xor_2_out), .S(C1), .cOut(fullAdder_2_cout));
  fullAdder fullAdder_3 (.cIn(fullAdder_2_cout), .Ia(A2), .Ib(xor_3_out), .S(C2), .cOut(fullAdder_3_cout));
  fullAdder fullAdder_4 (.cIn(fullAdder_3_cout), .Ia(A3), .Ib(xor_4_out), .S(C3), .cOut(C));
endmodule

module convert4sup (
  input  [3:0] S,
  output [3:0] dig0,
  output [3:0] dig1,
  output [3:0] dig2
);

  wire and_1_out, and_2_out, and_3_out, and_4_out, and_5_out, and_6_out, and_7_out, and_8_out, and_9_out,
       and_10_out, and_11_out, and_12_out, and_13_out, and_14_out, and_15_out, and_16_out, and_17_out,
       and_18_out, and_19_out, and_20_out, and_21_out, and_22_out, and_23_out, and_24_out, and_25_out,
       and_26_out, and_27_out, and_28_out, and_29_out, and_30_out, and_31_out, and_32_out, and_33_out,
       and_34_out, and_35_out, not_1_out, not_2_out, not_3_out, not_4_out, not_5_out, not_6_out, not_7_out,
       not_8_out, not_9_out, not_10_out, not_11_out, not_12_out, not_13_out, not_14_out, not_15_out,
       not_16_out, not_17_out, not_18_out, not_19_out, not_20_out, not_21_out, not_22_out, not_23_out,
       not_24_out, not_25_out, not_26_out, not_27_out, not_28_out, not_29_out, not_30_out, not_31_out,
       not_32_out, not_33_out, not_34_out, not_35_out, not_36_out, not_37_out, not_38_out, not_39_out,
       not_40_out, not_41_out, not_42_out, not_43_out, not_44_out, not_45_out, not_46_out, not_47_out,
       not_48_out, not_49_out, not_50_out, not_51_out, not_52_out, not_53_out, not_54_out, not_55_out;

  and and_1 (and_1_out, S[3], S[2], S[0]);
  and and_2 (and_2_out, S[3], S[2], S[1]);
  not not_1 (not_1_out, S[3]);
  not not_2 (not_2_out, S[2]);
  not not_3 (not_3_out, S[1]);
  not not_4 (not_4_out, S[0]);
  not not_5 (not_5_out, S[3]);
  not not_6 (not_6_out, S[1]);
  not not_7 (not_7_out, S[3]);
  not not_8 (not_8_out, S[0]);
  not not_9 (not_9_out, S[1]);
  not not_10 (not_10_out, S[0]);
  not not_11 (not_11_out, S[2]);
  not not_12 (not_12_out, S[3]);
  not not_13 (not_13_out, S[1]);
  not not_14 (not_14_out, S[0]);
  not not_15 (not_15_out, S[2]);
  not not_16 (not_16_out, S[2]);
  not not_17 (not_17_out, S[2]);
  not not_18 (not_18_out, S[0]);
  not not_19 (not_19_out, S[3]);
  not not_20 (not_20_out, S[1]);
  not not_21 (not_21_out, S[0]);
  not not_22 (not_22_out, S[2]);
  not not_23 (not_23_out, S[0]);
  not not_24 (not_24_out, S[2]);
  not not_25 (not_25_out, S[0]);
  not not_26 (not_26_out, S[3]);
  not not_27 (not_27_out, S[2]);
  not not_28 (not_28_out, S[1]);
  not not_29 (not_29_out, S[3]);
  not not_30 (not_30_out, S[0]);
  not not_31 (not_31_out, S[3]);
  not not_32 (not_32_out, S[2]);
  not not_33 (not_33_out, S[1]);
  not not_34 (not_34_out, S[0]);
  not not_35 (not_35_out, S[3]);
  not not_36 (not_36_out, S[2]);
  not not_37 (not_37_out, S[2]);
  not not_38 (not_38_out, S[1]);
  not not_39 (not_39_out, S[0]);
  not not_40 (not_40_out, S[1]);
  not not_41 (not_41_out, S[2]);
  not not_42 (not_42_out, S[1]);
  not not_43 (not_43_out, S[3]);
  not not_44 (not_44_out, S[0]);
  not not_45 (not_45_out, S[0]);
  not not_46 (not_46_out, S[2]);
  not not_47 (not_47_out, S[3]);
  not not_48 (not_48_out, S[2]);
  not not_49 (not_49_out, S[1]);
  not not_50 (not_50_out, S[3]);
  not not_51 (not_51_out, S[0]);
  not not_52 (not_52_out, S[3]);
  not not_53 (not_53_out, S[2]);
  not not_54 (not_54_out, S[1]);
  not not_55 (not_55_out, S[0]);
  or or_1 (dig2[1], and_1_out, and_2_out);
  and and_3 (and_3_out, not_1_out, S[2], S[1], S[0]);
  and and_4 (and_4_out, S[3], not_2_out);
  and and_5 (and_5_out, S[3], not_3_out, not_4_out);
  and and_6 (and_6_out, not_5_out, S[2], not_6_out, S[0]);
  and and_7 (and_7_out, not_7_out, S[2], S[1], not_8_out);
  and and_8 (and_8_out, S[3], S[2], not_9_out, not_10_out);
  and and_9 (and_9_out, not_11_out, S[1], S[0]);
  and and_10 (and_10_out, not_12_out, S[2], not_13_out, not_14_out);
  and and_11 (and_11_out, S[3], not_15_out, S[0]);
  and and_12 (and_12_out, S[3], not_16_out, S[1]);
  and and_13 (and_13_out, S[3], S[1], S[0]);
  and and_14 (and_14_out, not_17_out, S[1], not_18_out);
  and and_15 (and_15_out, not_19_out, S[2], not_20_out, not_21_out);
  and and_16 (and_16_out, S[3], not_22_out, not_23_out);
  and and_17 (and_17_out, S[3], not_24_out, S[1]);
  and and_18 (and_18_out, S[3], S[1], not_25_out);
  and and_19 (and_19_out, not_26_out, not_27_out, not_28_out, S[0]);
  and and_20 (and_20_out, not_29_out, S[1], not_30_out);
  and and_21 (and_21_out, not_31_out, S[2], S[1]);
  and and_22 (and_22_out, S[3], not_32_out, S[1], S[0]);
  and and_23 (and_23_out, S[3], S[2], not_33_out, not_34_out);
  and and_24 (and_24_out, not_35_out, not_36_out, S[1], S[0]);
  and and_25 (and_25_out, S[3], not_37_out, not_38_out, not_39_out);
  and and_26 (and_26_out, S[3], S[2], not_40_out, S[0]);
  and and_27 (and_27_out, not_41_out, not_42_out, S[0]);
  and and_28 (and_28_out, not_43_out, S[2], not_44_out);
  and and_29 (and_29_out, S[2], S[1], not_45_out);
  and and_30 (and_30_out, S[3], not_46_out, S[0]);
  and and_31 (and_31_out, not_47_out, not_48_out, not_49_out, S[0]);
  and and_32 (and_32_out, not_50_out, S[1], not_51_out);
  and and_33 (and_33_out, not_52_out, S[2], S[1]);
  and and_34 (and_34_out, S[3], not_53_out, S[1], S[0]);
  and and_35 (and_35_out, S[3], S[2], not_54_out, not_55_out);
  or or_2 (dig2[0], and_3_out, and_4_out, and_5_out);
  or or_3 (dig1[3], and_6_out, and_7_out, and_8_out);
  or or_4 (dig1[2], and_9_out, and_10_out, and_11_out, and_12_out, and_13_out);
  or or_5 (dig1[1], and_14_out, and_15_out, and_16_out, and_17_out, and_18_out);
  or or_6 (dig1[0], and_19_out, and_20_out, and_21_out, and_22_out, and_23_out);
  or or_7 (dig0[3], and_24_out, and_25_out, and_26_out);
  or or_8 (dig0[2], and_27_out, and_28_out, and_29_out, and_30_out);
  or or_9 (dig0[1], and_31_out, and_32_out, and_33_out, and_34_out, and_35_out);

  assign dig0[0] = 1'b0;
  assign dig2[3:2] = 2'b00;
endmodule

module change8_4 (
  input  [7:0] S,
  output [3:0] digit0,
  output [3:0] digit1,
  output [3:0] digit2
);

  wire add0_c, add0_c0, add0_c1, add0_c2, add0_c3, add1_c, add1_c0, add1_c1, add1_c2, add1_c3, add4bit_1_c0,
       add4bit_1_c1, add4bit_1_c2, add4bit_1_c3, filterDig_1_c, filterDig_2_c, filterDig_2_j0,
       filterDig_2_j1, filterDig_2_j2, filterDig_2_j3, filterDig_3_c;
  wire [3:0] con_dig0, con_dig1, con_dig2;

  filterDig filterDig_2 (
    .G0(S[0]), .G1(S[1]), .G2(S[2]), .G3(S[3]), .O(1'b0), .J0(filterDig_2_j0), .J1(filterDig_2_j1),
    .J2(filterDig_2_j2), .J3(filterDig_2_j3), .C(filterDig_2_c));
  convert4sup con (.S(S[7:4]), .dig0(con_dig0), .dig1(con_dig1), .dig2(con_dig2));
  add4bit add0 (
    .Cin(1'b0), .A0(filterDig_2_j0), .B0(con_dig0[0]), .A1(filterDig_2_j1), .B1(con_dig0[1]),
    .A2(filterDig_2_j2), .B2(con_dig0[2]), .A3(filterDig_2_j3), .B3(con_dig0[3]), .C0(add0_c0), .C1(add0_c1),
    .C2(add0_c2), .C3(add0_c3), .C(add0_c));
  add4bit add4bit_1 (
    .Cin(1'b0), .A0(con_dig1[0]), .B0(filterDig_2_c), .A1(con_dig1[1]), .B1(1'b0), .A2(con_dig1[2]),
    .B2(1'b0), .A3(con_dig1[3]), .B3(1'b0), .C0(add4bit_1_c0), .C1(add4bit_1_c1), .C2(add4bit_1_c2),
    .C3(add4bit_1_c3));  // open: C
  filterDig filterDig_1 (
    .G0(add0_c0), .G1(add0_c1), .G2(add0_c2), .G3(add0_c3), .O(add0_c), .J0(digit0[0]), .J1(digit0[1]),
    .J2(digit0[2]), .J3(digit0[3]), .C(filterDig_1_c));
  add4bit add1 (
    .Cin(1'b0), .A0(add4bit_1_c0), .B0(filterDig_1_c), .A1(add4bit_1_c1), .B1(1'b0), .A2(add4bit_1_c2),
    .B2(1'b0), .A3(add4bit_1_c3), .B3(1'b0), .C0(add1_c0), .C1(add1_c1), .C2(add1_c2), .C3(add1_c3),
    .C(add1_c));
  filterDig filterDig_3 (
    .G0(add1_c0), .G1(add1_c1), .G2(add1_c2), .G3(add1_c3), .O(add1_c), .J0(digit1[0]), .J1(digit1[1]),
    .J2(digit1[2]), .J3(digit1[3]), .C(filterDig_3_c));
  add4bit add2 (
    .Cin(1'b0), .A0(con_dig2[0]), .B0(filterDig_3_c), .A1(con_dig2[1]), .B1(1'b0), .A2(con_dig2[2]),
    .B2(1'b0), .A3(con_dig2[3]), .B3(1'b0), .C0(digit2[0]), .C1(digit2[1]), .C2(digit2[2]), .C3(digit2[3]));  // open: C
endmodule

module change4_8 (
  input  [3:0] V,
  output [7:0] W
);

  wire and_1_out, and_2_out, and_3_out, and_4_out, and_5_out, and_6_out, and_7_out, and_8_out, and_9_out,
       and_10_out, and_11_out, and_13_out, and_14_out, not_1_out, not_2_out, not_3_out, not_4_out, not_5_out,
       not_6_out, not_7_out, not_8_out, not_9_out, not_10_out, not_11_out, not_12_out, not_13_out,
       not_14_out, not_15_out, not_16_out, not_17_out, not_18_out, not_19_out, not_20_out, not_21_out,
       not_22_out, not_23_out, not_24_out, not_25_out;

  not not_1 (not_1_out, V[3]);
  not not_2 (not_2_out, V[2]);
  not not_3 (not_3_out, V[1]);
  not not_4 (not_4_out, V[3]);
  not not_5 (not_5_out, V[1]);
  not not_6 (not_6_out, V[3]);
  not not_7 (not_7_out, V[0]);
  not not_8 (not_8_out, V[3]);
  not not_9 (not_9_out, V[2]);
  not not_10 (not_10_out, V[3]);
  not not_11 (not_11_out, V[0]);
  not not_12 (not_12_out, V[3]);
  not not_13 (not_13_out, V[1]);
  not not_14 (not_14_out, V[2]);
  not not_15 (not_15_out, V[1]);
  not not_16 (not_16_out, V[3]);
  not not_17 (not_17_out, V[2]);
  not not_18 (not_18_out, V[2]);
  not not_19 (not_19_out, V[1]);
  not not_20 (not_20_out, V[3]);
  not not_21 (not_21_out, V[0]);
  not not_22 (not_22_out, V[3]);
  not not_23 (not_23_out, V[3]);
  not not_24 (not_24_out, V[2]);
  not not_25 (not_25_out, V[1]);
  and and_1 (and_1_out, not_1_out, V[2], V[1], V[0]);
  and and_2 (and_2_out, V[3], not_2_out, not_3_out);
  and and_3 (and_3_out, not_4_out, V[2], not_5_out);
  or or_1 (W[5], and_3_out, and_4_out);
  and and_4 (and_4_out, not_6_out, V[2], not_7_out);
  and and_5 (and_5_out, not_8_out, not_9_out, V[1]);
  and and_6 (and_6_out, not_10_out, V[1], not_11_out);
  and and_7 (and_7_out, not_12_out, V[2], not_13_out, V[0]);
  and and_8 (and_8_out, V[3], not_14_out, not_15_out);
  and and_9 (and_9_out, not_16_out, not_17_out, V[0]);
  and and_10 (and_10_out, not_18_out, not_19_out, V[0]);
  or or_2 (W[3], and_9_out, and_10_out, and_11_out);
  and and_11 (and_11_out, not_20_out, V[2], not_21_out);
  and and_12 (W[2], not_22_out, V[1]);
  and and_13 (and_13_out, not_23_out, V[0]);
  or or_3 (W[1], and_13_out, and_14_out);
  and and_14 (and_14_out, not_24_out, not_25_out, V[0]);
  or or_4 (W[6], and_1_out, and_2_out);
  or or_5 (W[4], and_5_out, and_6_out, and_7_out, and_8_out);

  assign {W[7], W[0]} = 2'b00;
endmodule

module change34_8 (
  input  [3:0] dig2,
  input  [3:0] dig1,
  input  [3:0] dig0,
  output [7:0] numb
);

  wire [7:0] addsub8bit_2_ao, change4_8_1_w, change40_8_1_y;

  change40_8 change40_8_1 (.x(dig2), .y(change40_8_1_y));
  change4_8 change4_8_1 (.V(dig1), .W(change4_8_1_w));
  addsub8bit addsub8bit_2 (.minus(1'b0), .aIA(change4_8_1_w), .aIB({4'b0000, dig0}), .AO(addsub8bit_2_ao));  // open: UF
  addsub8bit addsub8bit_1 (.minus(1'b0), .aIA(addsub8bit_2_ao), .aIB(change40_8_1_y), .AO(numb));  // open: UF
endmodule

module filterDig (
  input  G0,
  input  G1,
  input  G2,
  input  G3,
  input  O,
  output J0,
  output J1,
  output J2,
  output J3,
  output C
);

  wire and_1_out, and_2_out, and_3_out, and_4_out, and_5_out, and_6_out, and_7_out, and_8_out, and_9_out,
       and_10_out, and_11_out, and_12_out, and_13_out, and_14_out, and_15_out, and_16_out, not_1_out,
       not_2_out, not_3_out, not_4_out, not_5_out, not_6_out, not_7_out, not_8_out, not_9_out, not_10_out,
       not_11_out, not_12_out, not_13_out, not_14_out, not_15_out, not_16_out, not_17_out, not_18_out,
       not_19_out, not_20_out, not_21_out, not_22_out;

  and and_1 (and_1_out, G3, G1);
  and and_2 (and_2_out, G3, G2);
  not not_1 (not_1_out, G2);
  not not_2 (not_2_out, G1);
  not not_3 (not_3_out, G3);
  not not_4 (not_4_out, G3);
  not not_5 (not_5_out, O);
  not not_6 (not_6_out, G3);
  not not_7 (not_7_out, O);
  not not_8 (not_8_out, G3);
  not not_9 (not_9_out, G2);
  not not_10 (not_10_out, G1);
  not not_11 (not_11_out, O);
  not not_12 (not_12_out, G3);
  not not_13 (not_13_out, O);
  not not_14 (not_14_out, G1);
  not not_15 (not_15_out, G3);
  not not_16 (not_16_out, G1);
  not not_17 (not_17_out, G2);
  not not_18 (not_18_out, G1);
  not not_19 (not_19_out, O);
  not not_20 (not_20_out, G3);
  not not_21 (not_21_out, G2);
  not not_22 (not_22_out, G1);
  or or_1 (C, and_1_out, and_2_out, O);
  and and_3 (and_3_out, G3, not_1_out, not_2_out);
  and and_4 (and_4_out, O, not_3_out, G1);
  and and_5 (and_5_out, O, not_4_out, G2);
  and and_6 (and_6_out, not_5_out, not_6_out, G2);
  and and_7 (and_7_out, not_7_out, G2, G1);
  and and_8 (and_8_out, not_8_out, G2, G1);
  and and_9 (and_9_out, O, not_9_out, not_10_out);
  and and_10 (and_10_out, not_11_out, not_12_out, G1);
  and and_11 (and_11_out, not_13_out, G3, G2, not_14_out);
  and and_12 (and_12_out, O, not_15_out, not_16_out);
  and and_13 (and_13_out, O, not_17_out, not_18_out);
  and and_14 (and_14_out, not_19_out, G0);
  and and_15 (and_15_out, not_20_out, G0);
  and and_16 (and_16_out, not_21_out, not_22_out, G0);
  or or_2 (J3, and_3_out, and_4_out, and_5_out);
  or or_3 (J2, and_6_out, and_7_out, and_8_out, and_9_out);
  or or_4 (J1, and_10_out, and_11_out, and_12_out, and_13_out);
  or or_5 (J0, and_14_out, and_15_out, and_16_out);
endmodule

module neg_result (
  input  a_bUF,
  input  op1,
  input  op0,
  input  fneg,
  input  sneg,
  output rneg,
  output [2:0] Output_bus_1
);

  wire and_1_out, and_2_out, and_3_out, and_4_out, and_5_out, and_6_out, and_7_out, and_8_out, and_9_out,
       and_10_out, and_11_out, and_12_out, and_13_out, and_14_out, and_15_out, and_16_out, and_17_out,
       and_18_out, and_19_out, not_1_out, not_2_out, not_3_out, not_4_out, not_5_out, not_6_out, not_7_out,
       not_8_out, not_9_out, not_10_out, not_11_out, not_12_out, not_13_out, not_14_out, not_15_out,
       not_16_out, not_17_out, not_18_out, not_19_out, not_20_out, not_21_out, not_22_out, not_23_out,
       not_24_out, not_25_out, not_26_out, not_27_out, not_28_out, not_29_out, not_30_out, not_31_out,
       not_32_out, not_33_out, not_34_out, not_35_out, not_36_out, not_37_out, not_38_out, not_39_out,
       not_40_out, not_41_out, not_42_out, not_43_out, or_2_out, or_3_out, or_4_out;

  not not_1 (not_1_out, a_bUF);
  not not_2 (not_2_out, op1);
  not not_3 (not_3_out, fneg);
  not not_4 (not_4_out, sneg);
  not not_5 (not_5_out, op1);
  not not_6 (not_6_out, op0);
  not not_7 (not_7_out, op1);
  not not_8 (not_8_out, sneg);
  not not_9 (not_9_out, a_bUF);
  not not_10 (not_10_out, op1);
  not not_11 (not_11_out, op0);
  not not_12 (not_12_out, fneg);
  not not_13 (not_13_out, a_bUF);
  not not_14 (not_14_out, op1);
  not not_15 (not_15_out, op0);
  not not_16 (not_16_out, sneg);
  not not_17 (not_17_out, a_bUF);
  not not_18 (not_18_out, op1);
  not not_19 (not_19_out, fneg);
  not not_20 (not_20_out, sneg);
  not not_21 (not_21_out, a_bUF);
  not not_22 (not_22_out, op1);
  not not_23 (not_23_out, op1);
  not not_24 (not_24_out, op0);
  not not_25 (not_25_out, fneg);
  not not_26 (not_26_out, sneg);
  not not_27 (not_27_out, op1);
  not not_28 (not_28_out, op0);
  not not_29 (not_29_out, op1);
  not not_30 (not_30_out, fneg);
  not not_31 (not_31_out, op1);
  not not_32 (not_32_out, sneg);
  not not_33 (not_33_out, op1);
  not not_34 (not_34_out, op0);
  not not_35 (not_35_out, fneg);
  not not_36 (not_36_out, op1);
  not not_37 (not_37_out, op0);
  not not_38 (not_38_out, sneg);
  not not_39 (not_39_out, op1);
  not not_40 (not_40_out, fneg);
  not not_41 (not_41_out, sneg);
  not not_42 (not_42_out, op1);
  not not_43 (not_43_out, op0);
  and and_1 (and_1_out, op1, op0);
  and and_2 (and_2_out, not_1_out, not_2_out, fneg);
  and and_3 (and_3_out, op1, not_3_out, sneg);
  and and_4 (and_4_out, op1, fneg, not_4_out);
  and and_5 (and_5_out, a_bUF, not_5_out, not_6_out, sneg);
  and and_6 (and_6_out, a_bUF, not_7_out, op0, not_8_out);
  and and_7 (and_7_out, not_9_out, not_10_out, not_11_out, not_12_out, sneg);
  and and_8 (and_8_out, not_13_out, not_14_out, not_15_out, fneg, not_16_out);
  and and_9 (and_9_out, not_17_out, not_18_out, op0, not_19_out, not_20_out);
  and and_10 (and_10_out, not_21_out, not_22_out, op0, fneg, sneg);
  and and_11 (and_11_out, not_23_out, not_24_out, not_25_out, not_26_out);
  and and_12 (and_12_out, not_27_out, not_28_out, fneg, sneg);
  and and_13 (and_13_out, not_29_out, op0, not_30_out, sneg);
  and and_14 (and_14_out, not_31_out, op0, fneg, not_32_out);
  and and_15 (and_15_out, a_bUF, not_33_out, not_34_out, not_35_out, sneg);
  and and_16 (and_16_out, a_bUF, not_36_out, not_37_out, fneg, not_38_out);
  and and_17 (and_17_out, a_bUF, not_39_out, op0, not_40_out, not_41_out);
  and and_18 (and_18_out, a_bUF, not_42_out, op0, fneg, sneg);
  and and_19 (and_19_out, op1, not_43_out);
  or or_1 (rneg, and_2_out, and_3_out, and_4_out, and_5_out, and_6_out);
  or or_2 (or_2_out, and_7_out, and_8_out, and_9_out, and_10_out);
  or or_3 (or_3_out, and_11_out, and_12_out, and_13_out, and_14_out);
  or or_4 (or_4_out, and_15_out, and_16_out, and_17_out, and_18_out);
  op_code op_code_1 (
    .a_plus_b(or_3_out), .a_minus_b(or_2_out), .b_minus_a(or_4_out), .a_times_b(and_19_out),
    .a_div_b(and_1_out), .opcode2(Output_bus_1[2]), .opcode1(Output_bus_1[1]), .opcode0(Output_bus_1[0]));
endmodule

module op_code (
  input  a_plus_b,
  input  a_minus_b,
  input  b_minus_a,
  input  a_times_b,
  input  a_div_b,
  output opcode2,
  output opcode1,
  output opcode0
);

  wire and_2_out, and_3_out, and_4_out, and_5_out, not_1_out, not_2_out, not_3_out, not_4_out, not_5_out,
       not_6_out, not_7_out, not_8_out, not_9_out, not_10_out, not_11_out, not_12_out, not_13_out,
       not_14_out, not_15_out, not_16_out, not_17_out, not_18_out, not_19_out, not_20_out;

  not not_1 (not_1_out, a_plus_b);
  not not_2 (not_2_out, a_minus_b);
  not not_3 (not_3_out, a_times_b);
  not not_4 (not_4_out, a_div_b);
  not not_5 (not_5_out, a_plus_b);
  not not_6 (not_6_out, a_minus_b);
  not not_7 (not_7_out, b_minus_a);
  not not_8 (not_8_out, a_times_b);
  not not_9 (not_9_out, a_plus_b);
  not not_10 (not_10_out, a_minus_b);
  not not_11 (not_11_out, b_minus_a);
  not not_12 (not_12_out, a_div_b);
  not not_13 (not_13_out, a_plus_b);
  not not_14 (not_14_out, a_minus_b);
  not not_15 (not_15_out, b_minus_a);
  not not_16 (not_16_out, a_times_b);
  not not_17 (not_17_out, a_plus_b);
  not not_18 (not_18_out, b_minus_a);
  not not_19 (not_19_out, a_times_b);
  not not_20 (not_20_out, a_div_b);
  and and_1 (opcode2, not_1_out, not_2_out, b_minus_a, not_3_out, not_4_out);
  and and_2 (and_2_out, not_5_out, not_6_out, not_7_out, not_8_out, a_div_b);
  and and_3 (and_3_out, not_9_out, not_10_out, not_11_out, a_times_b, not_12_out);
  and and_4 (and_4_out, not_13_out, not_14_out, not_15_out, not_16_out, a_div_b);
  and and_5 (and_5_out, not_17_out, a_minus_b, not_18_out, not_19_out, not_20_out);
  or or_1 (opcode1, and_2_out, and_3_out);
  or or_2 (opcode0, and_4_out, and_5_out);
endmodule

module change40_8 (
  input  [3:0] x,
  output [7:0] y
);

  wire and_2_out, and_3_out, not_1_out, not_2_out, not_3_out, not_4_out, not_5_out, not_6_out, not_7_out,
       not_8_out, not_9_out, not_10_out, not_11_out, not_12_out, not_13_out, not_14_out, not_15_out,
       not_16_out, not_17_out, not_18_out;

  not not_1 (not_1_out, x[3]);
  not not_2 (not_2_out, x[2]);
  not not_3 (not_3_out, x[0]);
  not not_4 (not_4_out, x[3]);
  not not_5 (not_5_out, x[2]);
  not not_6 (not_6_out, x[1]);
  not not_7 (not_7_out, x[3]);
  not not_8 (not_8_out, x[2]);
  not not_9 (not_9_out, x[0]);
  not not_10 (not_10_out, x[3]);
  not not_11 (not_11_out, x[2]);
  not not_12 (not_12_out, x[1]);
  not not_13 (not_13_out, x[3]);
  not not_14 (not_14_out, x[2]);
  not not_15 (not_15_out, x[0]);
  not not_16 (not_16_out, x[3]);
  not not_17 (not_17_out, x[2]);
  not not_18 (not_18_out, x[1]);
  and and_1 (y[7], not_1_out, not_2_out, x[1], not_3_out);
  and and_2 (and_2_out, not_4_out, not_5_out, not_6_out, x[0]);
  and and_3 (and_3_out, not_7_out, not_8_out, x[1], not_9_out);
  and and_4 (y[5], not_10_out, not_11_out, not_12_out, x[0]);
  and and_5 (y[3], not_13_out, not_14_out, x[1], not_15_out);
  and and_6 (y[2], not_16_out, not_17_out, not_18_out, x[0]);
  or or_1 (y[6], and_2_out, and_3_out);

  assign {y[4], y[1:0]} = 3'b000;
endmodule

module select_op (
  input  cycleop,
  input  [1:0] P,
  output [1:0] op
);

  wire and_1_out, and_2_out, and_3_out, and_4_out, and_5_out, clock_1_out, not_1_out, not_2_out, not_3_out,
       not_4_out, not_5_out, or_1_out, or_2_out;

  not not_1 (not_1_out, cycleop);
  not not_2 (not_2_out, P[0]);
  not not_3 (not_3_out, P[1]);
  not not_4 (not_4_out, cycleop);
  not not_5 (not_5_out, P[0]);
  and and_1 (and_1_out, not_1_out, P[1]);
  and and_2 (and_2_out, P[1], not_2_out);
  and and_3 (and_3_out, cycleop, not_3_out, P[0]);
  and and_4 (and_4_out, not_4_out, P[0]);
  and and_5 (and_5_out, cycleop, not_5_out);
  or or_1 (or_1_out, and_1_out, and_2_out, and_3_out);
  or or_2 (or_2_out, and_4_out, and_5_out);
  Clock clock_1 (.out(clock_1_out));
  D_Flip_Flop d_ff_1 (.D(or_1_out), .clk(clock_1_out), .Q(op[1]));  // open: Qn, preset, reset
  D_Flip_Flop d_ff_2 (.D(or_2_out), .clk(clock_1_out), .Q(op[0]));  // open: Qn, preset, reset
endmodule

module change24_4 (
  input  [3:0] first1,
  input  [3:0] first0,
  output [3:0] numb
);

  wire and_1_out, not_1_out, not_2_out, not_3_out;

  not not_1 (not_1_out, first1[3]);
  not not_2 (not_2_out, first1[2]);
  and and_1 (and_1_out, not_1_out, not_2_out, not_3_out, first1[0]);
  not not_3 (not_3_out, first1[1]);
  add4bit add4bit_1 (
    .Cin(1'b0), .A0(first0[0]), .B0(1'b0), .A1(first0[1]), .B1(and_1_out), .A2(first0[2]), .B2(1'b0),
    .A3(first0[3]), .B3(and_1_out), .C0(numb[0]), .C1(numb[1]), .C2(numb[2]), .C3(numb[3]));  // open: C
endmodule
