// Logisim project chrono_time.circ as structural Verilog: 7 circuits, main circuit chronometre
module chronometre (
  input  RESET,
  input  EN,
  output [3:0] chrCS0,
  output [3:0] chrCS1,
  output [3:0] chrS0,
  output [3:0] chrS1,
  output [3:0] chrM0,
  output [3:0] chrM1
);

  wire and_1_out, and_2_out, centiSecond_1_start_next, secondsChrono_1_next_go, un_enable_1_start_stop;

  un_enable un_enable_1 (.res(RESET), .et(EN), .start_stop(un_enable_1_start_stop));
  and and_1 (and_1_out, centiSecond_1_start_next, un_enable_1_start_stop);
  and and_2 (and_2_out, secondsChrono_1_next_go, un_enable_1_start_stop);
  centiSecond centiSecond_1 (
    .Reset(RESET), .Enable(un_enable_1_start_stop), .cs0(chrCS0), .cs1(chrCS1),
    .start_next(centiSecond_1_start_next));
  secondsChrono secondsChrono_1 (
    .Reset(RESET), .EN(and_1_out), .seconds0(chrS0), .seconds1(chrS1), .next_go(secondsChrono_1_next_go));
  secondsChrono secondsChrono_2 (.Reset(RESET), .EN(and_2_out), .seconds0(chrM0), .seconds1(chrM1));  // open: next_go
endmodule

module counter09chrono (
  input  R,
  input  E,
  output is5,
  output is9,
  output [3:0] digit
);

  wire clock_1_out;
  wire [3:0] trans09_1_d;

  trans09 trans09_1 (.RE(R), .EN(E), .C(digit), .D(trans09_1_d));
  D_Flip_Flop d_ff_1 (.D(trans09_1_d[0]), .clk(clock_1_out), .Q(digit[0]));  // open: Qn, preset, reset
  D_Flip_Flop d_ff_2 (.D(trans09_1_d[1]), .clk(clock_1_out), .Q(digit[1]));  // open: Qn, preset, reset
  D_Flip_Flop d_ff_3 (.D(trans09_1_d[2]), .clk(clock_1_out), .Q(digit[2]));  // open: Qn, preset, reset
  D_Flip_Flop d_ff_4 (.D(trans09_1_d[3]), .clk(clock_1_out), .Q(digit[3]));  // open: Qn, preset, reset
  Clock #(.highDuration(320), .lowDuration(320)) clock_1 (.out(clock_1_out));
  check59 check59_1 (.x0(digit[0]), .x1(digit[1]), .x2(digit[2]), .x3(digit[3]), .dig5(is5), .dig9(is9));
endmodule

module centiSecond (
  input  Reset,
  input  Enable,
  output [3:0] cs0,
  output [3:0] cs1,
  output start_next
);

  wire and_1_out, centi0_is9, centi1_is9, or_1_out, or_2_out;

  or or_1 (or_1_out, Reset, start_next);
  or or_2 (or_2_out, Reset, start_next);
  and and_1 (and_1_out, centi0_is9, Enable);
  counter09chrono centi0 (.R(or_1_out), .E(Enable), .is9(centi0_is9), .digit(cs0));  // open: is5
  counter09chrono centi1 (.R(or_2_out), .E(and_1_out), .is9(centi1_is9), .digit(cs1));  // open: is5
  and and_2 (start_next, centi0_is9, centi1_is9);
endmodule

module check59 (
  input  x0,
  input  x1,
  input  x2,
  input  x3,
  output dig5,
  output dig9
);

  wire not_1_out, not_2_out, not_3_out, not_4_out;

  not not_1 (not_1_out, x3);
  not not_2 (not_2_out, x1);
  not not_3 (not_3_out, x2);
  not not_4 (not_4_out, x1);
  and and_1 (dig5, not_1_out, x2, not_2_out, x0);
  and and_2 (dig9, x3, not_3_out, not_4_out, x0);
endmodule

module secondsChrono (
  input  Reset,
  input  EN,
  output [3:0] seconds0,
  output [3:0] seconds1,
  output next_go
);

  wire and_1_out, or_1_out, or_2_out, sec0_is9, sec1_is5;

  or or_1 (or_1_out, Reset, next_go);
  or or_2 (or_2_out, Reset, next_go);
  and and_1 (and_1_out, sec0_is9, EN);
  counter09chrono sec0 (.R(or_1_out), .E(EN), .is9(sec0_is9), .digit(seconds0));  // open: is5
  counter09chrono sec1 (.R(or_2_out), .E(and_1_out), .is5(sec1_is5), .digit(seconds1));  // open: is9
  and and_2 (next_go, sec0_is9, sec1_is5);
endmodule

module un_enable (
  input  res,
  input  et,
  output start_stop
);

  wire and_1_out, and_2_out, and_3_out, clock_1_out, not_1_out, not_2_out, not_3_out, not_4_out, or_1_out,
       or_2_out;

  not not_1 (not_1_out, res);
  and and_1 (and_1_out, not_1_out, not_2_out, start_stop);
  not not_2 (not_2_out, et);
  not not_3 (not_3_out, res);
  and and_2 (and_2_out, not_3_out, et, not_4_out);
  not not_4 (not_4_out, start_stop);
  and and_3 (and_3_out, et, start_stop);
  or or_1 (or_1_out, and_1_out, and_2_out);
  or or_2 (or_2_out, and_3_out, res);
  S_R_Flip_Flop s_r_ff_1 (.S(or_1_out), .R(or_2_out), .clk(clock_1_out), .Q(start_stop));  // open: reset, Qn, preset
  Clock clock_1 (.out(clock_1_out));
endmodule

module trans09 (
  input  RE,
  input  EN,
  input  [3:0] C,
  output [3:0] D
);

  wire and_1_out, and_2_out, and_3_out, and_4_out, and_5_out, and_6_out, and_7_out, and_8_out, and_9_out,
       and_10_out, and_11_out, and_12_out, not_1_out, not_2_out, not_3_out, not_4_out, not_5_out, not_6_out,
       not_7_out, not_8_out, not_9_out, not_10_out, not_11_out, not_12_out, not_13_out, not_14_out,
       not_15_out, not_16_out, not_17_out, not_18_out, not_19_out, not_20_out, not_21_out, not_22_out,
       not_23_out, not_24_out;

  not not_1 (not_1_out, RE);
  not not_2 (not_2_out, EN);
  not not_3 (not_3_out, RE);
  not not_4 (not_4_out, C[0]);
  not not_5 (not_5_out, RE);
  not not_6 (not_6_out, RE);
  not not_7 (not_7_out, EN);
  not not_8 (not_8_out, RE);
  not not_9 (not_9_out, C[1]);
  not not_10 (not_10_out, RE);
  not not_11 (not_11_out, C[0]);
  not not_12 (not_12_out, RE);
  not not_13 (not_13_out, C[2]);
  not not_14 (not_14_out, RE);
  not not_15 (not_15_out, EN);
  not not_16 (not_16_out, RE);
  not not_17 (not_17_out, C[0]);
  not not_18 (not_18_out, RE);
  not not_19 (not_19_out, C[3]);
  not not_20 (not_20_out, C[1]);
  not not_21 (not_21_out, RE);
  not not_22 (not_22_out, EN);
  not not_23 (not_23_out, RE);
  not not_24 (not_24_out, C[0]);
  and and_1 (and_1_out, not_1_out, not_2_out, C[3]);
  and and_2 (and_2_out, not_3_out, C[3], not_4_out);
  and and_3 (and_3_out, not_5_out, EN, C[2], C[1], C[0]);
  and and_4 (and_4_out, not_6_out, not_7_out, C[2]);
  and and_5 (and_5_out, not_8_out, C[2], not_9_out);
  and and_6 (and_6_out, not_10_out, C[2], not_11_out);
  and and_7 (and_7_out, not_12_out, EN, not_13_out, C[1], C[0]);
  and and_8 (and_8_out, not_14_out, not_15_out, C[1]);
  and and_9 (and_9_out, not_16_out, C[1], not_17_out);
  and and_10 (and_10_out, not_18_out, EN, not_19_out, not_20_out, C[0]);
  and and_11 (and_11_out, not_21_out, not_22_out, C[0]);
  or or_1 (D[0], and_11_out, and_12_out);
  and and_12 (and_12_out, not_23_out, EN, not_24_out);
  or or_2 (D[3], and_1_out, and_2_out, and_3_out);
  or or_3 (D[2], and_4_out, and_5_out, and_6_out, and_7_out);
  or or_4 (D[1], and_8_out, and_9_out, and_10_out);
endmodule
