// Logisim project setAlarmTimer.circ as structural Verilog: 10 circuits, main circuit States0_9
module States0_9 (
  input  SET,
  input  RESET,
  input  P0,
  input  P1,
  input  P2,
  input  P3,
  output P0OUT,
  output P1OUT,
  output P2OUT,
  output P3OUT
);

  wire and_1_out, and_2_out, and_3_out, and_4_out, and_5_out, and_6_out, and_7_out, and_8_out, and_9_out,
       and_10_out, and_11_out, and_12_out, and_13_out, and_14_out, and_15_out, and_16_out, and_17_out,
       not_1_out, not_2_out, not_3_out, not_4_out, not_5_out, not_6_out, not_7_out, not_8_out, not_9_out,
       not_10_out, not_11_out, not_12_out, not_13_out, not_14_out, not_15_out, not_16_out, not_17_out,
       not_18_out, not_19_out, not_20_out, not_21_out, not_22_out, not_23_out, not_24_out, not_25_out,
       not_26_out, not_27_out, not_28_out, not_29_out, or_1_out, or_2_out;

  not not_1 (not_1_out, P0);
  not not_2 (not_2_out, P1);
  not not_3 (not_3_out, P0);
  not not_4 (not_4_out, P3);
  not not_5 (not_5_out, SET);
  not not_6 (not_6_out, P1);
  not not_7 (not_7_out, P1);
  not not_8 (not_8_out, P0);
  not not_9 (not_9_out, P3);
  not not_10 (not_10_out, SET);
  not not_11 (not_11_out, P1);
  not not_12 (not_12_out, P3);
  not not_13 (not_13_out, SET);
  not not_14 (not_14_out, RESET);
  not not_15 (not_15_out, RESET);
  not not_16 (not_16_out, P0);
  not not_17 (not_17_out, RESET);
  not not_18 (not_18_out, P1);
  not not_19 (not_19_out, RESET);
  not not_20 (not_20_out, RESET);
  not not_21 (not_21_out, P2);
  not not_22 (not_22_out, SET);
  not not_23 (not_23_out, RESET);
  not not_24 (not_24_out, RESET);
  not not_25 (not_25_out, P0);
  not not_26 (not_26_out, RESET);
  not not_27 (not_27_out, P3);
  and and_1 (and_1_out, not_1_out, not_2_out, SET);
  and and_2 (and_2_out, not_3_out, SET, not_4_out);
  and and_3 (and_3_out, P0, not_5_out);
  and and_4 (and_4_out, P0, not_6_out, P2, P3);
  and and_5 (and_5_out, not_7_out, SET, P2, P3);
  and and_6 (and_6_out, not_8_out, P1, not_9_out);
  and and_7 (and_7_out, P1, not_10_out);
  and and_8 (and_8_out, P0, not_11_out, SET, not_12_out);
  and and_9 (and_9_out, P0, P1, P3);
  and and_10 (and_10_out, not_13_out, not_14_out, P2);
  and and_11 (and_11_out, not_15_out, not_16_out, P2);
  and and_12 (and_12_out, not_17_out, not_18_out, P2);
  and and_13 (and_13_out, not_19_out, P2, P3);
  and and_14 (and_14_out, SET, not_20_out, P0, P1, not_21_out);
  and and_15 (and_15_out, not_22_out, not_23_out, P3);
  and and_16 (and_16_out, not_24_out, not_25_out, P3);
  and and_17 (and_17_out, SET, not_26_out, P0, P1, P2, not_27_out);
  or or_1 (or_1_out, and_1_out, and_2_out, and_3_out, and_4_out);
  not not_28 (not_28_out, RESET);
  or or_2 (or_2_out, and_5_out, and_6_out, and_7_out, and_8_out, and_9_out);
  not not_29 (not_29_out, RESET);
  or or_3 (P2OUT, and_10_out, and_11_out, and_12_out, and_13_out, and_14_out);
  or or_4 (P3OUT, and_15_out, and_16_out, and_17_out);
  and and_18 (P0OUT, or_1_out, not_28_out);
  and and_19 (P1OUT, or_2_out, not_29_out);
endmodule

module setAffichage (
  input  CYCLETIME,
  input  RESET,
  output P0,
  output P1,
  output P2,
  output P3
);

  wire clock_1_out, States0_9_1_p0out, States0_9_1_p1out, States0_9_1_p2out, States0_9_1_p3out;

  States0_9 States0_9_1 (
    .SET(CYCLETIME), .RESET(RESET), .P0(P0), .P1(P1), .P2(P2), .P3(P3), .P0OUT(States0_9_1_p0out),
    .P1OUT(States0_9_1_p1out), .P2OUT(States0_9_1_p2out), .P3OUT(States0_9_1_p3out));
  Clock clock_1 (.out(clock_1_out));
  D_Flip_Flop d_ff_1 (.D(States0_9_1_p0out), .clk(clock_1_out), .Q(P0));  // open: Qn, preset, reset
  D_Flip_Flop d_ff_2 (.D(States0_9_1_p1out), .clk(clock_1_out), .Q(P1));  // open: Qn, preset, reset
  D_Flip_Flop d_ff_3 (.D(States0_9_1_p2out), .clk(clock_1_out), .Q(P2));  // open: Qn, preset, reset
  D_Flip_Flop d_ff_4 (.D(States0_9_1_p3out), .clk(clock_1_out), .Q(P3));  // open: Qn, preset, reset
endmodule

module setHISEC_MIN (
  input  RESET,
  input  CYCLE,
  output P0,
  output P1,
  output P2,
  output P3
);

  wire and_1_out, and_2_out, not_1_out, not_2_out, not_3_out, not_4_out, not_5_out, not_6_out, not_7_out,
       or_1_out, or_2_out, setAffichage_1_p0, setAffichage_1_p1, setAffichage_1_p2, setAffichage_1_p3;

  or or_1 (or_1_out, or_2_out, RESET);
  or or_2 (or_2_out, setAffichage_1_p3, and_2_out, and_1_out);
  setAffichage setAffichage_1 (
    .CYCLETIME(CYCLE), .RESET(or_1_out), .P0(setAffichage_1_p0), .P1(setAffichage_1_p1),
    .P2(setAffichage_1_p2), .P3(setAffichage_1_p3));
  not not_1 (not_1_out, setAffichage_1_p0);
  not not_2 (not_2_out, setAffichage_1_p3);
  and and_1 (and_1_out, setAffichage_1_p1, not_1_out, not_2_out, setAffichage_1_p2);
  and and_2 (and_2_out, setAffichage_1_p2, setAffichage_1_p0, not_3_out, setAffichage_1_p1);
  not not_3 (not_3_out, setAffichage_1_p3);
  and and_3 (P0, setAffichage_1_p0, not_4_out);
  not not_4 (not_4_out, or_2_out);
  and and_4 (P1, setAffichage_1_p1, not_5_out);
  not not_5 (not_5_out, or_2_out);
  and and_5 (P2, setAffichage_1_p2, not_6_out);
  not not_6 (not_6_out, or_2_out);
  and and_6 (P3, setAffichage_1_p3, not_7_out);
  not not_7 (not_7_out, or_2_out);
endmodule

module setLOWSEC_MIN_MS (
  input  CYCLE,
  input  RESET,
  output P0,
  output P1,
  output P2,
  output P3
);

  setAffichage setAffichage_1 (.CYCLETIME(CYCLE), .RESET(RESET), .P0(P0), .P1(P1), .P2(P2), .P3(P3));
endmodule

module setHIHOUR (
  input  CYCLE,
  input  RESET,
  output P0,
  output P1,
  output P2,
  output P3
);

  wire and_1_out, not_1_out, not_2_out, not_3_out, not_4_out, or_1_out, or_2_out, setAffichage_1_p0,
       setAffichage_1_p1, setAffichage_1_p2, setAffichage_1_p3;

  or or_1 (or_1_out, RESET, or_2_out);
  setAffichage setAffichage_1 (
    .CYCLETIME(CYCLE), .RESET(or_1_out), .P0(setAffichage_1_p0), .P1(setAffichage_1_p1),
    .P2(setAffichage_1_p2), .P3(setAffichage_1_p3));
  and and_1 (and_1_out, setAffichage_1_p1, setAffichage_1_p0);
  or or_2 (or_2_out, setAffichage_1_p3, setAffichage_1_p2, and_1_out);
  not not_1 (not_1_out, or_2_out);
  not not_2 (not_2_out, or_2_out);
  not not_3 (not_3_out, or_2_out);
  not not_4 (not_4_out, or_2_out);
  and and_2 (P0, setAffichage_1_p0, not_1_out);
  and and_3 (P1, setAffichage_1_p1, not_2_out);
  and and_4 (P2, setAffichage_1_p2, not_3_out);
  and and_5 (P3, setAffichage_1_p3, not_4_out);
endmodule

module SETLOWHOUR (
  input  cycle,
  input  reset,
  input  twoactivated,
  output P0,
  output P1,
  output P2,
  output P3
);

  wire and_1_out, not_1_out, not_2_out, not_3_out, not_4_out, or_1_out, or_2_out, setLOWSEC_MIN_MS_1_p0,
       setLOWSEC_MIN_MS_1_p1, setLOWSEC_MIN_MS_1_p2, setLOWSEC_MIN_MS_1_p3;

  or or_1 (or_1_out, and_1_out, reset);
  setLOWSEC_MIN_MS setLOWSEC_MIN_MS_1 (
    .CYCLE(cycle), .RESET(or_1_out), .P0(setLOWSEC_MIN_MS_1_p0), .P1(setLOWSEC_MIN_MS_1_p1),
    .P2(setLOWSEC_MIN_MS_1_p2), .P3(setLOWSEC_MIN_MS_1_p3));
  or or_2 (or_2_out, setLOWSEC_MIN_MS_1_p2, setLOWSEC_MIN_MS_1_p3);
  and and_1 (and_1_out, twoactivated, or_2_out);
  not not_1 (not_1_out, and_1_out);
  not not_2 (not_2_out, and_1_out);
  not not_3 (not_3_out, and_1_out);
  not not_4 (not_4_out, and_1_out);
  and and_2 (P0, setLOWSEC_MIN_MS_1_p0, not_1_out);
  and and_3 (P1, setLOWSEC_MIN_MS_1_p1, not_2_out);
  and and_4 (P2, setLOWSEC_MIN_MS_1_p2, not_3_out);
  and and_5 (P3, setLOWSEC_MIN_MS_1_p3, not_4_out);
endmodule

module AlarmSetter (
  input  CYCLE,
  input  RESET,
  input  SHIHOUR,
  input  SLOWHOUR,
  input  SHIMIN,
  input  SLOWMIN,
  output [3:0] HIHOURCODE,
  output [3:0] LOWHOURCODE,
  output [3:0] HIMINCODE,
  output [3:0] LOWMINCODE
);

  wire and_1_out, and_2_out, and_3_out, and_4_out;

  and and_1 (and_1_out, SHIHOUR, CYCLE);
  and and_2 (and_2_out, SLOWHOUR, CYCLE);
  and and_3 (and_3_out, CYCLE, SHIMIN);
  and and_4 (and_4_out, SLOWMIN, CYCLE);
  setHIHOUR setHIHOUR_1 (
    .CYCLE(and_1_out), .RESET(RESET), .P0(HIHOURCODE[0]), .P1(HIHOURCODE[1]), .P2(HIHOURCODE[2]),
    .P3(HIHOURCODE[3]));
  SETLOWHOUR SETLOWHOUR_1 (
    .cycle(and_2_out), .reset(RESET), .twoactivated(HIHOURCODE[1]), .P0(LOWHOURCODE[0]), .P1(LOWHOURCODE[1]),
    .P2(LOWHOURCODE[2]), .P3(LOWHOURCODE[3]));
  setHISEC_MIN setHISEC_MIN_1 (
    .RESET(RESET), .CYCLE(and_3_out), .P0(HIMINCODE[0]), .P1(HIMINCODE[1]), .P2(HIMINCODE[2]),
    .P3(HIMINCODE[3]));
  setLOWSEC_MIN_MS setLOWSEC_MIN_MS_1 (
    .CYCLE(and_4_out), .RESET(RESET), .P0(LOWMINCODE[0]), .P1(LOWMINCODE[1]), .P2(LOWMINCODE[2]),
    .P3(LOWMINCODE[3]));
endmodule

module TIMERSETTER (
  input  CYCLE,
  input  RESET,
  input  SETLOWMS,
  input  SETHIMS,
  input  SETLOWSEC,
  input  SETHISEC,
  input  SETLOWMIN,
  input  SETHIMIN,
  output [3:0] LOWMS,
  output [3:0] HIMS,
  output [3:0] LOWSEC,
  output [3:0] HISEC,
  output [3:0] LOWMIN,
  output [3:0] HIMIN
);

  wire and_1_out, and_2_out, and_3_out, and_4_out, and_5_out, and_6_out;

  and and_1 (and_1_out, CYCLE, SETLOWMS);
  and and_2 (and_2_out, CYCLE, SETHIMS);
  and and_3 (and_3_out, CYCLE, SETLOWSEC);
  and and_4 (and_4_out, CYCLE, SETHISEC);
  and and_5 (and_5_out, CYCLE, SETLOWMIN);
  and and_6 (and_6_out, CYCLE, SETHIMIN);
  setLOWSEC_MIN_MS setLOWSEC_MIN_MS_1 (
    .CYCLE(and_1_out), .RESET(RESET), .P0(LOWMS[0]), .P1(LOWMS[1]), .P2(LOWMS[2]), .P3(LOWMS[3]));
  setLOWSEC_MIN_MS setLOWSEC_MIN_MS_2 (
    .CYCLE(and_2_out), .RESET(RESET), .P0(HIMS[0]), .P1(HIMS[1]), .P2(HIMS[2]), .P3(HIMS[3]));
  setLOWSEC_MIN_MS setLOWSEC_MIN_MS_3 (
    .CYCLE(and_3_out), .RESET(RESET), .P0(LOWSEC[0]), .P1(LOWSEC[1]), .P2(LOWSEC[2]), .P3(LOWSEC[3]));
  setHISEC_MIN setHISEC_MIN_1 (
    .RESET(RESET), .CYCLE(and_4_out), .P0(HISEC[0]), .P1(HISEC[1]), .P2(HISEC[2]), .P3(HISEC[3]));
  setLOWSEC_MIN_MS setLOWSEC_MIN_MS_4 (
    .CYCLE(and_5_out), .RESET(RESET), .P0(LOWMIN[0]), .P1(LOWMIN[1]), .P2(LOWMIN[2]), .P3(LOWMIN[3]));
  setLOWSEC_MIN_MS setLOWSEC_MIN_MS_5 (
    .CYCLE(and_6_out), .RESET(RESET), .P0(HIMIN[0]), .P1(HIMIN[1]), .P2(HIMIN[2]), .P3(HIMIN[3]));
endmodule

module calcNumbSetter (
  input  CYCLE,
  input  RESET,
  input  NEGATIVE,
  input  SETHINUMB,
  input  SETMIDNUMB,
  input  SETLOWNUMB,
  input  ENABLE,
  output [3:0] NEGORPOS,
  output [3:0] HINUM,
  output [3:0] MIDNUM,
  output [3:0] LOWNUMB
);

  wire and_1_out, and_2_out, and_3_out, and_4_out;

  and and_1 (and_1_out, ENABLE, NEGATIVE);
  and and_2 (and_2_out, CYCLE, ENABLE, SETHINUMB);
  and and_3 (and_3_out, CYCLE, ENABLE, SETMIDNUMB);
  and and_4 (and_4_out, CYCLE, ENABLE, SETLOWNUMB);
  negativeorpos negativeorpos_1 (
    .NEGATIVE(and_1_out), .RESET(RESET), .P0(NEGORPOS[0]), .P1(NEGORPOS[1]), .P2(NEGORPOS[2]),
    .P3(NEGORPOS[3]));
  setAffichage setAffichage_1 (
    .CYCLETIME(and_2_out), .RESET(RESET), .P0(HINUM[0]), .P1(HINUM[1]), .P2(HINUM[2]), .P3(HINUM[3]));
  setAffichage setAffichage_2 (
    .CYCLETIME(and_3_out), .RESET(RESET), .P0(MIDNUM[0]), .P1(MIDNUM[1]), .P2(MIDNUM[2]), .P3(MIDNUM[3]));
  setAffichage setAffichage_3 (
    .CYCLETIME(and_4_out), .RESET(RESET), .P0(LOWNUMB[0]), .P1(LOWNUMB[1]), .P2(LOWNUMB[2]), .P3(LOWNUMB[3]));
endmodule

module negativeorpos (
  input  NEGATIVE,
  input  RESET,
  output P0,
  output P1,
  output P2,
  output P3
);

  wire not_1_out;

  not not_1 (not_1_out, NEGATIVE);
  or or_1 (P0, not_1_out, RESET);

  assign P1 = 1'b1;
  assign P2 = 1'b1;
  assign P3 = 1'b1;
endmodule
