// Logisim project time_set_bus.circ as structural Verilog: 31 circuits, main circuit mode_clock
module mode_clock (
  input  RESET,
  input  FLIP,
  input  SETDIGIT,
  input  HHOUR,
  input  LHOUR,
  input  HMIN,
  input  LMIN,
  input  HSEC,
  input  LSEC,
  output [7:0] HIMIN,
  output [7:0] LOWMIN,
  output [7:0] HIHOUR,
  output [7:0] LOWHOUR,
  output [7:0] HIDAY,
  output [7:0] LOWDAY,
  output [3:0] DAY1OUT,
  output [3:0] DAY0OUT,
  output [3:0] H1OUT,
  output [3:0] H0OUT
);

  wire clock_1_out, d_ff_1_q, d_ff_2_q, hours_23_en_days, minutes_59_en_hour, or_1_out, seconds_59_en_min;
  wire [1:0] enable_digit_1_enable, enable_digit_2_enable, enable_digit_3_enable;
  wire [3:0] minutes_59_m0, minutes_59_m1;

  D_Flip_Flop d_ff_1 (.D(RESET), .clk(clock_1_out), .Q(d_ff_1_q));  // open: Qn, preset, reset
  Clock clock_1 (.out(clock_1_out));
  D_Flip_Flop d_ff_2 (.D(FLIP), .clk(clock_1_out), .Q(d_ff_2_q));  // open: Qn, preset, reset
  and and_1 (HIDAY[7], SETDIGIT, HHOUR);
  and and_2 (LOWDAY[7], SETDIGIT, LHOUR);
  and and_3 (HIHOUR[7], SETDIGIT, HMIN);
  and and_4 (LOWHOUR[7], SETDIGIT, LMIN);
  and and_5 (HIMIN[7], SETDIGIT, HSEC);
  and and_6 (LOWMIN[7], SETDIGIT, LSEC);
  or or_1 (or_1_out, SETDIGIT, d_ff_1_q);
  enable_digit enable_digit_1 (
    .set(SETDIGIT), .flip(d_ff_2_q), .choice({HIMIN[7], LOWMIN[7]}), .enable(enable_digit_1_enable));
  enable_digit enable_digit_2 (
    .set(SETDIGIT), .flip(d_ff_2_q), .choice({HIHOUR[7], LOWHOUR[7]}), .enable(enable_digit_2_enable));
  enable_digit enable_digit_3 (
    .set(SETDIGIT), .flip(d_ff_2_q), .choice({HIDAY[7], LOWDAY[7]}), .enable(enable_digit_3_enable));
  seconds seconds_59 (.Reset(or_1_out), .EN_min(seconds_59_en_min));
  minutes minutes_59 (
    .Reset(d_ff_1_q), .EN(seconds_59_en_min), .set_digits(enable_digit_1_enable),
    .EN_hour(minutes_59_en_hour), .m1(minutes_59_m1), .m0(minutes_59_m0));
  hours hours_23 (
    .Reset(d_ff_1_q), .EN(minutes_59_en_hour), .set_digits(enable_digit_2_enable), .h1(H1OUT), .h0(H0OUT),
    .EN_days(hours_23_en_days));
  daysV2 days31 (.Reset(d_ff_1_q), .EN(hours_23_en_days), .set_dig(enable_digit_3_enable), .d1(DAY1OUT), .d0(DAY0OUT));
  affiche_digit affiche_digit_1 (
    .e(HIMIN[4]), .digit(minutes_59_m1), .d(HIMIN[3]), .EN(1'b1), .c(HIMIN[2]), .a(HIMIN[0]), .b(HIMIN[1]),
    .f(HIMIN[5]), .g(HIMIN[6]));
  affiche_digit affiche_digit_2 (
    .e(LOWMIN[4]), .digit(minutes_59_m0), .d(LOWMIN[3]), .EN(1'b1), .c(LOWMIN[2]), .a(LOWMIN[0]),
    .b(LOWMIN[1]), .f(LOWMIN[5]), .g(LOWMIN[6]));
  affiche_digit affiche_digit_3 (
    .e(HIHOUR[4]), .digit(H1OUT), .d(HIHOUR[3]), .EN(1'b1), .c(HIHOUR[2]), .a(HIHOUR[0]), .b(HIHOUR[1]),
    .f(HIHOUR[5]), .g(HIHOUR[6]));
  affiche_digit affiche_digit_4 (
    .e(LOWHOUR[4]), .digit(H0OUT), .d(LOWHOUR[3]), .EN(1'b1), .c(LOWHOUR[2]), .a(LOWHOUR[0]), .b(LOWHOUR[1]),
    .f(LOWHOUR[5]), .g(LOWHOUR[6]));
  affiche_digit affiche_digit_5 (
    .e(HIDAY[4]), .digit(DAY1OUT), .d(HIDAY[3]), .EN(1'b1), .c(HIDAY[2]), .a(HIDAY[0]), .b(HIDAY[1]),
    .f(HIDAY[5]), .g(HIDAY[6]));
  affiche_digit affiche_digit_6 (
    .e(LOWDAY[4]), .digit(DAY0OUT), .d(LOWDAY[3]), .EN(1'b1), .c(LOWDAY[2]), .a(LOWDAY[0]), .b(LOWDAY[1]),
    .f(LOWDAY[5]), .g(LOWDAY[6]));
endmodule

module transition09 (
  input  Reset,
  input  EN,
  input  [3:0] C,
  output [3:0] D
);

  wire and_1_out, and_2_out, and_3_out, and_4_out, and_5_out, and_6_out, and_7_out, and_8_out, and_9_out,
       and_10_out, and_11_out, and_12_out, not_1_out, not_2_out, not_3_out, not_4_out, not_5_out, not_6_out,
       not_7_out, not_8_out, not_9_out, not_10_out, not_11_out, not_12_out, not_13_out, not_14_out,
       not_15_out, not_16_out, not_17_out, not_18_out, not_19_out, not_20_out, not_21_out, not_22_out,
       not_23_out, not_24_out;

  not not_1 (not_1_out, Reset);
  not not_2 (not_2_out, EN);
  not not_3 (not_3_out, Reset);
  not not_4 (not_4_out, C[0]);
  not not_5 (not_5_out, Reset);
  not not_6 (not_6_out, Reset);
  not not_7 (not_7_out, EN);
  not not_8 (not_8_out, Reset);
  not not_9 (not_9_out, C[1]);
  not not_10 (not_10_out, Reset);
  not not_11 (not_11_out, C[0]);
  not not_12 (not_12_out, Reset);
  not not_13 (not_13_out, C[2]);
  not not_14 (not_14_out, Reset);
  not not_15 (not_15_out, EN);
  not not_16 (not_16_out, Reset);
  not not_17 (not_17_out, C[0]);
  not not_18 (not_18_out, Reset);
  not not_19 (not_19_out, C[3]);
  not not_20 (not_20_out, C[1]);
  not not_21 (not_21_out, Reset);
  not not_22 (not_22_out, EN);
  not not_23 (not_23_out, Reset);
  not not_24 (not_24_out, C[0]);
  and and_1 (and_1_out, not_1_out, not_2_out, C[3]);
  and and_2 (and_2_out, not_3_out, C[3], not_4_out);
  and and_3 (and_3_out, not_5_out, EN, C[2], C[1], C[0]);
  and and_4 (and_4_out, not_6_out, not_7_out, C[2]);
  and and_5 (and_5_out, not_8_out, C[2], not_9_out);
  and and_6 (and_6_out, not_10_out, C[2], not_11_out);
  and and_7 (and_7_out, not_12_out, EN, not_13_out, C[1], C[0]);
  and and_8 (and_8_out, not_14_out, not_15_out, C[1]);
  and and_9 (and_9_out, not_16_out, C[1], not_17_out);
  and and_10 (and_10_out, not_18_out, EN, not_19_out, not_20_out, C[0]);
  and and_11 (and_11_out, not_21_out, not_22_out, C[0]);
  or or_1 (D[0], and_11_out, and_12_out);
  and and_12 (and_12_out, not_23_out, EN, not_24_out);
  or or_2 (D[3], and_1_out, and_2_out, and_3_out);
  or or_3 (D[2], and_4_out, and_5_out, and_6_out, and_7_out);
  or or_4 (D[1], and_8_out, and_9_out, and_10_out);
endmodule

module counter09 (
  input  Reset,
  input  EN,
  output [3:0] Digit
);

  wire clock_1_out;
  wire [3:0] predict_digit_d;

  transition09 predict_digit (.Reset(Reset), .EN(EN), .C(Digit), .D(predict_digit_d));
  Clock #(.highDuration(32000), .lowDuration(32000)) clock_1 (.out(clock_1_out));
  D_Flip_Flop d_ff_1 (.D(predict_digit_d[0]), .clk(clock_1_out), .Q(Digit[0]));  // open: Qn, preset, reset
  D_Flip_Flop d_ff_2 (.D(predict_digit_d[1]), .clk(clock_1_out), .Q(Digit[1]));  // open: Qn, preset, reset
  D_Flip_Flop d_ff_3 (.D(predict_digit_d[2]), .clk(clock_1_out), .Q(Digit[2]));  // open: Qn, preset, reset
  D_Flip_Flop d_ff_4 (.D(predict_digit_d[3]), .clk(clock_1_out), .Q(Digit[3]));  // open: Qn, preset, reset
endmodule

module seconds (
  input  Reset,
  output EN_min
);

  wire and_1_out, and_2_out, not_1_out, not_2_out, not_3_out, not_4_out, or_1_out;
  wire [3:0] s0_digit, s1_digit;

  or or_1 (or_1_out, Reset, and_2_out);
  counter09 s0 (.Reset(Reset), .EN(1'b1), .Digit(s0_digit));
  counter09 s1 (.Reset(or_1_out), .EN(and_1_out), .Digit(s1_digit));
  not not_1 (not_1_out, s0_digit[2]);
  not not_2 (not_2_out, s0_digit[1]);
  and and_1 (and_1_out, s0_digit[3], not_1_out, not_2_out, s0_digit[0]);
  not not_3 (not_3_out, s1_digit[3]);
  not not_4 (not_4_out, s1_digit[1]);
  and and_2 (and_2_out, not_3_out, s1_digit[2], and_1_out, not_4_out, s1_digit[0]);
  and and_3 (EN_min, and_1_out, and_2_out);
endmodule

module minutes (
  input  Reset,
  input  EN,
  input  [1:0] set_digits,
  output EN_hour,
  output [3:0] m1,
  output [3:0] m0
);

  wire and_1_out, and_2_out, en_min_1_en_min0, en_min_1_en_min1, en_min_1_r_min0, en_min_1_r_min1, not_1_out,
       not_2_out, not_3_out, not_4_out;

  en_min en_min_1 (
    .Reset(Reset), .EN(EN), .set_digits(set_digits), .min1_5(and_2_out), .min0_9(and_1_out),
    .R_min0(en_min_1_r_min0), .EN_min0(en_min_1_en_min0), .R_min1(en_min_1_r_min1),
    .EN_min1(en_min_1_en_min1), .EN_hr(EN_hour));
  counter09 calcul_m0 (.Reset(en_min_1_r_min0), .EN(en_min_1_en_min0), .Digit(m0));
  counter09 calcul_m1 (.Reset(en_min_1_r_min1), .EN(en_min_1_en_min1), .Digit(m1));
  not not_1 (not_1_out, m0[2]);
  not not_2 (not_2_out, m0[1]);
  not not_3 (not_3_out, m1[3]);
  not not_4 (not_4_out, m1[1]);
  and and_1 (and_1_out, m0[3], not_1_out, not_2_out, m0[0]);
  and and_2 (and_2_out, not_3_out, m1[2], not_4_out, m1[0]);
endmodule

module hours (
  input  Reset,
  input  EN,
  input  [1:0] set_digits,
  output [3:0] h1,
  output [3:0] h0,
  output EN_days
);

  wire en_hrs2_enhr0, en_hrs2_enhr1, en_hrs2_rhr0, en_hrs2_rhr1, testdighr_1_hr0e3, testdighr_1_hr0e9,
       testdighr_1_hr0g3, testdighr_1_hr1e1, testdighr_1_hr1e2;

  en_hrs_V2 en_hrs2 (
    .EN(EN), .RESET(Reset), .hr0e9(testdighr_1_hr0e9), .hr0e3(testdighr_1_hr0e3), .hr1e2(testdighr_1_hr1e2),
    .hr1e1(testdighr_1_hr1e1), .hr0g3(testdighr_1_hr0g3), .set0(set_digits[0]), .set1(set_digits[1]),
    .ENhr0(en_hrs2_enhr0), .ENhr1(en_hrs2_enhr1), .Rhr0(en_hrs2_rhr0), .Rhr1(en_hrs2_rhr1), .ENday(EN_days));
  counter09 counter09_1 (.Reset(en_hrs2_rhr0), .EN(en_hrs2_enhr0), .Digit(h0));
  counter09 counter09_2 (.Reset(en_hrs2_rhr1), .EN(en_hrs2_enhr1), .Digit(h1));
  testdighr testdighr_1 (
    .hour0(h0), .hour1(h1), .hr0e3(testdighr_1_hr0e3), .hr0e9(testdighr_1_hr0e9), .hr1e2(testdighr_1_hr1e2),
    .hr1e1(testdighr_1_hr1e1), .hr0g3(testdighr_1_hr0g3));
endmodule

module affiche_digit (
  input  [3:0] digit,
  input  EN,
  output a,
  output b,
  output c,
  output d,
  output e,
  output f,
  output g
);

  fonction_a fonction_a_1 (.EN(EN), .W(digit[3]), .X(digit[2]), .Y(digit[1]), .Z(digit[0]), .a(a));
  fonction_b fonction_b_1 (.EN(EN), .W(digit[3]), .X(digit[2]), .Y(digit[1]), .Z(digit[0]), .b(b));
  fonction_c fonction_c_1 (.EN(EN), .W(digit[3]), .X(digit[2]), .Y(digit[1]), .Z(digit[0]), .c(c));
  fonction_d fonction_d_1 (.EN(EN), .W(digit[3]), .X(digit[2]), .Y(digit[1]), .Z(digit[0]), .d(d));
  fonction_e fonction_e_1 (.EN(EN), .W(digit[3]), .X(digit[2]), .Y(digit[1]), .Z(digit[0]), .e(e));
  fonction_f fonction_f_1 (.EN(EN), .W(digit[3]), .X(digit[2]), .Y(digit[1]), .Z(digit[0]), .f(f));
  fonction_g fonction_g_1 (.EN(EN), .W(digit[3]), .X(digit[2]), .Y(digit[1]), .Z(digit[0]), .g(g));
endmodule

module fonction_a (
  input  EN,
  input  W,
  input  X,
  input  Y,
  input  Z,
  output a
);

  wire and_1_out, and_2_out, and_3_out, and_4_out, and_5_out, and_6_out, not_1_out, not_2_out, not_3_out,
       not_4_out, not_5_out, not_6_out, not_7_out;

  not not_1 (not_1_out, X);
  not not_2 (not_2_out, Z);
  not not_3 (not_3_out, W);
  not not_4 (not_4_out, W);
  not not_5 (not_5_out, X);
  not not_6 (not_6_out, Y);
  not not_7 (not_7_out, Z);
  and and_1 (and_1_out, EN, not_1_out, not_2_out);
  and and_2 (and_2_out, EN, not_3_out, Y);
  and and_3 (and_3_out, EN, not_4_out, X, Z);
  and and_4 (and_4_out, EN, X, Y);
  and and_5 (and_5_out, EN, W, not_5_out, not_6_out);
  and and_6 (and_6_out, EN, W, not_7_out);
  or or_1 (a, and_1_out, and_2_out, and_3_out, and_4_out, and_5_out, and_6_out);
endmodule

module fonction_b (
  input  EN,
  input  W,
  input  X,
  input  Y,
  input  Z,
  output b
);

  wire and_1_out, and_2_out, and_3_out, and_4_out, and_5_out, not_1_out, not_2_out, not_3_out, not_4_out,
       not_5_out, not_6_out, not_7_out, not_8_out, not_9_out;

  not not_1 (not_1_out, W);
  not not_2 (not_2_out, X);
  not not_3 (not_3_out, W);
  not not_4 (not_4_out, Y);
  not not_5 (not_5_out, Z);
  not not_6 (not_6_out, X);
  not not_7 (not_7_out, Z);
  not not_8 (not_8_out, W);
  not not_9 (not_9_out, Y);
  and and_1 (and_1_out, EN, not_1_out, not_2_out);
  and and_2 (and_2_out, EN, not_3_out, not_4_out, not_5_out);
  and and_3 (and_3_out, EN, not_6_out, not_7_out);
  and and_4 (and_4_out, EN, not_8_out, Y, Z);
  and and_5 (and_5_out, EN, W, not_9_out, Z);
  or or_1 (b, and_1_out, and_2_out, and_3_out, and_4_out, and_5_out);
endmodule

module fonction_c (
  input  EN,
  input  W,
  input  X,
  input  Y,
  input  Z,
  output c
);

  wire and_1_out, and_2_out, and_3_out, and_4_out, and_5_out, not_1_out, not_2_out, not_3_out, not_4_out,
       not_5_out, not_6_out;

  not not_1 (not_1_out, W);
  not not_2 (not_2_out, Y);
  not not_3 (not_3_out, W);
  not not_4 (not_4_out, Y);
  not not_5 (not_5_out, W);
  not not_6 (not_6_out, X);
  and and_1 (and_1_out, EN, not_1_out, not_2_out);
  and and_2 (and_2_out, EN, not_3_out, Z);
  and and_3 (and_3_out, EN, not_4_out, Z);
  and and_4 (and_4_out, EN, not_5_out, X);
  and and_5 (and_5_out, EN, W, not_6_out);
  or or_1 (c, and_1_out, and_2_out, and_3_out, and_4_out, and_5_out);
endmodule

module fonction_d (
  input  EN,
  input  W,
  input  X,
  input  Y,
  input  Z,
  output d
);

  wire and_1_out, and_2_out, and_3_out, and_4_out, and_5_out, not_1_out, not_2_out, not_3_out, not_4_out,
       not_5_out, not_6_out, not_7_out;

  not not_1 (not_1_out, W);
  not not_2 (not_2_out, X);
  not not_3 (not_3_out, Z);
  not not_4 (not_4_out, X);
  not not_5 (not_5_out, Y);
  not not_6 (not_6_out, Z);
  not not_7 (not_7_out, Y);
  and and_1 (and_1_out, EN, not_1_out, not_2_out, not_3_out);
  and and_2 (and_2_out, EN, not_4_out, Y, Z);
  and and_3 (and_3_out, EN, X, not_5_out, Z);
  and and_4 (and_4_out, EN, X, Y, not_6_out);
  and and_5 (and_5_out, EN, W, not_7_out);
  or or_1 (d, and_1_out, and_2_out, and_3_out, and_4_out, and_5_out);
endmodule

module fonction_e (
  input  EN,
  input  W,
  input  X,
  input  Y,
  input  Z,
  output e
);

  wire and_1_out, and_2_out, and_3_out, and_4_out, not_1_out, not_2_out, not_3_out;

  not not_1 (not_1_out, X);
  not not_2 (not_2_out, Z);
  not not_3 (not_3_out, Z);
  and and_1 (and_1_out, EN, not_1_out, not_2_out);
  and and_2 (and_2_out, EN, Y, not_3_out);
  and and_3 (and_3_out, EN, W, Y);
  and and_4 (and_4_out, EN, W, X);
  or or_1 (e, and_1_out, and_2_out, and_3_out, and_4_out);
endmodule

module fonction_f (
  input  EN,
  input  W,
  input  X,
  input  Y,
  input  Z,
  output f
);

  wire and_1_out, and_2_out, and_3_out, and_4_out, and_5_out, not_1_out, not_2_out, not_3_out, not_4_out,
       not_5_out, not_6_out;

  not not_1 (not_1_out, Y);
  not not_2 (not_2_out, Z);
  not not_3 (not_3_out, W);
  not not_4 (not_4_out, Y);
  not not_5 (not_5_out, Z);
  not not_6 (not_6_out, X);
  and and_1 (and_1_out, EN, not_1_out, not_2_out);
  and and_2 (and_2_out, EN, not_3_out, X, not_4_out);
  and and_3 (and_3_out, EN, X, not_5_out);
  and and_4 (and_4_out, EN, W, not_6_out);
  and and_5 (and_5_out, EN, W, Y);
  or or_1 (f, and_1_out, and_2_out, and_3_out, and_4_out, and_5_out);
endmodule

module fonction_g (
  input  EN,
  input  W,
  input  X,
  input  Y,
  input  Z,
  output g
);

  wire and_1_out, and_2_out, and_3_out, and_4_out, and_5_out, not_1_out, not_2_out, not_3_out, not_4_out,
       not_5_out;

  not not_1 (not_1_out, X);
  not not_2 (not_2_out, Z);
  not not_3 (not_3_out, W);
  not not_4 (not_4_out, Y);
  not not_5 (not_5_out, X);
  and and_1 (and_1_out, EN, not_1_out, Y);
  and and_2 (and_2_out, EN, Y, not_2_out);
  and and_3 (and_3_out, EN, not_3_out, X, not_4_out);
  and and_4 (and_4_out, EN, W, not_5_out);
  and and_5 (and_5_out, EN, W, Z);
  or or_1 (g, and_1_out, and_2_out, and_3_out, and_4_out, and_5_out);
endmodule

module set_digit (
  input  SET,
  input  c3,
  input  c2,
  input  c1,
  input  c0,
  input  n3,
  input  n2,
  input  n1,
  input  n0,
  output d3,
  output d2,
  output d1,
  output d0
);

  wire and_1_out, and_2_out, and_3_out, and_4_out, and_5_out, and_6_out, and_7_out, and_8_out, not_1_out,
       not_2_out, not_3_out, not_4_out;

  not not_1 (not_1_out, SET);
  not not_2 (not_2_out, SET);
  not not_3 (not_3_out, SET);
  not not_4 (not_4_out, SET);
  and and_1 (and_1_out, not_1_out, c3);
  and and_2 (and_2_out, SET, n3);
  and and_3 (and_3_out, not_2_out, c2);
  and and_4 (and_4_out, SET, n2);
  and and_5 (and_5_out, not_3_out, c1);
  and and_6 (and_6_out, SET, n1);
  and and_7 (and_7_out, not_4_out, c0);
  and and_8 (and_8_out, SET, n0);
  or or_1 (d3, and_1_out, and_2_out);
  or or_2 (d2, and_3_out, and_4_out);
  or or_3 (d1, and_5_out, and_6_out);
  or or_4 (d0, and_7_out, and_8_out);
endmodule

module affichage_total (
  input  mode_SetTime,
  input  [3:0] m1,
  input  [3:0] nm1,
  input  [3:0] m0,
  input  [3:0] nm0,
  input  [3:0] h1,
  input  [3:0] nh1,
  input  [3:0] h0,
  input  [3:0] nh0,
  input  [3:0] d1,
  input  [3:0] nd1,
  input  [3:0] d0,
  input  [3:0] nd0
);

  wire digit0_p3, digit0_p4, digit0_p5, digit0_p6, digit0_p7, digit1_p3, digit1_p4, digit1_p5, digit1_p6,
       digit1_p7, digit2_p3, digit2_p4, digit2_p5, digit2_p6, digit2_p7, digit3_p3, digit3_p4, digit3_p5,
       digit3_p6, digit3_p7, digit4_p3, digit4_p4, digit4_p5, digit4_p6, digit4_p7, digit5_p3, digit5_p4,
       digit5_p5, digit5_p6, digit5_p7, undriven, undriven_2, undriven_3, undriven_4, undriven_5, undriven_6,
       undriven_7, undriven_8, undriven_9, undriven_10, undriven_11, undriven_12;
  wire [3:0] control_affichage_1_d, control_affichage_2_d, control_affichage_3_d, control_affichage_4_d,
       control_affichage_5_d, control_affichage_6_d;

  control_affichage control_affichage_1 (.Set(mode_SetTime), .c(m1), .s(nm1), .d(control_affichage_1_d));
  control_affichage control_affichage_2 (.Set(mode_SetTime), .c(m0), .s(nm0), .d(control_affichage_2_d));
  control_affichage control_affichage_3 (.Set(mode_SetTime), .c(h1), .s(nh1), .d(control_affichage_3_d));
  control_affichage control_affichage_4 (.Set(mode_SetTime), .c(h0), .s(nh0), .d(control_affichage_4_d));
  control_affichage control_affichage_5 (.Set(mode_SetTime), .c(d1), .s(nd1), .d(control_affichage_5_d));
  control_affichage control_affichage_6 (.Set(mode_SetTime), .c(d0), .s(nd0), .d(control_affichage_6_d));
  // affiche_digit digit1: pin names not known; wires that end beside it: control_affichage_1_d, 1'b1, digit1_p3, digit1_p4, digit1_p5, digit1_p6, digit1_p7
  // affiche_digit digit0: pin names not known; wires that end beside it: control_affichage_2_d, 1'b1, digit0_p3, digit0_p4, digit0_p5, digit0_p6, digit0_p7
  // affiche_digit digit3: pin names not known; wires that end beside it: control_affichage_3_d, 1'b1, digit3_p3, digit3_p4, digit3_p5, digit3_p6, digit3_p7
  // affiche_digit digit2: pin names not known; wires that end beside it: control_affichage_4_d, 1'b1, digit2_p3, digit2_p4, digit2_p5, digit2_p6, digit2_p7
  // affiche_digit digit5: pin names not known; wires that end beside it: control_affichage_5_d, 1'b1, digit5_p3, digit5_p4, digit5_p5, digit5_p6, digit5_p7
  // affiche_digit digit4: pin names not known; wires that end beside it: control_affichage_6_d, 1'b1, digit4_p3, digit4_p4, digit4_p5, digit4_p6, digit4_p7
  _7_Segment_Display hour0 (
    .g(undriven_12), .f(undriven_11), .a(digit4_p3), .b(digit4_p4), .e(digit4_p7), .d(digit4_p6),
    .c(digit4_p5));  // open: dp
  _7_Segment_Display hour1 (
    .g(undriven_10), .f(undriven_9), .a(digit5_p3), .b(digit5_p4), .e(digit5_p7), .d(digit5_p6), .c(digit5_p5));  // open: dp
  _7_Segment_Display min1 (
    .g(undriven_6), .f(undriven_5), .a(digit3_p3), .b(digit3_p4), .e(digit3_p7), .d(digit3_p6), .c(digit3_p5));  // open: dp
  _7_Segment_Display min0 (
    .g(undriven_8), .f(undriven_7), .a(digit2_p3), .b(digit2_p4), .e(digit2_p7), .d(digit2_p6), .c(digit2_p5));  // open: dp
  _7_Segment_Display sec1 (
    .g(undriven_2), .f(undriven), .a(digit1_p3), .b(digit1_p4), .e(digit1_p7), .d(digit1_p6), .c(digit1_p5));  // open: dp
  _7_Segment_Display sec0 (
    .g(undriven_4), .f(undriven_3), .a(digit0_p3), .b(digit0_p4), .e(digit0_p7), .d(digit0_p6), .c(digit0_p5));  // open: dp
endmodule

module enable_digit (
  input  set,
  input  flip,
  input  [1:0] choice,
  output [1:0] enable
);

  and and_1 (enable[1], set, flip, choice[1]);
  and and_2 (enable[0], set, flip, choice[0]);
endmodule

module control_affichage (
  input  Set,
  input  [3:0] c,
  input  [3:0] s,
  output [3:0] d
);

  wire and_1_out, and_2_out, and_3_out, and_4_out, and_5_out, and_6_out, and_7_out, and_8_out, not_1_out,
       not_2_out, not_3_out, not_4_out;

  not not_1 (not_1_out, Set);
  and and_1 (and_1_out, not_1_out, c[3]);
  and and_2 (and_2_out, Set, s[3]);
  not not_2 (not_2_out, Set);
  and and_3 (and_3_out, not_2_out, c[2]);
  and and_4 (and_4_out, Set, s[2]);
  not not_3 (not_3_out, Set);
  and and_5 (and_5_out, not_3_out, c[1]);
  and and_6 (and_6_out, Set, s[1]);
  not not_4 (not_4_out, Set);
  and and_7 (and_7_out, not_4_out, c[0]);
  and and_8 (and_8_out, Set, s[0]);
  or or_1 (d[3], and_1_out, and_2_out);
  or or_2 (d[2], and_3_out, and_4_out);
  or or_3 (d[1], and_5_out, and_6_out);
  or or_4 (d[0], and_7_out, and_8_out);
endmodule

module en_min (
  input  Reset,
  input  EN,
  input  [1:0] set_digits,
  input  min1_5,
  input  min0_9,
  output R_min0,
  output EN_min0,
  output R_min1,
  output EN_min1,
  output EN_hr
);

  wire and_1_out, and_2_out, and_3_out, and_4_out, and_5_out, and_6_out, and_7_out, not_1_out, not_2_out,
       not_3_out, not_4_out, not_5_out, not_6_out, not_7_out, not_8_out, not_9_out, not_10_out, not_11_out;

  not not_1 (not_1_out, Reset);
  not not_2 (not_2_out, Reset);
  and and_1 (and_1_out, set_digits[1], min1_5);
  and and_2 (and_2_out, EN, min1_5, min0_9);
  not not_3 (not_3_out, Reset);
  not not_4 (not_4_out, min1_5);
  not not_5 (not_5_out, Reset);
  not not_6 (not_6_out, min1_5);
  not not_7 (not_7_out, Reset);
  not not_8 (not_8_out, min1_5);
  not not_9 (not_9_out, Reset);
  not not_10 (not_10_out, set_digits[0]);
  not not_11 (not_11_out, set_digits[1]);
  and and_3 (and_3_out, not_1_out, set_digits[0]);
  and and_4 (and_4_out, not_2_out, EN);
  or or_1 (R_min1, and_1_out, and_2_out, Reset);
  and and_5 (and_5_out, not_3_out, set_digits[1], not_4_out);
  and and_6 (and_6_out, not_5_out, set_digits[0], not_6_out, min0_9);
  and and_7 (and_7_out, not_7_out, EN, not_8_out, min0_9);
  and and_8 (EN_hr, not_9_out, EN, not_10_out, not_11_out, min1_5, min0_9);
  or or_2 (EN_min0, and_3_out, and_4_out);
  or or_3 (EN_min1, and_5_out, and_6_out, and_7_out);

  assign R_min0 = Reset;
endmodule

module en_hrs (
  input  Reset,
  input  EN,
  input  set0,
  input  set1,
  input  hr0_9,
  input  hr0_3,
  input  hr1_2,
  output ENhr0,
  output ENhr1,
  output Rhr0,
  output Rhr1,
  output EN_day
);

  wire and_1_out, and_2_out, and_3_out, and_4_out, and_5_out, and_6_out, and_7_out, and_8_out, and_9_out,
       and_10_out, and_11_out, and_12_out, and_13_out, and_14_out, and_15_out, and_16_out, and_17_out,
       and_18_out, and_19_out, and_20_out, and_21_out, and_22_out, and_23_out, and_24_out, and_25_out,
       not_1_out, not_2_out, not_3_out, not_4_out, not_5_out, not_6_out, not_7_out, not_8_out, not_9_out,
       not_10_out, not_11_out, not_12_out, not_13_out, not_14_out, not_15_out, not_16_out, not_17_out,
       not_18_out, not_19_out, not_20_out, not_21_out, not_22_out, not_23_out, not_24_out, not_25_out,
       not_26_out, not_27_out, not_28_out, not_29_out, not_30_out, not_31_out, not_32_out, not_33_out,
       not_34_out, not_35_out, not_36_out, not_37_out;

  not not_1 (not_1_out, Reset);
  not not_2 (not_2_out, EN);
  not not_3 (not_3_out, hr0_3);
  not not_4 (not_4_out, hr1_2);
  not not_5 (not_5_out, Reset);
  not not_6 (not_6_out, hr0_9);
  not not_7 (not_7_out, hr0_3);
  not not_8 (not_8_out, Reset);
  not not_9 (not_9_out, hr0_9);
  not not_10 (not_10_out, hr1_2);
  not not_11 (not_11_out, Reset);
  not not_12 (not_12_out, EN);
  not not_13 (not_13_out, hr0_9);
  not not_14 (not_14_out, Reset);
  not not_15 (not_15_out, set1);
  not not_16 (not_16_out, hr0_9);
  not not_17 (not_17_out, hr0_3);
  not not_18 (not_18_out, Reset);
  not not_19 (not_19_out, hr0_9);
  not not_20 (not_20_out, hr0_3);
  not not_21 (not_21_out, Reset);
  not not_22 (not_22_out, hr0_9);
  not not_23 (not_23_out, hr1_2);
  not not_24 (not_24_out, Reset);
  not not_25 (not_25_out, set0);
  not not_26 (not_26_out, hr0_3);
  not not_27 (not_27_out, hr1_2);
  not not_28 (not_28_out, Reset);
  not not_29 (not_29_out, hr0_9);
  not not_30 (not_30_out, hr1_2);
  not not_31 (not_31_out, Reset);
  not not_32 (not_32_out, set0);
  not not_33 (not_33_out, hr0_3);
  not not_34 (not_34_out, hr1_2);
  not not_35 (not_35_out, set1);
  and and_1 (and_1_out, set1, hr1_2);
  and and_2 (and_2_out, set1, hr0_9, hr0_3);
  and and_3 (and_3_out, set0, hr0_9, hr1_2);
  and and_4 (and_4_out, set0, hr0_9, hr0_3);
  and and_5 (and_5_out, EN, hr0_3, hr1_2);
  and and_6 (and_6_out, EN, hr0_9, hr1_2);
  and and_7 (and_7_out, EN, hr0_9, hr0_3);
  not not_36 (not_36_out, Reset);
  not not_37 (not_37_out, hr0_9);
  and and_8 (and_8_out, not_1_out, not_2_out, set0, not_3_out, not_4_out);
  and and_9 (and_9_out, not_5_out, set0, not_6_out, not_7_out);
  and and_10 (and_10_out, not_8_out, set0, not_9_out, not_10_out);
  and and_11 (and_11_out, not_11_out, not_12_out, set0, set1, not_13_out);
  and and_12 (and_12_out, not_14_out, EN, not_15_out, not_16_out, not_17_out);
  and and_13 (and_13_out, not_18_out, EN, not_19_out, not_20_out, hr1_2);
  and and_14 (and_14_out, not_21_out, EN, not_22_out, hr0_3, not_23_out);
  and and_15 (and_15_out, not_24_out, not_25_out, set1, not_26_out, not_27_out);
  and and_16 (and_16_out, not_28_out, set1, not_29_out, not_30_out);
  and and_17 (and_17_out, not_31_out, EN, not_32_out, hr0_9, not_33_out, not_34_out);
  and and_18 (and_18_out, set1, hr0_9, hr1_2);
  and and_19 (and_19_out, set1, hr0_9, hr0_3);
  and and_20 (and_20_out, set0, not_35_out, hr0_3, hr1_2);
  and and_21 (and_21_out, set0, hr0_9, hr1_2);
  and and_22 (and_22_out, set0, hr0_9, hr0_3);
  and and_23 (and_23_out, set0, set1, hr0_9);
  and and_24 (and_24_out, EN, hr0_3, hr1_2);
  and and_25 (and_25_out, EN, hr0_9);
  or or_1 (Rhr1, and_1_out, and_2_out, and_3_out, and_4_out, and_5_out, and_6_out, and_7_out, Reset);
  and and_26 (EN_day, not_36_out, EN, not_37_out, hr0_3, hr1_2);
  or or_2 (ENhr0, and_8_out, and_9_out, and_10_out, and_11_out, and_12_out, and_13_out, and_14_out);
  or or_3 (ENhr1, and_15_out, and_16_out, and_17_out);
  or or_4 (Rhr0, and_18_out, and_19_out, and_20_out, and_21_out, and_22_out, and_23_out, and_24_out, and_25_out, Reset);
endmodule

module AfficheurBUS (
  input  [7:0] in_1
);

  _7_Segment_Display u_7_segment_display_1 (
    .g(in_1[6]), .f(in_1[5]), .a(in_1[0]), .b(in_1[1]), .e(in_1[4]), .d(in_1[3]), .c(in_1[2]), .dp(in_1[7]));
endmodule

module adderdays (
  input  A3,
  input  B3,
  input  A2,
  input  B2,
  input  A1,
  input  B1,
  input  A0,
  input  B0,
  output overflow,
  output r3,
  output r2,
  output r1,
  output r0
);

  wire addfordays_2_cout, addfordays_3_cout, addfordays_4_cout;

  addfordays addfordays_1 (.A(A3), .B(B3), .CIN(addfordays_2_cout), .COUT(overflow), .R(r3));
  addfordays addfordays_2 (.A(A2), .B(B2), .CIN(addfordays_3_cout), .COUT(addfordays_2_cout), .R(r2));
  addfordays addfordays_3 (.A(A1), .B(B1), .CIN(addfordays_4_cout), .COUT(addfordays_3_cout), .R(r1));
  addfordays addfordays_4 (.A(A0), .B(B0), .CIN(1'b0), .COUT(addfordays_4_cout), .R(r0));
endmodule

module addOdays (
  input  O,
  input  R3,
  input  R2,
  input  R1,
  input  R0,
  output OVERFLOW,
  output N3,
  output N2,
  output N1,
  output N0
);

  wire and_1_out, and_2_out, and_3_out, and_4_out, and_5_out, and_6_out, and_7_out, and_8_out, and_9_out,
       and_10_out, and_11_out, and_12_out, and_13_out, and_14_out, and_15_out, and_16_out, not_1_out,
       not_2_out, not_3_out, not_4_out, not_5_out, not_6_out, not_7_out, not_8_out, not_9_out, not_10_out,
       not_11_out, not_12_out, not_13_out, not_14_out, not_15_out, not_16_out, not_17_out, not_18_out,
       not_19_out, not_20_out, not_21_out, not_22_out;

  and and_1 (and_1_out, R3, R1);
  and and_2 (and_2_out, R3, R2);
  not not_1 (not_1_out, R2);
  not not_2 (not_2_out, R1);
  not not_3 (not_3_out, R3);
  not not_4 (not_4_out, R3);
  not not_5 (not_5_out, O);
  not not_6 (not_6_out, R3);
  not not_7 (not_7_out, O);
  not not_8 (not_8_out, R3);
  not not_9 (not_9_out, R2);
  not not_10 (not_10_out, R1);
  not not_11 (not_11_out, O);
  not not_12 (not_12_out, R3);
  not not_13 (not_13_out, O);
  not not_14 (not_14_out, R1);
  not not_15 (not_15_out, R3);
  not not_16 (not_16_out, R1);
  not not_17 (not_17_out, R2);
  not not_18 (not_18_out, R1);
  not not_19 (not_19_out, O);
  not not_20 (not_20_out, R3);
  not not_21 (not_21_out, R2);
  not not_22 (not_22_out, R1);
  or or_1 (OVERFLOW, and_1_out, and_2_out, O);
  and and_3 (and_3_out, R3, not_1_out, not_2_out);
  and and_4 (and_4_out, O, not_3_out, R1);
  and and_5 (and_5_out, O, not_4_out, R2);
  and and_6 (and_6_out, not_5_out, not_6_out, R2);
  and and_7 (and_7_out, not_7_out, R2, R1);
  and and_8 (and_8_out, not_8_out, R2, R1);
  and and_9 (and_9_out, O, not_9_out, not_10_out);
  and and_10 (and_10_out, not_11_out, not_12_out, R1);
  and and_11 (and_11_out, not_13_out, R3, R2, not_14_out);
  and and_12 (and_12_out, O, not_15_out, not_16_out);
  and and_13 (and_13_out, O, not_17_out, not_18_out);
  and and_14 (and_14_out, not_19_out, R0);
  and and_15 (and_15_out, not_20_out, R0);
  and and_16 (and_16_out, not_21_out, not_22_out, R0);
  or or_2 (N3, and_3_out, and_4_out, and_5_out);
  or or_3 (N2, and_6_out, and_7_out, and_8_out, and_9_out);
  or or_4 (N1, and_10_out, and_11_out, and_12_out, and_13_out);
  or or_5 (N0, and_14_out, and_15_out, and_16_out);
endmodule

module dayOdays (
  input  [3:0] D0,
  input  [3:0] D1,
  output [7:0] ZD
);

  wire and_1_out, and_2_out, and_3_out, not_1_out, not_2_out, not_3_out, not_4_out, not_5_out;

  not not_1 (not_1_out, D1[3]);
  not not_2 (not_2_out, D1[2]);
  not not_3 (not_3_out, D0[3]);
  not not_4 (not_4_out, D0[2]);
  and and_1 (and_1_out, not_3_out, not_4_out, D0[1], not_5_out);
  not not_5 (not_5_out, D0[0]);
  and and_2 (and_2_out, not_1_out, not_2_out, D1[1], D1[0]);
  Multiplexer #(.width(8), .enable("false")) multiplexer_1 (.in0({D1, D0}), .in1({8{1'b0}}), .out(ZD), .sel(and_3_out));
  and and_3 (and_3_out, and_2_out, and_1_out);
endmodule

module addfordays (
  input  A,
  input  B,
  input  CIN,
  output COUT,
  output R
);

  wire and_1_out, and_2_out, and_3_out, and_4_out, and_5_out, and_6_out, and_7_out, not_1_out, not_2_out,
       not_3_out, not_4_out, not_5_out, not_6_out;

  and and_1 (and_1_out, B, CIN);
  and and_2 (and_2_out, A, CIN);
  and and_3 (and_3_out, A, B);
  not not_1 (not_1_out, A);
  not not_2 (not_2_out, B);
  not not_3 (not_3_out, A);
  not not_4 (not_4_out, CIN);
  not not_5 (not_5_out, B);
  not not_6 (not_6_out, CIN);
  or or_1 (COUT, and_1_out, and_2_out, and_3_out);
  and and_4 (and_4_out, not_1_out, not_2_out, CIN);
  and and_5 (and_5_out, not_3_out, B, not_4_out);
  and and_6 (and_6_out, A, not_5_out, not_6_out);
  and and_7 (and_7_out, A, B, CIN);
  or or_2 (R, and_4_out, and_5_out, and_6_out, and_7_out);
endmodule

module compare2 (
  input  a1,
  input  b1,
  input  a0,
  input  b0,
  output G
);

  wire and_1_out, and_2_out, and_3_out, and_4_out, and_5_out, and_6_out, and_7_out, not_1_out, not_2_out,
       not_3_out, not_4_out, not_5_out, not_6_out, or_1_out, or_2_out;

  not not_1 (not_1_out, a1);
  not not_2 (not_2_out, b1);
  not not_3 (not_3_out, a0);
  not not_4 (not_4_out, b0);
  and and_1 (and_1_out, not_1_out, b1);
  or or_1 (or_1_out, and_1_out, and_2_out);
  and and_2 (and_2_out, a1, not_2_out);
  and and_3 (and_3_out, not_3_out, b0);
  or or_2 (or_2_out, and_3_out, and_4_out);
  and and_4 (and_4_out, a0, not_4_out);
  not not_5 (not_5_out, or_1_out);
  not not_6 (not_6_out, or_2_out);
  and and_5 (and_5_out, not_2_out, a1);
  and and_6 (and_6_out, not_4_out, not_5_out, a0);
  and and_7 (and_7_out, not_5_out, not_6_out, 1'b0);
  or or_3 (G, and_5_out, and_6_out, and_7_out);
endmodule

module compare4 (
  input  [3:0] A,
  input  [3:0] B,
  output greater
);

  wire compare2_1_g, compare2_2_g;

  compare2 compare2_1 (.a1(A[1]), .b1(B[1]), .a0(A[0]), .b0(B[0]), .G(compare2_1_g));
  compare2 compare2_2 (.a1(A[3]), .b1(B[3]), .a0(A[2]), .b0(B[2]), .G(compare2_2_g));
  or or_1 (greater, compare2_1_g, compare2_2_g);
endmodule

module testdighr (
  input  [3:0] hour0,
  input  [3:0] hour1,
  output hr0e3,
  output hr0e9,
  output hr1e2,
  output hr1e1,
  output hr0g3
);

  wire not_1_out, not_2_out, not_3_out, not_4_out, not_5_out, not_6_out, not_7_out, not_8_out, not_9_out,
       not_10_out;

  not not_1 (not_1_out, hour1[3]);
  not not_2 (not_2_out, hour1[2]);
  not not_3 (not_3_out, hour1[1]);
  not not_4 (not_4_out, hour0[3]);
  not not_5 (not_5_out, hour0[2]);
  not not_6 (not_6_out, hour0[2]);
  not not_7 (not_7_out, hour0[1]);
  not not_8 (not_8_out, hour1[3]);
  not not_9 (not_9_out, hour1[2]);
  not not_10 (not_10_out, hour1[0]);
  and e1 (hr1e1, not_1_out, not_2_out, not_3_out, hour1[0]);
  and e3 (hr0e3, not_4_out, not_5_out, hour0[1], hour0[0]);
  and e9 (hr0e9, hour0[3], not_6_out, not_7_out, hour0[0]);
  and e2 (hr1e2, not_8_out, not_9_out, hour1[1], not_10_out);
  compare4 g3 (.A(hour0), .B(4'b0011), .greater(hr0g3));
endmodule

module en_hrs_V2 (
  input  EN,
  input  RESET,
  input  hr0e9,
  input  hr0e3,
  input  hr1e2,
  input  hr1e1,
  input  hr0g3,
  input  set0,
  input  set1,
  output ENhr0,
  output ENhr1,
  output Rhr0,
  output Rhr1,
  output ENday
);

  wire and_1_out, and_2_out, and_3_out, and_4_out, and_6_out, and_7_out, and_8_out, and_9_out, and_10_out,
       and_11_out, and_12_out, and_13_out, nand_1_out, nand_2_out, nand_3_out, not_1_out, not_2_out,
       not_3_out, or_1_out;

  not not_1 (not_1_out, hr0e9);
  nand nand_1 (nand_1_out, hr0e3, hr1e2);
  nand nand_2 (nand_2_out, hr1e2, hr0e3);
  not not_2 (not_2_out, hr0e9);
  not not_3 (not_3_out, hr1e2);
  nand nand_3 (nand_3_out, hr1e1, hr0g3);
  or or_1 (or_1_out, hr0g3, hr0e3);
  and and_1 (and_1_out, EN, hr0g3, hr1e2);
  and and_2 (and_2_out, EN, hr0e3, hr1e2);
  and and_3 (and_3_out, set1, hr1e2);
  and and_4 (and_4_out, set1, hr0g3, hr1e1);
  and and_5 (ENday, EN, hr0e3, hr1e2);
  and and_6 (and_6_out, EN, not_1_out, nand_1_out);
  and and_7 (and_7_out, set0, nand_2_out, not_2_out);
  and and_8 (and_8_out, EN, hr0e9, not_3_out);
  and and_9 (and_9_out, set1, nand_3_out);
  and and_10 (and_10_out, EN, hr0e9);
  and and_11 (and_11_out, set0, hr1e2, or_1_out);
  and and_12 (and_12_out, EN, hr0e3, hr1e2);
  and and_13 (and_13_out, set0, hr0e9);
  or or_2 (Rhr1, RESET, and_1_out, and_2_out, and_3_out, and_4_out);
  or or_3 (ENhr0, and_6_out, and_7_out);
  or or_4 (ENhr1, and_8_out, and_9_out);
  or or_5 (Rhr0, RESET, and_10_out, and_11_out, and_12_out, and_13_out);
endmodule

module testdigday (
  input  [3:0] day0,
  input  [3:0] day1,
  output d0e1,
  output d0e9,
  output d1e3,
  output d1e2,
  output d0g1
);

  wire not_1_out, not_2_out, not_3_out, not_4_out, not_5_out, not_6_out, not_7_out, not_8_out, not_9_out,
       not_10_out;

  not not_1 (not_1_out, day1[3]);
  not not_2 (not_2_out, day1[2]);
  not not_3 (not_3_out, day1[0]);
  not not_4 (not_4_out, day0[3]);
  not not_5 (not_5_out, day0[2]);
  not not_6 (not_6_out, day0[1]);
  not not_7 (not_7_out, day0[2]);
  not not_8 (not_8_out, day0[1]);
  not not_9 (not_9_out, day1[3]);
  not not_10 (not_10_out, day1[2]);
  and e0 (d1e2, not_1_out, not_2_out, day1[1], not_3_out);
  and e1 (d0e1, not_4_out, not_5_out, not_6_out, day0[0]);
  and e9 (d0e9, day0[3], not_7_out, not_8_out, day0[0]);
  and e3 (d1e3, not_9_out, not_10_out, day1[1], day1[0]);
  compare4 g1 (.A(day0), .B(4'b0001), .greater(d0g1));
endmodule

module daysV2 (
  input  Reset,
  input  EN,
  input  [1:0] set_dig,
  output [3:0] d1,
  output [3:0] d0
);

  wire and_1_out, compare4_1_greater, compare4_2_greater, en_hrs_V2_1_enhr0, en_hrs_V2_1_enhr1,
       en_hrs_V2_1_rhr0, en_hrs_V2_1_rhr1, not_1_out, not_2_out, testdigday_1_d0e1, testdigday_1_d0e9,
       testdigday_1_d0g1, testdigday_1_d1e2, testdigday_1_d1e3;
  wire [3:0] counter09_1_digit, counter09_2_digit, multiplexer_1_out;

  en_hrs_V2 en_hrs_V2_1 (
    .EN(EN), .RESET(Reset), .hr0e9(testdigday_1_d0e9), .hr0e3(testdigday_1_d0e1), .hr1e2(testdigday_1_d1e3),
    .hr1e1(testdigday_1_d1e2), .hr0g3(testdigday_1_d0g1), .set0(set_dig[0]), .set1(set_dig[1]),
    .ENhr0(en_hrs_V2_1_enhr0), .ENhr1(en_hrs_V2_1_enhr1), .Rhr0(en_hrs_V2_1_rhr0), .Rhr1(en_hrs_V2_1_rhr1));  // open: ENday
  counter09 counter09_1 (.Reset(en_hrs_V2_1_rhr0), .EN(en_hrs_V2_1_enhr0), .Digit(counter09_1_digit));
  counter09 counter09_2 (.Reset(en_hrs_V2_1_rhr1), .EN(en_hrs_V2_1_enhr1), .Digit(counter09_2_digit));
  compare4 compare4_1 (.A(counter09_2_digit), .B(4'b0000), .greater(compare4_1_greater));
  not not_1 (not_1_out, compare4_1_greater);
  not not_2 (not_2_out, compare4_2_greater);
  compare4 compare4_2 (.A(counter09_1_digit), .B(4'b0000), .greater(compare4_2_greater));
  and and_1 (and_1_out, not_1_out, not_2_out);
  Multiplexer #(.width(4), .enable("false")) multiplexer_1 (
    .in0(counter09_1_digit), .in1(4'b0001), .out(multiplexer_1_out), .sel(and_1_out));
  dayOdays dayOdays_1 (.D0(multiplexer_1_out), .D1(counter09_2_digit), .ZD({d1, d0}));
  testdigday testdigday_1 (
    .day0(d0), .day1(d1), .d0e1(testdigday_1_d0e1), .d0e9(testdigday_1_d0e9), .d1e3(testdigday_1_d1e3),
    .d1e2(testdigday_1_d1e2), .d0g1(testdigday_1_d0g1));

  // Notes on the sheet:
  //   31 days in every month for the time being
endmodule
