// Logisim project zone_time_final.circ as structural Verilog: 19 circuits, main circuit comp_2bit
module zone_mode (
  input  [3:0] OD1,
  input  [3:0] OD0,
  input  [3:0] OH1,
  input  [3:0] OH0,
  input  CYCLEZONE,
  input  RESET,
  output [3:0] ZD1,
  output [3:0] ZD0,
  output [3:0] ZH1,
  output [3:0] ZH0,
  output [2:0] Zcode
);

  wire condition_unadd_1_en_unadd, condition_unsub_1_en_unsub, filterZone_1_neg;
  wire [3:0] add_hour_2_zonedh0, add_hour_2_zonedh1, filterZone_1_zone, filterZone_1_zone_2,
       substract_hour_1_r0, substract_hour_1_r1, substract_hour_2_r0, substract_hour_2_r1,
       substract_hour_3_r0, substract_hour_3_r1;
  wire [7:0] add_hour_1_zonedh0, change_day_1_addedday, change_day_1_subbedday, multiplexer_1_out,
       multiplexer_2_out;

  select_zone select_zone_1 (.CYCLEZONE(CYCLEZONE), .Reset(RESET), .codeZ(Zcode));
  filterZone filterZone_1 (.zoneCode(Zcode), .ZONE({filterZone_1_zone_2, filterZone_1_zone}), .NEG(filterZone_1_neg));
  add_hour add_hour_1 (
    .H0(OH0), .Z0(filterZone_1_zone), .H1(OH1), .Z1(filterZone_1_zone_2), .zonedH0(add_hour_1_zonedh0[3:0]),
    .zonedH1(add_hour_1_zonedh0[7:4]));
  add_hour add_hour_2 (
    .H0(OH0), .Z0(4'b0100), .H1(OH1), .Z1(4'b0010), .zonedH0(add_hour_2_zonedh0), .zonedH1(add_hour_2_zonedh1));
  condition_unsub condition_unsub_1 (
    .H1(OH1), .H0(OH0), .Z1(filterZone_1_zone_2), .Z0(filterZone_1_zone),
    .en_unsub(condition_unsub_1_en_unsub));
  condition_unadd condition_unadd_1 (
    .H1(add_hour_1_zonedh0[7:4]), .H0(add_hour_1_zonedh0[3:0]), .EN_unadd(condition_unadd_1_en_unadd));
  substract_hour substract_hour_1 (
    .H0(add_hour_1_zonedh0[3:0]), .Z0(4'b0100), .H1(add_hour_1_zonedh0[7:4]), .Z1(4'b0010),
    .R0(substract_hour_1_r0), .R1(substract_hour_1_r1));
  substract_hour substract_hour_2 (
    .H0(OH0), .Z0(filterZone_1_zone), .H1(OH1), .Z1(filterZone_1_zone_2), .R0(substract_hour_2_r0),
    .R1(substract_hour_2_r1));
  substract_hour substract_hour_3 (
    .H0(add_hour_2_zonedh0), .Z0(filterZone_1_zone), .H1(add_hour_2_zonedh1), .Z1(filterZone_1_zone_2),
    .R0(substract_hour_3_r0), .R1(substract_hour_3_r1));
  Multiplexer #(.width(8), .enable("false")) multiplexer_1 (
    .in0(add_hour_1_zonedh0), .in1({substract_hour_1_r1, substract_hour_1_r0}), .out(multiplexer_1_out),
    .sel(condition_unadd_1_en_unadd));
  Multiplexer #(.width(8), .enable("false")) multiplexer_2 (
    .in0({substract_hour_2_r1, substract_hour_2_r0}), .in1({substract_hour_3_r1, substract_hour_3_r0}),
    .out(multiplexer_2_out), .sel(condition_unsub_1_en_unsub));
  Multiplexer #(.width(8), .enable("false")) multiplexer_3 (
    .in0(multiplexer_1_out), .in1(multiplexer_2_out), .out({ZH1, ZH0}), .sel(filterZone_1_neg));
  change_day change_day_1 (
    .D1(OD1), .D0(OD0), .addDay(condition_unadd_1_en_unadd), .subDay(condition_unsub_1_en_unsub),
    .addedDay(change_day_1_addedday), .subbedDay(change_day_1_subbedday));
  Multiplexer #(.width(8), .enable("false")) multiplexer_4 (
    .in0(change_day_1_addedday), .in1(change_day_1_subbedday), .out({ZD1, ZD0}), .sel(filterZone_1_neg));
endmodule

module addO (
  input  O,
  input  R3,
  input  R2,
  input  R1,
  input  R0,
  output Overflow,
  output N3,
  output N2,
  output N1,
  output N0
);

  wire and_1_out, and_2_out, and_3_out, and_4_out, and_5_out, and_6_out, and_7_out, and_8_out, and_9_out,
       and_10_out, and_11_out, and_12_out, and_13_out, and_14_out, and_15_out, and_16_out, not_1_out,
       not_2_out, not_3_out, not_4_out, not_5_out, not_6_out, not_7_out, not_8_out, not_9_out, not_10_out,
       not_11_out, not_12_out, not_13_out, not_14_out, not_15_out, not_16_out, not_17_out, not_18_out,
       not_19_out, not_20_out, not_21_out, not_22_out;

  and and_1 (and_1_out, R3, R1);
  and and_2 (and_2_out, R3, R2);
  not not_1 (not_1_out, R2);
  not not_2 (not_2_out, R1);
  not not_3 (not_3_out, R3);
  not not_4 (not_4_out, R3);
  not not_5 (not_5_out, O);
  not not_6 (not_6_out, R3);
  not not_7 (not_7_out, O);
  not not_8 (not_8_out, R3);
  not not_9 (not_9_out, R2);
  not not_10 (not_10_out, R1);
  not not_11 (not_11_out, O);
  not not_12 (not_12_out, R3);
  not not_13 (not_13_out, O);
  not not_14 (not_14_out, R1);
  not not_15 (not_15_out, R3);
  not not_16 (not_16_out, R1);
  not not_17 (not_17_out, R2);
  not not_18 (not_18_out, R1);
  not not_19 (not_19_out, O);
  not not_20 (not_20_out, R3);
  not not_21 (not_21_out, R2);
  not not_22 (not_22_out, R1);
  or or_1 (Overflow, and_1_out, and_2_out, O);
  and and_3 (and_3_out, R3, not_1_out, not_2_out);
  and and_4 (and_4_out, O, not_3_out, R1);
  and and_5 (and_5_out, O, not_4_out, R2);
  and and_6 (and_6_out, not_5_out, not_6_out, R2);
  and and_7 (and_7_out, not_7_out, R2, R1);
  and and_8 (and_8_out, not_8_out, R2, R1);
  and and_9 (and_9_out, O, not_9_out, not_10_out);
  and and_10 (and_10_out, not_11_out, not_12_out, R1);
  and and_11 (and_11_out, not_13_out, R3, R2, not_14_out);
  and and_12 (and_12_out, O, not_15_out, not_16_out);
  and and_13 (and_13_out, O, not_17_out, not_18_out);
  and and_14 (and_14_out, not_19_out, R0);
  and and_15 (and_15_out, not_20_out, R0);
  and and_16 (and_16_out, not_21_out, not_22_out, R0);
  or or_2 (N3, and_3_out, and_4_out, and_5_out);
  or or_3 (N2, and_6_out, and_7_out, and_8_out, and_9_out);
  or or_4 (N1, and_10_out, and_11_out, and_12_out, and_13_out);
  or or_5 (N0, and_14_out, and_15_out, and_16_out);
endmodule

module add_hour (
  input  [3:0] H0,
  input  [3:0] Z0,
  input  [3:0] H1,
  input  [3:0] Z1,
  output [3:0] zonedH0,
  output [3:0] zonedH1
);

  wire add_circuit_1_r0, add_circuit_1_r1, add_circuit_1_r2, add_circuit_1_r3, add_circuit_2_overflow,
       add_circuit_2_r0, add_circuit_2_r1, add_circuit_2_r2, add_circuit_2_r3, addO_1_overflow,
       hour0_overflow, hour0_r0, hour0_r1, hour0_r2, hour0_r3;

  add_circuit hour0 (
    .A3(H0[3]), .B3(Z0[3]), .A2(H0[2]), .B2(Z0[2]), .A1(H0[1]), .B1(Z0[1]), .A0(H0[0]), .B0(Z0[0]),
    .Overflow(hour0_overflow), .R3(hour0_r3), .R2(hour0_r2), .R1(hour0_r1), .R0(hour0_r0));
  add_circuit add_circuit_1 (
    .A3(H1[3]), .B3(Z1[3]), .A2(H1[2]), .B2(Z1[2]), .A1(H1[1]), .B1(Z1[1]), .A0(H1[0]), .B0(Z1[0]),
    .R3(add_circuit_1_r3), .R2(add_circuit_1_r2), .R1(add_circuit_1_r1), .R0(add_circuit_1_r0));  // open: Overflow
  addO addO_1 (
    .O(hour0_overflow), .R3(hour0_r3), .R2(hour0_r2), .R1(hour0_r1), .R0(hour0_r0),
    .Overflow(addO_1_overflow), .N3(zonedH0[3]), .N2(zonedH0[2]), .N1(zonedH0[1]), .N0(zonedH0[0]));
  add_circuit add_circuit_2 (
    .A3(1'b0), .B3(add_circuit_1_r3), .A2(1'b0), .B2(add_circuit_1_r2), .A1(1'b0), .B1(add_circuit_1_r1),
    .A0(addO_1_overflow), .B0(add_circuit_1_r0), .Overflow(add_circuit_2_overflow), .R3(add_circuit_2_r3),
    .R2(add_circuit_2_r2), .R1(add_circuit_2_r1), .R0(add_circuit_2_r0));
  addO addO_2 (
    .O(add_circuit_2_overflow), .R3(add_circuit_2_r3), .R2(add_circuit_2_r2), .R1(add_circuit_2_r1),
    .R0(add_circuit_2_r0), .N3(zonedH1[3]), .N2(zonedH1[2]), .N1(zonedH1[1]), .N0(zonedH1[0]));  // open: Overflow
endmodule

module add_circuit (
  input  A3,
  input  B3,
  input  A2,
  input  B2,
  input  A1,
  input  B1,
  input  A0,
  input  B0,
  output Overflow,
  output R3,
  output R2,
  output R1,
  output R0
);

  wire add_2_cout, add_3_cout, add_4_cout;

  add add_1 (.A(A3), .B(B3), .Cin(add_2_cout), .Cout(Overflow), .R(R3));
  add add_2 (.A(A2), .B(B2), .Cin(add_3_cout), .Cout(add_2_cout), .R(R2));
  add add_3 (.A(A1), .B(B1), .Cin(add_4_cout), .Cout(add_3_cout), .R(R1));
  add add_4 (.A(A0), .B(B0), .Cin(1'b0), .Cout(add_4_cout), .R(R0));
endmodule

module add (
  input  A,
  input  B,
  input  Cin,
  output Cout,
  output R
);

  wire and_1_out, and_2_out, and_3_out, and_4_out, and_5_out, and_6_out, and_7_out, not_1_out, not_2_out,
       not_3_out, not_4_out, not_5_out, not_6_out;

  and and_1 (and_1_out, B, Cin);
  and and_2 (and_2_out, A, Cin);
  and and_3 (and_3_out, A, B);
  not not_1 (not_1_out, A);
  not not_2 (not_2_out, B);
  not not_3 (not_3_out, A);
  not not_4 (not_4_out, Cin);
  not not_5 (not_5_out, B);
  not not_6 (not_6_out, Cin);
  or or_1 (Cout, and_1_out, and_2_out, and_3_out);
  and and_4 (and_4_out, not_1_out, not_2_out, Cin);
  and and_5 (and_5_out, not_3_out, B, not_4_out);
  and and_6 (and_6_out, A, not_5_out, not_6_out);
  and and_7 (and_7_out, A, B, Cin);
  or or_2 (R, and_4_out, and_5_out, and_6_out, and_7_out);
endmodule

module substract (
  input  A,
  input  B,
  input  Cin,
  output Cout,
  output R
);

  wire and_1_out, and_2_out, and_3_out, and_4_out, and_5_out, and_6_out, and_7_out, not_1_out, not_2_out,
       not_3_out, not_4_out, not_5_out, not_6_out, not_7_out, not_8_out;

  not not_1 (not_1_out, A);
  not not_2 (not_2_out, A);
  not not_3 (not_3_out, A);
  not not_4 (not_4_out, B);
  not not_5 (not_5_out, A);
  not not_6 (not_6_out, Cin);
  not not_7 (not_7_out, B);
  not not_8 (not_8_out, Cin);
  and and_1 (and_1_out, not_1_out, Cin);
  and and_2 (and_2_out, not_2_out, B);
  and and_3 (and_3_out, B, Cin);
  and and_4 (and_4_out, not_3_out, not_4_out, Cin);
  and and_5 (and_5_out, not_5_out, B, not_6_out);
  and and_6 (and_6_out, A, not_7_out, not_8_out);
  and and_7 (and_7_out, A, B, Cin);
  or or_1 (Cout, and_1_out, and_2_out, and_3_out);
  or or_2 (R, and_4_out, and_5_out, and_6_out, and_7_out);
endmodule

module substract_circuit (
  input  A3,
  input  B3,
  input  A2,
  input  B2,
  input  A1,
  input  B1,
  input  A0,
  input  B0,
  output Underflow,
  output R3,
  output R2,
  output R1,
  output R0
);

  wire substract_2_cout, substract_3_cout, substract_4_cout;

  substract substract_1 (.A(A3), .B(B3), .Cin(substract_2_cout), .Cout(Underflow), .R(R3));
  substract substract_2 (.A(A2), .B(B2), .Cin(substract_3_cout), .Cout(substract_2_cout), .R(R2));
  substract substract_3 (.A(A1), .B(B1), .Cin(substract_4_cout), .Cout(substract_3_cout), .R(R1));
  substract substract_4 (.A(A0), .B(B0), .Cin(1'b0), .Cout(substract_4_cout), .R(R0));
endmodule

module substract_hour (
  input  [3:0] H0,
  input  [3:0] Z0,
  input  [3:0] H1,
  input  [3:0] Z1,
  output [3:0] R0,
  output [3:0] R1
);

  wire subO_1_uu, substract_circuit_1_r0, substract_circuit_1_r1, substract_circuit_1_r2,
       substract_circuit_1_r3, substract_circuit_1_underflow, substract_circuit_2_r0, substract_circuit_2_r1,
       substract_circuit_2_r2, substract_circuit_2_r3, substract_circuit_3_r0, substract_circuit_3_r1,
       substract_circuit_3_r2, substract_circuit_3_r3, substract_circuit_3_underflow;

  substract_circuit substract_circuit_1 (
    .A3(H0[3]), .B3(Z0[3]), .A2(H0[2]), .B2(Z0[2]), .A1(H0[1]), .B1(Z0[1]), .A0(H0[0]), .B0(Z0[0]),
    .Underflow(substract_circuit_1_underflow), .R3(substract_circuit_1_r3), .R2(substract_circuit_1_r2),
    .R1(substract_circuit_1_r1), .R0(substract_circuit_1_r0));
  substract_circuit substract_circuit_2 (
    .A3(H1[3]), .B3(Z1[3]), .A2(H1[2]), .B2(Z1[2]), .A1(H1[1]), .B1(Z1[1]), .A0(H1[0]), .B0(Z1[0]),
    .R3(substract_circuit_2_r3), .R2(substract_circuit_2_r2), .R1(substract_circuit_2_r1),
    .R0(substract_circuit_2_r0));  // open: Underflow
  subO subO_1 (
    .U(substract_circuit_1_underflow), .Y3(substract_circuit_1_r3), .Y2(substract_circuit_1_r2),
    .Y1(substract_circuit_1_r1), .Y0(substract_circuit_1_r0), .UU(subO_1_uu), .W3(R0[3]), .W2(R0[2]),
    .W1(R0[1]), .W0(R0[0]));
  substract_circuit substract_circuit_3 (
    .A3(substract_circuit_2_r3), .B3(1'b0), .A2(substract_circuit_2_r2), .B2(1'b0),
    .A1(substract_circuit_2_r1), .B1(1'b0), .A0(substract_circuit_2_r0), .B0(subO_1_uu),
    .Underflow(substract_circuit_3_underflow), .R3(substract_circuit_3_r3), .R2(substract_circuit_3_r2),
    .R1(substract_circuit_3_r1), .R0(substract_circuit_3_r0));
  subO subO_2 (
    .U(substract_circuit_3_underflow), .Y3(substract_circuit_3_r3), .Y2(substract_circuit_3_r2),
    .Y1(substract_circuit_3_r1), .Y0(substract_circuit_3_r0), .W3(R1[3]), .W2(R1[2]), .W1(R1[1]), .W0(R1[0]));  // open: UU
endmodule

module subO (
  input  U,
  input  Y3,
  input  Y2,
  input  Y1,
  input  Y0,
  output UU,
  output W3,
  output W2,
  output W1,
  output W0
);

  wire and_1_out, and_2_out, and_3_out, and_4_out, and_5_out, and_6_out, and_7_out, and_8_out, and_9_out,
       and_10_out, and_11_out, and_12_out, and_13_out, and_14_out, not_1_out, not_2_out, not_3_out,
       not_4_out, not_5_out, not_6_out, not_7_out, not_8_out, not_9_out, not_10_out, not_11_out, not_12_out,
       not_13_out, not_14_out, not_15_out, not_16_out, not_17_out, not_18_out;

  and and_1 (and_1_out, Y3, Y1);
  and and_2 (and_2_out, Y3, Y2);
  not not_1 (not_1_out, U);
  not not_2 (not_2_out, Y2);
  not not_3 (not_3_out, Y1);
  not not_4 (not_4_out, Y3);
  not not_5 (not_5_out, Y1);
  not not_6 (not_6_out, U);
  not not_7 (not_7_out, Y3);
  not not_8 (not_8_out, U);
  not not_9 (not_9_out, Y3);
  not not_10 (not_10_out, Y2);
  not not_11 (not_11_out, Y2);
  not not_12 (not_12_out, Y1);
  not not_13 (not_13_out, U);
  not not_14 (not_14_out, Y3);
  not not_15 (not_15_out, Y3);
  not not_16 (not_16_out, Y2);
  not not_17 (not_17_out, Y1);
  not not_18 (not_18_out, Y1);
  or or_1 (UU, and_1_out, and_2_out, U);
  and and_3 (and_3_out, not_1_out, Y3, not_2_out, not_3_out);
  and and_4 (and_4_out, U, not_4_out, Y2, not_5_out);
  and and_5 (and_5_out, U, Y3, Y2, Y1);
  and and_6 (and_6_out, not_6_out, not_7_out, Y2);
  and and_7 (and_7_out, not_8_out, Y2, Y1);
  and and_8 (and_8_out, U, not_9_out, not_10_out);
  and and_9 (and_9_out, U, not_11_out, Y1);
  and and_10 (and_10_out, U, Y3, Y2, not_12_out);
  and and_11 (and_11_out, not_13_out, not_14_out, Y1);
  and and_12 (and_12_out, not_15_out, not_16_out, Y1);
  and and_13 (and_13_out, Y3, Y2, not_17_out);
  and and_14 (and_14_out, U, Y3, not_18_out);
  or or_2 (W3, and_3_out, and_4_out, and_5_out);
  or or_3 (W2, and_6_out, and_7_out, and_8_out, and_9_out, and_10_out);
  or or_4 (W1, and_11_out, and_12_out, and_13_out, and_14_out);

  assign W0 = Y0;
endmodule

module comp_2bit (
  input  A1,
  input  B1,
  input  A0,
  input  B0,
  output ZG
);

  wire and_1_out, and_2_out, and_3_out, and_4_out, and_5_out, and_6_out, and_7_out, not_1_out, not_2_out,
       not_3_out, not_4_out, not_5_out, not_6_out, or_1_out, or_2_out;

  not not_1 (not_1_out, A1);
  not not_2 (not_2_out, B1);
  not not_3 (not_3_out, A0);
  not not_4 (not_4_out, B0);
  and and_1 (and_1_out, not_1_out, B1);
  or or_1 (or_1_out, and_1_out, and_2_out);
  and and_2 (and_2_out, A1, not_2_out);
  and and_3 (and_3_out, not_3_out, B0);
  or or_2 (or_2_out, and_3_out, and_4_out);
  and and_4 (and_4_out, A0, not_4_out);
  not not_5 (not_5_out, or_1_out);
  not not_6 (not_6_out, or_2_out);
  and and_5 (and_5_out, not_2_out, A1);
  and and_6 (and_6_out, not_4_out, not_5_out, A0);
  and and_7 (and_7_out, not_5_out, not_6_out, 1'b0);
  or or_3 (ZG, and_5_out, and_6_out, and_7_out);
endmodule

module comp_4bit (
  input  [3:0] A,
  input  [3:0] B,
  output bigger
);

  wire part0_zg, part1_zg;

  comp_2bit part0 (.A1(A[1]), .B1(B[1]), .A0(A[0]), .B0(B[0]), .ZG(part0_zg));
  comp_2bit part1 (.A1(A[3]), .B1(B[3]), .A0(A[2]), .B0(B[2]), .ZG(part1_zg));
  or or_1 (bigger, part0_zg, part1_zg);
endmodule

module condition_unadd (
  input  [3:0] H1,
  input  [3:0] H0,
  output EN_unadd
);

  wire and_1_out, larger1_bigger, larger2_bigger, larger3_bigger;

  comp_4bit larger2 (.A(H1), .B(4'b0010), .bigger(larger2_bigger));
  comp_4bit larger1 (.A(H1), .B(4'b0001), .bigger(larger1_bigger));
  comp_4bit larger3 (.A(H0), .B(4'b0011), .bigger(larger3_bigger));
  and and_1 (and_1_out, larger1_bigger, larger3_bigger);
  or or_1 (EN_unadd, larger2_bigger, and_1_out);
endmodule

module condition_unsub (
  input  [3:0] H1,
  input  [3:0] H0,
  input  [3:0] Z1,
  input  [3:0] Z0,
  output en_unsub
);

  wire and_1_out, H1_Z1_bigger, not_1_out, Z0_H0_bigger, Z1_H1_bigger;

  comp_4bit Z1_H1 (.A(Z1), .B(H1), .bigger(Z1_H1_bigger));
  comp_4bit H1_Z1 (.A(H1), .B(Z1), .bigger(H1_Z1_bigger));
  not not_1 (not_1_out, H1_Z1_bigger);
  comp_4bit Z0_H0 (.A(Z0), .B(H0), .bigger(Z0_H0_bigger));
  and and_1 (and_1_out, not_1_out, Z0_H0_bigger);
  or or_1 (en_unsub, Z1_H1_bigger, and_1_out);
endmodule

module change_day (
  input  [3:0] D1,
  input  [3:0] D0,
  input  addDay,
  input  subDay,
  output [7:0] addedDay,
  output [7:0] subbedDay
);

  wire AD0_overflow, AD0_r0, AD0_r1, AD0_r2, AD0_r3, AD1_overflow, AD1_r0, AD1_r1, AD1_r2, AD1_r3,
       addO_1_overflow, SD0_r0, SD0_r1, SD0_r2, SD0_r3, SD0_underflow, SD1_r0, SD1_r1, SD1_r2, SD1_r3,
       SD1_underflow, subO_1_uu;
  wire [3:0] addO_1_n0, addO_2_n0, subO_1_w0, subO_2_w0;

  add_circuit AD0 (
    .A3(D0[3]), .B3(1'b0), .A2(D0[2]), .B2(1'b0), .A1(D0[1]), .B1(1'b0), .A0(D0[0]), .B0(addDay),
    .Overflow(AD0_overflow), .R3(AD0_r3), .R2(AD0_r2), .R1(AD0_r1), .R0(AD0_r0));
  add_circuit AD1 (
    .A3(1'b0), .B3(D1[3]), .A2(1'b0), .B2(D1[2]), .A1(1'b0), .B1(D1[1]), .A0(addO_1_overflow), .B0(D1[0]),
    .Overflow(AD1_overflow), .R3(AD1_r3), .R2(AD1_r2), .R1(AD1_r1), .R0(AD1_r0));
  substract_circuit SD0 (
    .A3(D0[3]), .B3(1'b0), .A2(D0[2]), .B2(1'b0), .A1(D0[1]), .B1(1'b0), .A0(D0[0]), .B0(subDay),
    .Underflow(SD0_underflow), .R3(SD0_r3), .R2(SD0_r2), .R1(SD0_r1), .R0(SD0_r0));
  substract_circuit SD1 (
    .A3(D1[3]), .B3(1'b0), .A2(D1[2]), .B2(1'b0), .A1(D1[1]), .B1(1'b0), .A0(D1[0]), .B0(subO_1_uu),
    .Underflow(SD1_underflow), .R3(SD1_r3), .R2(SD1_r2), .R1(SD1_r1), .R0(SD1_r0));
  addO addO_1 (
    .O(AD0_overflow), .R3(AD0_r3), .R2(AD0_r2), .R1(AD0_r1), .R0(AD0_r0), .Overflow(addO_1_overflow),
    .N3(addO_1_n0[3]), .N2(addO_1_n0[2]), .N1(addO_1_n0[1]), .N0(addO_1_n0[0]));
  addO addO_2 (
    .O(AD1_overflow), .R3(AD1_r3), .R2(AD1_r2), .R1(AD1_r1), .R0(AD1_r0), .N3(addO_2_n0[3]),
    .N2(addO_2_n0[2]), .N1(addO_2_n0[1]), .N0(addO_2_n0[0]));  // open: Overflow
  subO subO_1 (
    .U(SD0_underflow), .Y3(SD0_r3), .Y2(SD0_r2), .Y1(SD0_r1), .Y0(SD0_r0), .UU(subO_1_uu), .W3(subO_1_w0[3]),
    .W2(subO_1_w0[2]), .W1(subO_1_w0[1]), .W0(subO_1_w0[0]));
  subO subO_2 (
    .U(SD1_underflow), .Y3(SD1_r3), .Y2(SD1_r2), .Y1(SD1_r1), .Y0(SD1_r0), .W3(subO_2_w0[3]),
    .W2(subO_2_w0[2]), .W1(subO_2_w0[1]), .W0(subO_2_w0[0]));  // open: UU
  dayO dayO_1 (.D0(addO_1_n0), .D1(addO_2_n0), .ZD(addedDay));
  dayU dayU_1 (.D1(D1), .D0(D0), .neg(subDay), .ZD({subO_2_w0, subO_1_w0}), .SD(subbedDay));
endmodule

module dayO (
  input  [3:0] D0,
  input  [3:0] D1,
  output [7:0] ZD
);

  wire and_1_out, and_2_out, and_3_out, not_1_out, not_2_out, not_3_out, not_4_out, not_5_out;

  not not_1 (not_1_out, D1[3]);
  not not_2 (not_2_out, D1[2]);
  not not_3 (not_3_out, D0[3]);
  not not_4 (not_4_out, D0[2]);
  and and_1 (and_1_out, not_3_out, not_4_out, D0[1], not_5_out);
  not not_5 (not_5_out, D0[0]);
  and and_2 (and_2_out, not_1_out, not_2_out, D1[1], D1[0]);
  Multiplexer #(.width(8), .enable("false")) multiplexer_1 (.in0({D1, D0}), .in1({8{1'b0}}), .out(ZD), .sel(and_3_out));
  and and_3 (and_3_out, and_2_out, and_1_out);
endmodule

module dayU (
  input  [3:0] D1,
  input  [3:0] D0,
  input  neg,
  input  [7:0] ZD,
  output [7:0] SD
);

  wire and_1_out, and_2_out, and_3_out, not_1_out, not_2_out, not_3_out, not_4_out, not_5_out, not_6_out,
       not_7_out;

  not not_1 (not_1_out, D0[3]);
  not not_2 (not_2_out, D0[2]);
  not not_3 (not_3_out, D0[1]);
  not not_4 (not_4_out, D1[3]);
  not not_5 (not_5_out, D1[2]);
  and and_1 (and_1_out, not_4_out, not_5_out, not_6_out, not_7_out);
  not not_6 (not_6_out, D1[1]);
  not not_7 (not_7_out, D1[0]);
  and and_2 (and_2_out, not_1_out, not_2_out, not_3_out, D0[0]);
  Multiplexer #(.width(8), .enable("false")) multiplexer_1 (.in0(ZD), .in1(8'h31), .out(SD), .sel(and_3_out));
  and and_3 (and_3_out, and_2_out, neg, and_1_out);
endmodule

module transition_zone (
  input  SET,
  input  RESET,
  input  P2,
  input  P1,
  input  P0,
  output Q2,
  output Q1,
  output Q0
);

  wire and_1_out, and_2_out, and_3_out, and_4_out, and_5_out, and_6_out, and_7_out, and_8_out, and_9_out,
       and_10_out, not_1_out, not_2_out, not_3_out, not_4_out, not_5_out, not_6_out, not_7_out, not_8_out,
       not_9_out, not_10_out, not_11_out, not_12_out, not_13_out, not_14_out, not_15_out, not_16_out,
       not_17_out, not_18_out, not_19_out, not_20_out, not_21_out, not_22_out, not_23_out, not_24_out,
       not_25_out, not_26_out, not_27_out, not_28_out, not_29_out;

  not not_1 (not_1_out, SET);
  not not_2 (not_2_out, RESET);
  not not_3 (not_3_out, P1);
  not not_4 (not_4_out, RESET);
  not not_5 (not_5_out, P1);
  not not_6 (not_6_out, P0);
  not not_7 (not_7_out, RESET);
  not not_8 (not_8_out, P2);
  not not_9 (not_9_out, SET);
  not not_10 (not_10_out, RESET);
  not not_11 (not_11_out, P2);
  not not_12 (not_12_out, RESET);
  not not_13 (not_13_out, P2);
  not not_14 (not_14_out, P0);
  not not_15 (not_15_out, RESET);
  not not_16 (not_16_out, P2);
  not not_17 (not_17_out, P1);
  not not_18 (not_18_out, SET);
  not not_19 (not_19_out, RESET);
  not not_20 (not_20_out, P2);
  not not_21 (not_21_out, SET);
  not not_22 (not_22_out, RESET);
  not not_23 (not_23_out, P1);
  not not_24 (not_24_out, RESET);
  not not_25 (not_25_out, P2);
  not not_26 (not_26_out, P0);
  not not_27 (not_27_out, RESET);
  not not_28 (not_28_out, P1);
  not not_29 (not_29_out, P0);
  and and_1 (and_1_out, not_1_out, not_2_out, P2, not_3_out);
  and and_2 (and_2_out, not_4_out, P2, not_5_out, not_6_out);
  and and_3 (and_3_out, SET, not_7_out, not_8_out, P1, P0);
  and and_4 (and_4_out, not_9_out, not_10_out, not_11_out, P1);
  and and_5 (and_5_out, not_12_out, not_13_out, P1, not_14_out);
  and and_6 (and_6_out, SET, not_15_out, not_16_out, not_17_out, P0);
  and and_7 (and_7_out, not_18_out, not_19_out, not_20_out, P0);
  and and_8 (and_8_out, not_21_out, not_22_out, not_23_out, P0);
  and and_9 (and_9_out, SET, not_24_out, not_25_out, not_26_out);
  and and_10 (and_10_out, SET, not_27_out, not_28_out, not_29_out);
  or or_1 (Q2, and_1_out, and_2_out, and_3_out);
  or or_2 (Q1, and_4_out, and_5_out, and_6_out);
  or or_3 (Q0, and_7_out, and_8_out, and_9_out, and_10_out);
endmodule

module select_zone (
  input  CYCLEZONE,
  input  Reset,
  output [2:0] codeZ
);

  wire clock_1_out, transition_zone_1_q0, transition_zone_1_q1, transition_zone_1_q2;

  transition_zone transition_zone_1 (
    .SET(CYCLEZONE), .RESET(Reset), .P2(codeZ[2]), .P1(codeZ[1]), .P0(codeZ[0]), .Q2(transition_zone_1_q2),
    .Q1(transition_zone_1_q1), .Q0(transition_zone_1_q0));
  D_Flip_Flop d_ff_1 (.D(transition_zone_1_q2), .clk(clock_1_out), .Q(codeZ[2]));  // open: Qn, preset, reset
  D_Flip_Flop d_ff_2 (.D(transition_zone_1_q1), .clk(clock_1_out), .Q(codeZ[1]));  // open: Qn, preset, reset
  D_Flip_Flop d_ff_3 (.D(transition_zone_1_q0), .clk(clock_1_out), .Q(codeZ[0]));  // open: Qn, preset, reset
  Clock clock_1 (.out(clock_1_out));
endmodule

module filterZone (
  input  [2:0] zoneCode,
  output [7:0] ZONE,
  output NEG
);

  Multiplexer #(.select(3), .width(8), .enable("false")) multiplexer_1 (
    .in0({8{1'b0}}), .in1(8'h3), .in2(8'h4), .in3(8'h6), .in4(8'h11), .in5(8'h12), .in6({8{1'b0}}),
    .in7({8{1'b0}}), .out(ZONE), .sel(zoneCode));
  Multiplexer #(.select(3), .enable("false")) multiplexer_2 (
    .in0(1'b0), .in1(1'b0), .in2(1'b1), .in3(1'b1), .in4(1'b0), .in5(1'b1), .in6(1'b0), .in7(1'b0),
    .out(NEG), .sel(zoneCode));
endmodule
